// Logisim project cpu24-EX气泡流水线.circ as structural Verilog: 18 circuits, main circuit ◇单周期MIPS
module \单周期MIPS  (
  input  IR1,
  input  IR2,
  input  IR3,
  output RegWrite,
  output MemWrite,
  output [31:0] PC,
  output [31:0] IR,
  output [31:0] RDin,
  output [31:0] MDin,
  output [31:0] LedData
);

  wire and_1_out, CLK, clock_2_out, comparator_1_eq, comparator_1_lt, d_ff_1_q, EN, equal, Go, IR1_t, IR2_t,
       IR3_t, IRA, IRB, IRC, multiplexer_11_out, nand_1_out, not_1_out, or_4_out, or_5_out, RST, SignedExt,
       Syscall, W1, W2, W3, \单周期硬布线控制器_1_alu_src , \单周期硬布线控制器_1_beq , \单周期硬布线控制器_1_bne , \单周期硬布线控制器_1_jal ,
       \单周期硬布线控制器_1_jmp , \单周期硬布线控制器_1_jr , \单周期硬布线控制器_1_memtoreg , \单周期硬布线控制器_1_regdst ;
  wire [3:0] \单周期硬布线控制器_1_alu_op ;
  wire [4:0] multiplexer_4_out, multiplexer_5_out, multiplexer_6_out, multiplexer_7_out;
  wire [12:0] CNT_num;
  wire [15:0] \总周期数 ;
  wire [31:0] bit_extender_1_out, BR_ADDR, JR_ADDR, mips_alu_1_result, multiplexer_1_out, multiplexer_2_out,
       multiplexer_3_out, multiplexer_8_out, multiplexer_9_out, multiplexer_10_out, PC_4, ram_1_data,
       shifter_1_out;

  Button button_1 (.out(RST));
  Clock #(.highDuration(1), .lowDuration(1)) clock_1 ();  // open: out
  Button _1 (.out(IRA));
  Button _2 (.out(IRB));
  Button _3 (.out(IRC));
  Button \u_继续运行  (.out(Go));
  LED #(.active("true")) led_1 (.in(W1));
  LED #(.active("true")) led_2 (.in(W2));
  LED #(.active("true")) led_3 (.in(W3));
  Multiplexer #(.select(1), .width(32), .disabled("Z"), .enable("false")) multiplexer_1 (
    .in0({PC[31:28], IR[25:0], 2'b00}), .in1(JR_ADDR), .out(multiplexer_1_out), .sel(\单周期硬布线控制器_1_jr ));
  D_Flip_Flop #(.trigger("high"), .Pre_Clr_Positions("LEGACY"), .NegatePresetClear("false"), .enable("true"), .NewFFLayout("false")) d_ff_1 (.Q(d_ff_1_q));  // open: clk, D, Qn, preset, en, reset
  Hex_Digit_Display hex_digit_display_1 (.value(LedData[31:28]));  // open: dp
  Adder #(.width(32)) adder_1 (.a(PC), .b(32'h4), .out(PC_4));  // open: cin, cout
  // Probe on 13'hc
  Hex_Digit_Display hex_digit_display_2 (.value(LedData[27:24]));  // open: dp
  Hex_Digit_Display hex_digit_display_3 (.value(LedData[23:20]));  // open: dp
  Multiplexer #(.select(1), .width(32), .disabled("Z"), .enable("false")) multiplexer_2 (
    .in0(PC_4), .in1(multiplexer_1_out), .out(multiplexer_2_out), .sel(\单周期硬布线控制器_1_jmp ));
  Comparator #(.width(13), .mode("twosComplement")) comparator_1 (
    .a(CNT_num), .b(13'hc), .eq(comparator_1_eq), .lt(comparator_1_lt));  // open: gt
  Clock #(.highDuration(1), .lowDuration(1)) clock_2 (.out(clock_2_out));
  Hex_Digit_Display hex_digit_display_4 (.value(LedData[15:12]));  // open: dp
  Hex_Digit_Display hex_digit_display_5 (.value(LedData[19:16]));  // open: dp
  Multiplexer #(.select(1), .width(32), .disabled("Z"), .enable("false")) multiplexer_3 (
    .in0(multiplexer_2_out), .in1(BR_ADDR), .out(multiplexer_3_out), .sel(multiplexer_11_out));
  Hex_Digit_Display hex_digit_display_6 (.value(LedData[11:8]));  // open: dp
  Hex_Digit_Display hex_digit_display_7 (.value(LedData[7:4]));  // open: dp
  // Probe on \总周期数 
  Register #(.width(32), .trigger("rising"), .Select("low")) u_PC (
    .D(multiplexer_3_out), .en(EN), .Q(PC), .clk(CLK), .clr(RST));
  nand nand_1 (nand_1_out, d_ff_1_q, comparator_1_eq);
  Counter #(.width(13), .max('h1fff), .ongoal("stay"), .trigger("rising"), .behavior("old")) counter_1 (
    .count(comparator_1_lt), .Q(CNT_num), .clk(clock_2_out));  // open: load, D, carry, clr, preset
  Hex_Digit_Display hex_digit_display_8 (.value(LedData[3:0]));  // open: dp
  assign CLK = nand_1_out ? clock_2_out : 1'bz;  // Controlled_Buffer controlled_buffer_1
  ROM #(.addrWidth(10), .dataWidth(32), .Select("high")) rom_1 (.addr(PC[11:2]), .data(IR));
  Pull_Resistor #(.pull(1)) pull_resistor_1 (.node(CLK));
  or or_1 (IR1_t, IR1, IRA);
  // Mips_Probe mips_probe_1: pin names not known; wires that end beside it: IR
  or or_2 (IR2_t, IR2, IRB);
  \单周期硬布线控制器  \u_单周期硬布线控制器_1  (
    .Func(IR[5:0]), .OP(IR[31:26]), .ALU_OP(\单周期硬布线控制器_1_alu_op ), .MemToReg(\单周期硬布线控制器_1_memtoreg ),
    .MemWrite(MemWrite), .ALU_SRC(\单周期硬布线控制器_1_alu_src ), .RegWrite(RegWrite), .SysCALL(Syscall),
    .SignedExt(SignedExt), .RegDst(\单周期硬布线控制器_1_regdst ), .JR(\单周期硬布线控制器_1_jr ), .JMP(\单周期硬布线控制器_1_jmp ),
    .Beq(\单周期硬布线控制器_1_beq ), .JAL(\单周期硬布线控制器_1_jal ), .Bne(\单周期硬布线控制器_1_bne ));
  Multiplexer #(.select(1), .width(5), .disabled("Z"), .enable("false")) multiplexer_4 (
    .in0(IR[25:21]), .in1(5'b00010), .out(multiplexer_4_out), .sel(Syscall));
  Multiplexer #(.select(1), .width(5), .disabled("Z"), .enable("false")) multiplexer_5 (
    .in0(IR[20:16]), .in1(5'b00100), .out(multiplexer_5_out), .sel(Syscall));
  Multiplexer #(.select(1), .width(5), .disabled("Z"), .enable("false")) multiplexer_6 (
    .in0(IR[20:16]), .in1(IR[15:11]), .out(multiplexer_6_out), .sel(\单周期硬布线控制器_1_regdst ));
  Multiplexer #(.select(1), .width(5), .disabled("Z"), .enable("false")) multiplexer_7 (
    .in0(multiplexer_6_out), .in1({5{1'b1}}), .out(multiplexer_7_out), .sel(\单周期硬布线控制器_1_jal ));
  not not_1 (not_1_out, Syscall);
  or or_3 (IR3_t, IR3, IRC);
  MIPS_Regifile mips_regifile_1 (
    .Din(RDin), .Clk(CLK), .R1(JR_ADDR), .R2(MDin), .WE(RegWrite), .W_num(multiplexer_7_out),
    .R1_num(multiplexer_4_out), .R2_num(multiplexer_5_out));
  assign bit_extender_1_out = {{16{IR[15]}}, IR[15:0]};  // Bit_Extender bit_extender_1
  or or_4 (or_4_out, not_1_out, Go);
  or or_5 (or_5_out, equal, not_1_out);
  Multiplexer #(.select(1), .width(32), .disabled("Z"), .enable("false")) multiplexer_8 (
    .in0(MDin), .in1(bit_extender_1_out), .out(multiplexer_8_out), .sel(\单周期硬布线控制器_1_alu_src ));
  D_Flip_Flop #(.trigger("falling"), .Pre_Clr_Positions("ABOVE_BELOW"), .NegatePresetClear("false"), .enable("false"), .NewFFLayout("true")) d_ff_2 (
    .clk(CLK), .D(or_5_out), .Q(EN), .preset(or_4_out));  // open: Qn, reset
  Multiplexer #(.select(1), .width(32), .disabled("Z"), .enable("false")) multiplexer_9 (
    .in0(multiplexer_8_out), .in1(32'h22), .out(multiplexer_9_out), .sel(Syscall));
  Shifter #(.width(32), .shift("ll")) shifter_1 (.in(bit_extender_1_out), .\dist (5'b00010), .out(shifter_1_out));
  MIPS_ALU mips_alu_1 (
    .X(JR_ADDR), .Y(multiplexer_9_out), .AluOP(\单周期硬布线控制器_1_alu_op ), .Equal(equal),
    .Result(mips_alu_1_result), .shamt(IR[10:6]));  // open: Result_2
  Adder #(.width(32)) adder_2 (.a(shifter_1_out), .b(PC_4), .out(BR_ADDR));  // open: cin, cout
  Counter #(.width(16), .max('hffff), .ongoal("wrap"), .trigger("rising"), .behavior("new")) counter_2 (
    .count(EN), .Q(\总周期数 ), .clk(CLK), .clr(RST));  // open: load, D, carry, preset, down
  Multiplexer #(.select(1), .width(32), .disabled("Z"), .enable("false")) multiplexer_10 (
    .in0(mips_alu_1_result), .in1(ram_1_data), .out(multiplexer_10_out), .sel(\单周期硬布线控制器_1_memtoreg ));
  RAM #(.addrWidth(10), .dataWidth(32), .bus("separate"), .Select("high")) ram_1 (
    .addr(mips_alu_1_result[11:2]), .din(MDin), .data(ram_1_data), .str(MemWrite), .clk(CLK), .clr(RST));  // open: sel, ld
  and and_1 (and_1_out, Syscall, equal);
  Register #(.width(32), .trigger("rising"), .Select("low")) register_1 (
    .D(MDin), .en(and_1_out), .Q(LedData), .clk(CLK), .clr(RST));
  Multiplexer #(.select(1), .width(1), .disabled("Z"), .enable("false")) multiplexer_11 (
    .in0(\单周期硬布线控制器_1_bne ), .in1(\单周期硬布线控制器_1_beq ), .out(multiplexer_11_out), .sel(equal));
  Multiplexer #(.select(1), .width(32), .disabled("Z"), .enable("false")) multiplexer_12 (
    .in0(multiplexer_10_out), .in1(PC_4), .out(RDin), .sel(\单周期硬布线控制器_1_jal ));

  // Other names for the same wires on the sheet: Func[5:0] = IR[5:0]; J_ADDR[31:2] = {PC[31:28], IR[25:0]};
  //   offset[25:0] = IR[25:0]; OP[5:0] = IR[31:26]

  // Notes on the sheet:
  //   中断源
  //   中断等待指示
  //   总复位信号应将除ROM以外所有存储组件全部清零
  //   控制位
  //   暂停节拍，不能为0
  //   用这个时钟源需要去掉电路中的其他时钟源
  //   戳工具置1进入计数暂停模式，ctrl+k时钟自动运行到对应节拍暂停
  //   ctrl+k关闭时钟连续运行，将控制位置零，进入单步调试模式调试
  //   数码管输出
  //   数码管输出应该用寄存器锁存，否则显示数据只能一闪而过
  //   指令存储器
  //   指令字
  //   contents of rom_1 (hex, n*v repeats v):
  //   20110001 8000c05 20110001 20120002 20130003 8000c09 20110001 20120002 20130003 8000c0d 20110001
  //   20120002 20130003 8000c11 20110001 20120002 20130003 c000cb8 20100001 20110001 118fc0 112020
  //   20020022 c 118882 12200001 8000c15 112020 20020022 c 20110001 118880 112020 20020022 c 12200001
  //   8000c1f 20110001 118fc0 112020 20020022 c 1188c3 112020 20020022 c 118903 112020 20020022 c 118903
  //   112020 20020022 c 118903 112020 20020022 c 118903 112020 20020022 c 118903 112020 20020022 c 118903
  //   112020 20020022 c 118903 112020 20020022 c 20100001 109fc0 139fc3 8021 2012000c 24160003 26100001
  //   3210000f 20080008 20090001 139900 2709825 132020 20020022 c 1094022 1500fff9 22100001 2018000f
  //   2188024 108700 20080008 20090001 139902 2709825 132021 20020022 c 1094022 1500fff9 108702 2c9b022
  //   12c00001 8000c50 4020 1084027 84400 3508ffff 82021 20020022 c 2010ffff 20110000 ae300000 22100001
  //   22310004 ae300000 22100001 22310004 ae300000 22100001 22310004 ae300000 22100001 22310004 ae300000
  //   22100001 22310004 ae300000 22100001 22310004 ae300000 22100001 22310004 ae300000 22100001 22310004
  //   ae300000 22100001 22310004 ae300000 22100001 22310004 ae300000 22100001 22310004 ae300000 22100001
  //   22310004 ae300000 22100001 22310004 ae300000 22100001 22310004 ae300000 22100001 22310004 ae300000
  //   22100001 22310004 22100001 8020 2011003c 8e130000 8e340000 274402a 11000002 ae330000 ae140000
  //   2231fffc 1611fff8 102020 20020022 c 22100004 2011003c 1611fff2 20020032 c 20100000 22100001 102020
  //   20020022 c 22100002 102020 20020022 c 22100003 102020 20020022 c 22100004 102020 20020022 c 22100005
  //   102020 20020022 c 22100006 102020 20020022 c 22100007 102020 20020022 c 22100008 102020 20020022
  //   20020022 c 3e00008
  //   可计数暂停的时钟源
  //   JMP
  //   JR
  //   OP
  //   Func
  //   rs
  //   rt
  //   rd
  //   Beq
  //   Bne
  //   AluOP
  //   AluSrcB
  //   RegWrite
  //   JAL
  //   RegDst
  //   Syscall
  //   MemToReg
  //   MemWrite
  //   为方便自动评测，需要输出PC，IR，寄存器堆写如数据RDin
  //   RAM写使能MemWrite、RAM写入数据MDin等信号
  //   单周期MIPS
  //   控制与调试模块
endmodule

// 单周期硬布线控制器
module \单周期硬布线控制器  (
  input  [5:0] OP,
  input  [5:0] Func,
  output [3:0] ALU_OP,
  output MemToReg,
  output MemWrite,
  output ALU_SRC,
  output RegWrite,
  output SysCALL,
  output SignedExt,
  output RegDst,
  output Beq,
  output Bne,
  output JR,
  output JMP,
  output JAL
);

  \运算控制器自动生成  \u_运算控制器自动生成_1  (
    .OP0(OP[0]), .OP1(OP[1]), .OP2(OP[2]), .OP3(OP[3]), .OP4(OP[4]), .OP5(OP[5]), .F0(Func[0]), .F1(Func[1]),
    .F2(Func[2]), .F3(Func[3]), .F4(Func[4]), .F5(Func[5]), .S0(ALU_OP[0]), .S1(ALU_OP[1]), .S2(ALU_OP[2]),
    .S3(ALU_OP[3]));
  \控制信号自动生成  \u_控制信号自动生成_1  (
    .OP0(OP[0]), .OP1(OP[1]), .OP2(OP[2]), .OP3(OP[3]), .OP4(OP[4]), .OP5(OP[5]), .F0(Func[0]), .F1(Func[1]),
    .F2(Func[2]), .F3(Func[3]), .F4(Func[4]), .F5(Func[5]), .MemToReg(MemToReg), .MemWrite(MemWrite),
    .ALU_SRC(ALU_SRC), .RegWrite(RegWrite), .SysCALL(SysCALL), .SignedExt(SignedExt), .RegDst(RegDst),
    .BEQ(Beq), .BNE(Bne), .JR(JR), .JUMP(JMP), .JAL(JAL));

  // Other names for the same wires on the sheet: OP_CODE[5:0] = OP

  // Notes on the sheet:
  //   运算器控制器，根据指令生成运算器功能选择信号
  //   控制信号生成，产生数据通路需要的其他控制信号
endmodule

// 运算器控制器
module \运算控制器自动生成  (
  input  OP0,
  input  OP1,
  input  OP2,
  input  OP3,
  input  OP4,
  input  OP5,
  input  F0,
  input  F1,
  input  F2,
  input  F3,
  input  F4,
  input  F5,
  output S0,
  output S1,
  output S2,
  output S3
);

  wire and_1_out, and_2_out, and_3_out, and_4_out, and_5_out, and_6_out, and_7_out, and_8_out, and_9_out,
       and_10_out, and_11_out, and_12_out, and_13_out, and_14_out, and_15_out, and_16_out, and_17_out,
       and_18_out, and_19_out, and_20_out, and_21_out, and_22_out, and_23_out, and_24_out, and_25_out,
       and_26_out, and_27_out, and_28_out, and_29_out, and_30_out, and_31_out, and_32_out, and_33_out,
       and_34_out, not_1_out, not_2_out, not_3_out, not_4_out, not_5_out, not_6_out, not_7_out, not_8_out,
       not_9_out, not_10_out, not_11_out, not_12_out, not_13_out, not_14_out, not_15_out, not_16_out,
       not_17_out, not_18_out, not_19_out, not_20_out, not_21_out, not_22_out, not_23_out, not_24_out,
       not_25_out, not_26_out, not_27_out, not_28_out, not_29_out, not_30_out, not_31_out, not_32_out,
       not_33_out, not_34_out, not_35_out, not_36_out, not_37_out, not_38_out, not_39_out, not_40_out,
       not_41_out, not_42_out, not_43_out, not_44_out, not_45_out, not_46_out, not_47_out, not_48_out,
       not_49_out, not_50_out, not_51_out, not_52_out, not_53_out, not_54_out, not_55_out, not_56_out,
       not_57_out, not_58_out, not_59_out, not_60_out, not_61_out, not_62_out, not_63_out, not_64_out,
       not_65_out, not_66_out, not_67_out, not_68_out, not_69_out, not_70_out, not_71_out, not_72_out,
       not_73_out, not_74_out, not_75_out, not_76_out, not_77_out, not_78_out, not_79_out, not_80_out,
       not_81_out, not_82_out, not_83_out, not_84_out, not_85_out, not_86_out, not_87_out, not_88_out,
       not_89_out, not_90_out, not_91_out, not_92_out, not_93_out, not_94_out, not_95_out, not_96_out,
       not_97_out, not_98_out, not_99_out, not_100_out, not_101_out, not_102_out, not_103_out, not_104_out,
       not_105_out, not_106_out, not_107_out, not_108_out, not_109_out, not_110_out, not_111_out,
       not_112_out, not_113_out, not_114_out, not_115_out, not_116_out, not_117_out, not_118_out,
       not_119_out, not_120_out, not_121_out, not_122_out, not_123_out, not_124_out, not_125_out,
       not_126_out, not_127_out, not_128_out, not_129_out, not_130_out, not_131_out, not_132_out,
       not_133_out, not_134_out, not_135_out, not_136_out, not_137_out, not_138_out, not_139_out,
       not_140_out, not_141_out, not_142_out, not_143_out, not_144_out, not_145_out, not_146_out,
       not_147_out, not_148_out, not_149_out, not_150_out, not_151_out, not_152_out, not_153_out,
       not_154_out, not_155_out, not_156_out, not_157_out, not_158_out, not_159_out, not_160_out,
       not_161_out, not_162_out, not_163_out, not_164_out, not_165_out, not_166_out, not_167_out,
       not_168_out, not_169_out, not_170_out, not_171_out, not_172_out, not_173_out, not_174_out,
       not_175_out, not_176_out, not_177_out, not_178_out, not_179_out, not_180_out, not_181_out,
       not_182_out, not_183_out, not_184_out, not_185_out, not_186_out, not_187_out, not_188_out,
       not_189_out, not_190_out, not_191_out, not_192_out, not_193_out, not_194_out, not_195_out,
       not_196_out, not_197_out, not_198_out, not_199_out, not_200_out, not_201_out, not_202_out,
       not_203_out, not_204_out, not_205_out, not_206_out, not_207_out, not_208_out, not_209_out,
       not_210_out, not_211_out, not_212_out, not_213_out, not_214_out, not_215_out, not_216_out,
       not_217_out, not_218_out, not_219_out, not_220_out, not_221_out, not_222_out, not_223_out,
       not_224_out, not_225_out, not_226_out, not_227_out, not_228_out, not_229_out, not_230_out,
       not_231_out, not_232_out, not_233_out, not_234_out, not_235_out, not_236_out;

  not not_1 (not_1_out, OP5);
  not not_2 (not_2_out, OP4);
  not not_3 (not_3_out, OP3);
  not not_4 (not_4_out, OP2);
  not not_5 (not_5_out, OP1);
  not not_6 (not_6_out, OP0);
  not not_7 (not_7_out, F5);
  not not_8 (not_8_out, F4);
  not not_9 (not_9_out, F3);
  not not_10 (not_10_out, F2);
  not not_11 (not_11_out, OP5);
  not not_12 (not_12_out, OP4);
  not not_13 (not_13_out, OP3);
  not not_14 (not_14_out, OP2);
  not not_15 (not_15_out, OP1);
  not not_16 (not_16_out, OP0);
  not not_17 (not_17_out, F4);
  not not_18 (not_18_out, F3);
  not not_19 (not_19_out, F2);
  not not_20 (not_20_out, F1);
  not not_21 (not_21_out, F0);
  not not_22 (not_22_out, OP5);
  not not_23 (not_23_out, OP4);
  not not_24 (not_24_out, OP3);
  not not_25 (not_25_out, OP2);
  not not_26 (not_26_out, OP1);
  not not_27 (not_27_out, OP0);
  not not_28 (not_28_out, F4);
  not not_29 (not_29_out, F3);
  not not_30 (not_30_out, F2);
  not not_31 (not_31_out, F1);
  not not_32 (not_32_out, OP5);
  not not_33 (not_33_out, OP4);
  not not_34 (not_34_out, OP3);
  not not_35 (not_35_out, OP2);
  not not_36 (not_36_out, OP1);
  not not_37 (not_37_out, OP0);
  not not_38 (not_38_out, F4);
  not not_39 (not_39_out, F3);
  not not_40 (not_40_out, F1);
  not not_41 (not_41_out, F0);
  not not_42 (not_42_out, OP5);
  not not_43 (not_43_out, OP4);
  not not_44 (not_44_out, OP3);
  not not_45 (not_45_out, OP2);
  not not_46 (not_46_out, OP1);
  not not_47 (not_47_out, OP0);
  not not_48 (not_48_out, F4);
  not not_49 (not_49_out, F2);
  not not_50 (not_50_out, F0);
  not not_51 (not_51_out, OP5);
  not not_52 (not_52_out, OP4);
  not not_53 (not_53_out, OP2);
  not not_54 (not_54_out, OP1);
  not not_55 (not_55_out, OP0);
  not not_56 (not_56_out, OP5);
  not not_57 (not_57_out, OP4);
  not not_58 (not_58_out, OP1);
  not not_59 (not_59_out, OP0);
  not not_60 (not_60_out, OP5);
  not not_61 (not_61_out, OP4);
  not not_62 (not_62_out, OP2);
  not not_63 (not_63_out, OP1);
  not not_64 (not_64_out, OP5);
  not not_65 (not_65_out, OP4);
  not not_66 (not_66_out, OP2);
  not not_67 (not_67_out, OP0);
  not not_68 (not_68_out, OP4);
  not not_69 (not_69_out, OP3);
  not not_70 (not_70_out, OP2);
  not not_71 (not_71_out, OP4);
  not not_72 (not_72_out, OP2);
  not not_73 (not_73_out, OP5);
  not not_74 (not_74_out, OP4);
  not not_75 (not_75_out, OP3);
  not not_76 (not_76_out, OP2);
  not not_77 (not_77_out, OP1);
  not not_78 (not_78_out, OP0);
  not not_79 (not_79_out, F5);
  not not_80 (not_80_out, F4);
  not not_81 (not_81_out, F3);
  not not_82 (not_82_out, F2);
  not not_83 (not_83_out, F0);
  not not_84 (not_84_out, OP5);
  not not_85 (not_85_out, OP4);
  not not_86 (not_86_out, OP3);
  not not_87 (not_87_out, OP2);
  not not_88 (not_88_out, OP1);
  not not_89 (not_89_out, OP0);
  not not_90 (not_90_out, F4);
  not not_91 (not_91_out, F3);
  not not_92 (not_92_out, F2);
  not not_93 (not_93_out, F0);
  not not_94 (not_94_out, OP5);
  not not_95 (not_95_out, OP4);
  not not_96 (not_96_out, OP3);
  not not_97 (not_97_out, OP2);
  not not_98 (not_98_out, OP1);
  not not_99 (not_99_out, OP0);
  not not_100 (not_100_out, F4);
  not not_101 (not_101_out, F3);
  not not_102 (not_102_out, F1);
  not not_103 (not_103_out, F0);
  not not_104 (not_104_out, OP5);
  not not_105 (not_105_out, OP4);
  not not_106 (not_106_out, OP3);
  not not_107 (not_107_out, OP2);
  not not_108 (not_108_out, OP1);
  not not_109 (not_109_out, OP0);
  not not_110 (not_110_out, F4);
  not not_111 (not_111_out, F3);
  not not_112 (not_112_out, OP5);
  not not_113 (not_113_out, OP4);
  not not_114 (not_114_out, OP3);
  not not_115 (not_115_out, OP2);
  not not_116 (not_116_out, OP1);
  not not_117 (not_117_out, OP0);
  not not_118 (not_118_out, F4);
  not not_119 (not_119_out, F2);
  not not_120 (not_120_out, F0);
  not not_121 (not_121_out, OP5);
  not not_122 (not_122_out, OP4);
  not not_123 (not_123_out, OP1);
  not not_124 (not_124_out, OP0);
  not not_125 (not_125_out, OP5);
  not not_126 (not_126_out, OP4);
  not not_127 (not_127_out, OP2);
  not not_128 (not_128_out, OP0);
  not not_129 (not_129_out, OP5);
  not not_130 (not_130_out, OP4);
  not not_131 (not_131_out, OP3);
  not not_132 (not_132_out, OP2);
  not not_133 (not_133_out, OP1);
  not not_134 (not_134_out, OP0);
  not not_135 (not_135_out, F4);
  not not_136 (not_136_out, F3);
  not not_137 (not_137_out, F2);
  not not_138 (not_138_out, F1);
  not not_139 (not_139_out, F0);
  not not_140 (not_140_out, OP5);
  not not_141 (not_141_out, OP4);
  not not_142 (not_142_out, OP3);
  not not_143 (not_143_out, OP2);
  not not_144 (not_144_out, OP1);
  not not_145 (not_145_out, OP0);
  not not_146 (not_146_out, F4);
  not not_147 (not_147_out, F3);
  not not_148 (not_148_out, F2);
  not not_149 (not_149_out, F1);
  not not_150 (not_150_out, OP5);
  not not_151 (not_151_out, OP4);
  not not_152 (not_152_out, OP3);
  not not_153 (not_153_out, OP2);
  not not_154 (not_154_out, OP1);
  not not_155 (not_155_out, OP0);
  not not_156 (not_156_out, F4);
  not not_157 (not_157_out, F3);
  not not_158 (not_158_out, F2);
  not not_159 (not_159_out, F0);
  not not_160 (not_160_out, OP5);
  not not_161 (not_161_out, OP4);
  not not_162 (not_162_out, OP3);
  not not_163 (not_163_out, OP2);
  not not_164 (not_164_out, OP1);
  not not_165 (not_165_out, OP0);
  not not_166 (not_166_out, F4);
  not not_167 (not_167_out, F3);
  not not_168 (not_168_out, F1);
  not not_169 (not_169_out, F0);
  not not_170 (not_170_out, OP5);
  not not_171 (not_171_out, OP4);
  not not_172 (not_172_out, OP3);
  not not_173 (not_173_out, OP2);
  not not_174 (not_174_out, OP1);
  not not_175 (not_175_out, OP0);
  not not_176 (not_176_out, F4);
  not not_177 (not_177_out, F2);
  not not_178 (not_178_out, OP5);
  not not_179 (not_179_out, OP4);
  not not_180 (not_180_out, OP2);
  not not_181 (not_181_out, OP1);
  not not_182 (not_182_out, OP0);
  not not_183 (not_183_out, OP5);
  not not_184 (not_184_out, OP4);
  not not_185 (not_185_out, OP1);
  not not_186 (not_186_out, OP0);
  not not_187 (not_187_out, OP5);
  not not_188 (not_188_out, OP4);
  not not_189 (not_189_out, OP2);
  not not_190 (not_190_out, OP1);
  not not_191 (not_191_out, OP4);
  not not_192 (not_192_out, OP3);
  not not_193 (not_193_out, OP2);
  not not_194 (not_194_out, OP4);
  not not_195 (not_195_out, OP2);
  not not_196 (not_196_out, OP5);
  not not_197 (not_197_out, OP4);
  not not_198 (not_198_out, OP3);
  not not_199 (not_199_out, OP2);
  not not_200 (not_200_out, OP1);
  not not_201 (not_201_out, OP0);
  not not_202 (not_202_out, F4);
  not not_203 (not_203_out, F3);
  not not_204 (not_204_out, F1);
  not not_205 (not_205_out, OP5);
  not not_206 (not_206_out, OP4);
  not not_207 (not_207_out, OP3);
  not not_208 (not_208_out, OP2);
  not not_209 (not_209_out, OP1);
  not not_210 (not_210_out, OP0);
  not not_211 (not_211_out, F4);
  not not_212 (not_212_out, F3);
  not not_213 (not_213_out, OP5);
  not not_214 (not_214_out, OP4);
  not not_215 (not_215_out, OP3);
  not not_216 (not_216_out, OP2);
  not not_217 (not_217_out, OP1);
  not not_218 (not_218_out, OP0);
  not not_219 (not_219_out, F4);
  not not_220 (not_220_out, F2);
  not not_221 (not_221_out, F0);
  not not_222 (not_222_out, OP5);
  not not_223 (not_223_out, OP4);
  not not_224 (not_224_out, OP3);
  not not_225 (not_225_out, OP2);
  not not_226 (not_226_out, OP1);
  not not_227 (not_227_out, OP0);
  not not_228 (not_228_out, F4);
  not not_229 (not_229_out, F2);
  not not_230 (not_230_out, OP5);
  not not_231 (not_231_out, OP4);
  not not_232 (not_232_out, OP2);
  not not_233 (not_233_out, OP0);
  not not_234 (not_234_out, OP5);
  not not_235 (not_235_out, OP4);
  not not_236 (not_236_out, OP1);
  and and_1 (and_1_out, not_1_out, not_2_out, not_3_out, not_4_out, not_5_out, not_6_out, not_7_out, not_8_out, not_9_out, not_10_out, F1, F0);
  and and_2 (and_2_out, not_11_out, not_12_out, not_13_out, not_14_out, not_15_out, not_16_out, F5, not_17_out, not_18_out, not_19_out, not_20_out, not_21_out);
  and and_3 (and_3_out, not_22_out, not_23_out, not_24_out, not_25_out, not_26_out, not_27_out, F5, not_28_out, not_29_out, not_30_out, not_31_out, F0);
  and and_4 (and_4_out, not_32_out, not_33_out, not_34_out, not_35_out, not_36_out, not_37_out, F5, not_38_out, not_39_out, F2, not_40_out, not_41_out);
  and and_5 (and_5_out, not_42_out, not_43_out, not_44_out, not_45_out, not_46_out, not_47_out, F5, not_48_out, F3, not_49_out, F1, not_50_out);
  and and_6 (and_6_out, not_51_out, not_52_out, OP3, not_53_out, not_54_out, not_55_out);
  and and_7 (and_7_out, not_56_out, not_57_out, OP3, OP2, not_58_out, not_59_out);
  and and_8 (and_8_out, not_60_out, not_61_out, OP3, not_62_out, not_63_out, OP0);
  and and_9 (and_9_out, not_64_out, not_65_out, OP3, not_66_out, OP1, not_67_out);
  and and_10 (and_10_out, OP5, not_68_out, not_69_out, not_70_out, OP1, OP0);
  and and_11 (and_11_out, OP5, not_71_out, OP3, not_72_out, OP1, OP0);
  and and_12 (and_12_out, not_73_out, not_74_out, not_75_out, not_76_out, not_77_out, not_78_out, not_79_out, not_80_out, not_81_out, not_82_out, F1, not_83_out);
  and and_13 (and_13_out, not_84_out, not_85_out, not_86_out, not_87_out, not_88_out, not_89_out, F5, not_90_out, not_91_out, not_92_out, F1, not_93_out);
  and and_14 (and_14_out, not_94_out, not_95_out, not_96_out, not_97_out, not_98_out, not_99_out, F5, not_100_out, not_101_out, F2, not_102_out, not_103_out);
  and and_15 (and_15_out, not_104_out, not_105_out, not_106_out, not_107_out, not_108_out, not_109_out, F5, not_110_out, not_111_out, F2, F1, F0);
  and and_16 (and_16_out, not_112_out, not_113_out, not_114_out, not_115_out, not_116_out, not_117_out, F5, not_118_out, F3, not_119_out, F1, not_120_out);
  and and_17 (and_17_out, not_121_out, not_122_out, OP3, OP2, not_123_out, not_124_out);
  and and_18 (and_18_out, not_125_out, not_126_out, OP3, not_127_out, OP1, not_128_out);
  and and_19 (and_19_out, not_129_out, not_130_out, not_131_out, not_132_out, not_133_out, not_134_out, F5, not_135_out, not_136_out, not_137_out, not_138_out, not_139_out);
  and and_20 (and_20_out, not_140_out, not_141_out, not_142_out, not_143_out, not_144_out, not_145_out, F5, not_146_out, not_147_out, not_148_out, not_149_out, F0);
  and and_21 (and_21_out, not_150_out, not_151_out, not_152_out, not_153_out, not_154_out, not_155_out, F5, not_156_out, not_157_out, not_158_out, F1, not_159_out);
  and and_22 (and_22_out, not_160_out, not_161_out, not_162_out, not_163_out, not_164_out, not_165_out, F5, not_166_out, not_167_out, F2, not_168_out, not_169_out);
  and and_23 (and_23_out, not_170_out, not_171_out, not_172_out, not_173_out, not_174_out, not_175_out, F5, not_176_out, F3, not_177_out, F1, F0);
  and and_24 (and_24_out, not_178_out, not_179_out, OP3, not_180_out, not_181_out, not_182_out);
  and and_25 (and_25_out, not_183_out, not_184_out, OP3, OP2, not_185_out, not_186_out);
  and and_26 (and_26_out, not_187_out, not_188_out, OP3, not_189_out, not_190_out, OP0);
  and and_27 (and_27_out, OP5, not_191_out, not_192_out, not_193_out, OP1, OP0);
  and and_28 (and_28_out, OP5, not_194_out, OP3, not_195_out, OP1, OP0);
  and and_29 (and_29_out, not_196_out, not_197_out, not_198_out, not_199_out, not_200_out, not_201_out, F5, not_202_out, not_203_out, F2, not_204_out, F0);
  and and_30 (and_30_out, not_205_out, not_206_out, not_207_out, not_208_out, not_209_out, not_210_out, F5, not_211_out, not_212_out, F2, F1, F0);
  and and_31 (and_31_out, not_213_out, not_214_out, not_215_out, not_216_out, not_217_out, not_218_out, F5, not_219_out, F3, not_220_out, F1, not_221_out);
  and and_32 (and_32_out, not_222_out, not_223_out, not_224_out, not_225_out, not_226_out, not_227_out, F5, not_228_out, F3, not_229_out, F1, F0);
  and and_33 (and_33_out, not_230_out, not_231_out, OP3, not_232_out, OP1, not_233_out);
  and and_34 (and_34_out, not_234_out, not_235_out, OP3, OP2, not_236_out, OP0);
  or or_1 (S0, and_1_out, and_2_out, and_3_out, and_4_out, and_5_out, and_6_out, and_7_out, and_8_out, and_9_out, and_10_out, and_11_out);
  or or_2 (S1, and_12_out, and_13_out, and_14_out, and_15_out, and_16_out, and_17_out, and_18_out);
  or or_3 (S2, and_19_out, and_20_out, and_21_out, and_22_out, and_23_out, and_24_out, and_25_out, and_26_out, and_27_out, and_28_out);
  or or_4 (S3, and_29_out, and_30_out, and_31_out, and_32_out, and_33_out, and_34_out);
endmodule

// 控制信号生成
module \控制信号自动生成  (
  input  OP0,
  input  OP1,
  input  OP2,
  input  OP3,
  input  OP4,
  input  OP5,
  input  F0,
  input  F1,
  input  F2,
  input  F3,
  input  F4,
  input  F5,
  output MemToReg,
  output MemWrite,
  output ALU_SRC,
  output RegWrite,
  output SysCALL,
  output SignedExt,
  output RegDst,
  output BEQ,
  output BNE,
  output JR,
  output JUMP,
  output JAL
);

  wire and_3_out, and_4_out, and_5_out, and_6_out, and_7_out, and_8_out, and_9_out, and_10_out, and_11_out,
       and_12_out, and_13_out, and_14_out, and_15_out, and_16_out, and_17_out, and_18_out, and_19_out,
       and_20_out, and_21_out, and_22_out, and_23_out, and_25_out, and_26_out, and_27_out, and_28_out,
       and_29_out, and_30_out, and_31_out, and_32_out, and_33_out, and_34_out, and_35_out, and_36_out,
       and_37_out, and_38_out, and_39_out, and_40_out, and_41_out, and_45_out, and_46_out, and_47_out,
       not_1_out, not_2_out, not_3_out, not_4_out, not_5_out, not_6_out, not_7_out, not_8_out, not_9_out,
       not_10_out, not_11_out, not_12_out, not_13_out, not_14_out, not_15_out, not_16_out, not_17_out,
       not_18_out, not_19_out, not_20_out, not_21_out, not_22_out, not_23_out, not_24_out, not_25_out,
       not_26_out, not_27_out, not_28_out, not_29_out, not_30_out, not_31_out, not_32_out, not_33_out,
       not_34_out, not_35_out, not_36_out, not_37_out, not_38_out, not_39_out, not_40_out, not_41_out,
       not_42_out, not_43_out, not_44_out, not_45_out, not_46_out, not_47_out, not_48_out, not_49_out,
       not_50_out, not_51_out, not_52_out, not_53_out, not_54_out, not_55_out, not_56_out, not_57_out,
       not_58_out, not_59_out, not_60_out, not_61_out, not_62_out, not_63_out, not_64_out, not_65_out,
       not_66_out, not_67_out, not_68_out, not_69_out, not_70_out, not_71_out, not_72_out, not_73_out,
       not_74_out, not_75_out, not_76_out, not_77_out, not_78_out, not_79_out, not_80_out, not_81_out,
       not_82_out, not_83_out, not_84_out, not_85_out, not_86_out, not_87_out, not_88_out, not_89_out,
       not_90_out, not_91_out, not_92_out, not_93_out, not_94_out, not_95_out, not_96_out, not_97_out,
       not_98_out, not_99_out, not_100_out, not_101_out, not_102_out, not_103_out, not_104_out, not_105_out,
       not_106_out, not_107_out, not_108_out, not_109_out, not_110_out, not_111_out, not_112_out,
       not_113_out, not_114_out, not_115_out, not_116_out, not_117_out, not_118_out, not_119_out,
       not_120_out, not_121_out, not_122_out, not_123_out, not_124_out, not_125_out, not_126_out,
       not_127_out, not_128_out, not_129_out, not_130_out, not_131_out, not_132_out, not_133_out,
       not_134_out, not_135_out, not_136_out, not_137_out, not_138_out, not_139_out, not_140_out,
       not_141_out, not_142_out, not_143_out, not_144_out, not_145_out, not_146_out, not_147_out,
       not_148_out, not_149_out, not_150_out, not_151_out, not_152_out, not_153_out, not_154_out,
       not_155_out, not_156_out, not_157_out, not_158_out, not_159_out, not_160_out, not_161_out,
       not_162_out, not_163_out, not_164_out, not_165_out, not_166_out, not_167_out, not_168_out,
       not_169_out, not_170_out, not_171_out, not_172_out, not_173_out, not_174_out, not_175_out,
       not_176_out, not_177_out, not_178_out, not_179_out, not_180_out, not_181_out, not_182_out,
       not_183_out, not_184_out, not_185_out, not_186_out, not_187_out, not_188_out, not_189_out,
       not_190_out, not_191_out, not_192_out, not_193_out, not_194_out, not_195_out, not_196_out,
       not_197_out, not_198_out, not_199_out, not_200_out, not_201_out, not_202_out, not_203_out,
       not_204_out, not_205_out, not_206_out, not_207_out, not_208_out, not_209_out, not_210_out,
       not_211_out, not_212_out, not_213_out, not_214_out, not_215_out, not_216_out, not_217_out,
       not_218_out, not_219_out, not_220_out, not_221_out, not_222_out, not_223_out, not_224_out,
       not_225_out, not_226_out, not_227_out, not_228_out, not_229_out, not_230_out, not_231_out,
       not_232_out, not_233_out, not_234_out, not_235_out, not_236_out, not_237_out, not_238_out,
       not_239_out, not_240_out, not_241_out, not_242_out, not_243_out, not_244_out, not_245_out,
       not_246_out, not_247_out, not_248_out, not_249_out, not_250_out, not_251_out, not_252_out,
       not_253_out, not_254_out, not_255_out, not_256_out, not_257_out, not_258_out, not_259_out,
       not_260_out, not_261_out, not_262_out, not_263_out, not_264_out, not_265_out, not_266_out,
       not_267_out, not_268_out, not_269_out, not_270_out, not_271_out, not_272_out, not_273_out,
       not_274_out, not_275_out, not_276_out, not_277_out, not_278_out, not_279_out, not_280_out,
       not_281_out, not_282_out, not_283_out, not_284_out, not_285_out, not_286_out, not_287_out,
       not_288_out, not_289_out, not_290_out, not_291_out, not_292_out, not_293_out, not_294_out,
       not_295_out, not_296_out, not_297_out, not_298_out, not_299_out, not_300_out, not_301_out,
       not_302_out, not_303_out, not_304_out, not_305_out, not_306_out, not_307_out, not_308_out,
       not_309_out, not_310_out, not_311_out, not_312_out, not_313_out, not_314_out, not_315_out,
       not_316_out, not_317_out, not_318_out, not_319_out, not_320_out, not_321_out, not_322_out,
       not_323_out, not_324_out, not_325_out, not_326_out, not_327_out, not_328_out, not_329_out,
       not_330_out, not_331_out, not_332_out, not_333_out, not_334_out, not_335_out, not_336_out,
       not_337_out, not_338_out, not_339_out, not_340_out;

  not not_1 (not_1_out, OP4);
  not not_2 (not_2_out, OP3);
  not not_3 (not_3_out, OP2);
  not not_4 (not_4_out, OP2);
  not not_5 (not_5_out, OP4);
  not not_6 (not_6_out, OP0);
  not not_7 (not_7_out, OP2);
  not not_8 (not_8_out, OP4);
  not not_9 (not_9_out, OP5);
  not not_10 (not_10_out, OP1);
  not not_11 (not_11_out, OP4);
  not not_12 (not_12_out, OP5);
  not not_13 (not_13_out, OP2);
  not not_14 (not_14_out, OP4);
  not not_15 (not_15_out, OP5);
  not not_16 (not_16_out, OP4);
  not not_17 (not_17_out, OP3);
  not not_18 (not_18_out, OP2);
  not not_19 (not_19_out, OP1);
  not not_20 (not_20_out, OP0);
  not not_21 (not_21_out, F5);
  not not_22 (not_22_out, F4);
  not not_23 (not_23_out, F3);
  not not_24 (not_24_out, F2);
  not not_25 (not_25_out, F1);
  not not_26 (not_26_out, F0);
  not not_27 (not_27_out, OP5);
  not not_28 (not_28_out, OP4);
  not not_29 (not_29_out, OP3);
  not not_30 (not_30_out, OP2);
  not not_31 (not_31_out, OP1);
  not not_32 (not_32_out, OP0);
  not not_33 (not_33_out, F5);
  not not_34 (not_34_out, F4);
  not not_35 (not_35_out, F3);
  not not_36 (not_36_out, F2);
  not not_37 (not_37_out, OP5);
  not not_38 (not_38_out, OP4);
  not not_39 (not_39_out, OP3);
  not not_40 (not_40_out, OP2);
  not not_41 (not_41_out, OP1);
  not not_42 (not_42_out, OP0);
  not not_43 (not_43_out, F5);
  not not_44 (not_44_out, F4);
  not not_45 (not_45_out, F3);
  not not_46 (not_46_out, F2);
  not not_47 (not_47_out, F0);
  not not_48 (not_48_out, OP5);
  not not_49 (not_49_out, OP4);
  not not_50 (not_50_out, OP3);
  not not_51 (not_51_out, OP2);
  not not_52 (not_52_out, OP1);
  not not_53 (not_53_out, OP0);
  not not_54 (not_54_out, F4);
  not not_55 (not_55_out, F3);
  not not_56 (not_56_out, F2);
  not not_57 (not_57_out, F1);
  not not_58 (not_58_out, F0);
  not not_59 (not_59_out, OP5);
  not not_60 (not_60_out, OP4);
  not not_61 (not_61_out, OP3);
  not not_62 (not_62_out, OP2);
  not not_63 (not_63_out, OP1);
  not not_64 (not_64_out, OP0);
  not not_65 (not_65_out, F4);
  not not_66 (not_66_out, F3);
  not not_67 (not_67_out, F2);
  not not_68 (not_68_out, F1);
  not not_69 (not_69_out, OP5);
  not not_70 (not_70_out, OP4);
  not not_71 (not_71_out, OP3);
  not not_72 (not_72_out, OP2);
  not not_73 (not_73_out, OP1);
  not not_74 (not_74_out, OP0);
  not not_75 (not_75_out, F4);
  not not_76 (not_76_out, F3);
  not not_77 (not_77_out, F2);
  not not_78 (not_78_out, F0);
  not not_79 (not_79_out, OP5);
  not not_80 (not_80_out, OP4);
  not not_81 (not_81_out, OP3);
  not not_82 (not_82_out, OP2);
  not not_83 (not_83_out, OP1);
  not not_84 (not_84_out, OP0);
  not not_85 (not_85_out, F4);
  not not_86 (not_86_out, F3);
  not not_87 (not_87_out, F1);
  not not_88 (not_88_out, F0);
  not not_89 (not_89_out, OP5);
  not not_90 (not_90_out, OP4);
  not not_91 (not_91_out, OP3);
  not not_92 (not_92_out, OP2);
  not not_93 (not_93_out, OP1);
  not not_94 (not_94_out, OP0);
  not not_95 (not_95_out, F4);
  not not_96 (not_96_out, F3);
  not not_97 (not_97_out, F1);
  not not_98 (not_98_out, OP5);
  not not_99 (not_99_out, OP4);
  not not_100 (not_100_out, OP3);
  not not_101 (not_101_out, OP2);
  not not_102 (not_102_out, OP1);
  not not_103 (not_103_out, OP0);
  not not_104 (not_104_out, F4);
  not not_105 (not_105_out, F3);
  not not_106 (not_106_out, OP5);
  not not_107 (not_107_out, OP4);
  not not_108 (not_108_out, OP3);
  not not_109 (not_109_out, OP2);
  not not_110 (not_110_out, OP1);
  not not_111 (not_111_out, OP0);
  not not_112 (not_112_out, F4);
  not not_113 (not_113_out, F2);
  not not_114 (not_114_out, F0);
  not not_115 (not_115_out, OP5);
  not not_116 (not_116_out, OP4);
  not not_117 (not_117_out, OP3);
  not not_118 (not_118_out, OP2);
  not not_119 (not_119_out, OP1);
  not not_120 (not_120_out, OP0);
  not not_121 (not_121_out, F4);
  not not_122 (not_122_out, F2);
  not not_123 (not_123_out, OP5);
  not not_124 (not_124_out, OP4);
  not not_125 (not_125_out, OP3);
  not not_126 (not_126_out, OP2);
  not not_127 (not_127_out, OP5);
  not not_128 (not_128_out, OP4);
  not not_129 (not_129_out, OP2);
  not not_130 (not_130_out, OP1);
  not not_131 (not_131_out, OP0);
  not not_132 (not_132_out, OP5);
  not not_133 (not_133_out, OP4);
  not not_134 (not_134_out, OP1);
  not not_135 (not_135_out, OP0);
  not not_136 (not_136_out, OP5);
  not not_137 (not_137_out, OP4);
  not not_138 (not_138_out, OP2);
  not not_139 (not_139_out, OP1);
  not not_140 (not_140_out, OP5);
  not not_141 (not_141_out, OP4);
  not not_142 (not_142_out, OP2);
  not not_143 (not_143_out, OP0);
  not not_144 (not_144_out, OP5);
  not not_145 (not_145_out, OP4);
  not not_146 (not_146_out, OP1);
  not not_147 (not_147_out, OP4);
  not not_148 (not_148_out, OP3);
  not not_149 (not_149_out, OP2);
  not not_150 (not_150_out, OP0);
  not not_151 (not_151_out, OP1);
  not not_152 (not_152_out, OP2);
  not not_153 (not_153_out, OP3);
  not not_154 (not_154_out, OP4);
  not not_155 (not_155_out, OP5);
  not not_156 (not_156_out, F0);
  not not_157 (not_157_out, F1);
  not not_158 (not_158_out, F4);
  not not_159 (not_159_out, F5);
  not not_160 (not_160_out, OP5);
  not not_161 (not_161_out, OP4);
  not not_162 (not_162_out, OP2);
  not not_163 (not_163_out, OP1);
  not not_164 (not_164_out, OP0);
  not not_165 (not_165_out, OP5);
  not not_166 (not_166_out, OP4);
  not not_167 (not_167_out, OP2);
  not not_168 (not_168_out, OP1);
  not not_169 (not_169_out, OP5);
  not not_170 (not_170_out, OP4);
  not not_171 (not_171_out, OP2);
  not not_172 (not_172_out, OP0);
  not not_173 (not_173_out, OP4);
  not not_174 (not_174_out, OP3);
  not not_175 (not_175_out, OP2);
  not not_176 (not_176_out, OP4);
  not not_177 (not_177_out, OP2);
  not not_178 (not_178_out, OP5);
  not not_179 (not_179_out, OP4);
  not not_180 (not_180_out, OP3);
  not not_181 (not_181_out, OP2);
  not not_182 (not_182_out, OP1);
  not not_183 (not_183_out, OP0);
  not not_184 (not_184_out, F5);
  not not_185 (not_185_out, F4);
  not not_186 (not_186_out, F3);
  not not_187 (not_187_out, F2);
  not not_188 (not_188_out, F1);
  not not_189 (not_189_out, F0);
  not not_190 (not_190_out, OP5);
  not not_191 (not_191_out, OP4);
  not not_192 (not_192_out, OP3);
  not not_193 (not_193_out, OP2);
  not not_194 (not_194_out, OP1);
  not not_195 (not_195_out, OP0);
  not not_196 (not_196_out, F5);
  not not_197 (not_197_out, F4);
  not not_198 (not_198_out, F3);
  not not_199 (not_199_out, F2);
  not not_200 (not_200_out, OP5);
  not not_201 (not_201_out, OP4);
  not not_202 (not_202_out, OP3);
  not not_203 (not_203_out, OP2);
  not not_204 (not_204_out, OP1);
  not not_205 (not_205_out, OP0);
  not not_206 (not_206_out, F5);
  not not_207 (not_207_out, F4);
  not not_208 (not_208_out, F3);
  not not_209 (not_209_out, F2);
  not not_210 (not_210_out, F0);
  not not_211 (not_211_out, OP5);
  not not_212 (not_212_out, OP4);
  not not_213 (not_213_out, OP3);
  not not_214 (not_214_out, OP2);
  not not_215 (not_215_out, OP1);
  not not_216 (not_216_out, OP0);
  not not_217 (not_217_out, F4);
  not not_218 (not_218_out, F3);
  not not_219 (not_219_out, F2);
  not not_220 (not_220_out, F1);
  not not_221 (not_221_out, F0);
  not not_222 (not_222_out, OP5);
  not not_223 (not_223_out, OP4);
  not not_224 (not_224_out, OP3);
  not not_225 (not_225_out, OP2);
  not not_226 (not_226_out, OP1);
  not not_227 (not_227_out, OP0);
  not not_228 (not_228_out, F4);
  not not_229 (not_229_out, F3);
  not not_230 (not_230_out, F2);
  not not_231 (not_231_out, F1);
  not not_232 (not_232_out, OP5);
  not not_233 (not_233_out, OP4);
  not not_234 (not_234_out, OP3);
  not not_235 (not_235_out, OP2);
  not not_236 (not_236_out, OP1);
  not not_237 (not_237_out, OP0);
  not not_238 (not_238_out, F4);
  not not_239 (not_239_out, F3);
  not not_240 (not_240_out, F2);
  not not_241 (not_241_out, F0);
  not not_242 (not_242_out, OP5);
  not not_243 (not_243_out, OP4);
  not not_244 (not_244_out, OP3);
  not not_245 (not_245_out, OP2);
  not not_246 (not_246_out, OP1);
  not not_247 (not_247_out, OP0);
  not not_248 (not_248_out, F4);
  not not_249 (not_249_out, F3);
  not not_250 (not_250_out, F1);
  not not_251 (not_251_out, F0);
  not not_252 (not_252_out, OP5);
  not not_253 (not_253_out, OP4);
  not not_254 (not_254_out, OP3);
  not not_255 (not_255_out, OP2);
  not not_256 (not_256_out, OP1);
  not not_257 (not_257_out, OP0);
  not not_258 (not_258_out, F4);
  not not_259 (not_259_out, F3);
  not not_260 (not_260_out, F1);
  not not_261 (not_261_out, OP5);
  not not_262 (not_262_out, OP4);
  not not_263 (not_263_out, OP3);
  not not_264 (not_264_out, OP2);
  not not_265 (not_265_out, OP1);
  not not_266 (not_266_out, OP0);
  not not_267 (not_267_out, F4);
  not not_268 (not_268_out, F3);
  not not_269 (not_269_out, OP5);
  not not_270 (not_270_out, OP4);
  not not_271 (not_271_out, OP3);
  not not_272 (not_272_out, OP2);
  not not_273 (not_273_out, OP1);
  not not_274 (not_274_out, OP0);
  not not_275 (not_275_out, F4);
  not not_276 (not_276_out, F2);
  not not_277 (not_277_out, F0);
  not not_278 (not_278_out, OP5);
  not not_279 (not_279_out, OP4);
  not not_280 (not_280_out, OP3);
  not not_281 (not_281_out, OP2);
  not not_282 (not_282_out, OP1);
  not not_283 (not_283_out, OP0);
  not not_284 (not_284_out, F4);
  not not_285 (not_285_out, F2);
  not not_286 (not_286_out, OP5);
  not not_287 (not_287_out, OP4);
  not not_288 (not_288_out, OP3);
  not not_289 (not_289_out, OP2);
  not not_290 (not_290_out, OP1);
  not not_291 (not_291_out, OP0);
  not not_292 (not_292_out, F5);
  not not_293 (not_293_out, F4);
  not not_294 (not_294_out, F2);
  not not_295 (not_295_out, F1);
  not not_296 (not_296_out, F0);
  not not_297 (not_297_out, OP0);
  not not_298 (not_298_out, OP1);
  not not_299 (not_299_out, OP3);
  not not_300 (not_300_out, OP4);
  not not_301 (not_301_out, OP5);
  not not_302 (not_302_out, OP1);
  not not_303 (not_303_out, OP3);
  not not_304 (not_304_out, OP4);
  not not_305 (not_305_out, OP5);
  not not_306 (not_306_out, OP0);
  not not_307 (not_307_out, OP1);
  not not_308 (not_308_out, OP2);
  not not_309 (not_309_out, OP3);
  not not_310 (not_310_out, OP4);
  not not_311 (not_311_out, OP5);
  not not_312 (not_312_out, F0);
  not not_313 (not_313_out, F1);
  not not_314 (not_314_out, F2);
  not not_315 (not_315_out, F4);
  not not_316 (not_316_out, F5);
  not not_317 (not_317_out, OP5);
  not not_318 (not_318_out, OP4);
  not not_319 (not_319_out, OP3);
  not not_320 (not_320_out, OP2);
  not not_321 (not_321_out, OP1);
  not not_322 (not_322_out, OP0);
  not not_323 (not_323_out, F5);
  not not_324 (not_324_out, F4);
  not not_325 (not_325_out, F2);
  not not_326 (not_326_out, F1);
  not not_327 (not_327_out, F0);
  not not_328 (not_328_out, OP5);
  not not_329 (not_329_out, OP4);
  not not_330 (not_330_out, OP3);
  not not_331 (not_331_out, OP2);
  not not_332 (not_332_out, OP0);
  not not_333 (not_333_out, OP5);
  not not_334 (not_334_out, OP4);
  not not_335 (not_335_out, OP3);
  not not_336 (not_336_out, OP2);
  not not_337 (not_337_out, OP2);
  not not_338 (not_338_out, OP3);
  not not_339 (not_339_out, OP4);
  not not_340 (not_340_out, OP5);
  and and_1 (MemToReg, OP5, not_1_out, not_2_out, not_3_out, OP1, OP0);
  and and_2 (MemWrite, OP0, OP1, not_4_out, OP3, not_5_out, OP5);
  and and_3 (and_3_out, not_6_out, not_7_out, OP3, not_8_out, not_9_out);
  or or_1 (ALU_SRC, and_3_out, and_4_out, and_5_out);
  and and_4 (and_4_out, not_10_out, OP3, not_11_out, not_12_out);
  and and_5 (and_5_out, OP0, OP1, not_13_out, not_14_out, OP5);
  and and_6 (and_6_out, not_15_out, not_16_out, not_17_out, not_18_out, not_19_out, not_20_out, not_21_out, not_22_out, not_23_out, not_24_out, not_25_out, not_26_out);
  and and_7 (and_7_out, not_27_out, not_28_out, not_29_out, not_30_out, not_31_out, not_32_out, not_33_out, not_34_out, not_35_out, not_36_out, F1, F0);
  and and_8 (and_8_out, not_37_out, not_38_out, not_39_out, not_40_out, not_41_out, not_42_out, not_43_out, not_44_out, not_45_out, not_46_out, F1, not_47_out);
  and and_9 (and_9_out, not_48_out, not_49_out, not_50_out, not_51_out, not_52_out, not_53_out, F5, not_54_out, not_55_out, not_56_out, not_57_out, not_58_out);
  and and_10 (and_10_out, not_59_out, not_60_out, not_61_out, not_62_out, not_63_out, not_64_out, F5, not_65_out, not_66_out, not_67_out, not_68_out, F0);
  and and_11 (and_11_out, not_69_out, not_70_out, not_71_out, not_72_out, not_73_out, not_74_out, F5, not_75_out, not_76_out, not_77_out, F1, not_78_out);
  and and_12 (and_12_out, not_79_out, not_80_out, not_81_out, not_82_out, not_83_out, not_84_out, F5, not_85_out, not_86_out, F2, not_87_out, not_88_out);
  and and_13 (and_13_out, not_89_out, not_90_out, not_91_out, not_92_out, not_93_out, not_94_out, F5, not_95_out, not_96_out, F2, not_97_out, F0);
  and and_14 (and_14_out, not_98_out, not_99_out, not_100_out, not_101_out, not_102_out, not_103_out, F5, not_104_out, not_105_out, F2, F1, F0);
  and and_15 (and_15_out, not_106_out, not_107_out, not_108_out, not_109_out, not_110_out, not_111_out, F5, not_112_out, F3, not_113_out, F1, not_114_out);
  and and_16 (and_16_out, not_115_out, not_116_out, not_117_out, not_118_out, not_119_out, not_120_out, F5, not_121_out, F3, not_122_out, F1, F0);
  and and_17 (and_17_out, not_123_out, not_124_out, not_125_out, not_126_out, OP1, OP0);
  and and_18 (and_18_out, not_127_out, not_128_out, OP3, not_129_out, not_130_out, not_131_out);
  and and_19 (and_19_out, not_132_out, not_133_out, OP3, OP2, not_134_out, not_135_out);
  and and_20 (and_20_out, not_136_out, not_137_out, OP3, not_138_out, not_139_out, OP0);
  and and_21 (and_21_out, not_140_out, not_141_out, OP3, not_142_out, OP1, not_143_out);
  and and_22 (and_22_out, not_144_out, not_145_out, OP3, OP2, not_146_out, OP0);
  and and_23 (and_23_out, OP5, not_147_out, not_148_out, not_149_out, OP1, OP0);
  and and_24 (SysCALL, not_150_out, not_151_out, not_152_out, not_153_out, not_154_out, not_155_out, not_156_out, not_157_out, F2, F3, not_158_out, not_159_out);
  and and_25 (and_25_out, not_160_out, not_161_out, OP3, not_162_out, not_163_out, not_164_out);
  and and_26 (and_26_out, not_165_out, not_166_out, OP3, not_167_out, not_168_out, OP0);
  and and_27 (and_27_out, not_169_out, not_170_out, OP3, not_171_out, OP1, not_172_out);
  and and_28 (and_28_out, OP5, not_173_out, not_174_out, not_175_out, OP1, OP0);
  and and_29 (and_29_out, OP5, not_176_out, OP3, not_177_out, OP1, OP0);
  and and_30 (and_30_out, not_178_out, not_179_out, not_180_out, not_181_out, not_182_out, not_183_out, not_184_out, not_185_out, not_186_out, not_187_out, not_188_out, not_189_out);
  and and_31 (and_31_out, not_190_out, not_191_out, not_192_out, not_193_out, not_194_out, not_195_out, not_196_out, not_197_out, not_198_out, not_199_out, F1, F0);
  and and_32 (and_32_out, not_200_out, not_201_out, not_202_out, not_203_out, not_204_out, not_205_out, not_206_out, not_207_out, not_208_out, not_209_out, F1, not_210_out);
  and and_33 (and_33_out, not_211_out, not_212_out, not_213_out, not_214_out, not_215_out, not_216_out, F5, not_217_out, not_218_out, not_219_out, not_220_out, not_221_out);
  and and_34 (and_34_out, not_222_out, not_223_out, not_224_out, not_225_out, not_226_out, not_227_out, F5, not_228_out, not_229_out, not_230_out, not_231_out, F0);
  and and_35 (and_35_out, not_232_out, not_233_out, not_234_out, not_235_out, not_236_out, not_237_out, F5, not_238_out, not_239_out, not_240_out, F1, not_241_out);
  and and_36 (and_36_out, not_242_out, not_243_out, not_244_out, not_245_out, not_246_out, not_247_out, F5, not_248_out, not_249_out, F2, not_250_out, not_251_out);
  and and_37 (and_37_out, not_252_out, not_253_out, not_254_out, not_255_out, not_256_out, not_257_out, F5, not_258_out, not_259_out, F2, not_260_out, F0);
  and and_38 (and_38_out, not_261_out, not_262_out, not_263_out, not_264_out, not_265_out, not_266_out, F5, not_267_out, not_268_out, F2, F1, F0);
  and and_39 (and_39_out, not_269_out, not_270_out, not_271_out, not_272_out, not_273_out, not_274_out, F5, not_275_out, F3, not_276_out, F1, not_277_out);
  and and_40 (and_40_out, not_278_out, not_279_out, not_280_out, not_281_out, not_282_out, not_283_out, F5, not_284_out, F3, not_285_out, F1, F0);
  and and_41 (and_41_out, not_286_out, not_287_out, not_288_out, not_289_out, not_290_out, not_291_out, not_292_out, not_293_out, F3, not_294_out, not_295_out, not_296_out);
  and and_42 (BEQ, not_297_out, not_298_out, OP2, not_299_out, not_300_out, not_301_out);
  and and_43 (BNE, OP0, not_302_out, OP2, not_303_out, not_304_out, not_305_out);
  and and_44 (JR, not_306_out, not_307_out, not_308_out, not_309_out, not_310_out, not_311_out, not_312_out, not_313_out, not_314_out, F3, not_315_out, not_316_out);
  and and_45 (and_45_out, not_317_out, not_318_out, not_319_out, not_320_out, not_321_out, not_322_out, not_323_out, not_324_out, F3, not_325_out, not_326_out, not_327_out);
  and and_46 (and_46_out, not_328_out, not_329_out, not_330_out, not_331_out, OP1, not_332_out);
  and and_47 (and_47_out, not_333_out, not_334_out, not_335_out, not_336_out, OP1, OP0);
  and and_48 (JAL, OP0, OP1, not_337_out, not_338_out, not_339_out, not_340_out);
  or or_2 (SignedExt, and_25_out, and_26_out, and_27_out, and_28_out, and_29_out);
  or or_3 (JUMP, and_45_out, and_46_out, and_47_out);
  or or_4 (RegWrite, and_6_out, and_7_out, and_8_out, and_9_out, and_10_out, and_11_out, and_12_out, and_13_out, and_14_out, and_15_out, and_16_out, and_17_out, and_18_out, and_19_out, and_20_out, and_21_out, and_22_out, and_23_out);
  or or_5 (RegDst, and_30_out, and_31_out, and_32_out, and_33_out, and_34_out, and_35_out, and_36_out, and_37_out, and_38_out, and_39_out, and_40_out, and_41_out);
endmodule

// ALU
module MIPS_ALU (
  input  [4:0] shamt,
  input  [31:0] X,
  input  [31:0] Y,
  input  [3:0] AluOP,
  output Equal,
  output [31:0] Result,
  output [31:0] Result_2
);

  wire [0:0] comparator_1_lt, comparator_2_lt;
  wire [31:0] adder_1_out, AND_out, divider_1_out, divider_1_rem, multiplier_1_cout, multiplier_1_out,
       NOR_out, OR_out, shifter_1_out, shifter_2_out, shifter_3_out, subtractor_1_out, XOR_out;

  assign AND_out = X & Y;  // AND_Gate AND, 32 bits wide
  assign OR_out = X | Y;  // OR_Gate OR, 32 bits wide
  Shifter #(.width(32), .shift("ll")) shifter_1 (.in(Y), .\dist (shamt), .out(shifter_1_out));
  Shifter #(.width(32), .shift("ar")) shifter_2 (.in(Y), .\dist (shamt), .out(shifter_2_out));
  Shifter #(.width(32), .shift("lr")) shifter_3 (.in(Y), .\dist (shamt), .out(shifter_3_out));
  Multiplier #(.width(32)) multiplier_1 (.a(X), .b(Y), .out(multiplier_1_out), .cout(multiplier_1_cout));  // open: cin
  Divider #(.width(32)) divider_1 (.a(X), .b(Y), .out(divider_1_out), .rem(divider_1_rem));  // open: upper
  Adder #(.width(32)) adder_1 (.a(X), .b(Y), .out(adder_1_out));  // open: cin, cout
  Subtractor #(.width(32)) subtractor_1 (.a(X), .b(Y), .out(subtractor_1_out));  // open: bin, bout
  assign XOR_out = X ^ Y;  // XOR_Gate XOR, 32 bits wide
  assign NOR_out = ~(X | Y);  // NOR_Gate NOR, 32 bits wide
  Comparator #(.width(32), .mode("twosComplement")) comparator_1 (
    .a(X), .b(Y), .eq(Equal), .lt(comparator_1_lt[0]));  // open: gt
  Comparator #(.width(32), .mode("unsigned")) comparator_2 (.a(X), .b(Y), .lt(comparator_2_lt[0]));  // open: gt, eq
  Multiplexer #(.select(4), .width(32), .disabled("Z"), .enable("false")) multiplexer_1 (
    .in0(shifter_1_out), .in1(shifter_2_out), .in2(shifter_3_out), .in3(multiplier_1_out),
    .in4(divider_1_out), .in5(adder_1_out), .in6(subtractor_1_out), .in7(AND_out), .in8(OR_out),
    .in9(XOR_out), .in10(NOR_out), .in11({{31{1'b0}}, comparator_1_lt[0]}),
    .in12({{31{1'b0}}, comparator_2_lt[0]}), .in13({32{1'b0}}), .in14({32{1'b0}}), .in15({32{1'b0}}),
    .out(Result), .sel(AluOP));
  Multiplexer #(.select(4), .width(32), .disabled("Z"), .enable("false")) multiplexer_2 (
    .in0({32{1'b0}}), .in1({32{1'b0}}), .in2({32{1'b0}}), .in3(multiplier_1_cout), .in4(divider_1_rem),
    .in5({32{1'b0}}), .in6({32{1'b0}}), .in7({32{1'b0}}), .in8({32{1'b0}}), .in9({32{1'b0}}),
    .in10({32{1'b0}}), .in11({32{1'b0}}), .in12({32{1'b0}}), .in13({32{1'b0}}), .in14({32{1'b0}}),
    .in15({32{1'b0}}), .out(Result_2), .sel(AluOP));

  // Other names for the same wires on the sheet: Result2[31:0] = Result_2; S[3:0] = AluOP

  // Notes on the sheet:
  //   不要改变此引脚区域内容，也不要改变ALU封装形式
  //   输入引脚
  //   输出引脚
endmodule

module MIPS_Regifile (
  input  [31:0] Din,
  input  Clk,
  input  WE,
  input  [4:0] R1_num,
  input  [4:0] W_num,
  input  [4:0] R2_num,
  output [31:0] R1,
  output [31:0] R2
);

  // RegisterFile registerfile_1: pin names not known; wires that end beside it: Din, Clk, WE, W_num, R1_num, R2_num, R1, R2
endmodule

module \理想流水线  (
  output RegWrite,
  output MemWrite,
  output [31:0] IF_PC,
  output [31:0] ID_PC,
  output [31:0] EX_PC,
  output [31:0] M_PC,
  output [31:0] WB_PC,
  output [31:0] RDin,
  output [31:0] MDin,
  output [31:0] LedData
);

  wire and_1_out, CLK, clock_1_out, clock_2_out, comparator_1_eq, comparator_1_lt, d_ff_2_q, EN, Go, IR1,
       IR2, IR3, JMP, JR, mips_alu_1_equal, nand_1_out, not_1_out, or_1_out, or_2_out, RST, SignedExt, W1,
       W2, W3, \单周期硬布线控制器_1_alu_src , \单周期硬布线控制器_1_beq , \单周期硬布线控制器_1_bne , \单周期硬布线控制器_1_jal ,
       \单周期硬布线控制器_1_memtoreg , \单周期硬布线控制器_1_memwrite , \单周期硬布线控制器_1_regdst , \单周期硬布线控制器_1_regwrite ,
       \单周期硬布线控制器_1_syscall , \流水线寄存器_2_out_alusrcb , \流水线寄存器_2_out_memtoreg , \流水线寄存器_2_out_memwrite ,
       \流水线寄存器_2_out_regdst , \流水线寄存器_2_out_regwrite , \流水线寄存器_2_out_syscall , \流水线寄存器_3_out_equal ,
       \流水线寄存器_3_out_memtoreg , \流水线寄存器_3_out_regdst , \流水线寄存器_3_out_regwrite , \流水线寄存器_3_out_syscall ,
       \流水线寄存器_4_out_equal , \流水线寄存器_4_out_memtoreg , \流水线寄存器_4_out_regdst , \流水线寄存器_4_out_syscall ;
  wire [3:0] \单周期硬布线控制器_1_alu_op , \流水线寄存器_2_out_aluop ;
  wire [4:0] multiplexer_1_out, multiplexer_2_out, multiplexer_6_out, \流水线寄存器_2_out_shamt ;
  wire [5:0] Func;
  wire [12:0] CNT_num;
  wire [15:0] \LoadUse次数 , \总周期数 , \插入气泡数 , \无条件分支数 , \条件分支成功数 ;
  wire [31:0] bit_extender_1_out, EX_IR, IF_IR, MEM_IR, mips_alu_1_result, mips_regifile_1_r1,
       mips_regifile_1_r2, multiplexer_3_out, multiplexer_4_out, PC_4, ram_1_data, WB_IR, \流水线寄存器_2_out_imm ,
       \流水线寄存器_2_out_r1 , \流水线寄存器_2_out_r2 , \流水线寄存器_3_out_alu , \流水线寄存器_4_out_alu , \流水线寄存器_4_out_md ;
  wire [31:6] ID_IR;

  Button \u_总复位  (.out(RST));
  Button _1 (.out(IR1));
  Button _2 (.out(IR2));
  Button _3 (.out(IR3));
  // Probe on \总周期数 
  // Probe on \总周期数 
  Button \u_继续运行  (.out(Go));
  LED #(.active("true")) led_1 (.in(W1));
  LED #(.active("true")) led_2 (.in(W2));
  LED #(.active("true")) led_3 (.in(W3));
  Hex_Digit_Display hex_digit_display_1 (.value(LedData[31:28]));  // open: dp
  // Probe on IF_PC[19:0]
  // Mips_Probe mips_probe_1: pin names not known; wires that end beside it: IF_IR
  not not_1 (not_1_out, \流水线寄存器_4_out_syscall );
  Register #(.width(32), .trigger("rising"), .Select("low")) PC (.D(PC_4), .en(EN), .Q(IF_PC), .clk(CLK), .clr(RST));
  Hex_Digit_Display hex_digit_display_2 (.value(LedData[27:24]));  // open: dp
  Hex_Digit_Display hex_digit_display_3 (.value(LedData[23:20]));  // open: dp
  // Probe on ID_PC[19:0]
  // Mips_Probe mips_probe_2: pin names not known; wires that end beside it: {ID_IR, Func}
  or or_1 (or_1_out, not_1_out, Go);
  or or_2 (or_2_out, not_1_out, \流水线寄存器_4_out_equal );
  Hex_Digit_Display hex_digit_display_4 (.value(LedData[15:12]));  // open: dp
  Hex_Digit_Display hex_digit_display_5 (.value(LedData[19:16]));  // open: dp
  D_Flip_Flop #(.trigger("falling"), .Pre_Clr_Positions("ABOVE_BELOW"), .NegatePresetClear("false"), .enable("false"), .NewFFLayout("true")) d_ff_1 (
    .clk(CLK), .D(or_2_out), .Q(EN), .preset(or_1_out));  // open: Qn, reset
  Counter #(.width(16), .max('hffff), .ongoal("wrap"), .trigger("rising"), .behavior("new")) counter_1 (
    .count(EN), .Q(\总周期数 ), .clk(CLK), .clr(RST));  // open: load, D, carry, preset, down
  Adder #(.width(32)) adder_1 (.a(IF_PC), .b(32'h4), .out(PC_4));  // open: cin, cout
  Hex_Digit_Display hex_digit_display_6 (.value(LedData[7:4]));  // open: dp
  Hex_Digit_Display hex_digit_display_7 (.value(LedData[11:8]));  // open: dp
  Clock #(.highDuration(1), .lowDuration(1)) clock_1 (.out(clock_1_out));
  // Probe on EX_PC[19:0]
  // Mips_Probe mips_probe_3: pin names not known; wires that end beside it: clock_1_out, EX_IR, CLK
  ROM #(.addrWidth(10), .dataWidth(32), .Select("high")) rom_1 (.addr(IF_PC[11:2]), .data(IF_IR));
  Hex_Digit_Display hex_digit_display_8 (.value(LedData[3:0]));  // open: dp
  \流水线寄存器  \u_流水线寄存器_1  (
    .IN_PC(IF_PC), .IN_IR(IF_IR), .OUT_PC(ID_PC), .OUT_IR({ID_IR, Func}), .EN(EN), .CLK(CLK), .RST(RST),
    .CLR(1'b0));  // open: IN_MemToReg, IN_MemWrite, IN_AluOP, IN_AluSrcB, IN_RegWrite, IN_equal, IN_R1, IN_ALU, IN_R2, IN_MD, IN_Imm, OUT_MemToReg, OUT_MemWrite, OUT_AluOP, OUT_AluSrcB, OUT_RegWrite, OUT_Syscall, OUT_equal, OUT_R1, OUT_ALU, OUT_R2, OUT_MD, OUT_Imm, In_RegDst, OUT_RegDst, IN_Bne, OUT_Bne, IN_Beq, OUT_Beq, IN_shamt, OUT_shamt, IN_offset, OUT_offset, IN_JAL, OUT_JAL, IN_WriteReg_num, OUT_WriteReg_num, IN_JMP, OUT_JMP, IN_JR, OUT_JR, In_Syscall
  // Probe on \总周期数 
  // Probe on M_PC[19:0]
  // Mips_Probe mips_probe_4: pin names not known; wires that end beside it: MEM_IR
  // Mips_Probe mips_probe_5: pin names not known; wires that end beside it: {ID_IR, Func}
  // Probe on \总周期数 
  // Probe on \无条件分支数 
  // Probe on \条件分支成功数 
  // Probe on \插入气泡数 
  // Probe on \LoadUse次数 
  // Probe on IF_PC[11:0]
  // Probe on WB_PC[19:0]
  // Mips_Probe mips_probe_6: pin names not known; wires that end beside it: WB_IR
  \单周期硬布线控制器  \u_单周期硬布线控制器_1  (
    .Func(Func), .OP(ID_IR[31:26]), .ALU_OP(\单周期硬布线控制器_1_alu_op ), .MemToReg(\单周期硬布线控制器_1_memtoreg ),
    .MemWrite(\单周期硬布线控制器_1_memwrite ), .ALU_SRC(\单周期硬布线控制器_1_alu_src ), .RegWrite(\单周期硬布线控制器_1_regwrite ),
    .SysCALL(\单周期硬布线控制器_1_syscall ), .SignedExt(SignedExt), .RegDst(\单周期硬布线控制器_1_regdst ), .JR(JR),
    .JMP(JMP), .Beq(\单周期硬布线控制器_1_beq ), .JAL(\单周期硬布线控制器_1_jal ), .Bne(\单周期硬布线控制器_1_bne ));
  Multiplexer #(.select(1), .width(5), .disabled("Z"), .enable("false")) multiplexer_1 (
    .in0(ID_IR[25:21]), .in1(5'b00010), .out(multiplexer_1_out), .sel(\单周期硬布线控制器_1_syscall ));
  Multiplexer #(.select(1), .width(5), .disabled("Z"), .enable("false")) multiplexer_2 (
    .in0(ID_IR[20:16]), .in1(5'b00100), .out(multiplexer_2_out), .sel(\单周期硬布线控制器_1_syscall ));
  assign bit_extender_1_out = {{16{ID_IR[15]}}, {ID_IR[15:6], Func}};  // Bit_Extender bit_extender_1
  // Probe on ID_PC[11:0]
  // Probe on EX_PC[11:0]
  // Probe on M_PC[11:0]
  D_Flip_Flop #(.trigger("high"), .Pre_Clr_Positions("LEGACY"), .NegatePresetClear("false"), .enable("true"), .NewFFLayout("false")) d_ff_2 (.Q(d_ff_2_q));  // open: clk, D, Qn, preset, en, reset
  // Probe on 13'hc
  MIPS_Regifile mips_regifile_1 (
    .Din(RDin), .Clk(CLK), .R1(mips_regifile_1_r1), .R2(mips_regifile_1_r2), .WE(RegWrite),
    .W_num(multiplexer_6_out), .R1_num(multiplexer_1_out), .R2_num(multiplexer_2_out));
  // Probe on WB_PC[11:0]
  Comparator #(.width(13), .mode("twosComplement")) comparator_1 (
    .a(CNT_num), .b(13'hc), .eq(comparator_1_eq), .lt(comparator_1_lt));  // open: gt
  Clock #(.highDuration(1), .lowDuration(1)) clock_2 (.out(clock_2_out));
  nand nand_1 (nand_1_out, d_ff_2_q, comparator_1_eq);
  Counter #(.width(13), .max('h1fff), .ongoal("stay"), .trigger("rising"), .behavior("old")) counter_2 (
    .count(comparator_1_lt), .Q(CNT_num), .clk(clock_2_out));  // open: load, D, carry, clr, preset
  \流水线寄存器  \u_流水线寄存器_2  (
    .IN_MemToReg(\单周期硬布线控制器_1_memtoreg ), .IN_MemWrite(\单周期硬布线控制器_1_memwrite ),
    .IN_AluOP(\单周期硬布线控制器_1_alu_op ), .IN_AluSrcB(\单周期硬布线控制器_1_alu_src ),
    .IN_RegWrite(\单周期硬布线控制器_1_regwrite ), .IN_R1(mips_regifile_1_r1), .IN_R2(mips_regifile_1_r2),
    .IN_PC(ID_PC), .IN_IR({ID_IR, Func}), .IN_Imm(bit_extender_1_out),
    .OUT_MemToReg(\流水线寄存器_2_out_memtoreg ), .OUT_MemWrite(\流水线寄存器_2_out_memwrite ),
    .OUT_AluOP(\流水线寄存器_2_out_aluop ), .OUT_AluSrcB(\流水线寄存器_2_out_alusrcb ),
    .OUT_RegWrite(\流水线寄存器_2_out_regwrite ), .OUT_Syscall(\流水线寄存器_2_out_syscall ), .OUT_R1(\流水线寄存器_2_out_r1 ),
    .OUT_R2(\流水线寄存器_2_out_r2 ), .OUT_PC(EX_PC), .OUT_IR(EX_IR), .OUT_Imm(\流水线寄存器_2_out_imm ), .EN(EN),
    .CLK(CLK), .RST(RST), .In_RegDst(\单周期硬布线控制器_1_regdst ), .OUT_RegDst(\流水线寄存器_2_out_regdst ),
    .IN_Bne(\单周期硬布线控制器_1_bne ), .IN_Beq(\单周期硬布线控制器_1_beq ), .IN_shamt(ID_IR[10:6]),
    .OUT_shamt(\流水线寄存器_2_out_shamt ), .IN_offset({ID_IR[25:6], Func}), .IN_JAL(\单周期硬布线控制器_1_jal ),
    .CLR(1'b0), .In_Syscall(\单周期硬布线控制器_1_syscall ));  // open: IN_equal, IN_ALU, IN_MD, OUT_equal, OUT_ALU, OUT_MD, OUT_Bne, OUT_Beq, OUT_offset, OUT_JAL, IN_WriteReg_num, OUT_WriteReg_num, IN_JMP, OUT_JMP, IN_JR, OUT_JR
  assign CLK = nand_1_out ? clock_2_out : 1'bz;  // Controlled_Buffer controlled_buffer_1
  Multiplexer #(.select(1), .width(32), .disabled("Z"), .enable("false")) multiplexer_3 (
    .in0(\流水线寄存器_2_out_r2 ), .in1(\流水线寄存器_2_out_imm ), .out(multiplexer_3_out), .sel(\流水线寄存器_2_out_alusrcb ));
  Pull_Resistor #(.pull(1)) pull_resistor_1 (.node(CLK));
  Multiplexer #(.select(1), .width(32), .disabled("Z"), .enable("false")) multiplexer_4 (
    .in0(multiplexer_3_out), .in1(32'h22), .out(multiplexer_4_out), .sel(\流水线寄存器_2_out_syscall ));
  MIPS_ALU mips_alu_1 (
    .X(\流水线寄存器_2_out_r1 ), .Y(multiplexer_4_out), .AluOP(\流水线寄存器_2_out_aluop ), .Equal(mips_alu_1_equal),
    .Result(mips_alu_1_result), .shamt(\流水线寄存器_2_out_shamt ));  // open: Result_2
  \流水线寄存器  \u_流水线寄存器_3  (
    .IN_MemToReg(\流水线寄存器_2_out_memtoreg ), .IN_MemWrite(\流水线寄存器_2_out_memwrite ),
    .IN_RegWrite(\流水线寄存器_2_out_regwrite ), .IN_equal(mips_alu_1_equal), .IN_ALU(mips_alu_1_result),
    .IN_R2(\流水线寄存器_2_out_r2 ), .IN_PC(EX_PC), .IN_IR(EX_IR), .OUT_MemToReg(\流水线寄存器_3_out_memtoreg ),
    .OUT_MemWrite(MemWrite), .OUT_RegWrite(\流水线寄存器_3_out_regwrite ), .OUT_Syscall(\流水线寄存器_3_out_syscall ),
    .OUT_equal(\流水线寄存器_3_out_equal ), .OUT_ALU(\流水线寄存器_3_out_alu ), .OUT_R2(MDin), .OUT_PC(M_PC),
    .OUT_IR(MEM_IR), .EN(EN), .CLK(CLK), .RST(RST), .In_RegDst(\流水线寄存器_2_out_regdst ),
    .OUT_RegDst(\流水线寄存器_3_out_regdst ), .CLR(1'b0), .In_Syscall(\流水线寄存器_2_out_syscall ));  // open: IN_AluOP, IN_AluSrcB, IN_R1, IN_MD, IN_Imm, OUT_AluOP, OUT_AluSrcB, OUT_R1, OUT_MD, OUT_Imm, IN_Bne, OUT_Bne, IN_Beq, OUT_Beq, IN_shamt, OUT_shamt, IN_offset, OUT_offset, IN_JAL, OUT_JAL, IN_WriteReg_num, OUT_WriteReg_num, IN_JMP, OUT_JMP, IN_JR, OUT_JR
  and and_1 (and_1_out, \流水线寄存器_3_out_syscall , \流水线寄存器_3_out_equal );
  Register #(.width(32), .trigger("rising"), .Select("low")) register_1 (
    .D(MDin), .en(and_1_out), .Q(LedData), .clk(CLK), .clr(RST));
  RAM #(.addrWidth(10), .dataWidth(32), .bus("separate"), .Select("high")) ram_1 (
    .addr(\流水线寄存器_3_out_alu [11:2]), .din(MDin), .data(ram_1_data), .str(MemWrite), .clk(CLK), .clr(RST));  // open: sel, ld
  \流水线寄存器  \u_流水线寄存器_4  (
    .IN_MemToReg(\流水线寄存器_3_out_memtoreg ), .IN_RegWrite(\流水线寄存器_3_out_regwrite ),
    .IN_equal(\流水线寄存器_3_out_equal ), .IN_ALU(\流水线寄存器_3_out_alu ), .IN_MD(ram_1_data), .IN_PC(M_PC),
    .IN_IR(MEM_IR), .OUT_MemToReg(\流水线寄存器_4_out_memtoreg ), .OUT_RegWrite(RegWrite),
    .OUT_Syscall(\流水线寄存器_4_out_syscall ), .OUT_equal(\流水线寄存器_4_out_equal ), .OUT_ALU(\流水线寄存器_4_out_alu ),
    .OUT_MD(\流水线寄存器_4_out_md ), .OUT_PC(WB_PC), .OUT_IR(WB_IR), .EN(EN), .CLK(CLK), .RST(RST),
    .In_RegDst(\流水线寄存器_3_out_regdst ), .OUT_RegDst(\流水线寄存器_4_out_regdst ), .CLR(1'b0),
    .In_Syscall(\流水线寄存器_3_out_syscall ));  // open: IN_MemWrite, IN_AluOP, IN_AluSrcB, IN_R1, IN_R2, IN_Imm, OUT_MemWrite, OUT_AluOP, OUT_AluSrcB, OUT_R1, OUT_R2, OUT_Imm, IN_Bne, OUT_Bne, IN_Beq, OUT_Beq, IN_shamt, OUT_shamt, IN_offset, OUT_offset, IN_JAL, OUT_JAL, IN_WriteReg_num, OUT_WriteReg_num, IN_JMP, OUT_JMP, IN_JR, OUT_JR
  Multiplexer #(.select(1), .width(32), .disabled("Z"), .enable("false")) multiplexer_5 (
    .in0(\流水线寄存器_4_out_alu ), .in1(\流水线寄存器_4_out_md ), .out(RDin), .sel(\流水线寄存器_4_out_memtoreg ));
  Multiplexer #(.select(1), .width(5), .disabled("Z"), .enable("false")) multiplexer_6 (
    .in0(WB_IR[20:16]), .in1(WB_IR[15:11]), .out(multiplexer_6_out), .sel(\流水线寄存器_4_out_regdst ));

  // Other names for the same wires on the sheet: ID_IR[5:0] = Func; OP[5:0] = ID_IR[31:26]; MEM_PC[31:0] = M_PC;
  //   MEM_R2[31:0] = MDin

  // Notes on the sheet:
  //   中断源
  //   时空图监测，可删除
  //   中断等待指示
  //   数码管输出
  //   指令存储器
  //   contents of rom_1 (hex, n*v repeats v):
  //   20100000 20110000 20120000 20130000 36100000 36310001 36520002 36730003 ae100000 ae110004 ae120008
  //   ae13000c 2002000a 20110000 20120000 20130000 c
  //   指令字
  //   JMP
  //   JR
  //   OP
  //   Func
  //   Syscall
  //   rs
  //   rt
  //   Beq
  //   Bne
  //   MemToReg
  //   MemWrite
  //   AluOP
  //   AluSrcB
  //   RegWrite
  //   JAL
  //   RegDst
  //   控制位
  //   流水调试日志用
  //   暂停节拍，不能为0
  //   戳工具置1进入计数暂停模式，ctrl+k时钟自动运行到对应节拍暂停
  //   ctrl+k关闭时钟连续运行，将控制位置零，进入单步调试模式调试
  //   用这个时钟源需要去掉电路中的其他时钟源
  //   可计数暂停的时钟源
  //   为方便自动评测，需要输出流水线各段保存的PC值，注意是PC不是PC+4，另外ID段寄存器写入信息，Mem段内存写入信息也要输出
  //   rt
  //   rd
endmodule

module \气泡流水线  (
  output RegWrite,
  output MemWrite,
  output [31:0] IF_PC,
  output [31:0] ID_PC,
  output [31:0] EX_PC,
  output [31:0] M_PC,
  output [31:0] WB_PC,
  output [31:0] RDin,
  output [31:0] MDin,
  output [31:0] LedData
);

  wire and_1_out, and_2_out, CLK, clock_1_out, clock_2_out, comparator_1_eq, comparator_1_lt, d_ff_2_q, EN,
       Go, IR1, IR2, IR3, mips_alu_1_equal, multiplexer_10_out, nand_1_out, not_1_out, or_1_out, or_2_out,
       or_3_out, or_4_out, or_5_out, RST, SignedExt, W1, W2, W3, \单周期硬布线控制器_1_alu_src , \单周期硬布线控制器_1_beq ,
       \单周期硬布线控制器_1_bne , \单周期硬布线控制器_1_jal , \单周期硬布线控制器_1_jmp , \单周期硬布线控制器_1_jr , \单周期硬布线控制器_1_memtoreg ,
       \单周期硬布线控制器_1_memwrite , \单周期硬布线控制器_1_regdst , \单周期硬布线控制器_1_regwrite , \单周期硬布线控制器_1_syscall ,
       \数据相关处理_1_datahazard , \流水线寄存器_2_out_alusrcb , \流水线寄存器_2_out_beq , \流水线寄存器_2_out_bne ,
       \流水线寄存器_2_out_jal , \流水线寄存器_2_out_jmp , \流水线寄存器_2_out_jr , \流水线寄存器_2_out_memtoreg ,
       \流水线寄存器_2_out_memwrite , \流水线寄存器_2_out_regdst , \流水线寄存器_2_out_regwrite , \流水线寄存器_2_out_syscall ,
       \流水线寄存器_3_out_equal , \流水线寄存器_3_out_jal , \流水线寄存器_3_out_memtoreg , \流水线寄存器_3_out_regdst ,
       \流水线寄存器_3_out_regwrite , \流水线寄存器_3_out_syscall , \流水线寄存器_4_out_equal , \流水线寄存器_4_out_jal ,
       \流水线寄存器_4_out_memtoreg , \流水线寄存器_4_out_regdst , \流水线寄存器_4_out_syscall ;
  wire [3:0] \单周期硬布线控制器_1_alu_op , \流水线寄存器_2_out_aluop ;
  wire [4:0] multiplexer_4_out, multiplexer_5_out, multiplexer_6_out, multiplexer_7_out, multiplexer_12_out,
       multiplexer_14_out, \流水线寄存器_2_out_shamt , \流水线寄存器_2_out_writereg_num , \流水线寄存器_3_out_writereg_num ;
  wire [5:0] Func;
  wire [12:0] CNT_num;
  wire [15:0] \LoadUse次数 , \总周期数 , \插入气泡数 , \无条件分支数 , \条件分支成功数 ;
  wire [27:2] J_ADDR;
  wire [31:0] adder_2_out, adder_4_out, bit_extender_1_out, BR_ADDR, EX_IR, IF_IR, IF_PC_4, JR_ADDR, MEM_IR,
       mips_alu_1_result, mips_regifile_1_r1, mips_regifile_1_r2, multiplexer_1_out, multiplexer_2_out,
       multiplexer_3_out, multiplexer_8_out, multiplexer_9_out, multiplexer_11_out, ram_1_data,
       shifter_1_out, undriven, WB_IR, \流水线寄存器_2_out_imm , \流水线寄存器_2_out_r2 , \流水线寄存器_3_out_alu ,
       \流水线寄存器_4_out_alu , \流水线寄存器_4_out_md ;
  wire [31:6] ID_IR;

  Button \u_总复位  (.out(RST));
  Button _1 (.out(IR1));
  Button _2 (.out(IR2));
  Button _3 (.out(IR3));
  // Probe on \总周期数 
  // Probe on \总周期数 
  Button \u_继续运行  (.out(Go));
  LED #(.active("true")) led_1 (.in(W1));
  LED #(.active("true")) led_2 (.in(W2));
  LED #(.active("true")) led_3 (.in(W3));
  Multiplexer #(.select(1), .width(32), .disabled("Z"), .enable("false")) multiplexer_1 (
    .in0({EX_PC[31:28], J_ADDR, 2'b00}), .in1(JR_ADDR), .out(multiplexer_1_out), .sel(\流水线寄存器_2_out_jr ));
  Hex_Digit_Display hex_digit_display_1 (.value(LedData[31:28]));  // open: dp
  // Probe on IF_PC[19:0]
  // Mips_Probe mips_probe_1: pin names not known; wires that end beside it: IF_IR
  Multiplexer #(.select(1), .width(32), .disabled("Z"), .enable("false")) multiplexer_2 (
    .in0(IF_PC_4), .in1(multiplexer_1_out), .out(multiplexer_2_out), .sel(\流水线寄存器_2_out_jmp ));
  Hex_Digit_Display hex_digit_display_2 (.value(LedData[23:20]));  // open: dp
  Hex_Digit_Display hex_digit_display_3 (.value(LedData[27:24]));  // open: dp
  // Probe on ID_PC[19:0]
  // Mips_Probe mips_probe_2: pin names not known; wires that end beside it: {ID_IR, Func}
  Multiplexer #(.select(1), .width(32), .disabled("Z"), .enable("false")) multiplexer_3 (
    .in0(multiplexer_2_out), .in1(BR_ADDR), .out(multiplexer_3_out), .sel(multiplexer_10_out));
  Hex_Digit_Display hex_digit_display_4 (.value(LedData[15:12]));  // open: dp
  Hex_Digit_Display hex_digit_display_5 (.value(LedData[19:16]));  // open: dp
  \数据相关处理  \u_数据相关处理_1  (
    .Instruction({ID_IR, Func}), .EX_RegWrite(\流水线寄存器_2_out_regwrite ),
    .EX_WriteReg_num(\流水线寄存器_2_out_writereg_num ), .MEM_RegWrite(\流水线寄存器_3_out_regwrite ),
    .MEM_WriteReg_num(\流水线寄存器_3_out_writereg_num ), .DataHazard(\数据相关处理_1_datahazard ),
    .R1_num(multiplexer_4_out), .R2_num(multiplexer_5_out));
  and and_1 (and_1_out, ~\数据相关处理_1_datahazard , EN);  // AND_Gate
  Hex_Digit_Display hex_digit_display_6 (.value(LedData[7:4]));  // open: dp
  Hex_Digit_Display hex_digit_display_7 (.value(LedData[11:8]));  // open: dp
  Clock #(.highDuration(1), .lowDuration(1)) clock_1 (.out(clock_1_out));
  // Probe on EX_PC[19:0]
  // Mips_Probe mips_probe_3: pin names not known; wires that end beside it: clock_1_out, EX_IR, CLK
  not not_1 (not_1_out, \流水线寄存器_4_out_syscall );
  Register #(.width(32), .trigger("rising"), .Select("low")) PC (
    .D(multiplexer_3_out), .en(and_1_out), .Q(IF_PC), .clk(CLK), .clr(RST));
  Hex_Digit_Display hex_digit_display_8 (.value(LedData[3:0]));  // open: dp
  or or_1 (or_1_out, not_1_out, Go);
  or or_2 (or_2_out, not_1_out, \流水线寄存器_4_out_equal );
  // Probe on \总周期数 
  // Probe on M_PC[19:0]
  // Mips_Probe mips_probe_4: pin names not known; wires that end beside it: MEM_IR
  D_Flip_Flop #(.trigger("falling"), .Pre_Clr_Positions("ABOVE_BELOW"), .NegatePresetClear("false"), .enable("false"), .NewFFLayout("true")) d_ff_1 (
    .clk(CLK), .D(or_2_out), .Q(EN), .preset(or_1_out));  // open: Qn, reset
  Counter #(.width(16), .max('hffff), .ongoal("wrap"), .trigger("rising"), .behavior("new")) counter_1 (
    .count(EN), .Q(\总周期数 ), .clk(CLK), .clr(RST));  // open: load, D, carry, preset, down
  Adder #(.width(32)) adder_1 (.a(IF_PC), .b(32'h4), .out(IF_PC_4));  // open: cin, cout
  // Probe on \总周期数 
  // Probe on \无条件分支数 
  // Probe on \条件分支成功数 
  // Probe on \插入气泡数 
  // Probe on \LoadUse次数 
  ROM #(.addrWidth(10), .dataWidth(32), .Select("high")) rom_1 (.addr(IF_PC[11:2]), .data(IF_IR));
  // Probe on IF_PC[11:0]
  // Probe on WB_PC[19:0]
  // Mips_Probe mips_probe_5: pin names not known; wires that end beside it: WB_IR
  \流水线寄存器  \u_流水线寄存器_1  (
    .IN_PC(IF_PC), .IN_IR(IF_IR), .OUT_PC(ID_PC), .OUT_IR({ID_IR, Func}), .EN(and_1_out), .CLK(CLK),
    .RST(RST), .CLR(or_5_out));  // open: IN_MemToReg, IN_MemWrite, IN_AluOP, IN_AluSrcB, IN_RegWrite, IN_equal, IN_R1, IN_ALU, IN_R2, IN_MD, IN_Imm, OUT_MemToReg, OUT_MemWrite, OUT_AluOP, OUT_AluSrcB, OUT_RegWrite, OUT_Syscall, OUT_equal, OUT_R1, OUT_ALU, OUT_R2, OUT_MD, OUT_Imm, In_RegDst, OUT_RegDst, IN_Bne, OUT_Bne, IN_Beq, OUT_Beq, IN_shamt, OUT_shamt, IN_offset, OUT_offset, IN_JAL, OUT_JAL, IN_WriteReg_num, OUT_WriteReg_num, IN_JMP, OUT_JMP, IN_JR, OUT_JR, In_Syscall
  // Probe on EX_PC[11:0]
  // Probe on ID_PC[11:0]
  // Mips_Probe mips_probe_6: pin names not known
  // Probe on M_PC[11:0]
  D_Flip_Flop #(.trigger("high"), .Pre_Clr_Positions("LEGACY"), .NegatePresetClear("false"), .enable("true"), .NewFFLayout("false")) d_ff_2 (.Q(d_ff_2_q));  // open: clk, D, Qn, preset, en, reset
  // Probe on 13'hc
  // Probe on WB_PC[11:0]
  Comparator #(.width(13), .mode("twosComplement")) comparator_1 (
    .a(CNT_num), .b(13'hc), .eq(comparator_1_eq), .lt(comparator_1_lt));  // open: gt
  Clock #(.highDuration(1), .lowDuration(1)) clock_2 (.out(clock_2_out));
  \单周期硬布线控制器  \u_单周期硬布线控制器_1  (
    .Func(Func), .OP(ID_IR[31:26]), .ALU_OP(\单周期硬布线控制器_1_alu_op ), .MemToReg(\单周期硬布线控制器_1_memtoreg ),
    .MemWrite(\单周期硬布线控制器_1_memwrite ), .ALU_SRC(\单周期硬布线控制器_1_alu_src ), .RegWrite(\单周期硬布线控制器_1_regwrite ),
    .SysCALL(\单周期硬布线控制器_1_syscall ), .SignedExt(SignedExt), .RegDst(\单周期硬布线控制器_1_regdst ),
    .JR(\单周期硬布线控制器_1_jr ), .JMP(\单周期硬布线控制器_1_jmp ), .Beq(\单周期硬布线控制器_1_beq ), .JAL(\单周期硬布线控制器_1_jal ),
    .Bne(\单周期硬布线控制器_1_bne ));
  Multiplexer #(.select(1), .width(5), .disabled("Z"), .enable("false")) multiplexer_4 (
    .in0(ID_IR[25:21]), .in1(5'b00010), .out(multiplexer_4_out), .sel(\单周期硬布线控制器_1_syscall ));
  Multiplexer #(.select(1), .width(5), .disabled("Z"), .enable("false")) multiplexer_5 (
    .in0(ID_IR[20:16]), .in1(5'b00100), .out(multiplexer_5_out), .sel(\单周期硬布线控制器_1_syscall ));
  Multiplexer #(.select(1), .width(5), .disabled("Z"), .enable("false")) multiplexer_6 (
    .in0(ID_IR[20:16]), .in1(ID_IR[15:11]), .out(multiplexer_6_out), .sel(\单周期硬布线控制器_1_regdst ));
  assign bit_extender_1_out = {{16{ID_IR[15]}}, {ID_IR[15:6], Func}};  // Bit_Extender bit_extender_1
  nand nand_1 (nand_1_out, d_ff_2_q, comparator_1_eq);
  Counter #(.width(13), .max('h1fff), .ongoal("stay"), .trigger("rising"), .behavior("old")) counter_2 (
    .count(comparator_1_lt), .Q(CNT_num), .clk(clock_2_out));  // open: load, D, carry, clr, preset
  assign CLK = nand_1_out ? clock_2_out : 1'bz;  // Controlled_Buffer controlled_buffer_1
  MIPS_Regifile mips_regifile_1 (
    .Din(RDin), .Clk(CLK), .R1(mips_regifile_1_r1), .R2(mips_regifile_1_r2), .WE(RegWrite),
    .W_num(multiplexer_14_out), .R1_num(multiplexer_4_out), .R2_num(multiplexer_5_out));
  Multiplexer #(.select(1), .width(5), .disabled("Z"), .enable("false")) multiplexer_7 (
    .in0(multiplexer_6_out), .in1({5{1'b1}}), .out(multiplexer_7_out), .sel(\单周期硬布线控制器_1_jal ));
  Pull_Resistor #(.pull(1)) pull_resistor_1 (.node(CLK));
  or or_3 (or_3_out, \数据相关处理_1_datahazard , or_5_out);
  or or_4 (or_4_out, \流水线寄存器_2_out_jr , \流水线寄存器_2_out_jmp );
  \流水线寄存器  \u_流水线寄存器_2  (
    .IN_MemToReg(\单周期硬布线控制器_1_memtoreg ), .IN_MemWrite(\单周期硬布线控制器_1_memwrite ),
    .IN_AluOP(\单周期硬布线控制器_1_alu_op ), .IN_AluSrcB(\单周期硬布线控制器_1_alu_src ),
    .IN_RegWrite(\单周期硬布线控制器_1_regwrite ), .IN_R1(mips_regifile_1_r1), .IN_R2(mips_regifile_1_r2),
    .IN_PC(ID_PC), .IN_IR({ID_IR, Func}), .IN_Imm(bit_extender_1_out),
    .OUT_MemToReg(\流水线寄存器_2_out_memtoreg ), .OUT_MemWrite(\流水线寄存器_2_out_memwrite ),
    .OUT_AluOP(\流水线寄存器_2_out_aluop ), .OUT_AluSrcB(\流水线寄存器_2_out_alusrcb ),
    .OUT_RegWrite(\流水线寄存器_2_out_regwrite ), .OUT_Syscall(\流水线寄存器_2_out_syscall ), .OUT_R1(JR_ADDR),
    .OUT_R2(\流水线寄存器_2_out_r2 ), .OUT_PC(EX_PC), .OUT_IR(EX_IR), .OUT_Imm(\流水线寄存器_2_out_imm ), .EN(EN),
    .CLK(CLK), .RST(RST), .In_RegDst(\单周期硬布线控制器_1_regdst ), .OUT_RegDst(\流水线寄存器_2_out_regdst ),
    .IN_Bne(\单周期硬布线控制器_1_bne ), .OUT_Bne(\流水线寄存器_2_out_bne ), .IN_Beq(\单周期硬布线控制器_1_beq ),
    .OUT_Beq(\流水线寄存器_2_out_beq ), .IN_shamt(ID_IR[10:6]), .OUT_shamt(\流水线寄存器_2_out_shamt ),
    .IN_offset({ID_IR[25:6], Func}), .OUT_offset(J_ADDR), .IN_JAL(\单周期硬布线控制器_1_jal ),
    .OUT_JAL(\流水线寄存器_2_out_jal ), .CLR(or_3_out), .IN_WriteReg_num(multiplexer_7_out),
    .OUT_WriteReg_num(\流水线寄存器_2_out_writereg_num ), .IN_JMP(\单周期硬布线控制器_1_jmp ), .OUT_JMP(\流水线寄存器_2_out_jmp ),
    .IN_JR(\单周期硬布线控制器_1_jr ), .OUT_JR(\流水线寄存器_2_out_jr ), .In_Syscall(\单周期硬布线控制器_1_syscall ));  // open: IN_equal, IN_ALU, IN_MD, OUT_equal, OUT_ALU, OUT_MD
  Multiplexer #(.select(1), .width(32), .disabled("Z"), .enable("false")) multiplexer_8 (
    .in0(\流水线寄存器_2_out_r2 ), .in1(\流水线寄存器_2_out_imm ), .out(multiplexer_8_out), .sel(\流水线寄存器_2_out_alusrcb ));
  Shifter #(.width(32), .shift("ll")) shifter_1 (.in(\流水线寄存器_2_out_imm ), .\dist (5'b00010), .out(shifter_1_out));
  Multiplexer #(.select(1), .width(32), .disabled("Z"), .enable("false")) multiplexer_9 (
    .in0(multiplexer_8_out), .in1(32'h22), .out(multiplexer_9_out), .sel(\流水线寄存器_2_out_syscall ));
  or or_5 (or_5_out, or_4_out, multiplexer_10_out);
  Adder #(.width(32)) adder_2 (.a(EX_PC), .b(32'h4), .out(adder_2_out));  // open: cin, cout
  Multiplexer #(.select(1), .width(1), .disabled("Z"), .enable("false")) multiplexer_10 (
    .in0(\流水线寄存器_2_out_bne ), .in1(\流水线寄存器_2_out_beq ), .out(multiplexer_10_out), .sel(mips_alu_1_equal));
  MIPS_ALU mips_alu_1 (
    .X(JR_ADDR), .Y(multiplexer_9_out), .AluOP(\流水线寄存器_2_out_aluop ), .Equal(mips_alu_1_equal),
    .Result(mips_alu_1_result), .shamt(\流水线寄存器_2_out_shamt ));  // open: Result_2
  Adder #(.width(32)) adder_3 (.a(shifter_1_out), .b(adder_2_out), .out(BR_ADDR));  // open: cin, cout
  \流水线寄存器  \u_流水线寄存器_3  (
    .IN_MemToReg(\流水线寄存器_2_out_memtoreg ), .IN_MemWrite(\流水线寄存器_2_out_memwrite ),
    .IN_RegWrite(\流水线寄存器_2_out_regwrite ), .IN_equal(mips_alu_1_equal), .IN_R1(undriven),
    .IN_ALU(mips_alu_1_result), .IN_R2(\流水线寄存器_2_out_r2 ), .IN_PC(EX_PC), .IN_IR(EX_IR),
    .OUT_MemToReg(\流水线寄存器_3_out_memtoreg ), .OUT_MemWrite(MemWrite), .OUT_RegWrite(\流水线寄存器_3_out_regwrite ),
    .OUT_Syscall(\流水线寄存器_3_out_syscall ), .OUT_equal(\流水线寄存器_3_out_equal ), .OUT_ALU(\流水线寄存器_3_out_alu ),
    .OUT_R2(MDin), .OUT_PC(M_PC), .OUT_IR(MEM_IR), .EN(EN), .CLK(CLK), .RST(RST),
    .In_RegDst(\流水线寄存器_2_out_regdst ), .OUT_RegDst(\流水线寄存器_3_out_regdst ), .IN_JAL(\流水线寄存器_2_out_jal ),
    .OUT_JAL(\流水线寄存器_3_out_jal ), .CLR(1'b0), .IN_WriteReg_num(\流水线寄存器_2_out_writereg_num ),
    .OUT_WriteReg_num(\流水线寄存器_3_out_writereg_num ), .In_Syscall(\流水线寄存器_2_out_syscall ));  // open: IN_AluOP, IN_AluSrcB, IN_MD, IN_Imm, OUT_AluOP, OUT_AluSrcB, OUT_R1, OUT_MD, OUT_Imm, IN_Bne, OUT_Bne, IN_Beq, OUT_Beq, IN_shamt, OUT_shamt, IN_offset, OUT_offset, IN_JMP, OUT_JMP, IN_JR, OUT_JR
  and and_2 (and_2_out, \流水线寄存器_3_out_syscall , \流水线寄存器_3_out_equal );
  Register #(.width(32), .trigger("rising"), .Select("low")) register_1 (
    .D(MDin), .en(and_2_out), .Q(LedData), .clk(CLK), .clr(RST));
  RAM #(.addrWidth(10), .dataWidth(32), .bus("separate"), .Select("high")) ram_1 (
    .addr(\流水线寄存器_3_out_alu [11:2]), .din(MDin), .data(ram_1_data), .str(MemWrite), .clk(CLK), .clr(RST));  // open: sel, ld
  \流水线寄存器  \u_流水线寄存器_4  (
    .IN_MemToReg(\流水线寄存器_3_out_memtoreg ), .IN_RegWrite(\流水线寄存器_3_out_regwrite ),
    .IN_equal(\流水线寄存器_3_out_equal ), .IN_ALU(\流水线寄存器_3_out_alu ), .IN_MD(ram_1_data), .IN_PC(M_PC),
    .IN_IR(MEM_IR), .OUT_MemToReg(\流水线寄存器_4_out_memtoreg ), .OUT_RegWrite(RegWrite),
    .OUT_Syscall(\流水线寄存器_4_out_syscall ), .OUT_equal(\流水线寄存器_4_out_equal ), .OUT_ALU(\流水线寄存器_4_out_alu ),
    .OUT_MD(\流水线寄存器_4_out_md ), .OUT_PC(WB_PC), .OUT_IR(WB_IR), .EN(EN), .CLK(CLK), .RST(RST),
    .In_RegDst(\流水线寄存器_3_out_regdst ), .OUT_RegDst(\流水线寄存器_4_out_regdst ), .IN_JAL(\流水线寄存器_3_out_jal ),
    .OUT_JAL(\流水线寄存器_4_out_jal ), .CLR(1'b0), .IN_WriteReg_num(\流水线寄存器_3_out_writereg_num ),
    .In_Syscall(\流水线寄存器_3_out_syscall ));  // open: IN_MemWrite, IN_AluOP, IN_AluSrcB, IN_R1, IN_R2, IN_Imm, OUT_MemWrite, OUT_AluOP, OUT_AluSrcB, OUT_R1, OUT_R2, OUT_Imm, IN_Bne, OUT_Bne, IN_Beq, OUT_Beq, IN_shamt, OUT_shamt, IN_offset, OUT_offset, OUT_WriteReg_num, IN_JMP, OUT_JMP, IN_JR, OUT_JR
  Multiplexer #(.select(1), .width(32), .disabled("Z"), .enable("false")) multiplexer_11 (
    .in0(\流水线寄存器_4_out_alu ), .in1(\流水线寄存器_4_out_md ), .out(multiplexer_11_out), .sel(\流水线寄存器_4_out_memtoreg ));
  Multiplexer #(.select(1), .width(5), .disabled("Z"), .enable("false")) multiplexer_12 (
    .in0(WB_IR[20:16]), .in1(WB_IR[15:11]), .out(multiplexer_12_out), .sel(\流水线寄存器_4_out_regdst ));
  Multiplexer #(.select(1), .width(32), .disabled("Z"), .enable("false")) multiplexer_13 (
    .in0(multiplexer_11_out), .in1(adder_4_out), .out(RDin), .sel(\流水线寄存器_4_out_jal ));
  Multiplexer #(.select(1), .width(5), .disabled("Z"), .enable("false")) multiplexer_14 (
    .in0(multiplexer_12_out), .in1({5{1'b1}}), .out(multiplexer_14_out), .sel(\流水线寄存器_4_out_jal ));
  Adder #(.width(32)) adder_4 (.a(32'h4), .b(WB_PC), .out(adder_4_out));  // open: cin, cout

  // Other names for the same wires on the sheet: ID_IR[5:0] = Func; OP[5:0] = ID_IR[31:26];
  //   J_ADDR[31:28] = EX_PC[31:28]; MEM_PC[31:0] = M_PC; MEM_R2[31:0] = MDin

  // Notes on the sheet:
  //   中断源
  //   时空图监测，可删除
  //   中断等待指示
  //   数码管输出
  //   指令存储器
  //   contents of rom_1 (hex, n*v repeats v):
  //   20110001 8000c05 20110001 20120002 20130003 8000c09 20110001 20120002 20130003 8000c0d 20110001
  //   20120002 20130003 8000c11 20110001 20120002 20130003 c000cb8 20100001 20110001 118fc0 112020
  //   20020022 c 118882 12200001 8000c15 112020 20020022 c 20110001 118880 112020 20020022 c 12200001
  //   8000c1f 20110001 118fc0 112020 20020022 c 1188c3 112020 20020022 c 118903 112020 20020022 c 118903
  //   112020 20020022 c 118903 112020 20020022 c 118903 112020 20020022 c 118903 112020 20020022 c 118903
  //   112020 20020022 c 118903 112020 20020022 c 20100001 109fc0 139fc3 8021 2012000c 24160003 26100001
  //   3210000f 20080008 20090001 139900 2709825 132020 20020022 c 1094022 1500fff9 22100001 2018000f
  //   2188024 108700 20080008 20090001 139902 2709825 132021 20020022 c 1094022 1500fff9 108702 2c9b022
  //   12c00001 8000c50 4020 1084027 84400 3508ffff 82021 20020022 c 2010ffff 20110000 ae300000 22100001
  //   22310004 ae300000 22100001 22310004 ae300000 22100001 22310004 ae300000 22100001 22310004 ae300000
  //   22100001 22310004 ae300000 22100001 22310004 ae300000 22100001 22310004 ae300000 22100001 22310004
  //   ae300000 22100001 22310004 ae300000 22100001 22310004 ae300000 22100001 22310004 ae300000 22100001
  //   22310004 ae300000 22100001 22310004 ae300000 22100001 22310004 ae300000 22100001 22310004 ae300000
  //   22100001 22310004 22100001 8020 2011003c 8e130000 8e340000 274402a 11000002 ae330000 ae140000
  //   2231fffc 1611fff8 102020 20020022 c 22100004 2011003c 1611fff2 20020032 c 20100000 22100001 102020
  //   20020022 c 22100002 102020 20020022 c 22100003 102020 20020022 c 22100004 102020 20020022 c 22100005
  //   102020 20020022 c 22100006 102020 20020022 c 22100007 102020 20020022 c 22100008 102020 20020022
  //   20020022 c 3e00008
  //   控制位
  //   指令字
  //   流水调试日志用
  //   暂停节拍，不能为0
  //   JMP
  //   JR
  //   OP
  //   Func
  //   Syscall
  //   rs
  //   rt
  //   rd
  //   戳工具置1进入计数暂停模式，ctrl+k时钟自动运行到对应节拍暂停
  //   ctrl+k关闭时钟连续运行，将控制位置零，进入单步调试模式调试
  //   Beq
  //   Bne
  //   MemToReg
  //   MemWrite
  //   AluOP
  //   AluSrcB
  //   RegWrite
  //   JAL
  //   RegDst
  //   可计数暂停的时钟源
  //   为方便自动评测，需要输出流水线各段保存的PC值，注意是PC不是PC+4，另外ID段寄存器写入信息，Mem段内存写入信息也要输出
  //   rt
  //   rd
  //   rd
endmodule
module \重定向流水线  (
  output RegWrite,
  output MemWrite,
  output [31:0] IF_PC,
  output [31:0] ID_PC,
  output [31:0] EX_PC,
  output [31:0] M_PC,
  output [31:0] WB_PC,
  output [31:0] RDin,
  output [31:0] MDin,
  output [31:0] LedData
);

  wire and_1_out, and_2_out, CLK, clock_2_out, comparator_1_eq, comparator_1_lt, d_ff_2_q, EN, Go, IR1, IR2,
       IR3, mips_alu_1_equal, multiplexer_10_out, nand_1_out, not_1_out, or_1_out, or_2_out, or_3_out,
       or_4_out, or_5_out, RST, SignedExt, W1, W2, W3, \单周期硬布线控制器_1_alu_src , \单周期硬布线控制器_1_beq ,
       \单周期硬布线控制器_1_bne , \单周期硬布线控制器_1_jal , \单周期硬布线控制器_1_jmp , \单周期硬布线控制器_1_jr , \单周期硬布线控制器_1_memtoreg ,
       \单周期硬布线控制器_1_memwrite , \单周期硬布线控制器_1_regdst , \单周期硬布线控制器_1_regwrite , \单周期硬布线控制器_1_syscall ,
       \数据相关处理_1_datahazard , \流水线寄存器_2_out_alusrcb , \流水线寄存器_2_out_beq , \流水线寄存器_2_out_bne ,
       \流水线寄存器_2_out_jal , \流水线寄存器_2_out_jmp , \流水线寄存器_2_out_jr , \流水线寄存器_2_out_memtoreg ,
       \流水线寄存器_2_out_memwrite , \流水线寄存器_2_out_regdst , \流水线寄存器_2_out_regwrite , \流水线寄存器_2_out_syscall ,
       \流水线寄存器_3_out_equal , \流水线寄存器_3_out_jal , \流水线寄存器_3_out_memtoreg , \流水线寄存器_3_out_regdst ,
       \流水线寄存器_3_out_regwrite , \流水线寄存器_3_out_syscall , \流水线寄存器_4_out_equal , \流水线寄存器_4_out_jal ,
       \流水线寄存器_4_out_memtoreg , \流水线寄存器_4_out_regdst , \流水线寄存器_4_out_syscall ;
  wire [3:0] \单周期硬布线控制器_1_alu_op , \流水线寄存器_2_out_aluop ;
  wire [4:0] multiplexer_4_out, multiplexer_5_out, multiplexer_6_out, multiplexer_7_out, multiplexer_12_out,
       multiplexer_14_out, \流水线寄存器_2_out_shamt , \流水线寄存器_2_out_writereg_num , \流水线寄存器_3_out_writereg_num ;
  wire [5:0] Func;
  wire [12:0] CNT_num;
  wire [15:0] \LoadUse次数 , \总周期数 , \插入气泡数 , \无条件分支数 , \条件分支成功数 ;
  wire [27:2] J_ADDR;
  wire [31:0] adder_2_out, adder_4_out, bit_extender_1_out, BR_ADDR, EX_IR, IF_IR, IF_PC_4, JR_ADDR, MEM_IR,
       mips_alu_1_result, mips_regifile_1_r1, mips_regifile_1_r2, multiplexer_1_out, multiplexer_2_out,
       multiplexer_3_out, multiplexer_8_out, multiplexer_9_out, multiplexer_11_out, ram_1_data,
       shifter_1_out, undriven, WB_IR, \流水线寄存器_2_out_imm , \流水线寄存器_2_out_r2 , \流水线寄存器_3_out_alu ,
       \流水线寄存器_4_out_alu , \流水线寄存器_4_out_md ;
  wire [31:6] ID_IR;

  Button \u_总复位  (.out(RST));
  Button _1 (.out(IR1));
  Button _2 (.out(IR2));
  Button _3 (.out(IR3));
  // Probe on \总周期数 
  // Probe on \总周期数 
  Button \u_继续运行  (.out(Go));
  LED #(.active("true")) led_1 (.in(W1));
  LED #(.active("true")) led_2 (.in(W2));
  LED #(.active("true")) led_3 (.in(W3));
  Multiplexer #(.select(1), .width(32), .disabled("Z"), .enable("false")) multiplexer_1 (
    .in0({EX_PC[31:28], J_ADDR, 2'b00}), .in1(JR_ADDR), .out(multiplexer_1_out), .sel(\流水线寄存器_2_out_jr ));
  Hex_Digit_Display hex_digit_display_1 (.value(LedData[31:28]));  // open: dp
  // Probe on IF_PC[19:0]
  // Mips_Probe mips_probe_1: pin names not known; wires that end beside it: IF_IR
  Multiplexer #(.select(1), .width(32), .disabled("Z"), .enable("false")) multiplexer_2 (
    .in0(IF_PC_4), .in1(multiplexer_1_out), .out(multiplexer_2_out), .sel(\流水线寄存器_2_out_jmp ));
  Hex_Digit_Display hex_digit_display_2 (.value(LedData[23:20]));  // open: dp
  Hex_Digit_Display hex_digit_display_3 (.value(LedData[27:24]));  // open: dp
  // Probe on ID_PC[19:0]
  // Mips_Probe mips_probe_2: pin names not known; wires that end beside it: {ID_IR, Func}
  Multiplexer #(.select(1), .width(32), .disabled("Z"), .enable("false")) multiplexer_3 (
    .in0(multiplexer_2_out), .in1(BR_ADDR), .out(multiplexer_3_out), .sel(multiplexer_10_out));
  Hex_Digit_Display hex_digit_display_4 (.value(LedData[15:12]));  // open: dp
  Hex_Digit_Display hex_digit_display_5 (.value(LedData[19:16]));  // open: dp
  \数据相关处理  \u_数据相关处理_1  (
    .Instruction({ID_IR, Func}), .EX_RegWrite(\流水线寄存器_2_out_regwrite ),
    .EX_WriteReg_num(\流水线寄存器_2_out_writereg_num ), .MEM_RegWrite(\流水线寄存器_3_out_regwrite ),
    .MEM_WriteReg_num(\流水线寄存器_3_out_writereg_num ), .DataHazard(\数据相关处理_1_datahazard ),
    .R1_num(multiplexer_4_out), .R2_num(multiplexer_5_out));
  and and_1 (and_1_out, ~\数据相关处理_1_datahazard , EN);  // AND_Gate
  Hex_Digit_Display hex_digit_display_6 (.value(LedData[7:4]));  // open: dp
  Hex_Digit_Display hex_digit_display_7 (.value(LedData[11:8]));  // open: dp
  Clock #(.highDuration(1), .lowDuration(1)) clock_1 (.out(CLK));
  // Probe on EX_PC[19:0]
  // Mips_Probe mips_probe_3: pin names not known; wires that end beside it: EX_IR
  not not_1 (not_1_out, \流水线寄存器_4_out_syscall );
  Register #(.width(32), .trigger("rising"), .Select("low")) PC (
    .D(multiplexer_3_out), .en(and_1_out), .Q(IF_PC), .clk(CLK), .clr(RST));
  Hex_Digit_Display hex_digit_display_8 (.value(LedData[3:0]));  // open: dp
  or or_1 (or_1_out, not_1_out, Go);
  or or_2 (or_2_out, not_1_out, \流水线寄存器_4_out_equal );
  // Probe on \总周期数 
  // Probe on M_PC[19:0]
  // Mips_Probe mips_probe_4: pin names not known; wires that end beside it: MEM_IR
  D_Flip_Flop #(.trigger("falling"), .Pre_Clr_Positions("ABOVE_BELOW"), .NegatePresetClear("false"), .enable("false"), .NewFFLayout("true")) d_ff_1 (
    .clk(CLK), .D(or_2_out), .Q(EN), .preset(or_1_out));  // open: Qn, reset
  Counter #(.width(16), .max('hffff), .ongoal("wrap"), .trigger("rising"), .behavior("new")) counter_1 (
    .count(EN), .Q(\总周期数 ), .clk(CLK), .clr(RST));  // open: load, D, carry, preset, down
  Adder #(.width(32)) adder_1 (.a(IF_PC), .b(32'h4), .out(IF_PC_4));  // open: cin, cout
  // Probe on \总周期数 
  // Probe on \无条件分支数 
  // Probe on \条件分支成功数 
  // Probe on \插入气泡数 
  // Probe on \LoadUse次数 
  ROM #(.addrWidth(10), .dataWidth(32), .Select("high")) rom_1 (.addr(IF_PC[11:2]), .data(IF_IR));
  // Probe on IF_PC[11:0]
  // Probe on WB_PC[19:0]
  // Mips_Probe mips_probe_5: pin names not known; wires that end beside it: WB_IR
  \流水线寄存器  \u_流水线寄存器_1  (
    .IN_PC(IF_PC), .IN_IR(IF_IR), .OUT_PC(ID_PC), .OUT_IR({ID_IR, Func}), .EN(and_1_out), .CLK(CLK),
    .RST(RST), .CLR(or_5_out));  // open: IN_MemToReg, IN_MemWrite, IN_AluOP, IN_AluSrcB, IN_RegWrite, IN_equal, IN_R1, IN_ALU, IN_R2, IN_MD, IN_Imm, OUT_MemToReg, OUT_MemWrite, OUT_AluOP, OUT_AluSrcB, OUT_RegWrite, OUT_Syscall, OUT_equal, OUT_R1, OUT_ALU, OUT_R2, OUT_MD, OUT_Imm, In_RegDst, OUT_RegDst, IN_Bne, OUT_Bne, IN_Beq, OUT_Beq, IN_shamt, OUT_shamt, IN_offset, OUT_offset, IN_JAL, OUT_JAL, IN_WriteReg_num, OUT_WriteReg_num, IN_JMP, OUT_JMP, IN_JR, OUT_JR, In_Syscall
  // Probe on EX_PC[11:0]
  // Probe on ID_PC[11:0]
  // Mips_Probe mips_probe_6: pin names not known
  // Probe on M_PC[11:0]
  D_Flip_Flop #(.trigger("high"), .Pre_Clr_Positions("LEGACY"), .NegatePresetClear("false"), .enable("true"), .NewFFLayout("false")) d_ff_2 (.Q(d_ff_2_q));  // open: clk, D, Qn, preset, en, reset
  // Probe on 13'hc
  // Probe on WB_PC[11:0]
  Comparator #(.width(13), .mode("twosComplement")) comparator_1 (
    .a(CNT_num), .b(13'hc), .eq(comparator_1_eq), .lt(comparator_1_lt));  // open: gt
  Clock #(.highDuration(1), .lowDuration(1)) clock_2 (.out(clock_2_out));
  \单周期硬布线控制器  \u_单周期硬布线控制器_1  (
    .Func(Func), .OP(ID_IR[31:26]), .ALU_OP(\单周期硬布线控制器_1_alu_op ), .MemToReg(\单周期硬布线控制器_1_memtoreg ),
    .MemWrite(\单周期硬布线控制器_1_memwrite ), .ALU_SRC(\单周期硬布线控制器_1_alu_src ), .RegWrite(\单周期硬布线控制器_1_regwrite ),
    .SysCALL(\单周期硬布线控制器_1_syscall ), .SignedExt(SignedExt), .RegDst(\单周期硬布线控制器_1_regdst ),
    .JR(\单周期硬布线控制器_1_jr ), .JMP(\单周期硬布线控制器_1_jmp ), .Beq(\单周期硬布线控制器_1_beq ), .JAL(\单周期硬布线控制器_1_jal ),
    .Bne(\单周期硬布线控制器_1_bne ));
  Multiplexer #(.select(1), .width(5), .disabled("Z"), .enable("false")) multiplexer_4 (
    .in0(ID_IR[25:21]), .in1(5'b00010), .out(multiplexer_4_out), .sel(\单周期硬布线控制器_1_syscall ));
  Multiplexer #(.select(1), .width(5), .disabled("Z"), .enable("false")) multiplexer_5 (
    .in0(ID_IR[20:16]), .in1(5'b00100), .out(multiplexer_5_out), .sel(\单周期硬布线控制器_1_syscall ));
  Multiplexer #(.select(1), .width(5), .disabled("Z"), .enable("false")) multiplexer_6 (
    .in0(ID_IR[20:16]), .in1(ID_IR[15:11]), .out(multiplexer_6_out), .sel(\单周期硬布线控制器_1_regdst ));
  assign bit_extender_1_out = {{16{ID_IR[15]}}, {ID_IR[15:6], Func}};  // Bit_Extender bit_extender_1
  nand nand_1 (nand_1_out, d_ff_2_q, comparator_1_eq);
  Counter #(.width(13), .max('h1fff), .ongoal("stay"), .trigger("rising"), .behavior("old")) counter_2 (
    .count(comparator_1_lt), .Q(CNT_num), .clk(clock_2_out));  // open: load, D, carry, clr, preset
  assign CLK = nand_1_out ? clock_2_out : 1'bz;  // Controlled_Buffer controlled_buffer_1
  MIPS_Regifile mips_regifile_1 (
    .Din(RDin), .Clk(CLK), .R1(mips_regifile_1_r1), .R2(mips_regifile_1_r2), .WE(RegWrite),
    .W_num(multiplexer_14_out), .R1_num(multiplexer_4_out), .R2_num(multiplexer_5_out));
  Multiplexer #(.select(1), .width(5), .disabled("Z"), .enable("false")) multiplexer_7 (
    .in0(multiplexer_6_out), .in1({5{1'b1}}), .out(multiplexer_7_out), .sel(\单周期硬布线控制器_1_jal ));
  Pull_Resistor #(.pull(1)) pull_resistor_1 (.node(CLK));
  or or_3 (or_3_out, \数据相关处理_1_datahazard , or_5_out);
  or or_4 (or_4_out, \流水线寄存器_2_out_jr , \流水线寄存器_2_out_jmp );
  \流水线寄存器  \u_流水线寄存器_2  (
    .IN_MemToReg(\单周期硬布线控制器_1_memtoreg ), .IN_MemWrite(\单周期硬布线控制器_1_memwrite ),
    .IN_AluOP(\单周期硬布线控制器_1_alu_op ), .IN_AluSrcB(\单周期硬布线控制器_1_alu_src ),
    .IN_RegWrite(\单周期硬布线控制器_1_regwrite ), .IN_R1(mips_regifile_1_r1), .IN_R2(mips_regifile_1_r2),
    .IN_PC(ID_PC), .IN_IR({ID_IR, Func}), .IN_Imm(bit_extender_1_out),
    .OUT_MemToReg(\流水线寄存器_2_out_memtoreg ), .OUT_MemWrite(\流水线寄存器_2_out_memwrite ),
    .OUT_AluOP(\流水线寄存器_2_out_aluop ), .OUT_AluSrcB(\流水线寄存器_2_out_alusrcb ),
    .OUT_RegWrite(\流水线寄存器_2_out_regwrite ), .OUT_Syscall(\流水线寄存器_2_out_syscall ), .OUT_R1(JR_ADDR),
    .OUT_R2(\流水线寄存器_2_out_r2 ), .OUT_PC(EX_PC), .OUT_IR(EX_IR), .OUT_Imm(\流水线寄存器_2_out_imm ), .EN(EN),
    .CLK(CLK), .RST(RST), .In_RegDst(\单周期硬布线控制器_1_regdst ), .OUT_RegDst(\流水线寄存器_2_out_regdst ),
    .IN_Bne(\单周期硬布线控制器_1_bne ), .OUT_Bne(\流水线寄存器_2_out_bne ), .IN_Beq(\单周期硬布线控制器_1_beq ),
    .OUT_Beq(\流水线寄存器_2_out_beq ), .IN_shamt(ID_IR[10:6]), .OUT_shamt(\流水线寄存器_2_out_shamt ),
    .IN_offset({ID_IR[25:6], Func}), .OUT_offset(J_ADDR), .IN_JAL(\单周期硬布线控制器_1_jal ),
    .OUT_JAL(\流水线寄存器_2_out_jal ), .CLR(or_3_out), .IN_WriteReg_num(multiplexer_7_out),
    .OUT_WriteReg_num(\流水线寄存器_2_out_writereg_num ), .IN_JMP(\单周期硬布线控制器_1_jmp ), .OUT_JMP(\流水线寄存器_2_out_jmp ),
    .IN_JR(\单周期硬布线控制器_1_jr ), .OUT_JR(\流水线寄存器_2_out_jr ), .In_Syscall(\单周期硬布线控制器_1_syscall ));  // open: IN_equal, IN_ALU, IN_MD, OUT_equal, OUT_ALU, OUT_MD
  Multiplexer #(.select(1), .width(32), .disabled("Z"), .enable("false")) multiplexer_8 (
    .in0(\流水线寄存器_2_out_r2 ), .in1(\流水线寄存器_2_out_imm ), .out(multiplexer_8_out), .sel(\流水线寄存器_2_out_alusrcb ));
  Shifter #(.width(32), .shift("ll")) shifter_1 (.in(\流水线寄存器_2_out_imm ), .\dist (5'b00010), .out(shifter_1_out));
  Multiplexer #(.select(1), .width(32), .disabled("Z"), .enable("false")) multiplexer_9 (
    .in0(multiplexer_8_out), .in1(32'h22), .out(multiplexer_9_out), .sel(\流水线寄存器_2_out_syscall ));
  or or_5 (or_5_out, or_4_out, multiplexer_10_out);
  Adder #(.width(32)) adder_2 (.a(EX_PC), .b(32'h4), .out(adder_2_out));  // open: cin, cout
  Multiplexer #(.select(1), .width(1), .disabled("Z"), .enable("false")) multiplexer_10 (
    .in0(\流水线寄存器_2_out_bne ), .in1(\流水线寄存器_2_out_beq ), .out(multiplexer_10_out), .sel(mips_alu_1_equal));
  MIPS_ALU mips_alu_1 (
    .X(JR_ADDR), .Y(multiplexer_9_out), .AluOP(\流水线寄存器_2_out_aluop ), .Equal(mips_alu_1_equal),
    .Result(mips_alu_1_result), .shamt(\流水线寄存器_2_out_shamt ));  // open: Result_2
  Adder #(.width(32)) adder_3 (.a(shifter_1_out), .b(adder_2_out), .out(BR_ADDR));  // open: cin, cout
  \流水线寄存器  \u_流水线寄存器_3  (
    .IN_MemToReg(\流水线寄存器_2_out_memtoreg ), .IN_MemWrite(\流水线寄存器_2_out_memwrite ),
    .IN_RegWrite(\流水线寄存器_2_out_regwrite ), .IN_equal(mips_alu_1_equal), .IN_R1(undriven),
    .IN_ALU(mips_alu_1_result), .IN_R2(\流水线寄存器_2_out_r2 ), .IN_PC(EX_PC), .IN_IR(EX_IR),
    .OUT_MemToReg(\流水线寄存器_3_out_memtoreg ), .OUT_MemWrite(MemWrite), .OUT_RegWrite(\流水线寄存器_3_out_regwrite ),
    .OUT_Syscall(\流水线寄存器_3_out_syscall ), .OUT_equal(\流水线寄存器_3_out_equal ), .OUT_ALU(\流水线寄存器_3_out_alu ),
    .OUT_R2(MDin), .OUT_PC(M_PC), .OUT_IR(MEM_IR), .EN(EN), .CLK(CLK), .RST(RST),
    .In_RegDst(\流水线寄存器_2_out_regdst ), .OUT_RegDst(\流水线寄存器_3_out_regdst ), .IN_JAL(\流水线寄存器_2_out_jal ),
    .OUT_JAL(\流水线寄存器_3_out_jal ), .CLR(1'b0), .IN_WriteReg_num(\流水线寄存器_2_out_writereg_num ),
    .OUT_WriteReg_num(\流水线寄存器_3_out_writereg_num ), .In_Syscall(\流水线寄存器_2_out_syscall ));  // open: IN_AluOP, IN_AluSrcB, IN_MD, IN_Imm, OUT_AluOP, OUT_AluSrcB, OUT_R1, OUT_MD, OUT_Imm, IN_Bne, OUT_Bne, IN_Beq, OUT_Beq, IN_shamt, OUT_shamt, IN_offset, OUT_offset, IN_JMP, OUT_JMP, IN_JR, OUT_JR
  and and_2 (and_2_out, \流水线寄存器_3_out_syscall , \流水线寄存器_3_out_equal );
  Register #(.width(32), .trigger("rising"), .Select("low")) register_1 (
    .D(MDin), .en(and_2_out), .Q(LedData), .clk(CLK), .clr(RST));
  RAM #(.addrWidth(10), .dataWidth(32), .bus("separate"), .Select("high")) ram_1 (
    .addr(\流水线寄存器_3_out_alu [11:2]), .din(MDin), .data(ram_1_data), .str(MemWrite), .clk(CLK), .clr(RST));  // open: sel, ld
  \流水线寄存器  \u_流水线寄存器_4  (
    .IN_MemToReg(\流水线寄存器_3_out_memtoreg ), .IN_RegWrite(\流水线寄存器_3_out_regwrite ),
    .IN_equal(\流水线寄存器_3_out_equal ), .IN_ALU(\流水线寄存器_3_out_alu ), .IN_MD(ram_1_data), .IN_PC(M_PC),
    .IN_IR(MEM_IR), .OUT_MemToReg(\流水线寄存器_4_out_memtoreg ), .OUT_RegWrite(RegWrite),
    .OUT_Syscall(\流水线寄存器_4_out_syscall ), .OUT_equal(\流水线寄存器_4_out_equal ), .OUT_ALU(\流水线寄存器_4_out_alu ),
    .OUT_MD(\流水线寄存器_4_out_md ), .OUT_PC(WB_PC), .OUT_IR(WB_IR), .EN(EN), .CLK(CLK), .RST(RST),
    .In_RegDst(\流水线寄存器_3_out_regdst ), .OUT_RegDst(\流水线寄存器_4_out_regdst ), .IN_JAL(\流水线寄存器_3_out_jal ),
    .OUT_JAL(\流水线寄存器_4_out_jal ), .CLR(1'b0), .IN_WriteReg_num(\流水线寄存器_3_out_writereg_num ),
    .In_Syscall(\流水线寄存器_3_out_syscall ));  // open: IN_MemWrite, IN_AluOP, IN_AluSrcB, IN_R1, IN_R2, IN_Imm, OUT_MemWrite, OUT_AluOP, OUT_AluSrcB, OUT_R1, OUT_R2, OUT_Imm, IN_Bne, OUT_Bne, IN_Beq, OUT_Beq, IN_shamt, OUT_shamt, IN_offset, OUT_offset, OUT_WriteReg_num, IN_JMP, OUT_JMP, IN_JR, OUT_JR
  Multiplexer #(.select(1), .width(32), .disabled("Z"), .enable("false")) multiplexer_11 (
    .in0(\流水线寄存器_4_out_alu ), .in1(\流水线寄存器_4_out_md ), .out(multiplexer_11_out), .sel(\流水线寄存器_4_out_memtoreg ));
  Multiplexer #(.select(1), .width(5), .disabled("Z"), .enable("false")) multiplexer_12 (
    .in0(WB_IR[20:16]), .in1(WB_IR[15:11]), .out(multiplexer_12_out), .sel(\流水线寄存器_4_out_regdst ));
  Multiplexer #(.select(1), .width(32), .disabled("Z"), .enable("false")) multiplexer_13 (
    .in0(multiplexer_11_out), .in1(adder_4_out), .out(RDin), .sel(\流水线寄存器_4_out_jal ));
  Multiplexer #(.select(1), .width(5), .disabled("Z"), .enable("false")) multiplexer_14 (
    .in0(multiplexer_12_out), .in1({5{1'b1}}), .out(multiplexer_14_out), .sel(\流水线寄存器_4_out_jal ));
  Adder #(.width(32)) adder_4 (.a(32'h4), .b(WB_PC), .out(adder_4_out));  // open: cin, cout

  // Other names for the same wires on the sheet: ID_IR[5:0] = Func; OP[5:0] = ID_IR[31:26];
  //   J_ADDR[31:28] = EX_PC[31:28]; MEM_PC[31:0] = M_PC; MEM_R2[31:0] = MDin

  // Notes on the sheet:
  //   中断源
  //   时空图监测，可删除
  //   中断等待指示
  //   数码管输出
  //   指令存储器
  //   contents of rom_1 (hex, n*v repeats v):
  //   20110001 8000c05 20110001 20120002 20130003 8000c09 20110001 20120002 20130003 8000c0d 20110001
  //   20120002 20130003 8000c11 20110001 20120002 20130003 c000cb8 20100001 20110001 118fc0 112020
  //   20020022 c 118882 12200001 8000c15 112020 20020022 c 20110001 118880 112020 20020022 c 12200001
  //   8000c1f 20110001 118fc0 112020 20020022 c 1188c3 112020 20020022 c 118903 112020 20020022 c 118903
  //   112020 20020022 c 118903 112020 20020022 c 118903 112020 20020022 c 118903 112020 20020022 c 118903
  //   112020 20020022 c 118903 112020 20020022 c 20100001 109fc0 139fc3 8021 2012000c 24160003 26100001
  //   3210000f 20080008 20090001 139900 2709825 132020 20020022 c 1094022 1500fff9 22100001 2018000f
  //   2188024 108700 20080008 20090001 139902 2709825 132021 20020022 c 1094022 1500fff9 108702 2c9b022
  //   12c00001 8000c50 4020 1084027 84400 3508ffff 82021 20020022 c 2010ffff 20110000 ae300000 22100001
  //   22310004 ae300000 22100001 22310004 ae300000 22100001 22310004 ae300000 22100001 22310004 ae300000
  //   22100001 22310004 ae300000 22100001 22310004 ae300000 22100001 22310004 ae300000 22100001 22310004
  //   ae300000 22100001 22310004 ae300000 22100001 22310004 ae300000 22100001 22310004 ae300000 22100001
  //   22310004 ae300000 22100001 22310004 ae300000 22100001 22310004 ae300000 22100001 22310004 ae300000
  //   22100001 22310004 22100001 8020 2011003c 8e130000 8e340000 274402a 11000002 ae330000 ae140000
  //   2231fffc 1611fff8 102020 20020022 c 22100004 2011003c 1611fff2 20020032 c 20100000 22100001 102020
  //   20020022 c 22100002 102020 20020022 c 22100003 102020 20020022 c 22100004 102020 20020022 c 22100005
  //   102020 20020022 c 22100006 102020 20020022 c 22100007 102020 20020022 c 22100008 102020 20020022
  //   20020022 c 3e00008
  //   控制位
  //   指令字
  //   流水调试日志用
  //   暂停节拍，不能为0
  //   JMP
  //   JR
  //   OP
  //   Func
  //   Syscall
  //   rs
  //   rt
  //   rd
  //   戳工具置1进入计数暂停模式，ctrl+k时钟自动运行到对应节拍暂停
  //   ctrl+k关闭时钟连续运行，将控制位置零，进入单步调试模式调试
  //   Beq
  //   Bne
  //   MemToReg
  //   MemWrite
  //   AluOP
  //   AluSrcB
  //   RegWrite
  //   JAL
  //   RegDst
  //   可计数暂停的时钟源
  //   为方便自动评测，需要输出流水线各段保存的PC值，注意是PC不是PC+4，另外ID段寄存器写入信息，Mem段内存写入信息也要输出
  //   rt
  //   rd
  //   rd
endmodule

module \中断按键参考电路  (
  input  CLK,
  input  Eret,
  input  RST,
  input  IntR,
  input  Int1,
  input  Int2,
  input  Int3,
  output [1:0] IntNo,
  output PriorInt
);

  wire and_1_out, and_2_out, and_3_out, and_4_out, and_5_out, buffer_1_out, CLR1, CLR2, CLR3, d_ff_1_q,
       d_ff_2_q, d_ff_3_q, IR1_q, IR2_q, IR3_q, nand_1_out, not_1_out, or_1_out, or_2_out, or_3_out,
       or_4_out, or_5_out, or_6_out, or_7_out, priority_encoder_1_gs;
  wire [1:0] IntNo_t, xor_1_out;

  or or_1 (or_1_out, IR1_q, d_ff_1_q);
  LED #(.active("true")) \_1号中断等待指示灯  (.in(or_1_out));
  LED #(.active("true")) \_2号中断等待指示灯  (.in(or_2_out));
  or or_2 (or_2_out, IR2_q, d_ff_2_q);
  LED #(.active("true")) \_3号中断等待指示灯  (.in(or_3_out));
  or or_3 (or_3_out, IR3_q, d_ff_3_q);
  D_Flip_Flop #(.trigger("rising"), .Pre_Clr_Positions("LEGACY"), .NegatePresetClear("false"), .enable("true"), .NewFFLayout("false")) d_ff_1 (
    .clk(Int1), .D(1'b1), .Q(d_ff_1_q), .reset(IR1_q));  // open: Qn, preset, en
  D_Flip_Flop #(.trigger("rising"), .Pre_Clr_Positions("LEGACY"), .NegatePresetClear("false"), .enable("true"), .NewFFLayout("false")) d_ff_2 (
    .clk(Int2), .D(1'b1), .Q(d_ff_2_q), .reset(IR2_q));  // open: Qn, preset, en
  D_Flip_Flop #(.trigger("rising"), .Pre_Clr_Positions("LEGACY"), .NegatePresetClear("false"), .enable("true"), .NewFFLayout("false")) d_ff_3 (
    .clk(Int3), .D(1'b1), .Q(d_ff_3_q), .reset(IR3_q));  // open: Qn, preset, en
  or or_4 (or_4_out, d_ff_1_q, IR1_q);
  or or_5 (or_5_out, d_ff_2_q, IR2_q);
  or or_6 (or_6_out, d_ff_3_q, IR3_q);
  and and_1 (and_1_out, or_4_out, ~CLR1);  // AND_Gate
  and and_2 (and_2_out, or_5_out, ~CLR2);  // AND_Gate
  and and_3 (and_3_out, or_6_out, ~CLR3);  // AND_Gate
  D_Flip_Flop #(.trigger("rising"), .Pre_Clr_Positions("LEGACY"), .NegatePresetClear("false"), .enable("true"), .NewFFLayout("false")) IR1 (
    .clk(CLK), .D(and_1_out), .Q(IR1_q), .reset(RST));  // open: Qn, preset, en
  D_Flip_Flop #(.trigger("rising"), .Pre_Clr_Positions("LEGACY"), .NegatePresetClear("false"), .enable("true"), .NewFFLayout("false")) IR2 (
    .clk(CLK), .D(and_2_out), .Q(IR2_q), .reset(RST));  // open: Qn, preset, en
  D_Flip_Flop #(.trigger("rising"), .Pre_Clr_Positions("LEGACY"), .NegatePresetClear("false"), .enable("true"), .NewFFLayout("false")) IR3 (
    .clk(CLK), .D(and_3_out), .Q(IR3_q), .reset(RST));  // open: Qn, preset, en
  not not_1 (not_1_out, IntNo_t[1]);
  nand nand_1 (nand_1_out, IntNo_t[1], IntNo_t[0]);
  and and_4 (and_4_out, IR1_q, not_1_out);
  and and_5 (and_5_out, IR2_q, nand_1_out);
  buf buffer_1 (buffer_1_out, IR3_q);
  Pull_Resistor #(.pull(0)) pull_resistor_1 (.node(IntNo));
  Priority_Encoder #(.select(2), .disabled("Z")) priority_encoder_1 (
    .in0(1'b0), .in1(and_4_out), .in2(and_5_out), .in3(buffer_1_out), .out(IntNo), .gs(priority_encoder_1_gs));  // open: en_out, en_in
  Demultiplexer #(.select(2), .width(1), .tristate("false"), .disabled("Z"), .enable("false")) demultiplexer_1 (
    .out1(CLR1), .out2(CLR2), .out3(CLR3), .in(Eret), .sel(IntNo_t));  // open: out0
  \嵌套中断堆栈  \u_嵌套中断堆栈_1  (.PUSH(IntR), .Din(IntNo), .POP(Eret), .RST(RST), .CLK(CLK), .Dout(IntNo_t));
  or or_7 (or_7_out, xor_1_out[0], xor_1_out[1]);
  assign xor_1_out = IntNo ^ IntNo_t;  // XOR_Gate xor_1, 2 bits wide
  and and_6 (PriorInt, or_7_out, priority_encoder_1_gs);

  // Notes on the sheet:
  //   1号中断信号采样电路
  //   2号中断信号采样电路
  //   3号中断信号采样电路
  //   Reset 
  //   Reset 
  //   Reset 
endmodule

module \单周期MIPS_单级中断  (
  input  IR1,
  input  IR2,
  input  IR3,
  output RegWrite,
  output MemWrite,
  output [31:0] PC,
  output [31:0] IR,
  output [31:0] RDin,
  output [31:0] MDin,
  output [31:0] LedData
);

  wire and_1_out, CLK, clock_2_out, comparator_1_eq, comparator_1_lt, comparator_2_eq, comparator_3_eq,
       comparator_4_eq, comparator_5_eq, comparator_6_eq, comparator_7_eq, d_ff_1_q, d_ff_3_qn, d_ff_4_q,
       d_ff_5_q, EN, equal, Eret, Go, IntR, IntR_Eret, IR1_t, IR2_t, IR3_t, IRA, IRB, IRC,
       multiplexer_12_out, nand_1_out, not_1_out, or_3_out, or_5_out, or_6_out, or_7_out, RST, SignedExt,
       Syscall, W1, W2, W3, \中断按键参考电路_1_priorint , \单周期硬布线控制器_1_alu_src , \单周期硬布线控制器_1_beq ,
       \单周期硬布线控制器_1_bne , \单周期硬布线控制器_1_jal , \单周期硬布线控制器_1_jmp , \单周期硬布线控制器_1_jr , \单周期硬布线控制器_1_memtoreg ,
       \单周期硬布线控制器_1_regdst ;
  wire [1:0] IntNo;
  wire [3:0] \单周期硬布线控制器_1_alu_op ;
  wire [4:0] multiplexer_5_out, multiplexer_6_out, multiplexer_7_out, multiplexer_8_out;
  wire [12:0] CNT_num;
  wire [15:0] \总周期数 ;
  wire [31:0] bit_extender_1_out, BR_ADDR, EPCR_q, Int_EretAddr, IntAddr, JR_ADDR, mips_alu_1_result,
       multiplexer_1_out, multiplexer_2_out, multiplexer_4_out, multiplexer_9_out, multiplexer_10_out,
       multiplexer_11_out, NextPC, PC_4, ram_1_data, shifter_1_out;

  Button button_1 (.out(RST));
  Clock #(.highDuration(1), .lowDuration(1)) clock_1 ();  // open: out
  Button _1 ();  // open: out
  Button _2 ();  // open: out
  Button _3 ();  // open: out
  Button \u_继续运行  (.out(Go));
  LED #(.active("true")) led_1 (.in(W1));
  LED #(.active("true")) led_2 (.in(W2));
  LED #(.active("true")) led_3 (.in(W3));
  Multiplexer #(.select(1), .width(32), .disabled("Z"), .enable("false")) multiplexer_1 (
    .in0({PC[31:28], IR[25:0], 2'b00}), .in1(JR_ADDR), .out(multiplexer_1_out), .sel(\单周期硬布线控制器_1_jr ));
  D_Flip_Flop #(.trigger("high"), .Pre_Clr_Positions("LEGACY"), .NegatePresetClear("false"), .enable("true"), .NewFFLayout("false")) d_ff_1 (.Q(d_ff_1_q));  // open: clk, D, Qn, preset, en, reset
  // Probe on 13'hc
  Hex_Digit_Display hex_digit_display_1 (.value(LedData[31:28]));  // open: dp
  Multiplexer #(.select(1), .width(32), .disabled("Z"), .enable("false")) multiplexer_2 (
    .in0(PC_4), .in1(multiplexer_1_out), .out(multiplexer_2_out), .sel(\单周期硬布线控制器_1_jmp ));
  Adder #(.width(32)) adder_1 (.a(PC), .b(32'h4), .out(PC_4));  // open: cin, cout
  Clock #(.highDuration(1), .lowDuration(1)) clock_2 (.out(clock_2_out));
  Hex_Digit_Display hex_digit_display_2 (.value(LedData[23:20]));  // open: dp
  Hex_Digit_Display hex_digit_display_3 (.value(LedData[27:24]));  // open: dp
  Multiplexer #(.select(1), .width(32), .disabled("Z"), .enable("false")) multiplexer_3 (
    .in0(multiplexer_2_out), .in1(BR_ADDR), .out(NextPC), .sel(multiplexer_12_out));
  Comparator #(.width(13), .mode("twosComplement")) comparator_1 (
    .a(CNT_num), .b(13'hc), .eq(comparator_1_eq), .lt(comparator_1_lt));  // open: gt
  Hex_Digit_Display hex_digit_display_4 (.value(LedData[15:12]));  // open: dp
  Hex_Digit_Display hex_digit_display_5 (.value(LedData[19:16]));  // open: dp
  Multiplexer #(.select(1), .width(32), .disabled("Z"), .enable("false")) multiplexer_4 (
    .in0(NextPC), .in1(Int_EretAddr), .out(multiplexer_4_out), .sel(IntR_Eret));
  nand nand_1 (nand_1_out, d_ff_1_q, comparator_1_eq);
  Counter #(.width(13), .max('h1fff), .ongoal("stay"), .trigger("rising"), .behavior("old")) counter_1 (
    .count(comparator_1_lt), .Q(CNT_num), .clk(clock_2_out));  // open: load, D, carry, clr, preset
  Hex_Digit_Display hex_digit_display_6 (.value(LedData[11:8]));  // open: dp
  Hex_Digit_Display hex_digit_display_7 (.value(LedData[7:4]));  // open: dp
  // Probe on \总周期数 
  Register #(.width(32), .trigger("rising"), .Select("low")) u_PC (
    .D(multiplexer_4_out), .en(EN), .Q(PC), .clk(CLK), .clr(RST));
  Hex_Digit_Display hex_digit_display_8 (.value(LedData[3:0]));  // open: dp
  assign CLK = nand_1_out ? clock_2_out : 1'bz;  // Controlled_Buffer controlled_buffer_1
  Pull_Resistor #(.pull(1)) pull_resistor_1 (.node(CLK));
  ROM #(.addrWidth(10), .dataWidth(32), .Select("high")) rom_1 (.addr(PC[11:2]), .data(IR));
  or or_1 (IR1_t, IR1, IRA);
  // Mips_Probe mips_probe_1: pin names not known; wires that end beside it: IR
  or or_2 (IR2_t, IR2, IRB);
  \单周期硬布线控制器  \u_单周期硬布线控制器_1  (
    .Func(IR[5:0]), .OP(IR[31:26]), .ALU_OP(\单周期硬布线控制器_1_alu_op ), .MemToReg(\单周期硬布线控制器_1_memtoreg ),
    .MemWrite(MemWrite), .ALU_SRC(\单周期硬布线控制器_1_alu_src ), .RegWrite(RegWrite), .SysCALL(Syscall),
    .SignedExt(SignedExt), .RegDst(\单周期硬布线控制器_1_regdst ), .JR(\单周期硬布线控制器_1_jr ), .JMP(\单周期硬布线控制器_1_jmp ),
    .Beq(\单周期硬布线控制器_1_beq ), .JAL(\单周期硬布线控制器_1_jal ), .Bne(\单周期硬布线控制器_1_bne ));
  Multiplexer #(.select(1), .width(5), .disabled("Z"), .enable("false")) multiplexer_5 (
    .in0(IR[25:21]), .in1(5'b00010), .out(multiplexer_5_out), .sel(Syscall));
  not not_1 (not_1_out, Syscall);
  Multiplexer #(.select(1), .width(5), .disabled("Z"), .enable("false")) multiplexer_6 (
    .in0(IR[20:16]), .in1(5'b00100), .out(multiplexer_6_out), .sel(Syscall));
  Multiplexer #(.select(1), .width(5), .disabled("Z"), .enable("false")) multiplexer_7 (
    .in0(IR[20:16]), .in1(IR[15:11]), .out(multiplexer_7_out), .sel(\单周期硬布线控制器_1_regdst ));
  Multiplexer #(.select(1), .width(5), .disabled("Z"), .enable("false")) multiplexer_8 (
    .in0(multiplexer_7_out), .in1({5{1'b1}}), .out(multiplexer_8_out), .sel(\单周期硬布线控制器_1_jal ));
  or or_3 (or_3_out, equal, not_1_out);
  or or_4 (IR3_t, IR3, IRC);
  MIPS_Regifile mips_regifile_1 (
    .Din(RDin), .Clk(CLK), .R1(JR_ADDR), .R2(MDin), .WE(RegWrite), .W_num(multiplexer_8_out),
    .R1_num(multiplexer_5_out), .R2_num(multiplexer_6_out));
  assign bit_extender_1_out = {{16{IR[15]}}, IR[15:0]};  // Bit_Extender bit_extender_1
  or or_5 (or_5_out, not_1_out, Go);
  D_Flip_Flop #(.trigger("falling"), .Pre_Clr_Positions("ABOVE_BELOW"), .NegatePresetClear("false"), .enable("false"), .NewFFLayout("true")) d_ff_2 (
    .clk(CLK), .D(or_3_out), .Q(EN), .preset(or_5_out));  // open: Qn, reset
  Multiplexer #(.select(1), .width(32), .disabled("Z"), .enable("false")) multiplexer_9 (
    .in0(MDin), .in1(bit_extender_1_out), .out(multiplexer_9_out), .sel(\单周期硬布线控制器_1_alu_src ));
  Multiplexer #(.select(1), .width(32), .disabled("Z"), .enable("false")) multiplexer_10 (
    .in0(multiplexer_9_out), .in1(32'h22), .out(multiplexer_10_out), .sel(Syscall));
  Shifter #(.width(32), .shift("ll")) shifter_1 (.in(bit_extender_1_out), .\dist (5'b00010), .out(shifter_1_out));
  MIPS_ALU mips_alu_1 (
    .X(JR_ADDR), .Y(multiplexer_10_out), .AluOP(\单周期硬布线控制器_1_alu_op ), .Equal(equal),
    .Result(mips_alu_1_result), .shamt(IR[10:6]));  // open: Result_2
  Adder #(.width(32)) adder_2 (.a(shifter_1_out), .b(PC_4), .out(BR_ADDR));  // open: cin, cout
  Counter #(.width(16), .max('hffff), .ongoal("wrap"), .trigger("rising"), .behavior("new")) counter_2 (
    .count(EN), .Q(\总周期数 ), .clk(CLK), .clr(RST));  // open: load, D, carry, preset, down
  Multiplexer #(.select(1), .width(32), .disabled("Z"), .enable("false")) multiplexer_11 (
    .in0(mips_alu_1_result), .in1(ram_1_data), .out(multiplexer_11_out), .sel(\单周期硬布线控制器_1_memtoreg ));
  RAM #(.addrWidth(10), .dataWidth(32), .bus("separate"), .Select("high")) ram_1 (
    .addr(mips_alu_1_result[11:2]), .din(MDin), .data(ram_1_data), .str(MemWrite), .clk(CLK), .clr(RST));  // open: sel, ld
  and and_1 (and_1_out, Syscall, equal);
  Register #(.width(32), .trigger("rising"), .Select("low")) register_1 (
    .D(MDin), .en(and_1_out), .Q(LedData), .clk(CLK), .clr(RST));
  Multiplexer #(.select(1), .width(1), .disabled("Z"), .enable("false")) multiplexer_12 (
    .in0(\单周期硬布线控制器_1_bne ), .in1(\单周期硬布线控制器_1_beq ), .out(multiplexer_12_out), .sel(equal));
  Multiplexer #(.select(1), .width(32), .disabled("Z"), .enable("false")) multiplexer_13 (
    .in0(multiplexer_11_out), .in1(PC_4), .out(RDin), .sel(\单周期硬布线控制器_1_jal ));
  \中断按键参考电路  \u_中断按键参考电路_1  (
    .CLK(CLK), .RST(RST), .Eret(Eret), .Int1(IR1_t), .Int2(IR2_t), .Int3(IR3_t),
    .PriorInt(\中断按键参考电路_1_priorint ), .IntNo(IntNo), .IntR(IntR));
  D_Flip_Flop #(.trigger("rising"), .Pre_Clr_Positions("LEGACY"), .NegatePresetClear("false"), .enable("true"), .NewFFLayout("false")) d_ff_3 (
    .Qn(d_ff_3_qn), .preset(d_ff_4_q), .reset(or_6_out));  // open: clk, D, Q, en
  D_Flip_Flop #(.trigger("rising"), .Pre_Clr_Positions("LEGACY"), .NegatePresetClear("false"), .enable("true"), .NewFFLayout("false")) d_ff_4 (
    .clk(CLK), .D(IntR), .Q(d_ff_4_q), .reset(RST));  // open: Qn, preset, en
  or or_6 (or_6_out, d_ff_5_q, RST);
  D_Flip_Flop #(.trigger("rising"), .Pre_Clr_Positions("LEGACY"), .NegatePresetClear("false"), .enable("true"), .NewFFLayout("false")) d_ff_5 (
    .clk(CLK), .D(Eret), .Q(d_ff_5_q), .reset(RST));  // open: Qn, preset, en
  Comparator #(.width(16), .mode("twosComplement")) comparator_2 (
    .a(16'h23b), .b(\总周期数 ), .eq(comparator_2_eq));  // open: gt, lt
  Comparator #(.width(16), .mode("twosComplement")) comparator_3 (
    .a(\总周期数 ), .b(16'h1), .eq(comparator_3_eq));  // open: gt, lt
  Comparator #(.width(16), .mode("twosComplement")) comparator_4 (
    .a(\总周期数 ), .b(16'h4), .eq(comparator_4_eq));  // open: gt, lt
  Comparator #(.width(16), .mode("twosComplement")) comparator_5 (
    .a(\总周期数 ), .b(16'h7), .eq(comparator_5_eq));  // open: gt, lt
  and and_2 (IntR, \中断按键参考电路_1_priorint , d_ff_3_qn);
  Pull_Resistor #(.pull(0)) pull_resistor_2 (.node(IRA));
  or or_7 (or_7_out, comparator_2_eq, comparator_3_eq);
  assign IRA = or_7_out ? ~CLK : 1'bz;  // Controlled_Inverter controlled_inverter_1
  Pull_Resistor #(.pull(0)) pull_resistor_3 (.node(IRB));
  assign IRB = comparator_4_eq ? ~CLK : 1'bz;  // Controlled_Inverter controlled_inverter_2
  Pull_Resistor #(.pull(0)) pull_resistor_4 (.node(IRC));
  assign IRC = comparator_5_eq ? ~CLK : 1'bz;  // Controlled_Inverter controlled_inverter_3
  or or_8 (IntR_Eret, IntR, Eret);
  Multiplexer #(.select(2), .width(32), .disabled("Z"), .enable("false")) multiplexer_14 (
    .in1(32'h30ac), .in2(32'h3150), .in3(32'h31f4), .out(IntAddr), .sel(IntNo));  // open: in0
  Register #(.width(32), .trigger("rising"), .Select("low")) EPCR (
    .D(NextPC), .en(IntR), .Q(EPCR_q), .clk(CLK), .clr(RST));
  Comparator #(.width(6), .mode("twosComplement")) comparator_6 (
    .a(IR[31:26]), .b(6'b010000), .eq(comparator_6_eq));  // open: gt, lt
  Comparator #(.width(6), .mode("twosComplement")) comparator_7 (
    .a(IR[5:0]), .b(6'b011000), .eq(comparator_7_eq));  // open: gt, lt
  Multiplexer #(.select(1), .width(32), .disabled("Z"), .enable("false")) multiplexer_15 (
    .in0(IntAddr), .in1(EPCR_q), .out(Int_EretAddr), .sel(Eret));
  and and_3 (Eret, comparator_6_eq, comparator_7_eq);

  // Other names for the same wires on the sheet: Func[5:0] = IR[5:0]; imm[25:0] = IR[25:0];
  //   J_ADDR[31:2] = {PC[31:28], IR[25:0]}; OP[5:0] = IR[31:26]

  // Notes on the sheet:
  //   中断源
  //   控制位
  //   中断等待指示
  //   总复位信号应将除ROM以外所有存储组件全部清零
  //   暂停节拍，不能为0
  //   戳工具置1进入计数暂停模式，ctrl+k时钟自动运行到对应节拍暂停
  //   ctrl+k关闭时钟连续运行，将控制位置零，进入单步调试模式调试
  //   用这个时钟源需要去掉电路中的其他时钟源
  //   数码管输出
  //   数码管输出应该用寄存器锁存，否则显示数据只能一闪而过
  //   指令存储器
  //   指令字
  //   contents of rom_1 (hex, n*v repeats v):
  //   201d07d0 20100001 109fc0 139fc3 8021 2012000c 24160008 26100001 3210000f 20080008 20090001 139900
  //   2709825 132020 20020022 c 1094022 1500fff9 22100001 2018000f 2188024 108700 20080008 20090001 139902
  //   2709825 132021 20020022 c 1094022 1500fff9 108702 2c9b022 12c00001 8000c07 4020 1084027 84400
  //   3508ffff 82021 20020022 c 8000c01 afa20000 23bd0004 afa40000 23bd0004 afb00000 23bd0004 afb30000
  //   23bd0004 afb40000 23bd0004 afb50000 23bd0004 afb60000 23bd0004 20160001 20140003 20150001 168020
  //   108100 2149825 132020 20020022 c 1600fffa 295a022 1680fff7 23bdfffc 8fb60000 23bdfffc 8fb50000
  //   23bdfffc 8fb40000 23bdfffc 8fb30000 23bdfffc 8fb00000 23bdfffc 8fa40000 23bdfffc 8fa20000 42000018
  //   afa20000 23bd0004 afa40000 23bd0004 afb00000 23bd0004 afb30000 23bd0004 afb40000 23bd0004 afb50000
  //   23bd0004 afb60000 23bd0004 20160002 20140003 20150001 168020 108100 2149825 132020 20020022 c
  //   1600fffa 295a022 1680fff7 23bdfffc 8fb60000 23bdfffc 8fb50000 23bdfffc 8fb40000 23bdfffc 8fb30000
  //   23bdfffc 8fb00000 23bdfffc 8fa40000 23bdfffc 8fa20000 42000018 afa20000 23bd0004 afa40000 23bd0004
  //   afb00000 23bd0004 afb30000 23bd0004 afb40000 23bd0004 afb50000 23bd0004 afb60000 23bd0004 20160003
  //   20140003 20150001 168020 108100 2149825 132020 20020022 c 1600fffa 295a022 1680fff7 23bdfffc
  //   8fb60000 23bdfffc 8fb50000 23bdfffc 8fb40000 23bdfffc 8fb30000 23bdfffc 8fb00000 23bdfffc 8fa40000
  //   23bdfffc 8fa20000 42000018
  //   可计数暂停的时钟源
  //   JMP
  //   JR
  //   OP
  //   Func
  //   rs
  //   rt
  //   rd
  //   Beq
  //   Bne
  //   AluOP
  //   AluSrcB
  //   RegWrite
  //   JAL
  //   RegDst
  //   Syscall
  //   MemToReg
  //   MemWrite
  //   为方便自动评测，需要输出PC，IR，寄存器堆写如数据RDin
  //   RAM写使能MemWrite、RAM写入数据MDin等信号
  //   控制与调试模块
  //   中断响应/返回控制模块
  //   单级中断测试信号模拟器
  //   单级中断支持模块
  //   EPC寄存器保存中断返回地址
  //   Eret指令简单支持
endmodule

module \单周期MIPS_多级中断  (
  input  IR1,
  input  IR2,
  input  IR3,
  output RegWrite,
  output MemWrite,
  output [31:0] PC,
  output [31:0] IR,
  output [31:0] RDin,
  output [31:0] MDin,
  output [31:0] LedData
);

  wire and_1_out, CLK, clock_2_out, comparator_1_eq, comparator_1_lt, comparator_2_eq, comparator_3_eq,
       comparator_4_eq, comparator_5_eq, comparator_6_eq, comparator_7_eq, comparator_8_eq, d_ff_1_q,
       d_ff_3_q, d_ff_4_q, d_ff_5_qn, EN, equal, Eret, Go, IntR, IntR_Eret, IR1_t, IR2_t, IR3_t, IRA, IRB,
       IRC, mfc0, mtc0, multiplexer_13_out, nand_1_out, not_1_out, or_3_out, or_5_out, or_6_out, or_7_out,
       or_8_out, or_9_out, or_10_out, RST, SignedExt, Syscall, W1, W2, W3, \中断按键参考电路_1_priorint ,
       \单周期硬布线控制器_1_alu_src , \单周期硬布线控制器_1_beq , \单周期硬布线控制器_1_bne , \单周期硬布线控制器_1_jal , \单周期硬布线控制器_1_jmp ,
       \单周期硬布线控制器_1_jr , \单周期硬布线控制器_1_memtoreg , \单周期硬布线控制器_1_regdst ;
  wire [1:0] IntNo;
  wire [3:0] \单周期硬布线控制器_1_alu_op ;
  wire [4:0] multiplexer_5_out, multiplexer_6_out, multiplexer_7_out, multiplexer_8_out;
  wire [12:0] CNT_num;
  wire [15:0] \总周期数 ;
  wire [31:0] bit_extender_1_out, BR_ADDR, Int_EretAddr, IntAddr, JR_ADDR, mips_alu_1_result,
       multiplexer_1_out, multiplexer_2_out, multiplexer_4_out, multiplexer_9_out, multiplexer_10_out,
       multiplexer_11_out, NextPC, PC_4, ram_1_data, shifter_1_out, \硬件堆栈_1_dout ;

  Button button_1 (.out(RST));
  Clock #(.highDuration(1), .lowDuration(1)) clock_1 ();  // open: out
  Button _1 ();  // open: out
  Button _2 ();  // open: out
  Button _3 ();  // open: out
  Button \u_继续运行  (.out(Go));
  LED #(.active("true")) led_1 (.in(W1));
  LED #(.active("true")) led_2 (.in(W2));
  LED #(.active("true")) led_3 (.in(W3));
  Multiplexer #(.select(1), .width(32), .disabled("Z"), .enable("false")) multiplexer_1 (
    .in0({PC[31:28], IR[25:0], 2'b00}), .in1(JR_ADDR), .out(multiplexer_1_out), .sel(\单周期硬布线控制器_1_jr ));
  D_Flip_Flop #(.trigger("high"), .Pre_Clr_Positions("LEGACY"), .NegatePresetClear("false"), .enable("true"), .NewFFLayout("false")) d_ff_1 (.Q(d_ff_1_q));  // open: clk, D, Qn, preset, en, reset
  // Probe on 13'hc
  Hex_Digit_Display hex_digit_display_1 (.value(LedData[31:28]));  // open: dp
  Multiplexer #(.select(1), .width(32), .disabled("Z"), .enable("false")) multiplexer_2 (
    .in0(PC_4), .in1(multiplexer_1_out), .out(multiplexer_2_out), .sel(\单周期硬布线控制器_1_jmp ));
  Adder #(.width(32)) adder_1 (.a(PC), .b(32'h4), .out(PC_4));  // open: cin, cout
  Clock #(.highDuration(1), .lowDuration(1)) clock_2 (.out(clock_2_out));
  Hex_Digit_Display hex_digit_display_2 (.value(LedData[27:24]));  // open: dp
  Hex_Digit_Display hex_digit_display_3 (.value(LedData[23:20]));  // open: dp
  Multiplexer #(.select(1), .width(32), .disabled("Z"), .enable("false")) multiplexer_3 (
    .in0(multiplexer_2_out), .in1(BR_ADDR), .out(NextPC), .sel(multiplexer_13_out));
  Comparator #(.width(13), .mode("twosComplement")) comparator_1 (
    .a(CNT_num), .b(13'hc), .eq(comparator_1_eq), .lt(comparator_1_lt));  // open: gt
  Hex_Digit_Display hex_digit_display_4 (.value(LedData[19:16]));  // open: dp
  Hex_Digit_Display hex_digit_display_5 (.value(LedData[15:12]));  // open: dp
  Multiplexer #(.select(1), .width(32), .disabled("Z"), .enable("false")) multiplexer_4 (
    .in0(NextPC), .in1(Int_EretAddr), .out(multiplexer_4_out), .sel(IntR_Eret));
  nand nand_1 (nand_1_out, d_ff_1_q, comparator_1_eq);
  Counter #(.width(13), .max('h1fff), .ongoal("stay"), .trigger("rising"), .behavior("old")) counter_1 (
    .count(comparator_1_lt), .Q(CNT_num), .clk(clock_2_out));  // open: load, D, carry, clr, preset
  Hex_Digit_Display hex_digit_display_6 (.value(LedData[7:4]));  // open: dp
  Hex_Digit_Display hex_digit_display_7 (.value(LedData[11:8]));  // open: dp
  // Probe on \总周期数 
  Register #(.width(32), .trigger("rising"), .Select("low")) u_PC (
    .D(multiplexer_4_out), .en(EN), .Q(PC), .clk(CLK), .clr(RST));
  Hex_Digit_Display hex_digit_display_8 (.value(LedData[3:0]));  // open: dp
  assign CLK = nand_1_out ? clock_2_out : 1'bz;  // Controlled_Buffer controlled_buffer_1
  Pull_Resistor #(.pull(1)) pull_resistor_1 (.node(CLK));
  // Mips_Probe mips_probe_1: pin names not known; wires that end beside it: IR
  ROM #(.addrWidth(10), .dataWidth(32), .Select("high")) rom_1 (.addr(PC[11:2]), .data(IR));
  or or_1 (IR1_t, IR1, IRA);
  or or_2 (IR2_t, IR2, IRB);
  \单周期硬布线控制器  \u_单周期硬布线控制器_1  (
    .Func(IR[5:0]), .OP(IR[31:26]), .ALU_OP(\单周期硬布线控制器_1_alu_op ), .MemToReg(\单周期硬布线控制器_1_memtoreg ),
    .MemWrite(MemWrite), .ALU_SRC(\单周期硬布线控制器_1_alu_src ), .RegWrite(RegWrite), .SysCALL(Syscall),
    .SignedExt(SignedExt), .RegDst(\单周期硬布线控制器_1_regdst ), .JR(\单周期硬布线控制器_1_jr ), .JMP(\单周期硬布线控制器_1_jmp ),
    .Beq(\单周期硬布线控制器_1_beq ), .JAL(\单周期硬布线控制器_1_jal ), .Bne(\单周期硬布线控制器_1_bne ));
  Multiplexer #(.select(1), .width(5), .disabled("Z"), .enable("false")) multiplexer_5 (
    .in0(IR[25:21]), .in1(5'b00010), .out(multiplexer_5_out), .sel(Syscall));
  Multiplexer #(.select(1), .width(5), .disabled("Z"), .enable("false")) multiplexer_6 (
    .in0(IR[20:16]), .in1(IR[15:11]), .out(multiplexer_6_out), .sel(\单周期硬布线控制器_1_regdst ));
  not not_1 (not_1_out, Syscall);
  Multiplexer #(.select(1), .width(5), .disabled("Z"), .enable("false")) multiplexer_7 (
    .in0(IR[20:16]), .in1(5'b00100), .out(multiplexer_7_out), .sel(Syscall));
  Multiplexer #(.select(1), .width(5), .disabled("Z"), .enable("false")) multiplexer_8 (
    .in0(multiplexer_6_out), .in1({5{1'b1}}), .out(multiplexer_8_out), .sel(\单周期硬布线控制器_1_jal ));
  assign bit_extender_1_out = {{16{IR[15]}}, IR[15:0]};  // Bit_Extender bit_extender_1
  or or_3 (or_3_out, equal, not_1_out);
  or or_4 (IR3_t, IR3, IRC);
  MIPS_Regifile mips_regifile_1 (
    .Din(RDin), .Clk(CLK), .R1(JR_ADDR), .R2(MDin), .WE(RegWrite), .W_num(multiplexer_8_out),
    .R1_num(multiplexer_5_out), .R2_num(multiplexer_7_out));
  or or_5 (or_5_out, not_1_out, Go);
  D_Flip_Flop #(.trigger("falling"), .Pre_Clr_Positions("ABOVE_BELOW"), .NegatePresetClear("false"), .enable("false"), .NewFFLayout("true")) d_ff_2 (
    .clk(CLK), .D(or_3_out), .Q(EN), .preset(or_5_out));  // open: Qn, reset
  Multiplexer #(.select(1), .width(32), .disabled("Z"), .enable("false")) multiplexer_9 (
    .in0(MDin), .in1(bit_extender_1_out), .out(multiplexer_9_out), .sel(\单周期硬布线控制器_1_alu_src ));
  Shifter #(.width(32), .shift("ll")) shifter_1 (.in(bit_extender_1_out), .\dist (5'b00010), .out(shifter_1_out));
  Multiplexer #(.select(1), .width(32), .disabled("Z"), .enable("false")) multiplexer_10 (
    .in0(multiplexer_9_out), .in1(32'h22), .out(multiplexer_10_out), .sel(Syscall));
  MIPS_ALU mips_alu_1 (
    .X(JR_ADDR), .Y(multiplexer_10_out), .AluOP(\单周期硬布线控制器_1_alu_op ), .Equal(equal),
    .Result(mips_alu_1_result), .shamt(IR[10:6]));  // open: Result_2
  Adder #(.width(32)) adder_2 (.a(shifter_1_out), .b(PC_4), .out(BR_ADDR));  // open: cin, cout
  Counter #(.width(16), .max('hffff), .ongoal("wrap"), .trigger("rising"), .behavior("new")) counter_2 (
    .count(EN), .Q(\总周期数 ), .clk(CLK), .clr(RST));  // open: load, D, carry, preset, down
  Multiplexer #(.select(1), .width(32), .disabled("Z"), .enable("false")) multiplexer_11 (
    .in0(mips_alu_1_result), .in1(ram_1_data), .out(multiplexer_11_out), .sel(\单周期硬布线控制器_1_memtoreg ));
  RAM #(.addrWidth(10), .dataWidth(32), .bus("separate"), .Select("high")) ram_1 (
    .addr(mips_alu_1_result[11:2]), .din(MDin), .data(ram_1_data), .str(MemWrite), .clk(CLK), .clr(RST));  // open: sel, ld
  and and_1 (and_1_out, Syscall, equal);
  Multiplexer #(.select(1), .width(32), .disabled("Z"), .enable("false")) multiplexer_12 (
    .in0(multiplexer_11_out), .in1(PC_4), .out(RDin), .sel(\单周期硬布线控制器_1_jal ));
  Register #(.width(32), .trigger("rising"), .Select("low")) register_1 (
    .D(MDin), .en(and_1_out), .Q(LedData), .clk(CLK), .clr(RST));
  Multiplexer #(.select(1), .width(1), .disabled("Z"), .enable("false")) multiplexer_13 (
    .in0(\单周期硬布线控制器_1_bne ), .in1(\单周期硬布线控制器_1_beq ), .out(multiplexer_13_out), .sel(equal));
  or or_6 (or_6_out, mtc0, IntR);
  or or_7 (or_7_out, mfc0, Eret);
  \中断按键参考电路  \u_中断按键参考电路_1  (
    .CLK(CLK), .RST(RST), .Eret(Eret), .Int1(IR1_t), .Int2(IR2_t), .Int3(IR3_t),
    .PriorInt(\中断按键参考电路_1_priorint ), .IntNo(IntNo), .IntR(IntR));
  D_Flip_Flop #(.trigger("rising"), .Pre_Clr_Positions("LEGACY"), .NegatePresetClear("false"), .enable("true"), .NewFFLayout("false")) d_ff_3 (
    .clk(CLK), .D(or_6_out), .Q(d_ff_3_q), .reset(RST));  // open: Qn, preset, en
  D_Flip_Flop #(.trigger("rising"), .Pre_Clr_Positions("LEGACY"), .NegatePresetClear("false"), .enable("true"), .NewFFLayout("false")) d_ff_4 (
    .clk(CLK), .D(or_7_out), .Q(d_ff_4_q), .reset(RST));  // open: Qn, preset, en
  Comparator #(.width(16), .mode("twosComplement")) comparator_2 (
    .a(16'h258), .b(\总周期数 ), .eq(comparator_2_eq));  // open: gt, lt
  or or_8 (or_8_out, comparator_2_eq, comparator_3_eq);
  Comparator #(.width(16), .mode("twosComplement")) comparator_3 (
    .a(\总周期数 ), .b(16'h1), .eq(comparator_3_eq));  // open: gt, lt
  Comparator #(.width(16), .mode("twosComplement")) comparator_4 (
    .a(\总周期数 ), .b(16'h4), .eq(comparator_4_eq));  // open: gt, lt
  Comparator #(.width(16), .mode("twosComplement")) comparator_5 (
    .a(\总周期数 ), .b(16'h7), .eq(comparator_5_eq));  // open: gt, lt
  or or_9 (or_9_out, comparator_5_eq, comparator_6_eq);
  Comparator #(.width(16), .mode("twosComplement")) comparator_6 (
    .a(\总周期数 ), .b(16'h241), .eq(comparator_6_eq));  // open: gt, lt
  D_Flip_Flop #(.trigger("rising"), .Pre_Clr_Positions("LEGACY"), .NegatePresetClear("false"), .enable("true"), .NewFFLayout("false")) d_ff_5 (
    .Qn(d_ff_5_qn), .preset(d_ff_3_q), .reset(or_10_out));  // open: clk, D, Q, en
  or or_10 (or_10_out, d_ff_4_q, RST);
  Pull_Resistor #(.pull(0)) pull_resistor_2 (.node(IRA));
  assign IRA = or_8_out ? ~CLK : 1'bz;  // Controlled_Inverter controlled_inverter_1
  assign IRB = comparator_4_eq ? ~CLK : 1'bz;  // Controlled_Inverter controlled_inverter_2
  Pull_Resistor #(.pull(0)) pull_resistor_3 (.node(IRB));
  Pull_Resistor #(.pull(0)) pull_resistor_4 (.node(IRC));
  assign IRC = or_9_out ? ~CLK : 1'bz;  // Controlled_Inverter controlled_inverter_3
  and and_2 (IntR, \中断按键参考电路_1_priorint , d_ff_5_qn);
  or or_11 (IntR_Eret, IntR, Eret);
  Multiplexer #(.select(2), .width(32), .disabled("Z"), .enable("false")) multiplexer_14 (
    .in1(32'h30ac), .in2(32'h3158), .in3(32'h3204), .out(IntAddr), .sel(IntNo));  // open: in0
  Comparator #(.width(6), .mode("twosComplement")) comparator_7 (
    .a(IR[31:26]), .b(6'b010000), .eq(comparator_7_eq));  // open: gt, lt
  Comparator #(.width(6), .mode("twosComplement")) comparator_8 (
    .a(IR[5:0]), .b(6'b011000), .eq(comparator_8_eq));  // open: gt, lt
  Comparator #(.width(32), .mode("twosComplement")) comparator_9 (.a(IR), .b(32'h40800000), .eq(mtc0));  // open: gt, lt
  Comparator #(.width(32), .mode("twosComplement")) comparator_10 (
    .a(IR), .b(32'h40000000), .eq(mfc0));  // open: gt, lt
  \硬件堆栈  \u_硬件堆栈_1  (.PUSH(IntR), .POP(Eret), .CLK(CLK), .RST(RST), .Din(NextPC), .Dout(\硬件堆栈_1_dout ));
  and and_3 (Eret, comparator_7_eq, comparator_8_eq);
  Multiplexer #(.select(1), .width(32), .disabled("Z"), .enable("false")) multiplexer_15 (
    .in0(IntAddr), .in1(\硬件堆栈_1_dout ), .out(Int_EretAddr), .sel(Eret));

  // Other names for the same wires on the sheet: Func[5:0] = IR[5:0]; imm[25:0] = IR[25:0];
  //   J_ADDR[31:2] = {PC[31:28], IR[25:0]}; OP[5:0] = IR[31:26]

  // Notes on the sheet:
  //   中断源
  //   控制位
  //   中断等待指示
  //   总复位信号应将除ROM以外所有存储组件全部清零
  //   暂停节拍，不能为0
  //   戳工具置1进入计数暂停模式，ctrl+k时钟自动运行到对应节拍暂停
  //   ctrl+k关闭时钟连续运行，将控制位置零，进入单步调试模式调试
  //   用这个时钟源需要去掉电路中的其他时钟源
  //   数码管输出
  //   数码管输出应该用寄存器锁存，否则显示数据只能一闪而过
  //   指令存储器
  //   指令字
  //   contents of rom_1 (hex, n*v repeats v):
  //   201d07d0 20100001 109fc0 139fc3 8021 2012000c 24160008 26100001 3210000f 20080008 20090001 139900
  //   2709825 132020 20020022 c 1094022 1500fff9 22100001 2018000f 2188024 108700 20080008 20090001 139902
  //   2709825 132021 20020022 c 1094022 1500fff9 108702 2c9b022 12c00001 8000c07 4020 1084027 84400
  //   3508ffff 82021 20020022 c 8000c01 afa20000 23bd0004 afa40000 23bd0004 afb00000 23bd0004 afb30000
  //   23bd0004 afb40000 23bd0004 afb50000 23bd0004 afb60000 23bd0004 40000000 20160001 20140003 20150001
  //   168020 108100 2149825 132020 20020022 c 1600fffa 295a022 1680fff7 40800000 23bdfffc 8fb60000
  //   23bdfffc 8fb50000 23bdfffc 8fb40000 23bdfffc 8fb30000 23bdfffc 8fb00000 23bdfffc 8fa40000 23bdfffc
  //   8fa20000 42000018 afa20000 23bd0004 afa40000 23bd0004 afb00000 23bd0004 afb30000 23bd0004 afb40000
  //   23bd0004 afb50000 23bd0004 afb60000 23bd0004 40000000 20160002 20140003 20150001 168020 108100
  //   2149825 132020 20020022 c 1600fffa 295a022 1680fff7 40800000 23bdfffc 8fb60000 23bdfffc 8fb50000
  //   23bdfffc 8fb40000 23bdfffc 8fb30000 23bdfffc 8fb00000 23bdfffc 8fa40000 23bdfffc 8fa20000 42000018
  //   afa20000 23bd0004 afa40000 23bd0004 afb00000 23bd0004 afb30000 23bd0004 afb40000 23bd0004 afb50000
  //   23bd0004 afb60000 23bd0004 40000000 20160003 20140003 20150001 168020 108100 2149825 132020 20020022
  //   c 1600fffa 295a022 1680fff7 40800000 23bdfffc 8fb60000 23bdfffc 8fb50000 23bdfffc 8fb40000 23bdfffc
  //   8fb30000 23bdfffc 8fb00000 23bdfffc 8fa40000 23bdfffc 8fa20000 42000018
  //   可计数暂停的时钟源
  //   JMP
  //   JR
  //   OP
  //   Func
  //   Syscall
  //   rs
  //   rt
  //   rd
  //   Bne
  //   MemToReg
  //   MemWrite
  //   AluOP
  //   AluSrcB
  //   RegWrite
  //   JAL
  //   RegDst
  //   为方便自动评测，需要输出PC，IR，寄存器堆写如数据RDin
  //   RAM写使能MemWrite、RAM写入数据MDin等信号
  //   单周期MIPS
  //   控制与调试模块
  //   多级中断测试信号模拟器
  //   多级中断响应/返回控制模块
  //   Eret/mtc0/mfc0简易支持
  //   硬件堆栈保存多级中断返回地址
endmodule

module \封装正确性测试  (
);

  wire IR1, IR2, IR3, MemW, RegW;
  wire [31:0] EX_PC, ID_PC, IF_PC, IR, LED, MDin, MDinr, MEM_PC, PC, RDin, RDinr, WB_PC;

  \单周期MIPS  \u_单周期mips_1  (
    .RegWrite(RegW), .MemWrite(MemW), .PC(PC), .IR(IR), .RDin(RDin), .MDin(MDin), .LedData(LED));  // open: IR1, IR2, IR3
  \气泡流水线  \u_气泡流水线_1  (
    .RegWrite(RegW), .MemWrite(MemW), .IF_PC(IF_PC), .ID_PC(ID_PC), .EX_PC(EX_PC), .M_PC(MEM_PC),
    .WB_PC(WB_PC), .RDin(RDinr), .MDin(MDinr), .LedData(LED));
  \单周期MIPS_单级中断  \u_单周期mips_单级中断_1  (
    .IR1(IR1), .IR2(IR2), .IR3(IR3), .RegWrite(RegW), .MemWrite(MemW), .PC(PC), .IR(IR), .RDin(RDin),
    .MDin(MDin), .LedData(LED));
  \理想流水线  \u_理想流水线_1  (
    .RegWrite(RegW), .MemWrite(MemW), .IF_PC(IF_PC), .ID_PC(ID_PC), .EX_PC(EX_PC), .M_PC(MEM_PC),
    .WB_PC(WB_PC), .RDin(RDinr), .MDin(MDinr), .LedData(LED));
  \重定向流水线  \u_重定向流水线_1  (
    .RegWrite(RegW), .MemWrite(MemW), .IF_PC(IF_PC), .ID_PC(ID_PC), .EX_PC(EX_PC), .M_PC(MEM_PC),
    .WB_PC(WB_PC), .RDin(RDinr), .MDin(MDinr), .LedData(LED));
  \单周期MIPS_多级中断  \u_单周期mips_多级中断_1  (
    .IR1(IR1), .IR2(IR2), .IR3(IR3), .RegWrite(RegW), .MemWrite(MemW), .PC(PC), .IR(IR), .RDin(RDin),
    .MDin(MDin), .LedData(LED));

  // Notes on the sheet:
  //   单周期封装测试
  //   气泡流水封装测试
  //   单周期+单级中断封装测试
  //   请检查上面封装有无位宽不匹配，引脚标签是否和连接的标签相对应，否则无法在educoder平台上正确测试
  //   理想流水封装测试
  //   重定向流水封装测试
  //   单周期+多级中断封装测试
endmodule

module \硬件堆栈  (
  input  PUSH,
  input  [31:0] Din,
  input  POP,
  input  RST,
  input  CLK,
  output [31:0] Dout
);

  wire [31:0] controlled_buffer_1_out, controlled_buffer_2_out, controlled_buffer_4_out,
       controlled_buffer_6_out, controlled_buffer_8_out, controlled_buffer_11_out, controlled_buffer_13_out,
       controlled_buffer_14_out, register_2_q, register_3_q, register_4_q, register_5_q, register_6_q,
       register_7_q, register_8_q;

  assign controlled_buffer_1_out = PUSH ? Din : 32'bz;  // Controlled_Buffer controlled_buffer_1
  assign controlled_buffer_2_out = PUSH ? Dout : 32'bz;  // Controlled_Buffer controlled_buffer_2
  Register #(.width(32), .trigger("rising"), .Select("low")) register_1 (
    .D(controlled_buffer_1_out), .Q(Dout), .clk(CLK), .clr(RST));  // open: en
  assign controlled_buffer_1_out = POP ? register_2_q : 32'bz;  // Controlled_Buffer controlled_buffer_3
  Register #(.width(32), .trigger("rising"), .Select("low")) register_2 (
    .D(controlled_buffer_2_out), .Q(register_2_q), .clk(CLK), .clr(RST));  // open: en
  assign controlled_buffer_4_out = PUSH ? register_2_q : 32'bz;  // Controlled_Buffer controlled_buffer_4
  assign controlled_buffer_2_out = POP ? register_3_q : 32'bz;  // Controlled_Buffer controlled_buffer_5
  assign controlled_buffer_6_out = PUSH ? register_3_q : 32'bz;  // Controlled_Buffer controlled_buffer_6
  Register #(.width(32), .trigger("rising"), .Select("low")) register_3 (
    .D(controlled_buffer_4_out), .Q(register_3_q), .clk(CLK), .clr(RST));  // open: en
  assign controlled_buffer_4_out = POP ? register_4_q : 32'bz;  // Controlled_Buffer controlled_buffer_7
  Register #(.width(32), .trigger("rising"), .Select("low")) register_4 (
    .D(controlled_buffer_6_out), .Q(register_4_q), .clk(CLK), .clr(RST));  // open: en
  assign controlled_buffer_8_out = PUSH ? register_4_q : 32'bz;  // Controlled_Buffer controlled_buffer_8
  assign controlled_buffer_6_out = POP ? register_5_q : 32'bz;  // Controlled_Buffer controlled_buffer_9
  Register #(.width(32), .trigger("rising"), .Select("low")) register_5 (
    .D(controlled_buffer_8_out), .Q(register_5_q), .clk(CLK), .clr(RST));  // open: en
  assign controlled_buffer_8_out = POP ? register_6_q : 32'bz;  // Controlled_Buffer controlled_buffer_10
  Register #(.width(32), .trigger("rising"), .Select("low")) register_6 (
    .D(controlled_buffer_11_out), .Q(register_6_q), .clk(CLK), .clr(RST));  // open: en
  assign controlled_buffer_11_out = PUSH ? register_5_q : 32'bz;  // Controlled_Buffer controlled_buffer_11
  assign controlled_buffer_11_out = POP ? register_7_q : 32'bz;  // Controlled_Buffer controlled_buffer_12
  assign controlled_buffer_13_out = PUSH ? register_6_q : 32'bz;  // Controlled_Buffer controlled_buffer_13
  Register #(.width(32), .trigger("rising"), .Select("low")) register_7 (
    .D(controlled_buffer_13_out), .Q(register_7_q), .clk(CLK), .clr(RST));  // open: en
  Register #(.width(32), .trigger("rising"), .Select("low")) register_8 (
    .D(controlled_buffer_14_out), .Q(register_8_q), .clk(CLK), .clr(RST));  // open: en
  assign controlled_buffer_14_out = PUSH ? register_7_q : 32'bz;  // Controlled_Buffer controlled_buffer_14
  assign controlled_buffer_13_out = POP ? register_8_q : 32'bz;  // Controlled_Buffer controlled_buffer_15
endmodule

module \嵌套中断堆栈  (
  input  PUSH,
  input  [1:0] Din,
  input  POP,
  input  RST,
  input  CLK,
  output [1:0] Dout
);

  wire [1:0] controlled_buffer_1_out, controlled_buffer_2_out, controlled_buffer_4_out,
       controlled_buffer_6_out, controlled_buffer_9_out, controlled_buffer_11_out, controlled_buffer_12_out,
       controlled_buffer_14_out, register_2_q, register_3_q, register_4_q, register_5_q, register_6_q,
       register_7_q, register_8_q;

  assign controlled_buffer_1_out = PUSH ? Din : 2'bz;  // Controlled_Buffer controlled_buffer_1
  assign controlled_buffer_2_out = PUSH ? Dout : 2'bz;  // Controlled_Buffer controlled_buffer_2
  Register #(.width(2), .trigger("rising"), .Select("low")) register_1 (
    .D(controlled_buffer_1_out), .Q(Dout), .clk(CLK), .clr(RST));  // open: en
  assign controlled_buffer_1_out = POP ? register_2_q : 2'bz;  // Controlled_Buffer controlled_buffer_3
  assign controlled_buffer_4_out = PUSH ? register_2_q : 2'bz;  // Controlled_Buffer controlled_buffer_4
  Register #(.width(2), .trigger("rising"), .Select("low")) register_2 (
    .D(controlled_buffer_2_out), .Q(register_2_q), .clk(CLK), .clr(RST));  // open: en
  assign controlled_buffer_2_out = POP ? register_3_q : 2'bz;  // Controlled_Buffer controlled_buffer_5
  Register #(.width(2), .trigger("rising"), .Select("low")) register_3 (
    .D(controlled_buffer_4_out), .Q(register_3_q), .clk(CLK), .clr(RST));  // open: en
  assign controlled_buffer_6_out = PUSH ? register_3_q : 2'bz;  // Controlled_Buffer controlled_buffer_6
  assign controlled_buffer_4_out = POP ? register_4_q : 2'bz;  // Controlled_Buffer controlled_buffer_7
  Register #(.width(2), .trigger("rising"), .Select("low")) register_4 (
    .D(controlled_buffer_6_out), .Q(register_4_q), .clk(CLK), .clr(RST));  // open: en
  assign controlled_buffer_6_out = POP ? register_5_q : 2'bz;  // Controlled_Buffer controlled_buffer_8
  assign controlled_buffer_9_out = PUSH ? register_4_q : 2'bz;  // Controlled_Buffer controlled_buffer_9
  Register #(.width(2), .trigger("rising"), .Select("low")) register_5 (
    .D(controlled_buffer_9_out), .Q(register_5_q), .clk(CLK), .clr(RST));  // open: en
  assign controlled_buffer_9_out = POP ? register_6_q : 2'bz;  // Controlled_Buffer controlled_buffer_10
  assign controlled_buffer_11_out = PUSH ? register_5_q : 2'bz;  // Controlled_Buffer controlled_buffer_11
  Register #(.width(2), .trigger("rising"), .Select("low")) register_6 (
    .D(controlled_buffer_11_out), .Q(register_6_q), .clk(CLK), .clr(RST));  // open: en
  assign controlled_buffer_12_out = PUSH ? register_6_q : 2'bz;  // Controlled_Buffer controlled_buffer_12
  Register #(.width(2), .trigger("rising"), .Select("low")) register_7 (
    .D(controlled_buffer_12_out), .Q(register_7_q), .clk(CLK), .clr(RST));  // open: en
  assign controlled_buffer_11_out = POP ? register_7_q : 2'bz;  // Controlled_Buffer controlled_buffer_13
  assign controlled_buffer_14_out = PUSH ? register_7_q : 2'bz;  // Controlled_Buffer controlled_buffer_14
  Register #(.width(2), .trigger("rising"), .Select("low")) register_8 (
    .D(controlled_buffer_14_out), .Q(register_8_q), .clk(CLK), .clr(RST));  // open: en
  assign controlled_buffer_12_out = POP ? register_8_q : 2'bz;  // Controlled_Buffer controlled_buffer_15
endmodule

module \流水线寄存器  (
  input  IN_JMP,
  input  IN_JR,
  input  IN_Beq,
  input  IN_Bne,
  input  IN_MemToReg,
  input  IN_MemWrite,
  input  [3:0] IN_AluOP,
  input  IN_AluSrcB,
  input  IN_RegWrite,
  input  In_RegDst,
  input  In_Syscall,
  input  IN_equal,
  input  [31:0] IN_R1,
  input  [31:0] IN_ALU,
  input  [31:0] IN_R2,
  input  [31:0] IN_MD,
  input  [31:0] IN_PC,
  input  [31:0] IN_IR,
  input  [31:0] IN_Imm,
  input  [4:0] IN_shamt,
  input  [25:0] IN_offset,
  input  IN_JAL,
  input  [4:0] IN_WriteReg_num,
  input  CLR,
  input  EN,
  input  CLK,
  input  RST,
  output OUT_JMP,
  output OUT_JR,
  output OUT_Beq,
  output OUT_Bne,
  output OUT_MemToReg,
  output OUT_MemWrite,
  output [3:0] OUT_AluOP,
  output OUT_AluSrcB,
  output OUT_RegWrite,
  output OUT_RegDst,
  output OUT_Syscall,
  output OUT_equal,
  output [31:0] OUT_R1,
  output [31:0] OUT_ALU,
  output [31:0] OUT_R2,
  output [31:0] OUT_MD,
  output [31:0] OUT_PC,
  output [31:0] OUT_IR,
  output [31:0] OUT_Imm,
  output [4:0] OUT_shamt,
  output [25:0] OUT_offset,
  output OUT_JAL,
  output [4:0] OUT_WriteReg_num
);

  wire multiplexer_1_out, multiplexer_2_out, multiplexer_3_out, multiplexer_4_out, multiplexer_5_out,
       multiplexer_6_out, multiplexer_8_out, multiplexer_9_out, multiplexer_10_out, multiplexer_11_out,
       multiplexer_12_out, multiplexer_22_out;
  wire [3:0] multiplexer_7_out;
  wire [4:0] multiplexer_20_out, multiplexer_23_out;
  wire [25:0] multiplexer_21_out;
  wire [31:0] multiplexer_13_out, multiplexer_14_out, multiplexer_15_out, multiplexer_16_out,
       multiplexer_17_out, multiplexer_18_out, multiplexer_19_out;

  Multiplexer #(.select(1), .width(1), .disabled("Z"), .enable("false")) multiplexer_1 (
    .in0(IN_JMP), .in1(1'b0), .out(multiplexer_1_out), .sel(CLR));
  Multiplexer #(.select(1), .width(1), .disabled("Z"), .enable("false")) multiplexer_2 (
    .in0(IN_JR), .in1(1'b0), .out(multiplexer_2_out), .sel(CLR));
  Multiplexer #(.select(1), .width(1), .disabled("Z"), .enable("false")) multiplexer_3 (
    .in0(IN_Beq), .in1(1'b0), .out(multiplexer_3_out), .sel(CLR));
  Multiplexer #(.select(1), .width(1), .disabled("Z"), .enable("false")) multiplexer_4 (
    .in0(IN_Bne), .in1(1'b0), .out(multiplexer_4_out), .sel(CLR));
  Multiplexer #(.select(1), .width(1), .disabled("Z"), .enable("false")) multiplexer_5 (
    .in0(IN_MemToReg), .in1(1'b0), .out(multiplexer_5_out), .sel(CLR));
  Multiplexer #(.select(1), .width(1), .disabled("Z"), .enable("false")) multiplexer_6 (
    .in0(IN_MemWrite), .in1(1'b0), .out(multiplexer_6_out), .sel(CLR));
  Multiplexer #(.select(1), .width(4), .disabled("Z"), .enable("false")) multiplexer_7 (
    .in0(IN_AluOP), .in1(4'b0000), .out(multiplexer_7_out), .sel(CLR));
  Multiplexer #(.select(1), .width(1), .disabled("Z"), .enable("false")) multiplexer_8 (
    .in0(IN_AluSrcB), .in1(1'b0), .out(multiplexer_8_out), .sel(CLR));
  Multiplexer #(.select(1), .width(1), .disabled("Z"), .enable("false")) multiplexer_9 (
    .in0(IN_RegWrite), .in1(1'b0), .out(multiplexer_9_out), .sel(CLR));
  Multiplexer #(.select(1), .width(1), .disabled("Z"), .enable("false")) multiplexer_10 (
    .in0(In_RegDst), .in1(1'b0), .out(multiplexer_10_out), .sel(CLR));
  Multiplexer #(.select(1), .width(1), .disabled("Z"), .enable("false")) multiplexer_11 (
    .in0(In_Syscall), .in1(1'b0), .out(multiplexer_11_out), .sel(CLR));
  Multiplexer #(.select(1), .width(1), .disabled("Z"), .enable("false")) multiplexer_12 (
    .in0(IN_equal), .in1(1'b0), .out(multiplexer_12_out), .sel(CLR));
  Multiplexer #(.select(1), .width(32), .disabled("Z"), .enable("false")) multiplexer_13 (
    .in0(IN_R1), .in1({32{1'b0}}), .out(multiplexer_13_out), .sel(CLR));
  Multiplexer #(.select(1), .width(32), .disabled("Z"), .enable("false")) multiplexer_14 (
    .in0(IN_ALU), .in1({32{1'b0}}), .out(multiplexer_14_out), .sel(CLR));
  Multiplexer #(.select(1), .width(32), .disabled("Z"), .enable("false")) multiplexer_15 (
    .in0(IN_R2), .in1({32{1'b0}}), .out(multiplexer_15_out), .sel(CLR));
  Multiplexer #(.select(1), .width(32), .disabled("Z"), .enable("false")) multiplexer_16 (
    .in0(IN_MD), .in1({32{1'b0}}), .out(multiplexer_16_out), .sel(CLR));
  Multiplexer #(.select(1), .width(32), .disabled("Z"), .enable("false")) multiplexer_17 (
    .in0(IN_PC), .in1({32{1'b0}}), .out(multiplexer_17_out), .sel(CLR));
  Multiplexer #(.select(1), .width(32), .disabled("Z"), .enable("false")) multiplexer_18 (
    .in0(IN_IR), .in1({32{1'b0}}), .out(multiplexer_18_out), .sel(CLR));
  Multiplexer #(.select(1), .width(32), .disabled("Z"), .enable("false")) multiplexer_19 (
    .in0(IN_Imm), .in1({32{1'b0}}), .out(multiplexer_19_out), .sel(CLR));
  Multiplexer #(.select(1), .width(5), .disabled("Z"), .enable("false")) multiplexer_20 (
    .in0(IN_shamt), .in1({5{1'b0}}), .out(multiplexer_20_out), .sel(CLR));
  Multiplexer #(.select(1), .width(26), .disabled("Z"), .enable("false")) multiplexer_21 (
    .in0(IN_offset), .in1({26{1'b0}}), .out(multiplexer_21_out), .sel(CLR));
  Multiplexer #(.select(1), .width(1), .disabled("Z"), .enable("false")) multiplexer_22 (
    .in0(IN_JAL), .in1(1'b0), .out(multiplexer_22_out), .sel(CLR));
  Multiplexer #(.select(1), .width(5), .disabled("Z"), .enable("false")) multiplexer_23 (
    .in0(IN_WriteReg_num), .in1({5{1'b0}}), .out(multiplexer_23_out), .sel(CLR));
  Register #(.width(1), .trigger("rising"), .Select("low")) MemToReg (
    .D(multiplexer_1_out), .en(EN), .Q(OUT_JMP), .clk(CLK), .clr(RST));
  Register #(.width(1), .trigger("rising"), .Select("low")) MemToReg_2 (
    .D(multiplexer_2_out), .en(EN), .Q(OUT_JR), .clk(CLK), .clr(RST));
  Register #(.width(1), .trigger("rising"), .Select("low")) MemToReg_3 (
    .D(multiplexer_3_out), .en(EN), .Q(OUT_Beq), .clk(CLK), .clr(RST));
  Register #(.width(1), .trigger("rising"), .Select("low")) MemToReg_4 (
    .D(multiplexer_4_out), .en(EN), .Q(OUT_Bne), .clk(CLK), .clr(RST));
  Register #(.width(1), .trigger("rising"), .Select("low")) MemToReg_5 (
    .D(multiplexer_5_out), .en(EN), .Q(OUT_MemToReg), .clk(CLK), .clr(RST));
  Register #(.width(1), .trigger("rising"), .Select("low")) MemWrite (
    .D(multiplexer_6_out), .en(EN), .Q(OUT_MemWrite), .clk(CLK), .clr(RST));
  Register #(.width(4), .trigger("rising"), .Select("low")) AluOP (
    .D(multiplexer_7_out), .en(EN), .Q(OUT_AluOP), .clk(CLK), .clr(RST));
  Register #(.width(1), .trigger("rising"), .Select("low")) ALuSrcB (
    .D(multiplexer_8_out), .en(EN), .Q(OUT_AluSrcB), .clk(CLK), .clr(RST));
  Register #(.width(1), .trigger("rising"), .Select("low")) RegWrite (
    .D(multiplexer_9_out), .en(EN), .Q(OUT_RegWrite), .clk(CLK), .clr(RST));
  Register #(.width(1), .trigger("rising"), .Select("low")) RegDst (
    .D(multiplexer_10_out), .en(EN), .Q(OUT_RegDst), .clk(CLK), .clr(RST));
  Register #(.width(1), .trigger("rising"), .Select("low")) Syscall (
    .D(multiplexer_11_out), .en(EN), .Q(OUT_Syscall), .clk(CLK), .clr(RST));
  Register #(.width(1), .trigger("rising"), .Select("low")) equal (
    .D(multiplexer_12_out), .en(EN), .Q(OUT_equal), .clk(CLK), .clr(RST));
  Register #(.width(32), .trigger("rising"), .Select("low")) R1 (
    .D(multiplexer_13_out), .en(EN), .Q(OUT_R1), .clk(CLK), .clr(RST));
  Register #(.width(32), .trigger("rising"), .Select("low")) ALU (
    .D(multiplexer_14_out), .en(EN), .Q(OUT_ALU), .clk(CLK), .clr(RST));
  Register #(.width(32), .trigger("rising"), .Select("low")) R2 (
    .D(multiplexer_15_out), .en(EN), .Q(OUT_R2), .clk(CLK), .clr(RST));
  Register #(.width(32), .trigger("rising"), .Select("low")) MD (
    .D(multiplexer_16_out), .en(EN), .Q(OUT_MD), .clk(CLK), .clr(RST));
  Register #(.width(32), .trigger("rising"), .Select("low")) PC (
    .D(multiplexer_17_out), .en(EN), .Q(OUT_PC), .clk(CLK), .clr(RST));
  Register #(.width(32), .trigger("rising"), .Select("low")) IR (
    .D(multiplexer_18_out), .en(EN), .Q(OUT_IR), .clk(CLK), .clr(RST));
  Register #(.width(32), .trigger("rising"), .Select("low")) Imm (
    .D(multiplexer_19_out), .en(EN), .Q(OUT_Imm), .clk(CLK), .clr(RST));
  Register #(.width(5), .trigger("rising"), .Select("low")) shamt (
    .D(multiplexer_20_out), .en(EN), .Q(OUT_shamt), .clk(CLK), .clr(RST));
  Register #(.width(26), .trigger("rising"), .Select("low")) offset (
    .D(multiplexer_21_out), .en(EN), .Q(OUT_offset), .clk(CLK), .clr(RST));
  Register #(.width(1), .trigger("rising"), .Select("low")) JAL (
    .D(multiplexer_22_out), .en(EN), .Q(OUT_JAL), .clk(CLK), .clr(RST));
  Register #(.width(5), .trigger("rising"), .Select("low")) MemToReg_6 (
    .D(multiplexer_23_out), .Q(OUT_WriteReg_num), .clk(CLK), .clr(RST));  // open: en
endmodule

module \寄存器相关  (
  input  OP0,
  input  OP1,
  input  OP2,
  input  OP3,
  input  OP4,
  input  OP5,
  input  F0,
  input  F1,
  input  F2,
  input  F3,
  input  F4,
  input  F5,
  output RsUsed,
  output RtUsed
);

  wire and_1_out, and_2_out, and_3_out, and_4_out, and_5_out, and_6_out, and_7_out, and_8_out, and_9_out,
       and_10_out, and_11_out, and_12_out, and_13_out, and_14_out, and_15_out, and_16_out, and_17_out,
       and_18_out, and_19_out, and_20_out, and_21_out, and_22_out, and_23_out, and_24_out, and_25_out,
       and_26_out, and_27_out, and_28_out, and_29_out, and_30_out, and_31_out, and_32_out, and_33_out,
       and_34_out, not_1_out, not_2_out, not_3_out, not_4_out, not_5_out, not_6_out, not_7_out, not_8_out,
       not_9_out, not_10_out, not_11_out, not_12_out, not_13_out, not_14_out, not_15_out, not_16_out,
       not_17_out, not_18_out, not_19_out, not_20_out, not_21_out, not_22_out, not_23_out, not_24_out,
       not_25_out, not_26_out, not_27_out, not_28_out, not_29_out, not_30_out, not_31_out, not_32_out,
       not_33_out, not_34_out, not_35_out, not_36_out, not_37_out, not_38_out, not_39_out, not_40_out,
       not_41_out, not_42_out, not_43_out, not_44_out, not_45_out, not_46_out, not_47_out, not_48_out,
       not_49_out, not_50_out, not_51_out, not_52_out, not_53_out, not_54_out, not_55_out, not_56_out,
       not_57_out, not_58_out, not_59_out, not_60_out, not_61_out, not_62_out, not_63_out, not_64_out,
       not_65_out, not_66_out, not_67_out, not_68_out, not_69_out, not_70_out, not_71_out, not_72_out,
       not_73_out, not_74_out, not_75_out, not_76_out, not_77_out, not_78_out, not_79_out, not_80_out,
       not_81_out, not_82_out, not_83_out, not_84_out, not_85_out, not_86_out, not_87_out, not_88_out,
       not_89_out, not_90_out, not_91_out, not_92_out, not_93_out, not_94_out, not_95_out, not_96_out,
       not_97_out, not_98_out, not_99_out, not_100_out, not_101_out, not_102_out, not_103_out, not_104_out,
       not_105_out, not_106_out, not_107_out, not_108_out, not_109_out, not_110_out, not_111_out,
       not_112_out, not_113_out, not_114_out, not_115_out, not_116_out, not_117_out, not_118_out,
       not_119_out, not_120_out, not_121_out, not_122_out, not_123_out, not_124_out, not_125_out,
       not_126_out, not_127_out, not_128_out, not_129_out, not_130_out, not_131_out, not_132_out,
       not_133_out, not_134_out, not_135_out, not_136_out, not_137_out, not_138_out, not_139_out,
       not_140_out, not_141_out, not_142_out, not_143_out, not_144_out, not_145_out, not_146_out,
       not_147_out, not_148_out, not_149_out, not_150_out, not_151_out, not_152_out, not_153_out,
       not_154_out, not_155_out, not_156_out, not_157_out, not_158_out, not_159_out, not_160_out,
       not_161_out, not_162_out, not_163_out, not_164_out, not_165_out, not_166_out, not_167_out,
       not_168_out, not_169_out, not_170_out, not_171_out, not_172_out, not_173_out, not_174_out,
       not_175_out, not_176_out, not_177_out, not_178_out, not_179_out, not_180_out, not_181_out,
       not_182_out, not_183_out, not_184_out, not_185_out, not_186_out, not_187_out, not_188_out,
       not_189_out, not_190_out, not_191_out, not_192_out, not_193_out, not_194_out, not_195_out,
       not_196_out, not_197_out, not_198_out, not_199_out, not_200_out, not_201_out, not_202_out,
       not_203_out, not_204_out, not_205_out, not_206_out, not_207_out, not_208_out, not_209_out,
       not_210_out, not_211_out, not_212_out, not_213_out, not_214_out, not_215_out, not_216_out,
       not_217_out, not_218_out, not_219_out, not_220_out, not_221_out, not_222_out, not_223_out,
       not_224_out, not_225_out, not_226_out, not_227_out, not_228_out, not_229_out, not_230_out,
       not_231_out, not_232_out, not_233_out, not_234_out, not_235_out, not_236_out, not_237_out,
       not_238_out, not_239_out, not_240_out, not_241_out, not_242_out, not_243_out, not_244_out,
       not_245_out, not_246_out, not_247_out, not_248_out, not_249_out, not_250_out, not_251_out,
       not_252_out, not_253_out, not_254_out, not_255_out, not_256_out, not_257_out, not_258_out, not_259_out;

  not not_1 (not_1_out, OP5);
  not not_2 (not_2_out, OP4);
  not not_3 (not_3_out, OP3);
  not not_4 (not_4_out, OP2);
  not not_5 (not_5_out, OP1);
  not not_6 (not_6_out, OP0);
  not not_7 (not_7_out, F4);
  not not_8 (not_8_out, F3);
  not not_9 (not_9_out, F2);
  not not_10 (not_10_out, F1);
  not not_11 (not_11_out, F0);
  not not_12 (not_12_out, OP5);
  not not_13 (not_13_out, OP4);
  not not_14 (not_14_out, OP3);
  not not_15 (not_15_out, OP2);
  not not_16 (not_16_out, OP1);
  not not_17 (not_17_out, OP0);
  not not_18 (not_18_out, F4);
  not not_19 (not_19_out, F3);
  not not_20 (not_20_out, F2);
  not not_21 (not_21_out, F1);
  not not_22 (not_22_out, OP5);
  not not_23 (not_23_out, OP4);
  not not_24 (not_24_out, OP3);
  not not_25 (not_25_out, OP2);
  not not_26 (not_26_out, OP1);
  not not_27 (not_27_out, OP0);
  not not_28 (not_28_out, F4);
  not not_29 (not_29_out, F3);
  not not_30 (not_30_out, F2);
  not not_31 (not_31_out, F0);
  not not_32 (not_32_out, OP5);
  not not_33 (not_33_out, OP4);
  not not_34 (not_34_out, OP3);
  not not_35 (not_35_out, OP2);
  not not_36 (not_36_out, OP1);
  not not_37 (not_37_out, OP0);
  not not_38 (not_38_out, F4);
  not not_39 (not_39_out, F3);
  not not_40 (not_40_out, F1);
  not not_41 (not_41_out, F0);
  not not_42 (not_42_out, OP5);
  not not_43 (not_43_out, OP4);
  not not_44 (not_44_out, OP3);
  not not_45 (not_45_out, OP2);
  not not_46 (not_46_out, OP1);
  not not_47 (not_47_out, OP0);
  not not_48 (not_48_out, F4);
  not not_49 (not_49_out, F3);
  not not_50 (not_50_out, F1);
  not not_51 (not_51_out, OP5);
  not not_52 (not_52_out, OP4);
  not not_53 (not_53_out, OP3);
  not not_54 (not_54_out, OP2);
  not not_55 (not_55_out, OP1);
  not not_56 (not_56_out, OP0);
  not not_57 (not_57_out, F4);
  not not_58 (not_58_out, F3);
  not not_59 (not_59_out, OP5);
  not not_60 (not_60_out, OP4);
  not not_61 (not_61_out, OP3);
  not not_62 (not_62_out, OP2);
  not not_63 (not_63_out, OP1);
  not not_64 (not_64_out, OP0);
  not not_65 (not_65_out, F4);
  not not_66 (not_66_out, F2);
  not not_67 (not_67_out, F0);
  not not_68 (not_68_out, OP5);
  not not_69 (not_69_out, OP4);
  not not_70 (not_70_out, OP3);
  not not_71 (not_71_out, OP2);
  not not_72 (not_72_out, OP1);
  not not_73 (not_73_out, OP0);
  not not_74 (not_74_out, F4);
  not not_75 (not_75_out, F2);
  not not_76 (not_76_out, OP5);
  not not_77 (not_77_out, OP4);
  not not_78 (not_78_out, OP3);
  not not_79 (not_79_out, OP2);
  not not_80 (not_80_out, OP1);
  not not_81 (not_81_out, OP0);
  not not_82 (not_82_out, F5);
  not not_83 (not_83_out, F4);
  not not_84 (not_84_out, F2);
  not not_85 (not_85_out, F1);
  not not_86 (not_86_out, F0);
  not not_87 (not_87_out, OP5);
  not not_88 (not_88_out, OP4);
  not not_89 (not_89_out, OP3);
  not not_90 (not_90_out, OP2);
  not not_91 (not_91_out, OP1);
  not not_92 (not_92_out, OP0);
  not not_93 (not_93_out, F5);
  not not_94 (not_94_out, F4);
  not not_95 (not_95_out, F1);
  not not_96 (not_96_out, F0);
  not not_97 (not_97_out, OP5);
  not not_98 (not_98_out, OP4);
  not not_99 (not_99_out, OP3);
  not not_100 (not_100_out, OP1);
  not not_101 (not_101_out, OP0);
  not not_102 (not_102_out, OP5);
  not not_103 (not_103_out, OP4);
  not not_104 (not_104_out, OP3);
  not not_105 (not_105_out, OP1);
  not not_106 (not_106_out, OP5);
  not not_107 (not_107_out, OP4);
  not not_108 (not_108_out, OP2);
  not not_109 (not_109_out, OP1);
  not not_110 (not_110_out, OP0);
  not not_111 (not_111_out, OP5);
  not not_112 (not_112_out, OP4);
  not not_113 (not_113_out, OP1);
  not not_114 (not_114_out, OP0);
  not not_115 (not_115_out, OP5);
  not not_116 (not_116_out, OP4);
  not not_117 (not_117_out, OP2);
  not not_118 (not_118_out, OP1);
  not not_119 (not_119_out, OP5);
  not not_120 (not_120_out, OP4);
  not not_121 (not_121_out, OP2);
  not not_122 (not_122_out, OP0);
  not not_123 (not_123_out, OP5);
  not not_124 (not_124_out, OP4);
  not not_125 (not_125_out, OP1);
  not not_126 (not_126_out, OP4);
  not not_127 (not_127_out, OP3);
  not not_128 (not_128_out, OP2);
  not not_129 (not_129_out, OP4);
  not not_130 (not_130_out, OP2);
  not not_131 (not_131_out, OP5);
  not not_132 (not_132_out, OP4);
  not not_133 (not_133_out, OP3);
  not not_134 (not_134_out, OP2);
  not not_135 (not_135_out, OP1);
  not not_136 (not_136_out, OP0);
  not not_137 (not_137_out, F5);
  not not_138 (not_138_out, F4);
  not not_139 (not_139_out, F3);
  not not_140 (not_140_out, F2);
  not not_141 (not_141_out, F1);
  not not_142 (not_142_out, F0);
  not not_143 (not_143_out, OP5);
  not not_144 (not_144_out, OP4);
  not not_145 (not_145_out, OP3);
  not not_146 (not_146_out, OP2);
  not not_147 (not_147_out, OP1);
  not not_148 (not_148_out, OP0);
  not not_149 (not_149_out, F5);
  not not_150 (not_150_out, F4);
  not not_151 (not_151_out, F3);
  not not_152 (not_152_out, F2);
  not not_153 (not_153_out, OP5);
  not not_154 (not_154_out, OP4);
  not not_155 (not_155_out, OP3);
  not not_156 (not_156_out, OP2);
  not not_157 (not_157_out, OP1);
  not not_158 (not_158_out, OP0);
  not not_159 (not_159_out, F5);
  not not_160 (not_160_out, F4);
  not not_161 (not_161_out, F3);
  not not_162 (not_162_out, F2);
  not not_163 (not_163_out, F0);
  not not_164 (not_164_out, OP5);
  not not_165 (not_165_out, OP4);
  not not_166 (not_166_out, OP3);
  not not_167 (not_167_out, OP2);
  not not_168 (not_168_out, OP1);
  not not_169 (not_169_out, OP0);
  not not_170 (not_170_out, F4);
  not not_171 (not_171_out, F3);
  not not_172 (not_172_out, F2);
  not not_173 (not_173_out, F1);
  not not_174 (not_174_out, F0);
  not not_175 (not_175_out, OP5);
  not not_176 (not_176_out, OP4);
  not not_177 (not_177_out, OP3);
  not not_178 (not_178_out, OP2);
  not not_179 (not_179_out, OP1);
  not not_180 (not_180_out, OP0);
  not not_181 (not_181_out, F4);
  not not_182 (not_182_out, F3);
  not not_183 (not_183_out, F2);
  not not_184 (not_184_out, F1);
  not not_185 (not_185_out, OP5);
  not not_186 (not_186_out, OP4);
  not not_187 (not_187_out, OP3);
  not not_188 (not_188_out, OP2);
  not not_189 (not_189_out, OP1);
  not not_190 (not_190_out, OP0);
  not not_191 (not_191_out, F4);
  not not_192 (not_192_out, F3);
  not not_193 (not_193_out, F2);
  not not_194 (not_194_out, F0);
  not not_195 (not_195_out, OP5);
  not not_196 (not_196_out, OP4);
  not not_197 (not_197_out, OP3);
  not not_198 (not_198_out, OP2);
  not not_199 (not_199_out, OP1);
  not not_200 (not_200_out, OP0);
  not not_201 (not_201_out, F4);
  not not_202 (not_202_out, F3);
  not not_203 (not_203_out, F1);
  not not_204 (not_204_out, F0);
  not not_205 (not_205_out, OP5);
  not not_206 (not_206_out, OP4);
  not not_207 (not_207_out, OP3);
  not not_208 (not_208_out, OP2);
  not not_209 (not_209_out, OP1);
  not not_210 (not_210_out, OP0);
  not not_211 (not_211_out, F4);
  not not_212 (not_212_out, F3);
  not not_213 (not_213_out, F1);
  not not_214 (not_214_out, OP5);
  not not_215 (not_215_out, OP4);
  not not_216 (not_216_out, OP3);
  not not_217 (not_217_out, OP2);
  not not_218 (not_218_out, OP1);
  not not_219 (not_219_out, OP0);
  not not_220 (not_220_out, F4);
  not not_221 (not_221_out, F3);
  not not_222 (not_222_out, OP5);
  not not_223 (not_223_out, OP4);
  not not_224 (not_224_out, OP3);
  not not_225 (not_225_out, OP2);
  not not_226 (not_226_out, OP1);
  not not_227 (not_227_out, OP0);
  not not_228 (not_228_out, F4);
  not not_229 (not_229_out, F2);
  not not_230 (not_230_out, F0);
  not not_231 (not_231_out, OP5);
  not not_232 (not_232_out, OP4);
  not not_233 (not_233_out, OP3);
  not not_234 (not_234_out, OP2);
  not not_235 (not_235_out, OP1);
  not not_236 (not_236_out, OP0);
  not not_237 (not_237_out, F4);
  not not_238 (not_238_out, F2);
  not not_239 (not_239_out, OP5);
  not not_240 (not_240_out, OP4);
  not not_241 (not_241_out, OP3);
  not not_242 (not_242_out, OP2);
  not not_243 (not_243_out, OP1);
  not not_244 (not_244_out, OP0);
  not not_245 (not_245_out, F5);
  not not_246 (not_246_out, F4);
  not not_247 (not_247_out, F1);
  not not_248 (not_248_out, F0);
  not not_249 (not_249_out, OP5);
  not not_250 (not_250_out, OP4);
  not not_251 (not_251_out, OP3);
  not not_252 (not_252_out, OP1);
  not not_253 (not_253_out, OP0);
  not not_254 (not_254_out, OP5);
  not not_255 (not_255_out, OP4);
  not not_256 (not_256_out, OP3);
  not not_257 (not_257_out, OP1);
  not not_258 (not_258_out, OP4);
  not not_259 (not_259_out, OP2);
  and and_1 (and_1_out, not_1_out, not_2_out, not_3_out, not_4_out, not_5_out, not_6_out, F5, not_7_out, not_8_out, not_9_out, not_10_out, not_11_out);
  and and_2 (and_2_out, not_12_out, not_13_out, not_14_out, not_15_out, not_16_out, not_17_out, F5, not_18_out, not_19_out, not_20_out, not_21_out, F0);
  and and_3 (and_3_out, not_22_out, not_23_out, not_24_out, not_25_out, not_26_out, not_27_out, F5, not_28_out, not_29_out, not_30_out, F1, not_31_out);
  and and_4 (and_4_out, not_32_out, not_33_out, not_34_out, not_35_out, not_36_out, not_37_out, F5, not_38_out, not_39_out, F2, not_40_out, not_41_out);
  and and_5 (and_5_out, not_42_out, not_43_out, not_44_out, not_45_out, not_46_out, not_47_out, F5, not_48_out, not_49_out, F2, not_50_out, F0);
  and and_6 (and_6_out, not_51_out, not_52_out, not_53_out, not_54_out, not_55_out, not_56_out, F5, not_57_out, not_58_out, F2, F1, F0);
  and and_7 (and_7_out, not_59_out, not_60_out, not_61_out, not_62_out, not_63_out, not_64_out, F5, not_65_out, F3, not_66_out, F1, not_67_out);
  and and_8 (and_8_out, not_68_out, not_69_out, not_70_out, not_71_out, not_72_out, not_73_out, F5, not_74_out, F3, not_75_out, F1, F0);
  and and_9 (and_9_out, not_76_out, not_77_out, not_78_out, not_79_out, not_80_out, not_81_out, not_82_out, not_83_out, F3, not_84_out, not_85_out, not_86_out);
  and and_10 (and_10_out, not_87_out, not_88_out, not_89_out, not_90_out, not_91_out, not_92_out, not_93_out, not_94_out, F3, F2, not_95_out, not_96_out);
  and and_11 (and_11_out, not_97_out, not_98_out, not_99_out, OP2, not_100_out, not_101_out);
  and and_12 (and_12_out, not_102_out, not_103_out, not_104_out, OP2, not_105_out, OP0);
  and and_13 (and_13_out, not_106_out, not_107_out, OP3, not_108_out, not_109_out, not_110_out);
  and and_14 (and_14_out, not_111_out, not_112_out, OP3, OP2, not_113_out, not_114_out);
  and and_15 (and_15_out, not_115_out, not_116_out, OP3, not_117_out, not_118_out, OP0);
  and and_16 (and_16_out, not_119_out, not_120_out, OP3, not_121_out, OP1, not_122_out);
  and and_17 (and_17_out, not_123_out, not_124_out, OP3, OP2, not_125_out, OP0);
  and and_18 (and_18_out, OP5, not_126_out, not_127_out, not_128_out, OP1, OP0);
  and and_19 (and_19_out, OP5, not_129_out, OP3, not_130_out, OP1, OP0);
  and and_20 (and_20_out, not_131_out, not_132_out, not_133_out, not_134_out, not_135_out, not_136_out, not_137_out, not_138_out, not_139_out, not_140_out, not_141_out, not_142_out);
  and and_21 (and_21_out, not_143_out, not_144_out, not_145_out, not_146_out, not_147_out, not_148_out, not_149_out, not_150_out, not_151_out, not_152_out, F1, F0);
  and and_22 (and_22_out, not_153_out, not_154_out, not_155_out, not_156_out, not_157_out, not_158_out, not_159_out, not_160_out, not_161_out, not_162_out, F1, not_163_out);
  and and_23 (and_23_out, not_164_out, not_165_out, not_166_out, not_167_out, not_168_out, not_169_out, F5, not_170_out, not_171_out, not_172_out, not_173_out, not_174_out);
  and and_24 (and_24_out, not_175_out, not_176_out, not_177_out, not_178_out, not_179_out, not_180_out, F5, not_181_out, not_182_out, not_183_out, not_184_out, F0);
  and and_25 (and_25_out, not_185_out, not_186_out, not_187_out, not_188_out, not_189_out, not_190_out, F5, not_191_out, not_192_out, not_193_out, F1, not_194_out);
  and and_26 (and_26_out, not_195_out, not_196_out, not_197_out, not_198_out, not_199_out, not_200_out, F5, not_201_out, not_202_out, F2, not_203_out, not_204_out);
  and and_27 (and_27_out, not_205_out, not_206_out, not_207_out, not_208_out, not_209_out, not_210_out, F5, not_211_out, not_212_out, F2, not_213_out, F0);
  and and_28 (and_28_out, not_214_out, not_215_out, not_216_out, not_217_out, not_218_out, not_219_out, F5, not_220_out, not_221_out, F2, F1, F0);
  and and_29 (and_29_out, not_222_out, not_223_out, not_224_out, not_225_out, not_226_out, not_227_out, F5, not_228_out, F3, not_229_out, F1, not_230_out);
  and and_30 (and_30_out, not_231_out, not_232_out, not_233_out, not_234_out, not_235_out, not_236_out, F5, not_237_out, F3, not_238_out, F1, F0);
  and and_31 (and_31_out, not_239_out, not_240_out, not_241_out, not_242_out, not_243_out, not_244_out, not_245_out, not_246_out, F3, F2, not_247_out, not_248_out);
  and and_32 (and_32_out, not_249_out, not_250_out, not_251_out, OP2, not_252_out, not_253_out);
  and and_33 (and_33_out, not_254_out, not_255_out, not_256_out, OP2, not_257_out, OP0);
  and and_34 (and_34_out, OP5, not_258_out, OP3, not_259_out, OP1, OP0);
  or or_1 (RsUsed, and_1_out, and_2_out, and_3_out, and_4_out, and_5_out, and_6_out, and_7_out, and_8_out, and_9_out, and_10_out, and_11_out, and_12_out, and_13_out, and_14_out, and_15_out, and_16_out, and_17_out, and_18_out, and_19_out);
  or or_2 (RtUsed, and_20_out, and_21_out, and_22_out, and_23_out, and_24_out, and_25_out, and_26_out, and_27_out, and_28_out, and_29_out, and_30_out, and_31_out, and_32_out, and_33_out, and_34_out);
endmodule

module \数据相关处理  (
  input  [31:0] Instruction,
  input  EX_RegWrite,
  input  [4:0] R1_num,
  input  [4:0] EX_WriteReg_num,
  input  MEM_RegWrite,
  input  [4:0] MEM_WriteReg_num,
  input  [4:0] R2_num,
  output DataHazard
);

  wire and_1_out, and_2_out, and_3_out, and_4_out, comparator_1_eq, comparator_2_eq, comparator_3_eq,
       comparator_4_eq, comparator_5_eq, comparator_6_eq, \寄存器相关_1_rsused , \寄存器相关_1_rtused ;

  \寄存器相关  \u_寄存器相关_1  (
    .OP0(Instruction[26]), .OP1(Instruction[27]), .OP2(Instruction[28]), .OP3(Instruction[29]),
    .OP4(Instruction[30]), .OP5(Instruction[31]), .F0(Instruction[0]), .F1(Instruction[1]),
    .F2(Instruction[2]), .F3(Instruction[3]), .F4(Instruction[4]), .F5(Instruction[5]),
    .RsUsed(\寄存器相关_1_rsused ), .RtUsed(\寄存器相关_1_rtused ));
  Comparator #(.width(5), .mode("unsigned")) comparator_1 (
    .a(R1_num), .b({5{1'b0}}), .eq(comparator_1_eq));  // open: gt, lt
  Comparator #(.width(5), .mode("unsigned")) comparator_2 (
    .a({5{1'b0}}), .b(R2_num), .eq(comparator_2_eq));  // open: gt, lt
  Comparator #(.width(5), .mode("unsigned")) comparator_3 (
    .a(R1_num), .b(EX_WriteReg_num), .eq(comparator_3_eq));  // open: gt, lt
  Comparator #(.width(5), .mode("unsigned")) comparator_4 (
    .a(EX_WriteReg_num), .b(R2_num), .eq(comparator_4_eq));  // open: gt, lt
  Comparator #(.width(5), .mode("unsigned")) comparator_5 (
    .a(R1_num), .b(MEM_WriteReg_num), .eq(comparator_5_eq));  // open: gt, lt
  Comparator #(.width(5), .mode("unsigned")) comparator_6 (
    .a(MEM_WriteReg_num), .b(R2_num), .eq(comparator_6_eq));  // open: gt, lt
  and and_1 (and_1_out, ~comparator_1_eq, EX_RegWrite, comparator_3_eq, \寄存器相关_1_rsused );  // AND_Gate
  and and_2 (and_2_out, ~comparator_2_eq, EX_RegWrite, comparator_4_eq, \寄存器相关_1_rtused );  // AND_Gate
  and and_3 (and_3_out, ~comparator_1_eq, MEM_RegWrite, comparator_5_eq, \寄存器相关_1_rsused );  // AND_Gate
  and and_4 (and_4_out, ~comparator_2_eq, MEM_RegWrite, comparator_6_eq, \寄存器相关_1_rtused );  // AND_Gate
  or or_1 (DataHazard, and_1_out, and_2_out, and_3_out, and_4_out);

  // Notes on the sheet:
  //   rt
endmodule
