// Logisim project cpu24-EX重定向流水线(差异化指令+动态分支预测).circ as structural Verilog: 22 circuits, main circuit ◇单周期MIPS
module \单周期MIPS  (
  input  IR1,
  input  IR2,
  input  IR3,
  output RegWrite,
  output MemWrite,
  output [31:0] PC,
  output [31:0] IR,
  output [31:0] RDin,
  output [31:0] MDin,
  output [31:0] LedData
);

  wire and_1_out, CLK, clock_2_out, comparator_1_eq, comparator_1_lt, d_ff_1_q, EN, equal, Go, IR1_t, IR2_t,
       IR3_t, IRA, IRB, IRC, multiplexer_11_out, nand_1_out, not_1_out, or_4_out, or_5_out, RST, SignedExt,
       Syscall, W1, W2, W3, \单周期硬布线控制器_1_alu_src , \单周期硬布线控制器_1_beq , \单周期硬布线控制器_1_bne , \单周期硬布线控制器_1_jal ,
       \单周期硬布线控制器_1_jmp , \单周期硬布线控制器_1_jr , \单周期硬布线控制器_1_memtoreg , \单周期硬布线控制器_1_regdst ;
  wire [3:0] \单周期硬布线控制器_1_alu_op ;
  wire [4:0] multiplexer_4_out, multiplexer_5_out, multiplexer_6_out, multiplexer_7_out;
  wire [12:0] CNT_num;
  wire [15:0] \总周期数 ;
  wire [31:0] bit_extender_1_out, BR_ADDR, JR_ADDR, mips_alu_1_result, multiplexer_1_out, multiplexer_2_out,
       multiplexer_3_out, multiplexer_8_out, multiplexer_9_out, multiplexer_10_out, PC_4, ram_1_data,
       shifter_1_out;

  Button button_1 (.out(RST));
  Clock #(.highDuration(1), .lowDuration(1)) clock_1 ();  // open: out
  Button _1 (.out(IRA));
  Button _2 (.out(IRB));
  Button _3 (.out(IRC));
  Button \u_继续运行  (.out(Go));
  LED #(.active("true")) led_1 (.in(W1));
  LED #(.active("true")) led_2 (.in(W2));
  LED #(.active("true")) led_3 (.in(W3));
  Multiplexer #(.select(1), .width(32), .disabled("Z"), .enable("false")) multiplexer_1 (
    .in0({PC[31:28], IR[25:0], 2'b00}), .in1(JR_ADDR), .out(multiplexer_1_out), .sel(\单周期硬布线控制器_1_jr ));
  D_Flip_Flop #(.trigger("high"), .Pre_Clr_Positions("LEGACY"), .NegatePresetClear("false"), .enable("true"), .NewFFLayout("false")) d_ff_1 (.Q(d_ff_1_q));  // open: clk, D, Qn, preset, en, reset
  Hex_Digit_Display hex_digit_display_1 (.value(LedData[31:28]));  // open: dp
  Adder #(.width(32)) adder_1 (.a(PC), .b(32'h4), .out(PC_4));  // open: cin, cout
  // Probe on 13'hc
  Hex_Digit_Display hex_digit_display_2 (.value(LedData[23:20]));  // open: dp
  Hex_Digit_Display hex_digit_display_3 (.value(LedData[27:24]));  // open: dp
  Multiplexer #(.select(1), .width(32), .disabled("Z"), .enable("false")) multiplexer_2 (
    .in0(PC_4), .in1(multiplexer_1_out), .out(multiplexer_2_out), .sel(\单周期硬布线控制器_1_jmp ));
  Comparator #(.width(13), .mode("twosComplement")) comparator_1 (
    .a(CNT_num), .b(13'hc), .eq(comparator_1_eq), .lt(comparator_1_lt));  // open: gt
  Clock #(.highDuration(1), .lowDuration(1)) clock_2 (.out(clock_2_out));
  Hex_Digit_Display hex_digit_display_4 (.value(LedData[15:12]));  // open: dp
  Hex_Digit_Display hex_digit_display_5 (.value(LedData[19:16]));  // open: dp
  Multiplexer #(.select(1), .width(32), .disabled("Z"), .enable("false")) multiplexer_3 (
    .in0(multiplexer_2_out), .in1(BR_ADDR), .out(multiplexer_3_out), .sel(multiplexer_11_out));
  Hex_Digit_Display hex_digit_display_6 (.value(LedData[7:4]));  // open: dp
  Hex_Digit_Display hex_digit_display_7 (.value(LedData[11:8]));  // open: dp
  // Probe on \总周期数 
  Register #(.width(32), .trigger("rising"), .Select("low")) u_PC (
    .D(multiplexer_3_out), .en(EN), .Q(PC), .clk(CLK), .clr(RST));
  nand nand_1 (nand_1_out, d_ff_1_q, comparator_1_eq);
  Counter #(.width(13), .max('h1fff), .ongoal("stay"), .trigger("rising"), .behavior("old")) counter_1 (
    .count(comparator_1_lt), .Q(CNT_num), .clk(clock_2_out));  // open: load, D, carry, clr, preset
  Hex_Digit_Display hex_digit_display_8 (.value(LedData[3:0]));  // open: dp
  assign CLK = nand_1_out ? clock_2_out : 1'bz;  // Controlled_Buffer controlled_buffer_1
  ROM #(.addrWidth(10), .dataWidth(32), .Select("high")) rom_1 (.addr(PC[11:2]), .data(IR));
  Pull_Resistor #(.pull(1)) pull_resistor_1 (.node(CLK));
  or or_1 (IR1_t, IR1, IRA);
  // Mips_Probe mips_probe_1: pin names not known; wires that end beside it: IR
  or or_2 (IR2_t, IR2, IRB);
  \单周期硬布线控制器  \u_单周期硬布线控制器_1  (
    .Func(IR[5:0]), .OP(IR[31:26]), .ALU_OP(\单周期硬布线控制器_1_alu_op ), .MemToReg(\单周期硬布线控制器_1_memtoreg ),
    .MemWrite(MemWrite), .ALU_SRC(\单周期硬布线控制器_1_alu_src ), .RegWrite(RegWrite), .SysCALL(Syscall),
    .SignedExt(SignedExt), .RegDst(\单周期硬布线控制器_1_regdst ), .JR(\单周期硬布线控制器_1_jr ), .JMP(\单周期硬布线控制器_1_jmp ),
    .Beq(\单周期硬布线控制器_1_beq ), .JAL(\单周期硬布线控制器_1_jal ), .Bne(\单周期硬布线控制器_1_bne ));  // open: BGEZ, ERET, MFC0, MTC0, MF, SV, LB
  Multiplexer #(.select(1), .width(5), .disabled("Z"), .enable("false")) multiplexer_4 (
    .in0(IR[25:21]), .in1(5'b00010), .out(multiplexer_4_out), .sel(Syscall));
  Multiplexer #(.select(1), .width(5), .disabled("Z"), .enable("false")) multiplexer_5 (
    .in0(IR[20:16]), .in1(5'b00100), .out(multiplexer_5_out), .sel(Syscall));
  Multiplexer #(.select(1), .width(5), .disabled("Z"), .enable("false")) multiplexer_6 (
    .in0(IR[20:16]), .in1(IR[15:11]), .out(multiplexer_6_out), .sel(\单周期硬布线控制器_1_regdst ));
  Multiplexer #(.select(1), .width(5), .disabled("Z"), .enable("false")) multiplexer_7 (
    .in0(multiplexer_6_out), .in1({5{1'b1}}), .out(multiplexer_7_out), .sel(\单周期硬布线控制器_1_jal ));
  not not_1 (not_1_out, Syscall);
  or or_3 (IR3_t, IR3, IRC);
  MIPS_Regifile mips_regifile_1 (
    .Din(RDin), .Clk(CLK), .R1(JR_ADDR), .R2(MDin), .WE(RegWrite), .W_num(multiplexer_7_out),
    .R1_num(multiplexer_4_out), .R2_num(multiplexer_5_out));
  assign bit_extender_1_out = {{16{IR[15]}}, IR[15:0]};  // Bit_Extender bit_extender_1
  or or_4 (or_4_out, not_1_out, Go);
  or or_5 (or_5_out, equal, not_1_out);
  Multiplexer #(.select(1), .width(32), .disabled("Z"), .enable("false")) multiplexer_8 (
    .in0(MDin), .in1(bit_extender_1_out), .out(multiplexer_8_out), .sel(\单周期硬布线控制器_1_alu_src ));
  D_Flip_Flop #(.trigger("falling"), .Pre_Clr_Positions("ABOVE_BELOW"), .NegatePresetClear("false"), .enable("false"), .NewFFLayout("true")) d_ff_2 (
    .clk(CLK), .D(or_5_out), .Q(EN), .preset(or_4_out));  // open: Qn, reset
  Multiplexer #(.select(1), .width(32), .disabled("Z"), .enable("false")) multiplexer_9 (
    .in0(multiplexer_8_out), .in1(32'h22), .out(multiplexer_9_out), .sel(Syscall));
  Shifter #(.width(32), .shift("ll")) shifter_1 (.in(bit_extender_1_out), .\dist (5'b00010), .out(shifter_1_out));
  MIPS_ALU mips_alu_1 (
    .X(JR_ADDR), .Y(multiplexer_9_out), .AluOP(\单周期硬布线控制器_1_alu_op ), .Equal(equal),
    .Result(mips_alu_1_result), .shamt(IR[10:6]));  // open: Result_2
  Adder #(.width(32)) adder_2 (.a(shifter_1_out), .b(PC_4), .out(BR_ADDR));  // open: cin, cout
  Counter #(.width(16), .max('hffff), .ongoal("wrap"), .trigger("rising"), .behavior("new")) counter_2 (
    .count(EN), .Q(\总周期数 ), .clk(CLK), .clr(RST));  // open: load, D, carry, preset, down
  Multiplexer #(.select(1), .width(32), .disabled("Z"), .enable("false")) multiplexer_10 (
    .in0(mips_alu_1_result), .in1(ram_1_data), .out(multiplexer_10_out), .sel(\单周期硬布线控制器_1_memtoreg ));
  RAM #(.addrWidth(10), .dataWidth(32), .bus("separate"), .Select("high")) ram_1 (
    .addr(mips_alu_1_result[11:2]), .din(MDin), .data(ram_1_data), .str(MemWrite), .clk(CLK), .clr(RST));  // open: sel, ld
  and and_1 (and_1_out, Syscall, equal);
  Register #(.width(32), .trigger("rising"), .Select("low")) register_1 (
    .D(MDin), .en(and_1_out), .Q(LedData), .clk(CLK), .clr(RST));
  Multiplexer #(.select(1), .width(1), .disabled("Z"), .enable("false")) multiplexer_11 (
    .in0(\单周期硬布线控制器_1_bne ), .in1(\单周期硬布线控制器_1_beq ), .out(multiplexer_11_out), .sel(equal));
  Multiplexer #(.select(1), .width(32), .disabled("Z"), .enable("false")) multiplexer_12 (
    .in0(multiplexer_10_out), .in1(PC_4), .out(RDin), .sel(\单周期硬布线控制器_1_jal ));

  // Other names for the same wires on the sheet: Func[5:0] = IR[5:0]; J_ADDR[31:2] = {PC[31:28], IR[25:0]};
  //   offset[25:0] = IR[25:0]; OP[5:0] = IR[31:26]

  // Notes on the sheet:
  //   中断源
  //   中断等待指示
  //   总复位信号应将除ROM以外所有存储组件全部清零
  //   控制位
  //   暂停节拍，不能为0
  //   用这个时钟源需要去掉电路中的其他时钟源
  //   戳工具置1进入计数暂停模式，ctrl+k时钟自动运行到对应节拍暂停
  //   ctrl+k关闭时钟连续运行，将控制位置零，进入单步调试模式调试
  //   数码管输出
  //   数码管输出应该用寄存器锁存，否则显示数据只能一闪而过
  //   指令存储器
  //   指令字
  //   contents of rom_1 (hex, n*v repeats v):
  //   20110001 8000c05 20110001 20120002 20130003 8000c09 20110001 20120002 20130003 8000c0d 20110001
  //   20120002 20130003 8000c11 20110001 20120002 20130003 c000cb8 20100001 20110001 118fc0 112020
  //   20020022 c 118882 12200001 8000c15 112020 20020022 c 20110001 118880 112020 20020022 c 12200001
  //   8000c1f 20110001 118fc0 112020 20020022 c 1188c3 112020 20020022 c 118903 112020 20020022 c 118903
  //   112020 20020022 c 118903 112020 20020022 c 118903 112020 20020022 c 118903 112020 20020022 c 118903
  //   112020 20020022 c 118903 112020 20020022 c 20100001 109fc0 139fc3 8021 2012000c 24160003 26100001
  //   3210000f 20080008 20090001 139900 2709825 132020 20020022 c 1094022 1500fff9 22100001 2018000f
  //   2188024 108700 20080008 20090001 139902 2709825 132021 20020022 c 1094022 1500fff9 108702 2c9b022
  //   12c00001 8000c50 4020 1084027 84400 3508ffff 82021 20020022 c 2010ffff 20110000 ae300000 22100001
  //   22310004 ae300000 22100001 22310004 ae300000 22100001 22310004 ae300000 22100001 22310004 ae300000
  //   22100001 22310004 ae300000 22100001 22310004 ae300000 22100001 22310004 ae300000 22100001 22310004
  //   ae300000 22100001 22310004 ae300000 22100001 22310004 ae300000 22100001 22310004 ae300000 22100001
  //   22310004 ae300000 22100001 22310004 ae300000 22100001 22310004 ae300000 22100001 22310004 ae300000
  //   22100001 22310004 22100001 8020 2011003c 8e130000 8e340000 274402a 11000002 ae330000 ae140000
  //   2231fffc 1611fff8 102020 20020022 c 22100004 2011003c 1611fff2 20020032 c 20100000 22100001 102020
  //   20020022 c 22100002 102020 20020022 c 22100003 102020 20020022 c 22100004 102020 20020022 c 22100005
  //   102020 20020022 c 22100006 102020 20020022 c 22100007 102020 20020022 c 22100008 102020 20020022
  //   20020022 c 3e00008
  //   可计数暂停的时钟源
  //   JMP
  //   JR
  //   OP
  //   Func
  //   rs
  //   rt
  //   rd
  //   Beq
  //   Bne
  //   AluOP
  //   AluSrcB
  //   RegWrite
  //   JAL
  //   RegDst
  //   Syscall
  //   MemToReg
  //   MemWrite
  //   为方便自动评测，需要输出PC，IR，寄存器堆写如数据RDin
  //   RAM写使能MemWrite、RAM写入数据MDin等信号
  //   单周期MIPS
  //   控制与调试模块
endmodule

// 单周期硬布线控制器
module \单周期硬布线控制器  (
  input  [5:0] OP,
  input  [4:0] MF,
  input  [5:0] Func,
  output [3:0] ALU_OP,
  output MemToReg,
  output MemWrite,
  output ALU_SRC,
  output RegWrite,
  output SysCALL,
  output SignedExt,
  output RegDst,
  output Beq,
  output Bne,
  output JR,
  output JMP,
  output JAL,
  output BGEZ,
  output SV,
  output LB,
  output ERET,
  output MFC0,
  output MTC0
);

  \运算控制器自动生成  \u_运算控制器自动生成_1  (
    .OP0(OP[0]), .OP1(OP[1]), .OP2(OP[2]), .OP3(OP[3]), .OP4(OP[4]), .OP5(OP[5]), .F0(Func[0]), .F1(Func[1]),
    .F2(Func[2]), .F3(Func[3]), .F4(Func[4]), .F5(Func[5]), .S0(ALU_OP[0]), .S1(ALU_OP[1]), .S2(ALU_OP[2]),
    .S3(ALU_OP[3]));
  \控制信号自动生成  \u_控制信号自动生成_1  (
    .OP0(OP[0]), .OP1(OP[1]), .OP2(OP[2]), .OP3(OP[3]), .OP4(OP[4]), .OP5(OP[5]), .F0(Func[0]), .F1(Func[1]),
    .F2(Func[2]), .F3(Func[3]), .F4(Func[4]), .F5(Func[5]), .MemToReg(MemToReg), .MemWrite(MemWrite),
    .ALU_SRC(ALU_SRC), .RegWrite(RegWrite), .SysCALL(SysCALL), .SignedExt(SignedExt), .RegDst(RegDst),
    .BEQ(Beq), .BNE(Bne), .JR(JR), .JUMP(JMP), .JAL(JAL), .BGEZ(BGEZ), .SV(SV), .LB(LB));
  and and_1 (ERET, ~OP[0], ~OP[1], ~OP[2], ~OP[3], OP[4], ~OP[5], ~Func[0], ~Func[1], ~Func[2], Func[3], Func[4], ~Func[5]);  // AND_Gate
  and and_2 (MFC0, ~OP[0], ~OP[1], ~OP[2], ~OP[3], OP[4], ~OP[5], ~MF[0], ~MF[1], ~MF[2], ~MF[3], ~MF[4]);  // AND_Gate
  and and_3 (MTC0, ~OP[0], ~OP[1], ~OP[2], ~OP[3], OP[4], ~OP[5], ~MF[0], ~MF[1], MF[2], ~MF[3], ~MF[4]);  // AND_Gate

  // Other names for the same wires on the sheet: OP_CODE[5:0] = OP

  // Notes on the sheet:
  //   运算器控制器，根据指令生成运算器功能选择信号
  //   控制信号生成，产生数据通路需要的其他控制信号
endmodule

// 运算器控制器
module \运算控制器自动生成  (
  input  OP0,
  input  OP1,
  input  OP2,
  input  OP3,
  input  OP4,
  input  OP5,
  input  F0,
  input  F1,
  input  F2,
  input  F3,
  input  F4,
  input  F5,
  output S0,
  output S1,
  output S2,
  output S3
);

  wire and_1_out, and_2_out, and_3_out, and_4_out, and_5_out, and_6_out, and_7_out, and_8_out, and_9_out,
       and_10_out, and_11_out, and_12_out, and_13_out, and_14_out, and_15_out, and_16_out, and_17_out,
       and_18_out, and_19_out, and_20_out, and_21_out, and_22_out, and_23_out, and_24_out, and_25_out,
       and_26_out, and_27_out, and_28_out, and_29_out, and_30_out, and_31_out, and_32_out, and_33_out,
       and_34_out, not_1_out, not_2_out, not_3_out, not_4_out, not_5_out, not_6_out, not_7_out, not_8_out,
       not_9_out, not_10_out, not_11_out, not_12_out, not_13_out, not_14_out, not_15_out, not_16_out,
       not_17_out, not_18_out, not_19_out, not_20_out, not_21_out, not_22_out, not_23_out, not_24_out,
       not_25_out, not_26_out, not_27_out, not_28_out, not_29_out, not_30_out, not_31_out, not_32_out,
       not_33_out, not_34_out, not_35_out, not_36_out, not_37_out, not_38_out, not_39_out, not_40_out,
       not_41_out, not_42_out, not_43_out, not_44_out, not_45_out, not_46_out, not_47_out, not_48_out,
       not_49_out, not_50_out, not_51_out, not_52_out, not_53_out, not_54_out, not_55_out, not_56_out,
       not_57_out, not_58_out, not_59_out, not_60_out, not_61_out, not_62_out, not_63_out, not_64_out,
       not_65_out, not_66_out, not_67_out, not_68_out, not_69_out, not_70_out, not_71_out, not_72_out,
       not_73_out, not_74_out, not_75_out, not_76_out, not_77_out, not_78_out, not_79_out, not_80_out,
       not_81_out, not_82_out, not_83_out, not_84_out, not_85_out, not_86_out, not_87_out, not_88_out,
       not_89_out, not_90_out, not_91_out, not_92_out, not_93_out, not_94_out, not_95_out, not_96_out,
       not_97_out, not_98_out, not_99_out, not_100_out, not_101_out, not_102_out, not_103_out, not_104_out,
       not_105_out, not_106_out, not_107_out, not_108_out, not_109_out, not_110_out, not_111_out,
       not_112_out, not_113_out, not_114_out, not_115_out, not_116_out, not_117_out, not_118_out,
       not_119_out, not_120_out, not_121_out, not_122_out, not_123_out, not_124_out, not_125_out,
       not_126_out, not_127_out, not_128_out, not_129_out, not_130_out, not_131_out, not_132_out,
       not_133_out, not_134_out, not_135_out, not_136_out, not_137_out, not_138_out, not_139_out,
       not_140_out, not_141_out, not_142_out, not_143_out, not_144_out, not_145_out, not_146_out,
       not_147_out, not_148_out, not_149_out, not_150_out, not_151_out, not_152_out, not_153_out,
       not_154_out, not_155_out, not_156_out, not_157_out, not_158_out, not_159_out, not_160_out,
       not_161_out, not_162_out, not_163_out, not_164_out, not_165_out, not_166_out, not_167_out,
       not_168_out, not_169_out, not_170_out, not_171_out, not_172_out, not_173_out, not_174_out,
       not_175_out, not_176_out, not_177_out, not_178_out, not_179_out, not_180_out, not_181_out,
       not_182_out, not_183_out, not_184_out, not_185_out, not_186_out, not_187_out, not_188_out,
       not_189_out, not_190_out, not_191_out, not_192_out, not_193_out, not_194_out, not_195_out,
       not_196_out, not_197_out, not_198_out, not_199_out, not_200_out, not_201_out, not_202_out,
       not_203_out, not_204_out, not_205_out, not_206_out, not_207_out, not_208_out, not_209_out,
       not_210_out, not_211_out, not_212_out, not_213_out, not_214_out, not_215_out, not_216_out,
       not_217_out, not_218_out, not_219_out;

  not not_1 (not_1_out, OP5);
  not not_2 (not_2_out, OP4);
  not not_3 (not_3_out, OP3);
  not not_4 (not_4_out, OP2);
  not not_5 (not_5_out, OP1);
  not not_6 (not_6_out, OP0);
  not not_7 (not_7_out, F5);
  not not_8 (not_8_out, F4);
  not not_9 (not_9_out, F3);
  not not_10 (not_10_out, F2);
  not not_11 (not_11_out, OP5);
  not not_12 (not_12_out, OP4);
  not not_13 (not_13_out, OP3);
  not not_14 (not_14_out, OP2);
  not not_15 (not_15_out, OP1);
  not not_16 (not_16_out, OP0);
  not not_17 (not_17_out, F4);
  not not_18 (not_18_out, F3);
  not not_19 (not_19_out, F2);
  not not_20 (not_20_out, F1);
  not not_21 (not_21_out, F0);
  not not_22 (not_22_out, OP5);
  not not_23 (not_23_out, OP4);
  not not_24 (not_24_out, OP3);
  not not_25 (not_25_out, OP2);
  not not_26 (not_26_out, OP1);
  not not_27 (not_27_out, OP0);
  not not_28 (not_28_out, F4);
  not not_29 (not_29_out, F3);
  not not_30 (not_30_out, F2);
  not not_31 (not_31_out, F1);
  not not_32 (not_32_out, OP5);
  not not_33 (not_33_out, OP4);
  not not_34 (not_34_out, OP3);
  not not_35 (not_35_out, OP2);
  not not_36 (not_36_out, OP1);
  not not_37 (not_37_out, OP0);
  not not_38 (not_38_out, F4);
  not not_39 (not_39_out, F3);
  not not_40 (not_40_out, F1);
  not not_41 (not_41_out, F0);
  not not_42 (not_42_out, OP5);
  not not_43 (not_43_out, OP4);
  not not_44 (not_44_out, OP3);
  not not_45 (not_45_out, OP2);
  not not_46 (not_46_out, OP1);
  not not_47 (not_47_out, OP0);
  not not_48 (not_48_out, F4);
  not not_49 (not_49_out, F2);
  not not_50 (not_50_out, F0);
  not not_51 (not_51_out, OP5);
  not not_52 (not_52_out, OP4);
  not not_53 (not_53_out, OP2);
  not not_54 (not_54_out, OP1);
  not not_55 (not_55_out, OP0);
  not not_56 (not_56_out, OP5);
  not not_57 (not_57_out, OP4);
  not not_58 (not_58_out, OP1);
  not not_59 (not_59_out, OP0);
  not not_60 (not_60_out, OP5);
  not not_61 (not_61_out, OP4);
  not not_62 (not_62_out, OP2);
  not not_63 (not_63_out, OP1);
  not not_64 (not_64_out, OP5);
  not not_65 (not_65_out, OP4);
  not not_66 (not_66_out, OP2);
  not not_67 (not_67_out, OP0);
  not not_68 (not_68_out, OP4);
  not not_69 (not_69_out, OP3);
  not not_70 (not_70_out, OP2);
  not not_71 (not_71_out, OP4);
  not not_72 (not_72_out, OP2);
  not not_73 (not_73_out, OP5);
  not not_74 (not_74_out, OP4);
  not not_75 (not_75_out, OP0);
  not not_76 (not_76_out, OP4);
  not not_77 (not_77_out, OP3);
  not not_78 (not_78_out, OP2);
  not not_79 (not_79_out, OP1);
  not not_80 (not_80_out, OP0);
  not not_81 (not_81_out, OP0);
  not not_82 (not_82_out, OP1);
  not not_83 (not_83_out, OP2);
  not not_84 (not_84_out, OP3);
  not not_85 (not_85_out, OP4);
  not not_86 (not_86_out, OP5);
  not not_87 (not_87_out, F0);
  not not_88 (not_88_out, F1);
  not not_89 (not_89_out, F3);
  not not_90 (not_90_out, F4);
  not not_91 (not_91_out, OP0);
  not not_92 (not_92_out, OP1);
  not not_93 (not_93_out, OP2);
  not not_94 (not_94_out, OP3);
  not not_95 (not_95_out, OP4);
  not not_96 (not_96_out, OP5);
  not not_97 (not_97_out, F0);
  not not_98 (not_98_out, F3);
  not not_99 (not_99_out, F4);
  not not_100 (not_100_out, F5);
  not not_101 (not_101_out, OP0);
  not not_102 (not_102_out, OP1);
  not not_103 (not_103_out, OP2);
  not not_104 (not_104_out, OP3);
  not not_105 (not_105_out, OP4);
  not not_106 (not_106_out, OP5);
  not not_107 (not_107_out, F0);
  not not_108 (not_108_out, F2);
  not not_109 (not_109_out, F4);
  not not_110 (not_110_out, OP0);
  not not_111 (not_111_out, OP1);
  not not_112 (not_112_out, OP2);
  not not_113 (not_113_out, OP3);
  not not_114 (not_114_out, OP4);
  not not_115 (not_115_out, OP5);
  not not_116 (not_116_out, F3);
  not not_117 (not_117_out, F4);
  not not_118 (not_118_out, OP0);
  not not_119 (not_119_out, OP1);
  not not_120 (not_120_out, OP4);
  not not_121 (not_121_out, OP5);
  not not_122 (not_122_out, OP0);
  not not_123 (not_123_out, OP2);
  not not_124 (not_124_out, OP4);
  not not_125 (not_125_out, OP5);
  not not_126 (not_126_out, OP5);
  not not_127 (not_127_out, OP4);
  not not_128 (not_128_out, OP3);
  not not_129 (not_129_out, OP2);
  not not_130 (not_130_out, OP1);
  not not_131 (not_131_out, OP0);
  not not_132 (not_132_out, F4);
  not not_133 (not_133_out, F3);
  not not_134 (not_134_out, F2);
  not not_135 (not_135_out, F1);
  not not_136 (not_136_out, F0);
  not not_137 (not_137_out, OP5);
  not not_138 (not_138_out, OP4);
  not not_139 (not_139_out, OP3);
  not not_140 (not_140_out, OP2);
  not not_141 (not_141_out, OP1);
  not not_142 (not_142_out, OP0);
  not not_143 (not_143_out, F4);
  not not_144 (not_144_out, F3);
  not not_145 (not_145_out, F2);
  not not_146 (not_146_out, F1);
  not not_147 (not_147_out, OP5);
  not not_148 (not_148_out, OP4);
  not not_149 (not_149_out, OP3);
  not not_150 (not_150_out, OP2);
  not not_151 (not_151_out, OP1);
  not not_152 (not_152_out, OP0);
  not not_153 (not_153_out, F4);
  not not_154 (not_154_out, F3);
  not not_155 (not_155_out, F2);
  not not_156 (not_156_out, F0);
  not not_157 (not_157_out, OP5);
  not not_158 (not_158_out, OP4);
  not not_159 (not_159_out, OP3);
  not not_160 (not_160_out, OP2);
  not not_161 (not_161_out, OP1);
  not not_162 (not_162_out, OP0);
  not not_163 (not_163_out, F4);
  not not_164 (not_164_out, F3);
  not not_165 (not_165_out, F1);
  not not_166 (not_166_out, F0);
  not not_167 (not_167_out, OP5);
  not not_168 (not_168_out, OP4);
  not not_169 (not_169_out, OP3);
  not not_170 (not_170_out, OP2);
  not not_171 (not_171_out, OP1);
  not not_172 (not_172_out, OP0);
  not not_173 (not_173_out, F4);
  not not_174 (not_174_out, F2);
  not not_175 (not_175_out, OP5);
  not not_176 (not_176_out, OP4);
  not not_177 (not_177_out, OP2);
  not not_178 (not_178_out, OP1);
  not not_179 (not_179_out, OP0);
  not not_180 (not_180_out, OP5);
  not not_181 (not_181_out, OP4);
  not not_182 (not_182_out, OP1);
  not not_183 (not_183_out, OP0);
  not not_184 (not_184_out, OP5);
  not not_185 (not_185_out, OP4);
  not not_186 (not_186_out, OP2);
  not not_187 (not_187_out, OP1);
  not not_188 (not_188_out, OP4);
  not not_189 (not_189_out, OP3);
  not not_190 (not_190_out, OP2);
  not not_191 (not_191_out, OP4);
  not not_192 (not_192_out, OP2);
  not not_193 (not_193_out, OP4);
  not not_194 (not_194_out, OP3);
  not not_195 (not_195_out, OP2);
  not not_196 (not_196_out, OP1);
  not not_197 (not_197_out, OP0);
  not not_198 (not_198_out, OP0);
  not not_199 (not_199_out, OP1);
  not not_200 (not_200_out, OP2);
  not not_201 (not_201_out, OP3);
  not not_202 (not_202_out, OP4);
  not not_203 (not_203_out, OP5);
  not not_204 (not_204_out, F2);
  not not_205 (not_205_out, F4);
  not not_206 (not_206_out, OP0);
  not not_207 (not_207_out, OP1);
  not not_208 (not_208_out, OP2);
  not not_209 (not_209_out, OP3);
  not not_210 (not_210_out, OP4);
  not not_211 (not_211_out, OP5);
  not not_212 (not_212_out, F3);
  not not_213 (not_213_out, F4);
  not not_214 (not_214_out, OP0);
  not not_215 (not_215_out, OP4);
  not not_216 (not_216_out, OP5);
  not not_217 (not_217_out, OP1);
  not not_218 (not_218_out, OP4);
  not not_219 (not_219_out, OP5);
  and and_1 (and_1_out, not_1_out, not_2_out, not_3_out, not_4_out, not_5_out, not_6_out, not_7_out, not_8_out, not_9_out, not_10_out, F1, F0);
  and and_2 (and_2_out, not_11_out, not_12_out, not_13_out, not_14_out, not_15_out, not_16_out, F5, not_17_out, not_18_out, not_19_out, not_20_out, not_21_out);
  and and_3 (and_3_out, not_22_out, not_23_out, not_24_out, not_25_out, not_26_out, not_27_out, F5, not_28_out, not_29_out, not_30_out, not_31_out, F0);
  and and_4 (and_4_out, not_32_out, not_33_out, not_34_out, not_35_out, not_36_out, not_37_out, F5, not_38_out, not_39_out, F2, not_40_out, not_41_out);
  and and_5 (and_5_out, not_42_out, not_43_out, not_44_out, not_45_out, not_46_out, not_47_out, F5, not_48_out, F3, not_49_out, F1, not_50_out);
  and and_6 (and_6_out, not_51_out, not_52_out, OP3, not_53_out, not_54_out, not_55_out);
  and and_7 (and_7_out, not_56_out, not_57_out, OP3, OP2, not_58_out, not_59_out);
  and and_8 (and_8_out, not_60_out, not_61_out, OP3, not_62_out, not_63_out, OP0);
  and and_9 (and_9_out, not_64_out, not_65_out, OP3, not_66_out, OP1, not_67_out);
  and and_10 (and_10_out, OP5, not_68_out, not_69_out, not_70_out, OP1, OP0);
  and and_11 (and_11_out, OP5, not_71_out, OP3, not_72_out, OP1, OP0);
  and and_12 (and_12_out, not_73_out, not_74_out, OP3, OP2, OP1, not_75_out);
  and and_13 (and_13_out, OP5, not_76_out, not_77_out, not_78_out, not_79_out, not_80_out);
  and and_14 (and_14_out, not_81_out, not_82_out, not_83_out, not_84_out, not_85_out, not_86_out, not_87_out, not_88_out, F2, not_89_out, not_90_out, F5);
  and and_15 (and_15_out, not_91_out, not_92_out, not_93_out, not_94_out, not_95_out, not_96_out, not_97_out, F1, not_98_out, not_99_out, not_100_out);
  and and_16 (and_16_out, not_101_out, not_102_out, not_103_out, not_104_out, not_105_out, not_106_out, not_107_out, F1, not_108_out, not_109_out, F5);
  and and_17 (and_17_out, not_110_out, not_111_out, not_112_out, not_113_out, not_114_out, not_115_out, F0, F1, F2, not_116_out, not_117_out, F5);
  and and_18 (and_18_out, not_118_out, not_119_out, OP2, OP3, not_120_out, not_121_out);
  and and_19 (and_19_out, not_122_out, OP1, not_123_out, OP3, not_124_out, not_125_out);
  and and_20 (and_20_out, not_126_out, not_127_out, not_128_out, not_129_out, not_130_out, not_131_out, F5, not_132_out, not_133_out, not_134_out, not_135_out, not_136_out);
  and and_21 (and_21_out, not_137_out, not_138_out, not_139_out, not_140_out, not_141_out, not_142_out, F5, not_143_out, not_144_out, not_145_out, not_146_out, F0);
  and and_22 (and_22_out, not_147_out, not_148_out, not_149_out, not_150_out, not_151_out, not_152_out, F5, not_153_out, not_154_out, not_155_out, F1, not_156_out);
  and and_23 (and_23_out, not_157_out, not_158_out, not_159_out, not_160_out, not_161_out, not_162_out, F5, not_163_out, not_164_out, F2, not_165_out, not_166_out);
  and and_24 (and_24_out, not_167_out, not_168_out, not_169_out, not_170_out, not_171_out, not_172_out, F5, not_173_out, F3, not_174_out, F1, F0);
  and and_25 (and_25_out, not_175_out, not_176_out, OP3, not_177_out, not_178_out, not_179_out);
  and and_26 (and_26_out, not_180_out, not_181_out, OP3, OP2, not_182_out, not_183_out);
  and and_27 (and_27_out, not_184_out, not_185_out, OP3, not_186_out, not_187_out, OP0);
  and and_28 (and_28_out, OP5, not_188_out, not_189_out, not_190_out, OP1, OP0);
  and and_29 (and_29_out, OP5, not_191_out, OP3, not_192_out, OP1, OP0);
  and and_30 (and_30_out, OP5, not_193_out, not_194_out, not_195_out, not_196_out, not_197_out);
  and and_31 (and_31_out, not_198_out, not_199_out, not_200_out, not_201_out, not_202_out, not_203_out, F1, not_204_out, F3, not_205_out, F5);
  and and_32 (and_32_out, not_206_out, not_207_out, not_208_out, not_209_out, not_210_out, not_211_out, F0, F2, not_212_out, not_213_out, F5);
  and and_33 (and_33_out, not_214_out, OP1, OP3, not_215_out, not_216_out);
  and and_34 (and_34_out, OP0, not_217_out, OP2, OP3, not_218_out, not_219_out);
  or or_1 (S1, and_14_out, and_15_out, and_16_out, and_17_out, and_18_out, and_19_out);
  or or_2 (S2, and_20_out, and_21_out, and_22_out, and_23_out, and_24_out, and_25_out, and_26_out, and_27_out, and_28_out, and_29_out, and_30_out);
  or or_3 (S3, and_31_out, and_32_out, and_33_out, and_34_out);
  or or_4 (S0, and_1_out, and_2_out, and_3_out, and_4_out, and_5_out, and_6_out, and_7_out, and_8_out, and_9_out, and_10_out, and_11_out, and_12_out, and_13_out);
endmodule

// 控制信号生成
module \控制信号自动生成  (
  input  OP0,
  input  OP1,
  input  OP2,
  input  OP3,
  input  OP4,
  input  OP5,
  input  F0,
  input  F1,
  input  F2,
  input  F3,
  input  F4,
  input  F5,
  output MemToReg,
  output MemWrite,
  output ALU_SRC,
  output RegWrite,
  output SysCALL,
  output SignedExt,
  output RegDst,
  output BEQ,
  output BNE,
  output JR,
  output JUMP,
  output JAL,
  output BGEZ,
  output SV,
  output LB
);

  wire and_1_out, and_2_out, and_4_out, and_5_out, and_6_out, and_7_out, and_8_out, and_9_out, and_10_out,
       and_11_out, and_12_out, and_13_out, and_14_out, and_15_out, and_16_out, and_17_out, and_19_out,
       and_20_out, and_21_out, and_22_out, and_23_out, and_24_out, and_25_out, and_26_out, and_27_out,
       and_28_out, and_29_out, and_30_out, and_34_out, and_35_out, not_1_out, not_2_out, not_3_out,
       not_4_out, not_5_out, not_6_out, not_7_out, not_8_out, not_9_out, not_10_out, not_11_out, not_12_out,
       not_13_out, not_14_out, not_15_out, not_16_out, not_17_out, not_18_out, not_19_out, not_20_out,
       not_21_out, not_22_out, not_23_out, not_24_out, not_25_out, not_26_out, not_27_out, not_28_out,
       not_29_out, not_30_out, not_31_out, not_32_out, not_33_out, not_34_out, not_35_out, not_36_out,
       not_37_out, not_38_out, not_39_out, not_40_out, not_41_out, not_42_out, not_43_out, not_44_out,
       not_45_out, not_46_out, not_47_out, not_48_out, not_49_out, not_50_out, not_51_out, not_52_out,
       not_53_out, not_54_out, not_55_out, not_56_out, not_57_out, not_58_out, not_59_out, not_60_out,
       not_61_out, not_62_out, not_63_out, not_64_out, not_65_out, not_66_out, not_67_out, not_68_out,
       not_69_out, not_70_out, not_71_out, not_72_out, not_73_out, not_74_out, not_75_out, not_76_out,
       not_77_out, not_78_out, not_79_out, not_80_out, not_81_out, not_82_out, not_83_out, not_84_out,
       not_85_out, not_86_out, not_87_out, not_88_out, not_89_out, not_90_out, not_91_out, not_92_out,
       not_93_out, not_94_out, not_95_out, not_96_out, not_97_out, not_98_out, not_99_out, not_100_out,
       not_101_out, not_102_out, not_103_out, not_104_out, not_105_out, not_106_out, not_107_out,
       not_108_out, not_109_out, not_110_out, not_111_out, not_112_out, not_113_out, not_114_out,
       not_115_out, not_116_out, not_117_out, not_118_out, not_119_out, not_120_out, not_121_out,
       not_122_out, not_123_out, not_124_out, not_125_out, not_126_out, not_127_out, not_128_out,
       not_129_out, not_130_out, not_131_out, not_132_out, not_133_out, not_134_out, not_135_out,
       not_136_out, not_137_out, not_138_out, not_139_out, not_140_out, not_141_out, not_142_out,
       not_143_out, not_144_out, not_145_out, not_146_out, not_147_out, not_148_out, not_149_out,
       not_150_out, not_151_out, not_152_out, not_153_out, not_154_out, not_155_out, not_156_out,
       not_157_out, not_158_out, not_159_out, not_160_out, not_161_out, not_162_out, not_163_out,
       not_164_out, not_165_out, not_166_out, not_167_out, not_168_out, not_169_out, not_170_out,
       not_171_out, not_172_out, not_173_out, not_174_out, not_175_out, not_176_out, not_177_out,
       not_178_out, not_179_out, not_180_out, not_181_out, not_182_out, not_183_out, not_184_out,
       not_185_out, not_186_out, not_187_out, not_188_out, not_189_out, not_190_out, not_191_out,
       not_192_out, not_193_out, not_194_out, not_195_out, not_196_out, not_197_out, not_198_out,
       not_199_out, not_200_out, not_201_out, not_202_out, not_203_out, not_204_out, not_205_out,
       not_206_out, not_207_out, not_208_out, not_209_out, not_210_out, not_211_out, not_212_out,
       not_213_out, not_214_out, not_215_out, not_216_out, not_217_out, not_218_out, not_219_out,
       not_220_out, not_221_out, not_222_out, not_223_out, not_224_out, not_225_out, not_226_out,
       not_227_out, not_228_out, not_229_out, not_230_out, not_231_out, not_232_out, not_233_out,
       not_234_out, not_235_out, not_236_out, not_237_out, not_238_out, not_239_out;

  not not_1 (not_1_out, OP4);
  not not_2 (not_2_out, OP3);
  not not_3 (not_3_out, OP2);
  not not_4 (not_4_out, OP4);
  not not_5 (not_5_out, OP3);
  not not_6 (not_6_out, OP2);
  not not_7 (not_7_out, OP1);
  not not_8 (not_8_out, OP0);
  not not_9 (not_9_out, OP2);
  not not_10 (not_10_out, OP4);
  not not_11 (not_11_out, OP0);
  not not_12 (not_12_out, OP1);
  not not_13 (not_13_out, OP2);
  not not_14 (not_14_out, OP3);
  not not_15 (not_15_out, OP4);
  not not_16 (not_16_out, OP0);
  not not_17 (not_17_out, OP4);
  not not_18 (not_18_out, OP5);
  not not_19 (not_19_out, OP1);
  not not_20 (not_20_out, OP4);
  not not_21 (not_21_out, OP5);
  not not_22 (not_22_out, OP2);
  not not_23 (not_23_out, OP4);
  not not_24 (not_24_out, OP0);
  not not_25 (not_25_out, OP1);
  not not_26 (not_26_out, OP2);
  not not_27 (not_27_out, OP3);
  not not_28 (not_28_out, OP4);
  not not_29 (not_29_out, F0);
  not not_30 (not_30_out, F2);
  not not_31 (not_31_out, F3);
  not not_32 (not_32_out, F4);
  not not_33 (not_33_out, OP0);
  not not_34 (not_34_out, OP1);
  not not_35 (not_35_out, OP2);
  not not_36 (not_36_out, OP3);
  not not_37 (not_37_out, OP4);
  not not_38 (not_38_out, F1);
  not not_39 (not_39_out, F3);
  not not_40 (not_40_out, F4);
  not not_41 (not_41_out, OP0);
  not not_42 (not_42_out, OP1);
  not not_43 (not_43_out, OP2);
  not not_44 (not_44_out, OP3);
  not not_45 (not_45_out, OP4);
  not not_46 (not_46_out, F0);
  not not_47 (not_47_out, F3);
  not not_48 (not_48_out, F4);
  not not_49 (not_49_out, F5);
  not not_50 (not_50_out, OP0);
  not not_51 (not_51_out, OP1);
  not not_52 (not_52_out, OP2);
  not not_53 (not_53_out, OP3);
  not not_54 (not_54_out, OP4);
  not not_55 (not_55_out, F2);
  not not_56 (not_56_out, F3);
  not not_57 (not_57_out, F4);
  not not_58 (not_58_out, F5);
  not not_59 (not_59_out, OP0);
  not not_60 (not_60_out, OP1);
  not not_61 (not_61_out, OP2);
  not not_62 (not_62_out, OP3);
  not not_63 (not_63_out, OP4);
  not not_64 (not_64_out, F2);
  not not_65 (not_65_out, F4);
  not not_66 (not_66_out, OP0);
  not not_67 (not_67_out, OP1);
  not not_68 (not_68_out, OP2);
  not not_69 (not_69_out, OP3);
  not not_70 (not_70_out, OP4);
  not not_71 (not_71_out, F3);
  not not_72 (not_72_out, F4);
  not not_73 (not_73_out, OP0);
  not not_74 (not_74_out, OP1);
  not not_75 (not_75_out, OP2);
  not not_76 (not_76_out, OP3);
  not not_77 (not_77_out, OP4);
  not not_78 (not_78_out, OP0);
  not not_79 (not_79_out, OP4);
  not not_80 (not_80_out, OP5);
  not not_81 (not_81_out, OP1);
  not not_82 (not_82_out, OP4);
  not not_83 (not_83_out, OP5);
  not not_84 (not_84_out, OP2);
  not not_85 (not_85_out, OP3);
  not not_86 (not_86_out, OP4);
  not not_87 (not_87_out, OP0);
  not not_88 (not_88_out, OP1);
  not not_89 (not_89_out, OP2);
  not not_90 (not_90_out, OP3);
  not not_91 (not_91_out, OP4);
  not not_92 (not_92_out, OP5);
  not not_93 (not_93_out, F0);
  not not_94 (not_94_out, F1);
  not not_95 (not_95_out, F4);
  not not_96 (not_96_out, F5);
  not not_97 (not_97_out, OP0);
  not not_98 (not_98_out, OP1);
  not not_99 (not_99_out, OP2);
  not not_100 (not_100_out, OP3);
  not not_101 (not_101_out, OP4);
  not not_102 (not_102_out, OP0);
  not not_103 (not_103_out, OP2);
  not not_104 (not_104_out, OP4);
  not not_105 (not_105_out, OP5);
  not not_106 (not_106_out, OP1);
  not not_107 (not_107_out, OP2);
  not not_108 (not_108_out, OP4);
  not not_109 (not_109_out, OP5);
  not not_110 (not_110_out, OP1);
  not not_111 (not_111_out, OP3);
  not not_112 (not_112_out, OP4);
  not not_113 (not_113_out, OP5);
  not not_114 (not_114_out, OP2);
  not not_115 (not_115_out, OP4);
  not not_116 (not_116_out, OP0);
  not not_117 (not_117_out, OP1);
  not not_118 (not_118_out, OP2);
  not not_119 (not_119_out, OP3);
  not not_120 (not_120_out, OP4);
  not not_121 (not_121_out, OP5);
  not not_122 (not_122_out, F0);
  not not_123 (not_123_out, F1);
  not not_124 (not_124_out, F2);
  not not_125 (not_125_out, F4);
  not not_126 (not_126_out, F5);
  not not_127 (not_127_out, OP0);
  not not_128 (not_128_out, OP1);
  not not_129 (not_129_out, OP2);
  not not_130 (not_130_out, OP3);
  not not_131 (not_131_out, OP4);
  not not_132 (not_132_out, OP5);
  not not_133 (not_133_out, F0);
  not not_134 (not_134_out, F2);
  not not_135 (not_135_out, F3);
  not not_136 (not_136_out, F4);
  not not_137 (not_137_out, OP0);
  not not_138 (not_138_out, OP1);
  not not_139 (not_139_out, OP2);
  not not_140 (not_140_out, OP3);
  not not_141 (not_141_out, OP4);
  not not_142 (not_142_out, OP5);
  not not_143 (not_143_out, F1);
  not not_144 (not_144_out, F3);
  not not_145 (not_145_out, F4);
  not not_146 (not_146_out, OP0);
  not not_147 (not_147_out, OP1);
  not not_148 (not_148_out, OP2);
  not not_149 (not_149_out, OP3);
  not not_150 (not_150_out, OP4);
  not not_151 (not_151_out, OP5);
  not not_152 (not_152_out, F0);
  not not_153 (not_153_out, F3);
  not not_154 (not_154_out, F4);
  not not_155 (not_155_out, F5);
  not not_156 (not_156_out, OP0);
  not not_157 (not_157_out, OP1);
  not not_158 (not_158_out, OP2);
  not not_159 (not_159_out, OP3);
  not not_160 (not_160_out, OP4);
  not not_161 (not_161_out, OP5);
  not not_162 (not_162_out, F2);
  not not_163 (not_163_out, F3);
  not not_164 (not_164_out, F4);
  not not_165 (not_165_out, F5);
  not not_166 (not_166_out, OP0);
  not not_167 (not_167_out, OP1);
  not not_168 (not_168_out, OP2);
  not not_169 (not_169_out, OP3);
  not not_170 (not_170_out, OP4);
  not not_171 (not_171_out, OP5);
  not not_172 (not_172_out, F2);
  not not_173 (not_173_out, F4);
  not not_174 (not_174_out, OP0);
  not not_175 (not_175_out, OP1);
  not not_176 (not_176_out, OP2);
  not not_177 (not_177_out, OP3);
  not not_178 (not_178_out, OP4);
  not not_179 (not_179_out, OP5);
  not not_180 (not_180_out, F3);
  not not_181 (not_181_out, F4);
  not not_182 (not_182_out, OP0);
  not not_183 (not_183_out, OP1);
  not not_184 (not_184_out, OP3);
  not not_185 (not_185_out, OP4);
  not not_186 (not_186_out, OP5);
  not not_187 (not_187_out, OP1);
  not not_188 (not_188_out, OP3);
  not not_189 (not_189_out, OP4);
  not not_190 (not_190_out, OP5);
  not not_191 (not_191_out, OP0);
  not not_192 (not_192_out, OP1);
  not not_193 (not_193_out, OP2);
  not not_194 (not_194_out, OP3);
  not not_195 (not_195_out, OP4);
  not not_196 (not_196_out, OP5);
  not not_197 (not_197_out, F0);
  not not_198 (not_198_out, F1);
  not not_199 (not_199_out, F2);
  not not_200 (not_200_out, F4);
  not not_201 (not_201_out, F5);
  not not_202 (not_202_out, OP0);
  not not_203 (not_203_out, OP2);
  not not_204 (not_204_out, OP3);
  not not_205 (not_205_out, OP4);
  not not_206 (not_206_out, OP5);
  not not_207 (not_207_out, F0);
  not not_208 (not_208_out, F1);
  not not_209 (not_209_out, F2);
  not not_210 (not_210_out, F4);
  not not_211 (not_211_out, F5);
  not not_212 (not_212_out, OP2);
  not not_213 (not_213_out, OP3);
  not not_214 (not_214_out, OP4);
  not not_215 (not_215_out, OP5);
  not not_216 (not_216_out, OP2);
  not not_217 (not_217_out, OP3);
  not not_218 (not_218_out, OP4);
  not not_219 (not_219_out, OP5);
  not not_220 (not_220_out, OP1);
  not not_221 (not_221_out, OP2);
  not not_222 (not_222_out, OP3);
  not not_223 (not_223_out, OP4);
  not not_224 (not_224_out, OP5);
  not not_225 (not_225_out, OP0);
  not not_226 (not_226_out, OP1);
  not not_227 (not_227_out, OP2);
  not not_228 (not_228_out, OP3);
  not not_229 (not_229_out, OP4);
  not not_230 (not_230_out, OP5);
  not not_231 (not_231_out, F0);
  not not_232 (not_232_out, F3);
  not not_233 (not_233_out, F4);
  not not_234 (not_234_out, F5);
  not not_235 (not_235_out, OP0);
  not not_236 (not_236_out, OP1);
  not not_237 (not_237_out, OP2);
  not not_238 (not_238_out, OP3);
  not not_239 (not_239_out, OP4);
  and and_1 (and_1_out, OP5, not_1_out, not_2_out, not_3_out, OP1, OP0);
  and and_2 (and_2_out, OP5, not_4_out, not_5_out, not_6_out, not_7_out, not_8_out);
  and and_3 (MemWrite, OP0, OP1, not_9_out, OP3, not_10_out, OP5);
  and and_4 (and_4_out, not_11_out, not_12_out, not_13_out, not_14_out, not_15_out, OP5);
  and and_5 (and_5_out, not_16_out, OP3, not_17_out, not_18_out);
  and and_6 (and_6_out, not_19_out, OP3, not_20_out, not_21_out);
  and and_7 (and_7_out, OP0, OP1, not_22_out, not_23_out, OP5);
  and and_8 (and_8_out, not_24_out, not_25_out, not_26_out, not_27_out, not_28_out, not_29_out, not_30_out, not_31_out, not_32_out);
  and and_9 (and_9_out, not_33_out, not_34_out, not_35_out, not_36_out, not_37_out, not_38_out, not_39_out, not_40_out, F5);
  and and_10 (and_10_out, not_41_out, not_42_out, not_43_out, not_44_out, not_45_out, not_46_out, F1, not_47_out, not_48_out, not_49_out);
  and and_11 (and_11_out, not_50_out, not_51_out, not_52_out, not_53_out, not_54_out, F1, not_55_out, not_56_out, not_57_out, not_58_out);
  and and_12 (and_12_out, not_59_out, not_60_out, not_61_out, not_62_out, not_63_out, F1, not_64_out, F3, not_65_out, F5);
  and and_13 (and_13_out, not_66_out, not_67_out, not_68_out, not_69_out, not_70_out, F0, F2, not_71_out, not_72_out, F5);
  and and_14 (and_14_out, not_73_out, not_74_out, not_75_out, not_76_out, not_77_out, OP5);
  and and_15 (and_15_out, not_78_out, OP3, not_79_out, not_80_out);
  and and_16 (and_16_out, not_81_out, OP3, not_82_out, not_83_out);
  and and_17 (and_17_out, OP0, OP1, not_84_out, not_85_out, not_86_out);
  and and_18 (SysCALL, not_87_out, not_88_out, not_89_out, not_90_out, not_91_out, not_92_out, not_93_out, not_94_out, F2, F3, not_95_out, not_96_out);
  and and_19 (and_19_out, not_97_out, not_98_out, not_99_out, not_100_out, not_101_out, OP5);
  and and_20 (and_20_out, not_102_out, not_103_out, OP3, not_104_out, not_105_out);
  and and_21 (and_21_out, not_106_out, not_107_out, OP3, not_108_out, not_109_out);
  and and_22 (and_22_out, not_110_out, OP2, not_111_out, not_112_out, not_113_out);
  and and_23 (and_23_out, OP0, OP1, not_114_out, not_115_out, OP5);
  and and_24 (and_24_out, not_116_out, not_117_out, not_118_out, not_119_out, not_120_out, not_121_out, not_122_out, not_123_out, not_124_out, not_125_out, not_126_out);
  and and_25 (and_25_out, not_127_out, not_128_out, not_129_out, not_130_out, not_131_out, not_132_out, not_133_out, not_134_out, not_135_out, not_136_out);
  and and_26 (and_26_out, not_137_out, not_138_out, not_139_out, not_140_out, not_141_out, not_142_out, not_143_out, not_144_out, not_145_out, F5);
  and and_27 (and_27_out, not_146_out, not_147_out, not_148_out, not_149_out, not_150_out, not_151_out, not_152_out, F1, not_153_out, not_154_out, not_155_out);
  and and_28 (and_28_out, not_156_out, not_157_out, not_158_out, not_159_out, not_160_out, not_161_out, F1, not_162_out, not_163_out, not_164_out, not_165_out);
  and and_29 (and_29_out, not_166_out, not_167_out, not_168_out, not_169_out, not_170_out, not_171_out, F1, not_172_out, F3, not_173_out, F5);
  and and_30 (and_30_out, not_174_out, not_175_out, not_176_out, not_177_out, not_178_out, not_179_out, F0, F2, not_180_out, not_181_out, F5);
  and and_31 (BEQ, not_182_out, not_183_out, OP2, not_184_out, not_185_out, not_186_out);
  and and_32 (BNE, OP0, not_187_out, OP2, not_188_out, not_189_out, not_190_out);
  and and_33 (JR, not_191_out, not_192_out, not_193_out, not_194_out, not_195_out, not_196_out, not_197_out, not_198_out, not_199_out, F3, not_200_out, not_201_out);
  and and_34 (and_34_out, not_202_out, not_203_out, not_204_out, not_205_out, not_206_out, not_207_out, not_208_out, not_209_out, F3, not_210_out, not_211_out);
  and and_35 (and_35_out, OP1, not_212_out, not_213_out, not_214_out, not_215_out);
  and and_36 (JAL, OP0, OP1, not_216_out, not_217_out, not_218_out, not_219_out);
  and and_37 (BGEZ, OP0, not_220_out, not_221_out, not_222_out, not_223_out, not_224_out);
  and and_38 (SV, not_225_out, not_226_out, not_227_out, not_228_out, not_229_out, not_230_out, not_231_out, F1, F2, not_232_out, not_233_out, not_234_out);
  and and_39 (LB, not_235_out, not_236_out, not_237_out, not_238_out, not_239_out, OP5);
  or or_1 (MemToReg, and_1_out, and_2_out);
  or or_2 (ALU_SRC, and_4_out, and_5_out, and_6_out, and_7_out);
  or or_3 (RegWrite, and_8_out, and_9_out, and_10_out, and_11_out, and_12_out, and_13_out, and_14_out, and_15_out, and_16_out, and_17_out);
  or or_4 (SignedExt, and_19_out, and_20_out, and_21_out, and_22_out, and_23_out);
  or or_5 (RegDst, and_24_out, and_25_out, and_26_out, and_27_out, and_28_out, and_29_out, and_30_out);
  or or_6 (JUMP, and_34_out, and_35_out);
endmodule

// ALU
module MIPS_ALU (
  input  [4:0] shamt,
  input  [31:0] X,
  input  [31:0] Y,
  input  [3:0] AluOP,
  output Equal,
  output [31:0] Result,
  output [31:0] Result_2
);

  wire [0:0] comparator_1_lt, comparator_2_lt;
  wire [31:0] adder_1_out, AND_out, divider_1_out, divider_1_rem, multiplier_1_cout, multiplier_1_out,
       NOR_out, OR_out, shifter_1_out, shifter_2_out, shifter_3_out, subtractor_1_out, XOR_out;

  assign AND_out = X & Y;  // AND_Gate AND, 32 bits wide
  assign OR_out = X | Y;  // OR_Gate OR, 32 bits wide
  Shifter #(.width(32), .shift("ll")) shifter_1 (.in(Y), .\dist (shamt), .out(shifter_1_out));
  Shifter #(.width(32), .shift("ar")) shifter_2 (.in(Y), .\dist (shamt), .out(shifter_2_out));
  Shifter #(.width(32), .shift("lr")) shifter_3 (.in(Y), .\dist (shamt), .out(shifter_3_out));
  Multiplier #(.width(32)) multiplier_1 (.a(X), .b(Y), .out(multiplier_1_out), .cout(multiplier_1_cout));  // open: cin
  Divider #(.width(32)) divider_1 (.a(X), .b(Y), .out(divider_1_out), .rem(divider_1_rem));  // open: upper
  Adder #(.width(32)) adder_1 (.a(X), .b(Y), .out(adder_1_out));  // open: cin, cout
  Subtractor #(.width(32)) subtractor_1 (.a(X), .b(Y), .out(subtractor_1_out));  // open: bin, bout
  assign XOR_out = X ^ Y;  // XOR_Gate XOR, 32 bits wide
  assign NOR_out = ~(X | Y);  // NOR_Gate NOR, 32 bits wide
  Comparator #(.width(32), .mode("twosComplement")) comparator_1 (
    .a(X), .b(Y), .eq(Equal), .lt(comparator_1_lt[0]));  // open: gt
  Comparator #(.width(32), .mode("unsigned")) comparator_2 (.a(X), .b(Y), .lt(comparator_2_lt[0]));  // open: gt, eq
  Multiplexer #(.select(4), .width(32), .disabled("Z"), .enable("false")) multiplexer_1 (
    .in0(shifter_1_out), .in1(shifter_2_out), .in2(shifter_3_out), .in3(multiplier_1_out),
    .in4(divider_1_out), .in5(adder_1_out), .in6(subtractor_1_out), .in7(AND_out), .in8(OR_out),
    .in9(XOR_out), .in10(NOR_out), .in11({{31{1'b0}}, comparator_1_lt[0]}),
    .in12({{31{1'b0}}, comparator_2_lt[0]}), .in13({32{1'b0}}), .in14({32{1'b0}}), .in15({32{1'b0}}),
    .out(Result), .sel(AluOP));
  Multiplexer #(.select(4), .width(32), .disabled("Z"), .enable("false")) multiplexer_2 (
    .in0({32{1'b0}}), .in1({32{1'b0}}), .in2({32{1'b0}}), .in3(multiplier_1_cout), .in4(divider_1_rem),
    .in5({32{1'b0}}), .in6({32{1'b0}}), .in7({32{1'b0}}), .in8({32{1'b0}}), .in9({32{1'b0}}),
    .in10({32{1'b0}}), .in11({32{1'b0}}), .in12({32{1'b0}}), .in13({32{1'b0}}), .in14({32{1'b0}}),
    .in15({32{1'b0}}), .out(Result_2), .sel(AluOP));

  // Other names for the same wires on the sheet: Result2[31:0] = Result_2; S[3:0] = AluOP

  // Notes on the sheet:
  //   不要改变此引脚区域内容，也不要改变ALU封装形式
  //   输入引脚
  //   输出引脚
endmodule

module MIPS_Regifile (
  input  [31:0] Din,
  input  Clk,
  input  WE,
  input  [4:0] R1_num,
  input  [4:0] W_num,
  input  [4:0] R2_num,
  output [31:0] R1,
  output [31:0] R2
);

  // RegisterFile registerfile_1: pin names not known; wires that end beside it: Din, Clk, WE, W_num, R1_num, R2_num, R1, R2
endmodule

module \理想流水线  (
  output RegWrite,
  output MemWrite,
  output [31:0] IF_PC,
  output [31:0] ID_PC,
  output [31:0] EX_PC,
  output [31:0] M_PC,
  output [31:0] WB_PC,
  output [31:0] RDin,
  output [31:0] MDin,
  output [31:0] LedData
);

  wire and_1_out, CLK, clock_1_out, clock_2_out, comparator_1_eq, comparator_1_lt, d_ff_2_q, EN, Go, IR1,
       IR2, IR3, JMP, JR, mips_alu_1_equal, nand_1_out, not_1_out, or_1_out, or_2_out, RST, SignedExt, W1,
       W2, W3, \单周期硬布线控制器_1_alu_src , \单周期硬布线控制器_1_beq , \单周期硬布线控制器_1_bne , \单周期硬布线控制器_1_jal ,
       \单周期硬布线控制器_1_memtoreg , \单周期硬布线控制器_1_memwrite , \单周期硬布线控制器_1_regdst , \单周期硬布线控制器_1_regwrite ,
       \单周期硬布线控制器_1_syscall , \流水线寄存器_2_out_alusrcb , \流水线寄存器_2_out_memtoreg , \流水线寄存器_2_out_memwrite ,
       \流水线寄存器_2_out_regdst , \流水线寄存器_2_out_regwrite , \流水线寄存器_2_out_syscall , \流水线寄存器_3_out_equal ,
       \流水线寄存器_3_out_memtoreg , \流水线寄存器_3_out_regdst , \流水线寄存器_3_out_regwrite , \流水线寄存器_3_out_syscall ,
       \流水线寄存器_4_out_equal , \流水线寄存器_4_out_memtoreg , \流水线寄存器_4_out_regdst , \流水线寄存器_4_out_syscall ;
  wire [3:0] \单周期硬布线控制器_1_alu_op , \流水线寄存器_2_out_aluop ;
  wire [4:0] multiplexer_1_out, multiplexer_2_out, multiplexer_6_out, \流水线寄存器_2_out_shamt ;
  wire [5:0] Func;
  wire [12:0] CNT_num;
  wire [15:0] \LoadUse次数 , \总周期数 , \插入气泡数 , \无条件分支数 , \条件分支成功数 ;
  wire [31:0] bit_extender_1_out, EX_IR, IF_IR, MEM_IR, mips_alu_1_result, mips_regifile_1_r1,
       mips_regifile_1_r2, multiplexer_3_out, multiplexer_4_out, PC_4, ram_1_data, WB_IR, \流水线寄存器_2_out_imm ,
       \流水线寄存器_2_out_r1 , \流水线寄存器_2_out_r2 , \流水线寄存器_3_out_alu , \流水线寄存器_4_out_alu , \流水线寄存器_4_out_md ;
  wire [31:6] ID_IR;

  Button \u_总复位  (.out(RST));
  Button _1 (.out(IR1));
  Button _2 (.out(IR2));
  Button _3 (.out(IR3));
  // Probe on \总周期数 
  // Probe on \总周期数 
  Button \u_继续运行  (.out(Go));
  LED #(.active("true")) led_1 (.in(W1));
  LED #(.active("true")) led_2 (.in(W2));
  LED #(.active("true")) led_3 (.in(W3));
  Hex_Digit_Display hex_digit_display_1 (.value(LedData[31:28]));  // open: dp
  // Probe on IF_PC[19:0]
  // Mips_Probe mips_probe_1: pin names not known; wires that end beside it: IF_IR
  not not_1 (not_1_out, \流水线寄存器_4_out_syscall );
  Register #(.width(32), .trigger("rising"), .Select("low")) PC (.D(PC_4), .en(EN), .Q(IF_PC), .clk(CLK), .clr(RST));
  Hex_Digit_Display hex_digit_display_2 (.value(LedData[27:24]));  // open: dp
  Hex_Digit_Display hex_digit_display_3 (.value(LedData[23:20]));  // open: dp
  // Probe on ID_PC[19:0]
  // Mips_Probe mips_probe_2: pin names not known; wires that end beside it: {ID_IR, Func}
  or or_1 (or_1_out, not_1_out, Go);
  or or_2 (or_2_out, not_1_out, \流水线寄存器_4_out_equal );
  Hex_Digit_Display hex_digit_display_4 (.value(LedData[15:12]));  // open: dp
  Hex_Digit_Display hex_digit_display_5 (.value(LedData[19:16]));  // open: dp
  D_Flip_Flop #(.trigger("falling"), .Pre_Clr_Positions("ABOVE_BELOW"), .NegatePresetClear("false"), .enable("false"), .NewFFLayout("true")) d_ff_1 (
    .clk(CLK), .D(or_2_out), .Q(EN), .preset(or_1_out));  // open: Qn, reset
  Counter #(.width(16), .max('hffff), .ongoal("wrap"), .trigger("rising"), .behavior("new")) counter_1 (
    .count(EN), .Q(\总周期数 ), .clk(CLK), .clr(RST));  // open: load, D, carry, preset, down
  Adder #(.width(32)) adder_1 (.a(IF_PC), .b(32'h4), .out(PC_4));  // open: cin, cout
  Hex_Digit_Display hex_digit_display_6 (.value(LedData[11:8]));  // open: dp
  Hex_Digit_Display hex_digit_display_7 (.value(LedData[7:4]));  // open: dp
  Clock #(.highDuration(1), .lowDuration(1)) clock_1 (.out(clock_1_out));
  // Probe on EX_PC[19:0]
  // Mips_Probe mips_probe_3: pin names not known; wires that end beside it: clock_1_out, EX_IR, CLK
  ROM #(.addrWidth(10), .dataWidth(32), .Select("high")) rom_1 (.addr(IF_PC[11:2]), .data(IF_IR));
  Hex_Digit_Display hex_digit_display_8 (.value(LedData[3:0]));  // open: dp
  \流水线寄存器  \u_流水线寄存器_1  (
    .IN_PC(IF_PC), .IN_IR(IF_IR), .OUT_PC(ID_PC), .OUT_IR({ID_IR, Func}), .EN(EN), .CLK(CLK), .RST(RST),
    .CLR(1'b0));  // open: IN_MemToReg, IN_MemWrite, IN_AluOP, IN_AluSrcB, IN_RegWrite, IN_equal, IN_R1, IN_ALU, IN_R2, IN_MD, IN_Imm, OUT_MemToReg, OUT_MemWrite, OUT_AluOP, OUT_AluSrcB, OUT_RegWrite, OUT_Syscall, OUT_equal, OUT_R1, OUT_ALU, OUT_R2, OUT_MD, OUT_Imm, In_RegDst, OUT_RegDst, IN_Bne, OUT_Bne, IN_Beq, OUT_Beq, IN_shamt, OUT_shamt, IN_offset, OUT_offset, IN_JAL, OUT_JAL, IN_WriteReg_num, OUT_WriteReg_num, IN_JMP, OUT_JMP, IN_JR, OUT_JR, In_Syscall, IN_BGEZ, OUT_BGEZ, IN_SV, OUT_SV, IN_LB, OUT_LB, IN_Rs_num, IN_Rt_num, OUT_Rs_num, OUT_Rt_num
  // Probe on \总周期数 
  // Probe on M_PC[19:0]
  // Mips_Probe mips_probe_4: pin names not known; wires that end beside it: MEM_IR
  // Mips_Probe mips_probe_5: pin names not known; wires that end beside it: {ID_IR, Func}
  // Probe on \总周期数 
  // Probe on \无条件分支数 
  // Probe on \条件分支成功数 
  // Probe on \插入气泡数 
  // Probe on \LoadUse次数 
  // Probe on IF_PC[11:0]
  // Probe on WB_PC[19:0]
  // Mips_Probe mips_probe_6: pin names not known; wires that end beside it: WB_IR
  \单周期硬布线控制器  \u_单周期硬布线控制器_1  (
    .Func(Func), .OP(ID_IR[31:26]), .ALU_OP(\单周期硬布线控制器_1_alu_op ), .MemToReg(\单周期硬布线控制器_1_memtoreg ),
    .MemWrite(\单周期硬布线控制器_1_memwrite ), .ALU_SRC(\单周期硬布线控制器_1_alu_src ), .RegWrite(\单周期硬布线控制器_1_regwrite ),
    .SysCALL(\单周期硬布线控制器_1_syscall ), .SignedExt(SignedExt), .RegDst(\单周期硬布线控制器_1_regdst ), .JR(JR),
    .JMP(JMP), .Beq(\单周期硬布线控制器_1_beq ), .JAL(\单周期硬布线控制器_1_jal ), .Bne(\单周期硬布线控制器_1_bne ));  // open: BGEZ, ERET, MFC0, MTC0, MF, SV, LB
  Multiplexer #(.select(1), .width(5), .disabled("Z"), .enable("false")) multiplexer_1 (
    .in0(ID_IR[25:21]), .in1(5'b00010), .out(multiplexer_1_out), .sel(\单周期硬布线控制器_1_syscall ));
  Multiplexer #(.select(1), .width(5), .disabled("Z"), .enable("false")) multiplexer_2 (
    .in0(ID_IR[20:16]), .in1(5'b00100), .out(multiplexer_2_out), .sel(\单周期硬布线控制器_1_syscall ));
  assign bit_extender_1_out = {{16{ID_IR[15]}}, {ID_IR[15:6], Func}};  // Bit_Extender bit_extender_1
  // Probe on ID_PC[11:0]
  // Probe on EX_PC[11:0]
  // Probe on M_PC[11:0]
  D_Flip_Flop #(.trigger("high"), .Pre_Clr_Positions("LEGACY"), .NegatePresetClear("false"), .enable("true"), .NewFFLayout("false")) d_ff_2 (.Q(d_ff_2_q));  // open: clk, D, Qn, preset, en, reset
  // Probe on 13'hc
  MIPS_Regifile mips_regifile_1 (
    .Din(RDin), .Clk(CLK), .R1(mips_regifile_1_r1), .R2(mips_regifile_1_r2), .WE(RegWrite),
    .W_num(multiplexer_6_out), .R1_num(multiplexer_1_out), .R2_num(multiplexer_2_out));
  // Probe on WB_PC[11:0]
  Comparator #(.width(13), .mode("twosComplement")) comparator_1 (
    .a(CNT_num), .b(13'hc), .eq(comparator_1_eq), .lt(comparator_1_lt));  // open: gt
  Clock #(.highDuration(1), .lowDuration(1)) clock_2 (.out(clock_2_out));
  nand nand_1 (nand_1_out, d_ff_2_q, comparator_1_eq);
  Counter #(.width(13), .max('h1fff), .ongoal("stay"), .trigger("rising"), .behavior("old")) counter_2 (
    .count(comparator_1_lt), .Q(CNT_num), .clk(clock_2_out));  // open: load, D, carry, clr, preset
  \流水线寄存器  \u_流水线寄存器_2  (
    .IN_MemToReg(\单周期硬布线控制器_1_memtoreg ), .IN_MemWrite(\单周期硬布线控制器_1_memwrite ),
    .IN_AluOP(\单周期硬布线控制器_1_alu_op ), .IN_AluSrcB(\单周期硬布线控制器_1_alu_src ),
    .IN_RegWrite(\单周期硬布线控制器_1_regwrite ), .IN_R1(mips_regifile_1_r1), .IN_R2(mips_regifile_1_r2),
    .IN_PC(ID_PC), .IN_IR({ID_IR, Func}), .IN_Imm(bit_extender_1_out),
    .OUT_MemToReg(\流水线寄存器_2_out_memtoreg ), .OUT_MemWrite(\流水线寄存器_2_out_memwrite ),
    .OUT_AluOP(\流水线寄存器_2_out_aluop ), .OUT_AluSrcB(\流水线寄存器_2_out_alusrcb ),
    .OUT_RegWrite(\流水线寄存器_2_out_regwrite ), .OUT_Syscall(\流水线寄存器_2_out_syscall ), .OUT_R1(\流水线寄存器_2_out_r1 ),
    .OUT_R2(\流水线寄存器_2_out_r2 ), .OUT_PC(EX_PC), .OUT_IR(EX_IR), .OUT_Imm(\流水线寄存器_2_out_imm ), .EN(EN),
    .CLK(CLK), .RST(RST), .In_RegDst(\单周期硬布线控制器_1_regdst ), .OUT_RegDst(\流水线寄存器_2_out_regdst ),
    .IN_Bne(\单周期硬布线控制器_1_bne ), .IN_Beq(\单周期硬布线控制器_1_beq ), .IN_shamt(ID_IR[10:6]),
    .OUT_shamt(\流水线寄存器_2_out_shamt ), .IN_offset({ID_IR[25:6], Func}), .IN_JAL(\单周期硬布线控制器_1_jal ),
    .CLR(1'b0), .In_Syscall(\单周期硬布线控制器_1_syscall ));  // open: IN_equal, IN_ALU, IN_MD, OUT_equal, OUT_ALU, OUT_MD, OUT_Bne, OUT_Beq, OUT_offset, OUT_JAL, IN_WriteReg_num, OUT_WriteReg_num, IN_JMP, OUT_JMP, IN_JR, OUT_JR, IN_BGEZ, OUT_BGEZ, IN_SV, OUT_SV, IN_LB, OUT_LB, IN_Rs_num, IN_Rt_num, OUT_Rs_num, OUT_Rt_num
  assign CLK = nand_1_out ? clock_2_out : 1'bz;  // Controlled_Buffer controlled_buffer_1
  Multiplexer #(.select(1), .width(32), .disabled("Z"), .enable("false")) multiplexer_3 (
    .in0(\流水线寄存器_2_out_r2 ), .in1(\流水线寄存器_2_out_imm ), .out(multiplexer_3_out), .sel(\流水线寄存器_2_out_alusrcb ));
  Pull_Resistor #(.pull(1)) pull_resistor_1 (.node(CLK));
  Multiplexer #(.select(1), .width(32), .disabled("Z"), .enable("false")) multiplexer_4 (
    .in0(multiplexer_3_out), .in1(32'h22), .out(multiplexer_4_out), .sel(\流水线寄存器_2_out_syscall ));
  MIPS_ALU mips_alu_1 (
    .X(\流水线寄存器_2_out_r1 ), .Y(multiplexer_4_out), .AluOP(\流水线寄存器_2_out_aluop ), .Equal(mips_alu_1_equal),
    .Result(mips_alu_1_result), .shamt(\流水线寄存器_2_out_shamt ));  // open: Result_2
  \流水线寄存器  \u_流水线寄存器_3  (
    .IN_MemToReg(\流水线寄存器_2_out_memtoreg ), .IN_MemWrite(\流水线寄存器_2_out_memwrite ),
    .IN_RegWrite(\流水线寄存器_2_out_regwrite ), .IN_equal(mips_alu_1_equal), .IN_ALU(mips_alu_1_result),
    .IN_R2(\流水线寄存器_2_out_r2 ), .IN_PC(EX_PC), .IN_IR(EX_IR), .OUT_MemToReg(\流水线寄存器_3_out_memtoreg ),
    .OUT_MemWrite(MemWrite), .OUT_RegWrite(\流水线寄存器_3_out_regwrite ), .OUT_Syscall(\流水线寄存器_3_out_syscall ),
    .OUT_equal(\流水线寄存器_3_out_equal ), .OUT_ALU(\流水线寄存器_3_out_alu ), .OUT_R2(MDin), .OUT_PC(M_PC),
    .OUT_IR(MEM_IR), .EN(EN), .CLK(CLK), .RST(RST), .In_RegDst(\流水线寄存器_2_out_regdst ),
    .OUT_RegDst(\流水线寄存器_3_out_regdst ), .CLR(1'b0), .In_Syscall(\流水线寄存器_2_out_syscall ));  // open: IN_AluOP, IN_AluSrcB, IN_R1, IN_MD, IN_Imm, OUT_AluOP, OUT_AluSrcB, OUT_R1, OUT_MD, OUT_Imm, IN_Bne, OUT_Bne, IN_Beq, OUT_Beq, IN_shamt, OUT_shamt, IN_offset, OUT_offset, IN_JAL, OUT_JAL, IN_WriteReg_num, OUT_WriteReg_num, IN_JMP, OUT_JMP, IN_JR, OUT_JR, IN_BGEZ, OUT_BGEZ, IN_SV, OUT_SV, IN_LB, OUT_LB, IN_Rs_num, IN_Rt_num, OUT_Rs_num, OUT_Rt_num
  and and_1 (and_1_out, \流水线寄存器_3_out_syscall , \流水线寄存器_3_out_equal );
  Register #(.width(32), .trigger("rising"), .Select("low")) register_1 (
    .D(MDin), .en(and_1_out), .Q(LedData), .clk(CLK), .clr(RST));
  RAM #(.addrWidth(10), .dataWidth(32), .bus("separate"), .Select("high")) ram_1 (
    .addr(\流水线寄存器_3_out_alu [11:2]), .din(MDin), .data(ram_1_data), .str(MemWrite), .clk(CLK), .clr(RST));  // open: sel, ld
  \流水线寄存器  \u_流水线寄存器_4  (
    .IN_MemToReg(\流水线寄存器_3_out_memtoreg ), .IN_RegWrite(\流水线寄存器_3_out_regwrite ),
    .IN_equal(\流水线寄存器_3_out_equal ), .IN_ALU(\流水线寄存器_3_out_alu ), .IN_MD(ram_1_data), .IN_PC(M_PC),
    .IN_IR(MEM_IR), .OUT_MemToReg(\流水线寄存器_4_out_memtoreg ), .OUT_RegWrite(RegWrite),
    .OUT_Syscall(\流水线寄存器_4_out_syscall ), .OUT_equal(\流水线寄存器_4_out_equal ), .OUT_ALU(\流水线寄存器_4_out_alu ),
    .OUT_MD(\流水线寄存器_4_out_md ), .OUT_PC(WB_PC), .OUT_IR(WB_IR), .EN(EN), .CLK(CLK), .RST(RST),
    .In_RegDst(\流水线寄存器_3_out_regdst ), .OUT_RegDst(\流水线寄存器_4_out_regdst ), .CLR(1'b0),
    .In_Syscall(\流水线寄存器_3_out_syscall ));  // open: IN_MemWrite, IN_AluOP, IN_AluSrcB, IN_R1, IN_R2, IN_Imm, OUT_MemWrite, OUT_AluOP, OUT_AluSrcB, OUT_R1, OUT_R2, OUT_Imm, IN_Bne, OUT_Bne, IN_Beq, OUT_Beq, IN_shamt, OUT_shamt, IN_offset, OUT_offset, IN_JAL, OUT_JAL, IN_WriteReg_num, OUT_WriteReg_num, IN_JMP, OUT_JMP, IN_JR, OUT_JR, IN_BGEZ, OUT_BGEZ, IN_SV, OUT_SV, IN_LB, OUT_LB, IN_Rs_num, IN_Rt_num, OUT_Rs_num, OUT_Rt_num
  Multiplexer #(.select(1), .width(32), .disabled("Z"), .enable("false")) multiplexer_5 (
    .in0(\流水线寄存器_4_out_alu ), .in1(\流水线寄存器_4_out_md ), .out(RDin), .sel(\流水线寄存器_4_out_memtoreg ));
  Multiplexer #(.select(1), .width(5), .disabled("Z"), .enable("false")) multiplexer_6 (
    .in0(WB_IR[20:16]), .in1(WB_IR[15:11]), .out(multiplexer_6_out), .sel(\流水线寄存器_4_out_regdst ));

  // Other names for the same wires on the sheet: ID_IR[5:0] = Func; OP[5:0] = ID_IR[31:26]; MEM_PC[31:0] = M_PC;
  //   MEM_R2[31:0] = MDin

  // Notes on the sheet:
  //   中断源
  //   时空图监测，可删除
  //   中断等待指示
  //   数码管输出
  //   指令存储器
  //   contents of rom_1 (hex, n*v repeats v):
  //   20100000 20110000 20120000 20130000 36100000 36310001 36520002 36730003 ae100000 ae110004 ae120008
  //   ae13000c 2002000a 20110000 20120000 20130000 c
  //   指令字
  //   JMP
  //   JR
  //   OP
  //   Func
  //   MF
  //   Syscall
  //   rs
  //   rt
  //   Beq
  //   Bne
  //   MemToReg
  //   MemWrite
  //   AluOP
  //   AluSrcB
  //   RegWrite
  //   JAL
  //   RegDst
  //   控制位
  //   流水调试日志用
  //   暂停节拍，不能为0
  //   戳工具置1进入计数暂停模式，ctrl+k时钟自动运行到对应节拍暂停
  //   ctrl+k关闭时钟连续运行，将控制位置零，进入单步调试模式调试
  //   用这个时钟源需要去掉电路中的其他时钟源
  //   可计数暂停的时钟源
  //   为方便自动评测，需要输出流水线各段保存的PC值，注意是PC不是PC+4，另外ID段寄存器写入信息，Mem段内存写入信息也要输出
  //   rt
  //   rd
endmodule

module \气泡流水线  (
  output RegWrite,
  output MemWrite,
  output [31:0] IF_PC,
  output [31:0] ID_PC,
  output [31:0] EX_PC,
  output [31:0] M_PC,
  output [31:0] WB_PC,
  output [31:0] RDin,
  output [31:0] MDin,
  output [31:0] LedData
);

  wire and_1_out, and_2_out, and_3_out, CLK, clock_1_out, clock_2_out, comparator_1_eq, comparator_1_lt,
       d_ff_2_q, EN, Go, IR1, IR2, IR3, mips_alu_1_equal, multiplexer_12_out, nand_1_out, not_1_out,
       or_1_out, or_2_out, or_3_out, or_4_out, or_5_out, or_6_out, RST, W1, W2, W3, \单周期硬布线控制器_1_alu_src ,
       \单周期硬布线控制器_1_beq , \单周期硬布线控制器_1_bgez , \单周期硬布线控制器_1_bne , \单周期硬布线控制器_1_jal , \单周期硬布线控制器_1_jmp ,
       \单周期硬布线控制器_1_jr , \单周期硬布线控制器_1_lb , \单周期硬布线控制器_1_memtoreg , \单周期硬布线控制器_1_memwrite ,
       \单周期硬布线控制器_1_regdst , \单周期硬布线控制器_1_regwrite , \单周期硬布线控制器_1_signedext , \单周期硬布线控制器_1_sv ,
       \单周期硬布线控制器_1_syscall , \数据相关处理_1_datahazard , \流水线寄存器_2_out_alusrcb , \流水线寄存器_2_out_beq ,
       \流水线寄存器_2_out_bgez , \流水线寄存器_2_out_bne , \流水线寄存器_2_out_jal , \流水线寄存器_2_out_jmp , \流水线寄存器_2_out_jr ,
       \流水线寄存器_2_out_lb , \流水线寄存器_2_out_memtoreg , \流水线寄存器_2_out_memwrite , \流水线寄存器_2_out_regdst ,
       \流水线寄存器_2_out_regwrite , \流水线寄存器_2_out_sv , \流水线寄存器_2_out_syscall , \流水线寄存器_3_out_equal ,
       \流水线寄存器_3_out_jal , \流水线寄存器_3_out_lb , \流水线寄存器_3_out_memtoreg , \流水线寄存器_3_out_regdst ,
       \流水线寄存器_3_out_regwrite , \流水线寄存器_3_out_syscall , \流水线寄存器_4_out_equal , \流水线寄存器_4_out_jal ,
       \流水线寄存器_4_out_memtoreg , \流水线寄存器_4_out_regdst , \流水线寄存器_4_out_syscall ;
  wire [3:0] \单周期硬布线控制器_1_alu_op , \流水线寄存器_2_out_aluop ;
  wire [4:0] multiplexer_4_out, multiplexer_5_out, multiplexer_6_out, multiplexer_8_out, multiplexer_11_out,
       multiplexer_15_out, multiplexer_17_out, \流水线寄存器_2_out_shamt , \流水线寄存器_2_out_writereg_num ,
       \流水线寄存器_3_out_writereg_num ;
  wire [5:0] Func;
  wire [7:0] bitselector_1_out;
  wire [12:0] CNT_num;
  wire [15:0] \LoadUse次数 , \总周期数 , \插入气泡数 , \无条件分支数 , \条件分支成功数 ;
  wire [27:2] J_ADDR;
  wire [31:0] adder_2_out, adder_4_out, bit_extender_1_out, bit_extender_2_out, bit_extender_3_out, BR_ADDR,
       EX_IR, IF_IR, IF_PC_4, JR_ADDR, MEM_IR, mips_alu_1_result, mips_regifile_1_r1, mips_regifile_1_r2,
       multiplexer_1_out, multiplexer_2_out, multiplexer_3_out, multiplexer_7_out, multiplexer_9_out,
       multiplexer_10_out, multiplexer_13_out, multiplexer_14_out, ram_1_data, shifter_1_out, undriven,
       WB_IR, \流水线寄存器_2_out_imm , \流水线寄存器_2_out_r2 , \流水线寄存器_3_out_alu , \流水线寄存器_4_out_alu ,
       \流水线寄存器_4_out_md ;
  wire [31:6] ID_IR;

  Button \u_总复位  (.out(RST));
  Button _1 (.out(IR1));
  Button _2 (.out(IR2));
  Button _3 (.out(IR3));
  // Probe on \总周期数 
  // Probe on \总周期数 
  Button \u_继续运行  (.out(Go));
  LED #(.active("true")) led_1 (.in(W1));
  LED #(.active("true")) led_2 (.in(W2));
  LED #(.active("true")) led_3 (.in(W3));
  Multiplexer #(.select(1), .width(32), .disabled("Z"), .enable("false")) multiplexer_1 (
    .in0({EX_PC[31:28], J_ADDR, 2'b00}), .in1(JR_ADDR), .out(multiplexer_1_out), .sel(\流水线寄存器_2_out_jr ));
  Hex_Digit_Display hex_digit_display_1 (.value(LedData[31:28]));  // open: dp
  // Probe on IF_PC[19:0]
  // Mips_Probe mips_probe_1: pin names not known; wires that end beside it: IF_IR
  Multiplexer #(.select(1), .width(32), .disabled("Z"), .enable("false")) multiplexer_2 (
    .in0(IF_PC_4), .in1(multiplexer_1_out), .out(multiplexer_2_out), .sel(\流水线寄存器_2_out_jmp ));
  Hex_Digit_Display hex_digit_display_2 (.value(LedData[23:20]));  // open: dp
  Hex_Digit_Display hex_digit_display_3 (.value(LedData[27:24]));  // open: dp
  // Probe on ID_PC[19:0]
  // Mips_Probe mips_probe_2: pin names not known; wires that end beside it: {ID_IR, Func}
  Multiplexer #(.select(1), .width(32), .disabled("Z"), .enable("false")) multiplexer_3 (
    .in0(multiplexer_2_out), .in1(BR_ADDR), .out(multiplexer_3_out), .sel(or_6_out));
  Hex_Digit_Display hex_digit_display_4 (.value(LedData[19:16]));  // open: dp
  Hex_Digit_Display hex_digit_display_5 (.value(LedData[15:12]));  // open: dp
  \数据相关处理  \u_数据相关处理_1  (
    .Instruction({ID_IR, Func}), .EX_RegWrite(\流水线寄存器_2_out_regwrite ),
    .EX_WriteReg_num(\流水线寄存器_2_out_writereg_num ), .MEM_RegWrite(\流水线寄存器_3_out_regwrite ),
    .MEM_WriteReg_num(\流水线寄存器_3_out_writereg_num ), .DataHazard(\数据相关处理_1_datahazard ),
    .R1_num(multiplexer_4_out), .R2_num(multiplexer_5_out));
  and and_1 (and_1_out, ~\数据相关处理_1_datahazard , EN);  // AND_Gate
  Hex_Digit_Display hex_digit_display_6 (.value(LedData[11:8]));  // open: dp
  Hex_Digit_Display hex_digit_display_7 (.value(LedData[7:4]));  // open: dp
  Clock #(.highDuration(1), .lowDuration(1)) clock_1 (.out(clock_1_out));
  // Probe on EX_PC[19:0]
  // Mips_Probe mips_probe_3: pin names not known; wires that end beside it: clock_1_out, EX_IR, CLK
  not not_1 (not_1_out, \流水线寄存器_4_out_syscall );
  Register #(.width(32), .trigger("rising"), .Select("low")) PC (
    .D(multiplexer_3_out), .en(and_1_out), .Q(IF_PC), .clk(CLK), .clr(RST));
  Hex_Digit_Display hex_digit_display_8 (.value(LedData[3:0]));  // open: dp
  or or_1 (or_1_out, not_1_out, Go);
  or or_2 (or_2_out, not_1_out, \流水线寄存器_4_out_equal );
  // Probe on \总周期数 
  // Probe on M_PC[19:0]
  // Mips_Probe mips_probe_4: pin names not known; wires that end beside it: MEM_IR
  D_Flip_Flop #(.trigger("falling"), .Pre_Clr_Positions("ABOVE_BELOW"), .NegatePresetClear("false"), .enable("false"), .NewFFLayout("true")) d_ff_1 (
    .clk(CLK), .D(or_2_out), .Q(EN), .preset(or_1_out));  // open: Qn, reset
  Counter #(.width(16), .max('hffff), .ongoal("wrap"), .trigger("rising"), .behavior("new")) counter_1 (
    .count(EN), .Q(\总周期数 ), .clk(CLK), .clr(RST));  // open: load, D, carry, preset, down
  Adder #(.width(32)) adder_1 (.a(IF_PC), .b(32'h4), .out(IF_PC_4));  // open: cin, cout
  // Probe on \总周期数 
  // Probe on \无条件分支数 
  // Probe on \条件分支成功数 
  // Probe on \插入气泡数 
  // Probe on \LoadUse次数 
  ROM #(.addrWidth(10), .dataWidth(32), .Select("high")) rom_1 (.addr(IF_PC[11:2]), .data(IF_IR));
  // Probe on IF_PC[11:0]
  // Probe on WB_PC[19:0]
  // Mips_Probe mips_probe_5: pin names not known; wires that end beside it: WB_IR
  \流水线寄存器  \u_流水线寄存器_1  (
    .IN_PC(IF_PC), .IN_IR(IF_IR), .OUT_PC(ID_PC), .OUT_IR({ID_IR, Func}), .EN(and_1_out), .CLK(CLK),
    .RST(RST), .CLR(or_5_out));  // open: IN_MemToReg, IN_MemWrite, IN_AluOP, IN_AluSrcB, IN_RegWrite, IN_equal, IN_R1, IN_ALU, IN_R2, IN_MD, IN_Imm, OUT_MemToReg, OUT_MemWrite, OUT_AluOP, OUT_AluSrcB, OUT_RegWrite, OUT_Syscall, OUT_equal, OUT_R1, OUT_ALU, OUT_R2, OUT_MD, OUT_Imm, In_RegDst, OUT_RegDst, IN_Bne, OUT_Bne, IN_Beq, OUT_Beq, IN_shamt, OUT_shamt, IN_offset, OUT_offset, IN_JAL, OUT_JAL, IN_WriteReg_num, OUT_WriteReg_num, IN_JMP, OUT_JMP, IN_JR, OUT_JR, In_Syscall, IN_BGEZ, OUT_BGEZ, IN_SV, OUT_SV, IN_LB, OUT_LB, IN_Rs_num, IN_Rt_num, OUT_Rs_num, OUT_Rt_num
  // Probe on ID_PC[11:0]
  // Probe on EX_PC[11:0]
  // Mips_Probe mips_probe_6: pin names not known
  // Probe on M_PC[11:0]
  D_Flip_Flop #(.trigger("high"), .Pre_Clr_Positions("LEGACY"), .NegatePresetClear("false"), .enable("true"), .NewFFLayout("false")) d_ff_2 (.Q(d_ff_2_q));  // open: clk, D, Qn, preset, en, reset
  // Probe on 13'hc
  // Probe on WB_PC[11:0]
  Comparator #(.width(13), .mode("twosComplement")) comparator_1 (
    .a(CNT_num), .b(13'hc), .eq(comparator_1_eq), .lt(comparator_1_lt));  // open: gt
  Clock #(.highDuration(1), .lowDuration(1)) clock_2 (.out(clock_2_out));
  \单周期硬布线控制器  \u_单周期硬布线控制器_1  (
    .Func(Func), .OP(ID_IR[31:26]), .ALU_OP(\单周期硬布线控制器_1_alu_op ), .MemToReg(\单周期硬布线控制器_1_memtoreg ),
    .MemWrite(\单周期硬布线控制器_1_memwrite ), .ALU_SRC(\单周期硬布线控制器_1_alu_src ), .RegWrite(\单周期硬布线控制器_1_regwrite ),
    .SysCALL(\单周期硬布线控制器_1_syscall ), .SignedExt(\单周期硬布线控制器_1_signedext ), .RegDst(\单周期硬布线控制器_1_regdst ),
    .JR(\单周期硬布线控制器_1_jr ), .JMP(\单周期硬布线控制器_1_jmp ), .Beq(\单周期硬布线控制器_1_beq ), .JAL(\单周期硬布线控制器_1_jal ),
    .Bne(\单周期硬布线控制器_1_bne ), .BGEZ(\单周期硬布线控制器_1_bgez ), .SV(\单周期硬布线控制器_1_sv ), .LB(\单周期硬布线控制器_1_lb ));  // open: ERET, MFC0, MTC0, MF
  Multiplexer #(.select(1), .width(5), .disabled("Z"), .enable("false")) multiplexer_4 (
    .in0(ID_IR[25:21]), .in1(5'b00010), .out(multiplexer_4_out), .sel(\单周期硬布线控制器_1_syscall ));
  Multiplexer #(.select(1), .width(5), .disabled("Z"), .enable("false")) multiplexer_5 (
    .in0(ID_IR[20:16]), .in1(5'b00100), .out(multiplexer_5_out), .sel(\单周期硬布线控制器_1_syscall ));
  Multiplexer #(.select(1), .width(5), .disabled("Z"), .enable("false")) multiplexer_6 (
    .in0(ID_IR[20:16]), .in1(ID_IR[15:11]), .out(multiplexer_6_out), .sel(\单周期硬布线控制器_1_regdst ));
  assign bit_extender_1_out = {{16{1'b0}}, {ID_IR[15:6], Func}};  // Bit_Extender bit_extender_1
  assign bit_extender_2_out = {{16{ID_IR[15]}}, {ID_IR[15:6], Func}};  // Bit_Extender bit_extender_2
  nand nand_1 (nand_1_out, d_ff_2_q, comparator_1_eq);
  Counter #(.width(13), .max('h1fff), .ongoal("stay"), .trigger("rising"), .behavior("old")) counter_2 (
    .count(comparator_1_lt), .Q(CNT_num), .clk(clock_2_out));  // open: load, D, carry, clr, preset
  assign CLK = nand_1_out ? clock_2_out : 1'bz;  // Controlled_Buffer controlled_buffer_1
  MIPS_Regifile mips_regifile_1 (
    .Din(RDin), .Clk(CLK), .R1(mips_regifile_1_r1), .R2(mips_regifile_1_r2), .WE(RegWrite),
    .W_num(multiplexer_17_out), .R1_num(multiplexer_4_out), .R2_num(multiplexer_5_out));
  Multiplexer #(.select(1), .width(32), .disabled("Z"), .enable("false")) multiplexer_7 (
    .in0(bit_extender_1_out), .in1(bit_extender_2_out), .out(multiplexer_7_out), .sel(\单周期硬布线控制器_1_signedext ));
  Multiplexer #(.select(1), .width(5), .disabled("Z"), .enable("false")) multiplexer_8 (
    .in0(multiplexer_6_out), .in1({5{1'b1}}), .out(multiplexer_8_out), .sel(\单周期硬布线控制器_1_jal ));
  Pull_Resistor #(.pull(1)) pull_resistor_1 (.node(CLK));
  or or_3 (or_3_out, \数据相关处理_1_datahazard , or_5_out);
  or or_4 (or_4_out, \流水线寄存器_2_out_jr , \流水线寄存器_2_out_jmp );
  \流水线寄存器  \u_流水线寄存器_2  (
    .IN_MemToReg(\单周期硬布线控制器_1_memtoreg ), .IN_MemWrite(\单周期硬布线控制器_1_memwrite ),
    .IN_AluOP(\单周期硬布线控制器_1_alu_op ), .IN_AluSrcB(\单周期硬布线控制器_1_alu_src ),
    .IN_RegWrite(\单周期硬布线控制器_1_regwrite ), .IN_R1(mips_regifile_1_r1), .IN_R2(mips_regifile_1_r2),
    .IN_PC(ID_PC), .IN_IR({ID_IR, Func}), .IN_Imm(multiplexer_7_out), .OUT_MemToReg(\流水线寄存器_2_out_memtoreg ),
    .OUT_MemWrite(\流水线寄存器_2_out_memwrite ), .OUT_AluOP(\流水线寄存器_2_out_aluop ),
    .OUT_AluSrcB(\流水线寄存器_2_out_alusrcb ), .OUT_RegWrite(\流水线寄存器_2_out_regwrite ),
    .OUT_Syscall(\流水线寄存器_2_out_syscall ), .OUT_R1(JR_ADDR), .OUT_R2(\流水线寄存器_2_out_r2 ), .OUT_PC(EX_PC),
    .OUT_IR(EX_IR), .OUT_Imm(\流水线寄存器_2_out_imm ), .EN(EN), .CLK(CLK), .RST(RST),
    .In_RegDst(\单周期硬布线控制器_1_regdst ), .OUT_RegDst(\流水线寄存器_2_out_regdst ), .IN_Bne(\单周期硬布线控制器_1_bne ),
    .OUT_Bne(\流水线寄存器_2_out_bne ), .IN_Beq(\单周期硬布线控制器_1_beq ), .OUT_Beq(\流水线寄存器_2_out_beq ),
    .IN_shamt(ID_IR[10:6]), .OUT_shamt(\流水线寄存器_2_out_shamt ), .IN_offset({ID_IR[25:6], Func}),
    .OUT_offset(J_ADDR), .IN_JAL(\单周期硬布线控制器_1_jal ), .OUT_JAL(\流水线寄存器_2_out_jal ), .CLR(or_3_out),
    .IN_WriteReg_num(multiplexer_8_out), .OUT_WriteReg_num(\流水线寄存器_2_out_writereg_num ),
    .IN_JMP(\单周期硬布线控制器_1_jmp ), .OUT_JMP(\流水线寄存器_2_out_jmp ), .IN_JR(\单周期硬布线控制器_1_jr ),
    .OUT_JR(\流水线寄存器_2_out_jr ), .In_Syscall(\单周期硬布线控制器_1_syscall ), .IN_BGEZ(\单周期硬布线控制器_1_bgez ),
    .OUT_BGEZ(\流水线寄存器_2_out_bgez ), .IN_SV(\单周期硬布线控制器_1_sv ), .OUT_SV(\流水线寄存器_2_out_sv ),
    .IN_LB(\单周期硬布线控制器_1_lb ), .OUT_LB(\流水线寄存器_2_out_lb ));  // open: IN_equal, IN_ALU, IN_MD, OUT_equal, OUT_ALU, OUT_MD, IN_Rs_num, IN_Rt_num, OUT_Rs_num, OUT_Rt_num
  and and_2 (and_2_out, ~JR_ADDR[31], \流水线寄存器_2_out_bgez );  // AND_Gate
  Multiplexer #(.select(1), .width(32), .disabled("Z"), .enable("false")) multiplexer_9 (
    .in0(\流水线寄存器_2_out_r2 ), .in1(\流水线寄存器_2_out_imm ), .out(multiplexer_9_out), .sel(\流水线寄存器_2_out_alusrcb ));
  Shifter #(.width(32), .shift("ll")) shifter_1 (.in(\流水线寄存器_2_out_imm ), .\dist (5'b00010), .out(shifter_1_out));
  Multiplexer #(.select(1), .width(32), .disabled("Z"), .enable("false")) multiplexer_10 (
    .in0(multiplexer_9_out), .in1(32'h22), .out(multiplexer_10_out), .sel(\流水线寄存器_2_out_syscall ));
  Multiplexer #(.select(1), .width(5), .disabled("Z"), .enable("false")) multiplexer_11 (
    .in0(\流水线寄存器_2_out_shamt ), .in1(JR_ADDR[4:0]), .out(multiplexer_11_out), .sel(\流水线寄存器_2_out_sv ));
  or or_5 (or_5_out, or_4_out, or_6_out);
  Adder #(.width(32)) adder_2 (.a(EX_PC), .b(32'h4), .out(adder_2_out));  // open: cin, cout
  Multiplexer #(.select(1), .width(1), .disabled("Z"), .enable("false")) multiplexer_12 (
    .in0(\流水线寄存器_2_out_bne ), .in1(\流水线寄存器_2_out_beq ), .out(multiplexer_12_out), .sel(mips_alu_1_equal));
  MIPS_ALU mips_alu_1 (
    .X(JR_ADDR), .Y(multiplexer_10_out), .AluOP(\流水线寄存器_2_out_aluop ), .Equal(mips_alu_1_equal),
    .Result(mips_alu_1_result), .shamt(multiplexer_11_out));  // open: Result_2
  or or_6 (or_6_out, and_2_out, multiplexer_12_out);
  Adder #(.width(32)) adder_3 (.a(shifter_1_out), .b(adder_2_out), .out(BR_ADDR));  // open: cin, cout
  \流水线寄存器  \u_流水线寄存器_3  (
    .IN_MemToReg(\流水线寄存器_2_out_memtoreg ), .IN_MemWrite(\流水线寄存器_2_out_memwrite ),
    .IN_RegWrite(\流水线寄存器_2_out_regwrite ), .IN_equal(mips_alu_1_equal), .IN_R1(undriven),
    .IN_ALU(mips_alu_1_result), .IN_R2(\流水线寄存器_2_out_r2 ), .IN_PC(EX_PC), .IN_IR(EX_IR),
    .OUT_MemToReg(\流水线寄存器_3_out_memtoreg ), .OUT_MemWrite(MemWrite), .OUT_RegWrite(\流水线寄存器_3_out_regwrite ),
    .OUT_Syscall(\流水线寄存器_3_out_syscall ), .OUT_equal(\流水线寄存器_3_out_equal ), .OUT_ALU(\流水线寄存器_3_out_alu ),
    .OUT_R2(MDin), .OUT_PC(M_PC), .OUT_IR(MEM_IR), .EN(EN), .CLK(CLK), .RST(RST),
    .In_RegDst(\流水线寄存器_2_out_regdst ), .OUT_RegDst(\流水线寄存器_3_out_regdst ), .IN_JAL(\流水线寄存器_2_out_jal ),
    .OUT_JAL(\流水线寄存器_3_out_jal ), .CLR(1'b0), .IN_WriteReg_num(\流水线寄存器_2_out_writereg_num ),
    .OUT_WriteReg_num(\流水线寄存器_3_out_writereg_num ), .In_Syscall(\流水线寄存器_2_out_syscall ),
    .IN_LB(\流水线寄存器_2_out_lb ), .OUT_LB(\流水线寄存器_3_out_lb ));  // open: IN_AluOP, IN_AluSrcB, IN_MD, IN_Imm, OUT_AluOP, OUT_AluSrcB, OUT_R1, OUT_MD, OUT_Imm, IN_Bne, OUT_Bne, IN_Beq, OUT_Beq, IN_shamt, OUT_shamt, IN_offset, OUT_offset, IN_JMP, OUT_JMP, IN_JR, OUT_JR, IN_BGEZ, OUT_BGEZ, IN_SV, OUT_SV, IN_Rs_num, IN_Rt_num, OUT_Rs_num, OUT_Rt_num
  and and_3 (and_3_out, \流水线寄存器_3_out_syscall , \流水线寄存器_3_out_equal );
  BitSelector #(.width(32), .group(8)) bitselector_1 (
    .in(ram_1_data), .out(bitselector_1_out), .sel(\流水线寄存器_3_out_alu [1:0]));
  Register #(.width(32), .trigger("rising"), .Select("low")) register_1 (
    .D(MDin), .en(and_3_out), .Q(LedData), .clk(CLK), .clr(RST));
  assign bit_extender_3_out = {{24{bitselector_1_out[7]}}, bitselector_1_out};  // Bit_Extender bit_extender_3
  RAM #(.addrWidth(10), .dataWidth(32), .bus("separate"), .Select("high")) ram_1 (
    .addr(\流水线寄存器_3_out_alu [11:2]), .din(MDin), .data(ram_1_data), .str(MemWrite), .clk(CLK), .clr(RST));  // open: sel, ld
  Multiplexer #(.select(1), .width(32), .disabled("Z"), .enable("false")) multiplexer_13 (
    .in0(ram_1_data), .in1(bit_extender_3_out), .out(multiplexer_13_out), .sel(\流水线寄存器_3_out_lb ));
  \流水线寄存器  \u_流水线寄存器_4  (
    .IN_MemToReg(\流水线寄存器_3_out_memtoreg ), .IN_RegWrite(\流水线寄存器_3_out_regwrite ),
    .IN_equal(\流水线寄存器_3_out_equal ), .IN_ALU(\流水线寄存器_3_out_alu ), .IN_MD(multiplexer_13_out), .IN_PC(M_PC),
    .IN_IR(MEM_IR), .OUT_MemToReg(\流水线寄存器_4_out_memtoreg ), .OUT_RegWrite(RegWrite),
    .OUT_Syscall(\流水线寄存器_4_out_syscall ), .OUT_equal(\流水线寄存器_4_out_equal ), .OUT_ALU(\流水线寄存器_4_out_alu ),
    .OUT_MD(\流水线寄存器_4_out_md ), .OUT_PC(WB_PC), .OUT_IR(WB_IR), .EN(EN), .CLK(CLK), .RST(RST),
    .In_RegDst(\流水线寄存器_3_out_regdst ), .OUT_RegDst(\流水线寄存器_4_out_regdst ), .IN_JAL(\流水线寄存器_3_out_jal ),
    .OUT_JAL(\流水线寄存器_4_out_jal ), .CLR(1'b0), .IN_WriteReg_num(\流水线寄存器_3_out_writereg_num ),
    .In_Syscall(\流水线寄存器_3_out_syscall ));  // open: IN_MemWrite, IN_AluOP, IN_AluSrcB, IN_R1, IN_R2, IN_Imm, OUT_MemWrite, OUT_AluOP, OUT_AluSrcB, OUT_R1, OUT_R2, OUT_Imm, IN_Bne, OUT_Bne, IN_Beq, OUT_Beq, IN_shamt, OUT_shamt, IN_offset, OUT_offset, OUT_WriteReg_num, IN_JMP, OUT_JMP, IN_JR, OUT_JR, IN_BGEZ, OUT_BGEZ, IN_SV, OUT_SV, IN_LB, OUT_LB, IN_Rs_num, IN_Rt_num, OUT_Rs_num, OUT_Rt_num
  Multiplexer #(.select(1), .width(32), .disabled("Z"), .enable("false")) multiplexer_14 (
    .in0(\流水线寄存器_4_out_alu ), .in1(\流水线寄存器_4_out_md ), .out(multiplexer_14_out), .sel(\流水线寄存器_4_out_memtoreg ));
  Multiplexer #(.select(1), .width(5), .disabled("Z"), .enable("false")) multiplexer_15 (
    .in0(WB_IR[20:16]), .in1(WB_IR[15:11]), .out(multiplexer_15_out), .sel(\流水线寄存器_4_out_regdst ));
  Multiplexer #(.select(1), .width(32), .disabled("Z"), .enable("false")) multiplexer_16 (
    .in0(multiplexer_14_out), .in1(adder_4_out), .out(RDin), .sel(\流水线寄存器_4_out_jal ));
  Multiplexer #(.select(1), .width(5), .disabled("Z"), .enable("false")) multiplexer_17 (
    .in0(multiplexer_15_out), .in1({5{1'b1}}), .out(multiplexer_17_out), .sel(\流水线寄存器_4_out_jal ));
  Adder #(.width(32)) adder_4 (.a(32'h4), .b(WB_PC), .out(adder_4_out));  // open: cin, cout

  // Other names for the same wires on the sheet: ID_IR[5:0] = Func; OP[5:0] = ID_IR[31:26];
  //   J_ADDR[31:28] = EX_PC[31:28]; MEM_PC[31:0] = M_PC; MEM_R2[31:0] = MDin

  // Notes on the sheet:
  //   中断源
  //   时空图监测，可删除
  //   中断等待指示
  //   数码管输出
  //   指令存储器
  //   contents of rom_1 (hex, n*v repeats v):
  //   20110001 8000c05 20110001 20120002 20130003 8000c09 20110001 20120002 20130003 8000c0d 20110001
  //   20120002 20130003 8000c11 20110001 20120002 20130003 c000cb8 20100001 20110001 118fc0 112020
  //   20020022 c 118882 12200001 8000c15 112020 20020022 c 20110001 118880 112020 20020022 c 12200001
  //   8000c1f 20110001 118fc0 112020 20020022 c 1188c3 112020 20020022 c 118903 112020 20020022 c 118903
  //   112020 20020022 c 118903 112020 20020022 c 118903 112020 20020022 c 118903 112020 20020022 c 118903
  //   112020 20020022 c 118903 112020 20020022 c 20100001 109fc0 139fc3 8021 2012000c 24160003 26100001
  //   3210000f 20080008 20090001 139900 2709825 132020 20020022 c 1094022 1500fff9 22100001 2018000f
  //   2188024 108700 20080008 20090001 139902 2709825 132021 20020022 c 1094022 1500fff9 108702 2c9b022
  //   12c00001 8000c50 4020 1084027 84400 3508ffff 82021 20020022 c 2010ffff 20110000 ae300000 22100001
  //   22310004 ae300000 22100001 22310004 ae300000 22100001 22310004 ae300000 22100001 22310004 ae300000
  //   22100001 22310004 ae300000 22100001 22310004 ae300000 22100001 22310004 ae300000 22100001 22310004
  //   ae300000 22100001 22310004 ae300000 22100001 22310004 ae300000 22100001 22310004 ae300000 22100001
  //   22310004 ae300000 22100001 22310004 ae300000 22100001 22310004 ae300000 22100001 22310004 ae300000
  //   22100001 22310004 22100001 8020 2011003c 8e130000 8e340000 274402a 11000002 ae330000 ae140000
  //   2231fffc 1611fff8 102020 20020022 c 22100004 2011003c 1611fff2 20020032 c 20100000 22100001 102020
  //   20020022 c 22100002 102020 20020022 c 22100003 102020 20020022 c 22100004 102020 20020022 c 22100005
  //   102020 20020022 c 22100006 102020 20020022 c 22100007 102020 20020022 c 22100008 102020 20020022
  //   20020022 c 3e00008
  //   控制位
  //   指令字
  //   流水调试日志用
  //   暂停节拍，不能为0
  //   JMP
  //   JR
  //   SignedExt
  //   OP
  //   Func
  //   Syscall
  //   rs
  //   rt
  //   rd
  //   戳工具置1进入计数暂停模式，ctrl+k时钟自动运行到对应节拍暂停
  //   ctrl+k关闭时钟连续运行，将控制位置零，进入单步调试模式调试
  //   BGEZ
  //   Beq
  //   Bne
  //   MemToReg
  //   MemWrite
  //   AluOP
  //   AluSrcB
  //   RegWrite
  //   JAL
  //   RegDst
  //   可计数暂停的时钟源
  //   为方便自动评测，需要输出流水线各段保存的PC值，注意是PC不是PC+4，另外ID段寄存器写入信息，Mem段内存写入信息也要输出
  //   rt
  //   rd
  //   rd
endmodule
module \重定向流水线  (
  output RegWrite,
  output MemWrite,
  output [31:0] IF_PC,
  output [31:0] ID_PC,
  output [31:0] EX_PC,
  output [31:0] M_PC,
  output [31:0] WB_PC,
  output [31:0] RDin,
  output [31:0] MDin,
  output [31:0] LedData
);

  wire and_2_out, and_4_out, btb_1_predictjump, CLK, clock_1_out, clock_2_out, comparator_1_eq,
       comparator_1_lt, d_ff_2_q, EN, EX_Beq, EX_BGEZ, EX_Bne, EX_Branch, EX_BranchTaken, EX_JAL, EX_JMP,
       EX_JR, EX_PredictErr, Go, ID_IF_EN, IR1, IR2, IR3, mips_alu_1_equal, multiplexer_14_out, nand_1_out,
       not_1_out, or_2_out, or_3_out, or_4_out, or_5_out, or_7_out, register_1_q, register_2_q, RST, W1, W2,
       W3, xor_1_out, \单周期硬布线控制器_1_alu_src , \单周期硬布线控制器_1_beq , \单周期硬布线控制器_1_bgez , \单周期硬布线控制器_1_bne ,
       \单周期硬布线控制器_1_jal , \单周期硬布线控制器_1_jmp , \单周期硬布线控制器_1_jr , \单周期硬布线控制器_1_lb , \单周期硬布线控制器_1_memtoreg ,
       \单周期硬布线控制器_1_memwrite , \单周期硬布线控制器_1_regdst , \单周期硬布线控制器_1_regwrite , \单周期硬布线控制器_1_signedext ,
       \单周期硬布线控制器_1_sv , \单周期硬布线控制器_1_syscall , \流水线寄存器_2_p36 , \流水线寄存器_2_p37 , \流水线寄存器_2_p38 ,
       \流水线寄存器_2_p40 , \流水线寄存器_2_p41 , \流水线寄存器_2_p43 , \流水线寄存器_2_p44 , \流水线寄存器_2_p45 , \流水线寄存器_3_out_equal ,
       \流水线寄存器_3_out_jal , \流水线寄存器_3_out_lb , \流水线寄存器_3_out_memtoreg , \流水线寄存器_3_out_regdst ,
       \流水线寄存器_3_out_regwrite , \流水线寄存器_3_out_syscall , \流水线寄存器_4_out_equal , \流水线寄存器_4_out_jal ,
       \流水线寄存器_4_out_memtoreg , \流水线寄存器_4_out_regdst , \流水线寄存器_4_out_syscall , \重定向逻辑_1_load_use ;
  wire [3:0] \单周期硬布线控制器_1_alu_op , \流水线寄存器_2_p39 ;
  wire [4:0] multiplexer_6_out, multiplexer_7_out, multiplexer_8_out, multiplexer_10_out, multiplexer_13_out,
       multiplexer_17_out, multiplexer_19_out, \流水线寄存器_2_p46 , \流水线寄存器_2_p47 , \流水线寄存器_2_p50 ,
       \流水线寄存器_2_p53 , \流水线寄存器_3_out_writereg_num , \流水线寄存器_4_out_writereg_num ;
  wire [5:0] Func;
  wire [7:0] bitselector_1_out;
  wire [12:0] CNT_num;
  wire [15:0] \LoadUse次数 , \总周期数 , \插入气泡数 , \无条件分支数 , \条件分支成功数 ;
  wire [27:2] J_ADDR;
  wire [31:0] adder_4_out, B_ADDR, bit_extender_1_out, bit_extender_2_out, bit_extender_3_out, BR_ADDR,
       btb_1_jumpaddr, EX_IR, EX_PC_4, IF_IR, IF_PC_4, JR_ADDR, MEM_IR, mips_alu_1_result,
       mips_regifile_1_r1, mips_regifile_1_r2, multiplexer_1_out, multiplexer_3_out, multiplexer_4_out,
       multiplexer_5_out, multiplexer_9_out, multiplexer_11_out, multiplexer_12_out, multiplexer_15_out,
       multiplexer_16_out, ram_1_data, shifter_1_out, undriven, WB_IR, \流水线寄存器_2_p48 , \流水线寄存器_2_p49 ,
       \流水线寄存器_2_p52 , \流水线寄存器_3_out_alu , \流水线寄存器_4_out_alu , \流水线寄存器_4_out_md , \重定向逻辑_1_rt_f ;
  wire [31:6] ID_IR;

  Button \u_总复位  (.out(RST));
  Button _1 (.out(IR1));
  Button _2 (.out(IR2));
  Button _3 (.out(IR3));
  // Probe on \总周期数 
  // Probe on \总周期数 
  Button \u_继续运行  (.out(Go));
  LED #(.active("true")) led_1 (.in(W1));
  LED #(.active("true")) led_2 (.in(W2));
  LED #(.active("true")) led_3 (.in(W3));
  Hex_Digit_Display hex_digit_display_1 (.value(LedData[31:28]));  // open: dp
  // Probe on IF_PC[19:0]
  // Mips_Probe mips_probe_1: pin names not known; wires that end beside it: IF_IR
  Multiplexer #(.select(1), .width(32), .disabled("Z"), .enable("false")) multiplexer_1 (
    .in0({EX_PC[31:28], J_ADDR, 2'b00}), .in1(JR_ADDR), .out(multiplexer_1_out), .sel(EX_JR));
  Hex_Digit_Display hex_digit_display_2 (.value(LedData[23:20]));  // open: dp
  Hex_Digit_Display hex_digit_display_3 (.value(LedData[27:24]));  // open: dp
  // Probe on ID_PC[19:0]
  // Mips_Probe mips_probe_2: pin names not known; wires that end beside it: {ID_IR, Func}
  Multiplexer #(.select(1), .width(32), .disabled("Z"), .enable("false")) multiplexer_2 (
    .in0(BR_ADDR), .in1(multiplexer_1_out), .out(B_ADDR), .sel(EX_JMP));
  Multiplexer #(.select(1), .width(32), .disabled("Z"), .enable("false")) multiplexer_3 (
    .in0(EX_PC_4), .in1(B_ADDR), .out(multiplexer_3_out), .sel(EX_BranchTaken));
  Hex_Digit_Display hex_digit_display_4 (.value(LedData[19:16]));  // open: dp
  Hex_Digit_Display hex_digit_display_5 (.value(LedData[15:12]));  // open: dp
  \重定向逻辑  \u_重定向逻辑_1  (
    .EX_IR(EX_IR), .WB_RegWrite(RegWrite), .Rs_num(\流水线寄存器_2_p46 ),
    .WB_WriteReg_num(\流水线寄存器_4_out_writereg_num ), .MEM_RegWrite(\流水线寄存器_3_out_regwrite ),
    .MEM_WriteReg_num(\流水线寄存器_3_out_writereg_num ), .Rt_num(\流水线寄存器_2_p47 ), .Rs(\流水线寄存器_2_p48 ),
    .WB_RDin(RDin), .MEM_ALU(\流水线寄存器_3_out_alu ), .Rt(\流水线寄存器_2_p49 ), .Rs_F(JR_ADDR), .Rt_F(\重定向逻辑_1_rt_f ),
    .ID_IR({ID_IR, Func}), .Load_Use(\重定向逻辑_1_load_use ));
  Multiplexer #(.select(1), .width(32), .disabled("Z"), .enable("false")) multiplexer_4 (
    .in0(multiplexer_5_out), .in1(multiplexer_3_out), .out(multiplexer_4_out), .sel(EX_PredictErr));
  and and_1 (ID_IF_EN, ~\重定向逻辑_1_load_use , EN);  // AND_Gate
  or or_1 (EX_Branch, EX_JMP, EX_JR, EX_JAL, EX_Beq, EX_Bne, EX_BGEZ);
  Hex_Digit_Display hex_digit_display_6 (.value(LedData[11:8]));  // open: dp
  Hex_Digit_Display hex_digit_display_7 (.value(LedData[7:4]));  // open: dp
  Clock #(.highDuration(1), .lowDuration(1)) clock_1 (.out(clock_1_out));
  // Probe on EX_PC[19:0]
  // Mips_Probe mips_probe_3: pin names not known; wires that end beside it: clock_1_out, EX_IR, CLK
  not not_1 (not_1_out, \流水线寄存器_4_out_syscall );
  Register #(.width(32), .trigger("rising"), .Select("low")) PC (
    .D(multiplexer_4_out), .en(ID_IF_EN), .Q(IF_PC), .clk(CLK), .clr(RST));
  Hex_Digit_Display hex_digit_display_8 (.value(LedData[3:0]));  // open: dp
  or or_2 (or_2_out, not_1_out, Go);
  or or_3 (or_3_out, not_1_out, \流水线寄存器_4_out_equal );
  // Probe on \总周期数 
  // Probe on M_PC[19:0]
  // Mips_Probe mips_probe_4: pin names not known; wires that end beside it: MEM_IR
  D_Flip_Flop #(.trigger("falling"), .Pre_Clr_Positions("ABOVE_BELOW"), .NegatePresetClear("false"), .enable("false"), .NewFFLayout("true")) d_ff_1 (
    .clk(CLK), .D(or_3_out), .Q(EN), .preset(or_2_out));  // open: Qn, reset
  Counter #(.width(16), .max('hffff), .ongoal("wrap"), .trigger("rising"), .behavior("new")) counter_1 (
    .count(EN), .Q(\总周期数 ), .clk(CLK), .clr(RST));  // open: load, D, carry, preset, down
  Adder #(.width(32)) adder_1 (.a(IF_PC), .b(32'h4), .out(IF_PC_4));  // open: cin, cout
  BTB btb_1 (
    .CLK(CLK), .EX_PC(EX_PC), .EX_Branch(EX_Branch), .EX_BranchAddr(B_ADDR), .EX_BranchTaken(EX_BranchTaken),
    .PC(IF_PC), .PredictJump(btb_1_predictjump), .JumpAddr(btb_1_jumpaddr));
  // Probe on \总周期数 
  // Probe on \无条件分支数 
  // Probe on \条件分支成功数 
  // Probe on \插入气泡数 
  // Probe on \LoadUse次数 
  ROM #(.addrWidth(10), .dataWidth(32), .Select("high")) rom_1 (.addr(IF_PC[11:2]), .data(IF_IR));
  Multiplexer #(.select(1), .width(32), .disabled("Z"), .enable("false")) multiplexer_5 (
    .in0(IF_PC_4), .in1(btb_1_jumpaddr), .out(multiplexer_5_out), .sel(btb_1_predictjump));
  // Probe on IF_PC[11:0]
  // Probe on WB_PC[19:0]
  // Mips_Probe mips_probe_5: pin names not known; wires that end beside it: WB_IR
  \流水线寄存器  \u_流水线寄存器_1  (
    .IN_PC(IF_PC), .IN_IR(IF_IR), .OUT_PC(ID_PC), .OUT_IR({ID_IR, Func}), .EN(ID_IF_EN), .CLK(CLK),
    .RST(RST), .CLR(EX_PredictErr));  // open: IN_MemToReg, IN_MemWrite, IN_AluOP, IN_AluSrcB, IN_RegWrite, IN_equal, IN_R1, IN_ALU, IN_R2, IN_MD, IN_Imm, OUT_MemToReg, OUT_MemWrite, OUT_AluOP, OUT_AluSrcB, OUT_RegWrite, OUT_Syscall, OUT_equal, OUT_R1, OUT_ALU, OUT_R2, OUT_MD, OUT_Imm, In_RegDst, OUT_RegDst, IN_Bne, OUT_Bne, IN_Beq, OUT_Beq, IN_shamt, OUT_shamt, IN_offset, OUT_offset, IN_JAL, OUT_JAL, IN_WriteReg_num, OUT_WriteReg_num, IN_JMP, OUT_JMP, IN_JR, OUT_JR, In_Syscall, IN_BGEZ, OUT_BGEZ, IN_SV, OUT_SV, IN_LB, OUT_LB, IN_Rs_num, IN_Rt_num, OUT_Rs_num, OUT_Rt_num
  Register #(.width(1), .trigger("rising"), .Select("low")) register_1 (
    .D(btb_1_predictjump), .en(ID_IF_EN), .Q(register_1_q), .clk(CLK), .clr(RST));
  // Probe on EX_PC[11:0]
  // Probe on ID_PC[11:0]
  // Mips_Probe mips_probe_6: pin names not known
  // Probe on M_PC[11:0]
  D_Flip_Flop #(.trigger("high"), .Pre_Clr_Positions("LEGACY"), .NegatePresetClear("false"), .enable("true"), .NewFFLayout("false")) d_ff_2 (.Q(d_ff_2_q));  // open: clk, D, Qn, preset, en, reset
  // Probe on 13'h46
  // Probe on WB_PC[11:0]
  Comparator #(.width(13), .mode("twosComplement")) comparator_1 (
    .a(CNT_num), .b(13'h46), .eq(comparator_1_eq), .lt(comparator_1_lt));  // open: gt
  Clock #(.highDuration(1), .lowDuration(1)) clock_2 (.out(clock_2_out));
  \单周期硬布线控制器  \u_单周期硬布线控制器_1  (
    .Func(Func), .OP(ID_IR[31:26]), .ALU_OP(\单周期硬布线控制器_1_alu_op ), .MemToReg(\单周期硬布线控制器_1_memtoreg ),
    .MemWrite(\单周期硬布线控制器_1_memwrite ), .ALU_SRC(\单周期硬布线控制器_1_alu_src ), .RegWrite(\单周期硬布线控制器_1_regwrite ),
    .SysCALL(\单周期硬布线控制器_1_syscall ), .SignedExt(\单周期硬布线控制器_1_signedext ), .RegDst(\单周期硬布线控制器_1_regdst ),
    .JR(\单周期硬布线控制器_1_jr ), .JMP(\单周期硬布线控制器_1_jmp ), .Beq(\单周期硬布线控制器_1_beq ), .JAL(\单周期硬布线控制器_1_jal ),
    .Bne(\单周期硬布线控制器_1_bne ), .BGEZ(\单周期硬布线控制器_1_bgez ), .SV(\单周期硬布线控制器_1_sv ), .LB(\单周期硬布线控制器_1_lb ));  // open: ERET, MFC0, MTC0, MF
  Multiplexer #(.select(1), .width(5), .disabled("Z"), .enable("false")) multiplexer_6 (
    .in0(ID_IR[25:21]), .in1(5'b00010), .out(multiplexer_6_out), .sel(\单周期硬布线控制器_1_syscall ));
  Multiplexer #(.select(1), .width(5), .disabled("Z"), .enable("false")) multiplexer_7 (
    .in0(ID_IR[20:16]), .in1(5'b00100), .out(multiplexer_7_out), .sel(\单周期硬布线控制器_1_syscall ));
  Multiplexer #(.select(1), .width(5), .disabled("Z"), .enable("false")) multiplexer_8 (
    .in0(ID_IR[20:16]), .in1(ID_IR[15:11]), .out(multiplexer_8_out), .sel(\单周期硬布线控制器_1_regdst ));
  assign bit_extender_1_out = {{16{1'b0}}, {ID_IR[15:6], Func}};  // Bit_Extender bit_extender_1
  assign bit_extender_2_out = {{16{ID_IR[15]}}, {ID_IR[15:6], Func}};  // Bit_Extender bit_extender_2
  nand nand_1 (nand_1_out, d_ff_2_q, comparator_1_eq);
  Counter #(.width(13), .max('h1fff), .ongoal("stay"), .trigger("rising"), .behavior("old")) counter_2 (
    .count(comparator_1_lt), .Q(CNT_num), .clk(clock_2_out));  // open: load, D, carry, clr, preset
  assign CLK = nand_1_out ? clock_2_out : 1'bz;  // Controlled_Buffer controlled_buffer_1
  MIPS_Regifile mips_regifile_1 (
    .Din(RDin), .Clk(CLK), .R1(mips_regifile_1_r1), .R2(mips_regifile_1_r2), .WE(RegWrite),
    .W_num(multiplexer_19_out), .R1_num(multiplexer_6_out), .R2_num(multiplexer_7_out));
  Multiplexer #(.select(1), .width(32), .disabled("Z"), .enable("false")) multiplexer_9 (
    .in0(bit_extender_1_out), .in1(bit_extender_2_out), .out(multiplexer_9_out), .sel(\单周期硬布线控制器_1_signedext ));
  Multiplexer #(.select(1), .width(5), .disabled("Z"), .enable("false")) multiplexer_10 (
    .in0(multiplexer_8_out), .in1({5{1'b1}}), .out(multiplexer_10_out), .sel(\单周期硬布线控制器_1_jal ));
  Pull_Resistor #(.pull(1)) pull_resistor_1 (.node(CLK));
  or or_4 (or_4_out, \重定向逻辑_1_load_use , EX_PredictErr);
  // 流水线寄存器 流水线寄存器_2: pin names not known; wires that end beside it: \单周期硬布线控制器_1_bgez , \单周期硬布线控制器_1_beq , \单周期硬布线控制器_1_bne , \单周期硬布线控制器_1_memtoreg , \单周期硬布线控制器_1_lb , \单周期硬布线控制器_1_memwrite , \单周期硬布线控制器_1_alu_op , \单周期硬布线控制器_1_alu_src , \单周期硬布线控制器_1_regwrite , \单周期硬布线控制器_1_jal , \单周期硬布线控制器_1_regdst , \单周期硬布线控制器_1_sv , \单周期硬布线控制器_1_syscall , multiplexer_6_out, multiplexer_7_out, mips_regifile_1_r1, mips_regifile_1_r2, ID_IR[10:6], {ID_IR[25:6], Func}, multiplexer_9_out, multiplexer_10_out, ID_PC, {ID_IR, Func}, \单周期硬布线控制器_1_jmp , \单周期硬布线控制器_1_jr , EN, RegWrite, CLK, EX_JMP, RST, EX_JR, or_4_out, EX_BGEZ, EX_Beq, EX_Bne, \流水线寄存器_2_p36 , \流水线寄存器_2_p37 , \流水线寄存器_2_p38 , \流水线寄存器_2_p39 , \流水线寄存器_2_p40 , \流水线寄存器_2_p41 , EX_JAL, \流水线寄存器_2_p43 , \流水线寄存器_2_p44 , \流水线寄存器_2_p45 , \流水线寄存器_2_p46 , \流水线寄存器_2_p47 , \流水线寄存器_2_p48 , \流水线寄存器_2_p49 , \流水线寄存器_2_p50 , J_ADDR, \流水线寄存器_2_p52 , \流水线寄存器_2_p53 , EX_PC, EX_IR, EX_PC[31:28]
  and and_2 (and_2_out, ~JR_ADDR[31], EX_BGEZ);  // AND_Gate
  Register #(.width(1), .trigger("rising"), .Select("low")) register_2 (
    .D(register_1_q), .en(EN), .Q(register_2_q), .clk(CLK), .clr(RST));
  or or_5 (or_5_out, EX_JR, EX_JMP);
  Multiplexer #(.select(1), .width(32), .disabled("Z"), .enable("false")) multiplexer_11 (
    .in0(\重定向逻辑_1_rt_f ), .in1(\流水线寄存器_2_p52 ), .out(multiplexer_11_out), .sel(\流水线寄存器_2_p40 ));
  Shifter #(.width(32), .shift("ll")) shifter_1 (.in(\流水线寄存器_2_p52 ), .\dist (5'b00010), .out(shifter_1_out));
  Multiplexer #(.select(1), .width(32), .disabled("Z"), .enable("false")) multiplexer_12 (
    .in0(multiplexer_11_out), .in1(32'h22), .out(multiplexer_12_out), .sel(\流水线寄存器_2_p45 ));
  Multiplexer #(.select(1), .width(5), .disabled("Z"), .enable("false")) multiplexer_13 (
    .in0(\流水线寄存器_2_p50 ), .in1(JR_ADDR[4:0]), .out(multiplexer_13_out), .sel(\流水线寄存器_2_p44 ));
  or or_6 (EX_BranchTaken, or_5_out, or_7_out);
  Adder #(.width(32)) adder_2 (.a(EX_PC), .b(32'h4), .out(EX_PC_4));  // open: cin, cout
  Multiplexer #(.select(1), .width(1), .disabled("Z"), .enable("false")) multiplexer_14 (
    .in0(EX_Bne), .in1(EX_Beq), .out(multiplexer_14_out), .sel(mips_alu_1_equal));
  MIPS_ALU mips_alu_1 (
    .X(JR_ADDR), .Y(multiplexer_12_out), .AluOP(\流水线寄存器_2_p39 ), .Equal(mips_alu_1_equal),
    .Result(mips_alu_1_result), .shamt(multiplexer_13_out));  // open: Result_2
  or or_7 (or_7_out, and_2_out, multiplexer_14_out);
  Adder #(.width(32)) adder_3 (.a(shifter_1_out), .b(EX_PC_4), .out(BR_ADDR));  // open: cin, cout
  xor xor_1 (xor_1_out, register_2_q, EX_BranchTaken);
  and and_3 (EX_PredictErr, EX_Branch, xor_1_out);
  \流水线寄存器  \u_流水线寄存器_3  (
    .IN_MemToReg(\流水线寄存器_2_p36 ), .IN_MemWrite(\流水线寄存器_2_p38 ), .IN_RegWrite(\流水线寄存器_2_p41 ),
    .IN_equal(mips_alu_1_equal), .IN_R1(undriven), .IN_ALU(mips_alu_1_result), .IN_R2(\重定向逻辑_1_rt_f ),
    .IN_PC(EX_PC), .IN_IR(EX_IR), .OUT_MemToReg(\流水线寄存器_3_out_memtoreg ), .OUT_MemWrite(MemWrite),
    .OUT_RegWrite(\流水线寄存器_3_out_regwrite ), .OUT_Syscall(\流水线寄存器_3_out_syscall ),
    .OUT_equal(\流水线寄存器_3_out_equal ), .OUT_ALU(\流水线寄存器_3_out_alu ), .OUT_R2(MDin), .OUT_PC(M_PC),
    .OUT_IR(MEM_IR), .EN(EN), .CLK(CLK), .RST(RST), .In_RegDst(\流水线寄存器_2_p43 ),
    .OUT_RegDst(\流水线寄存器_3_out_regdst ), .IN_JAL(EX_JAL), .OUT_JAL(\流水线寄存器_3_out_jal ), .CLR(1'b0),
    .IN_WriteReg_num(\流水线寄存器_2_p53 ), .OUT_WriteReg_num(\流水线寄存器_3_out_writereg_num ),
    .In_Syscall(\流水线寄存器_2_p45 ), .IN_LB(\流水线寄存器_2_p37 ), .OUT_LB(\流水线寄存器_3_out_lb ));  // open: IN_AluOP, IN_AluSrcB, IN_MD, IN_Imm, OUT_AluOP, OUT_AluSrcB, OUT_R1, OUT_MD, OUT_Imm, IN_Bne, OUT_Bne, IN_Beq, OUT_Beq, IN_shamt, OUT_shamt, IN_offset, OUT_offset, IN_JMP, OUT_JMP, IN_JR, OUT_JR, IN_BGEZ, OUT_BGEZ, IN_SV, OUT_SV, IN_Rs_num, IN_Rt_num, OUT_Rs_num, OUT_Rt_num
  and and_4 (and_4_out, \流水线寄存器_3_out_syscall , \流水线寄存器_3_out_equal );
  BitSelector #(.width(32), .group(8)) bitselector_1 (
    .in(ram_1_data), .out(bitselector_1_out), .sel(\流水线寄存器_3_out_alu [1:0]));
  Register #(.width(32), .trigger("rising"), .Select("low")) register_3 (
    .D(MDin), .en(and_4_out), .Q(LedData), .clk(CLK), .clr(RST));
  assign bit_extender_3_out = {{24{bitselector_1_out[7]}}, bitselector_1_out};  // Bit_Extender bit_extender_3
  RAM #(.addrWidth(10), .dataWidth(32), .bus("separate"), .Select("high")) ram_1 (
    .addr(\流水线寄存器_3_out_alu [11:2]), .din(MDin), .data(ram_1_data), .str(MemWrite), .clk(CLK), .clr(RST));  // open: sel, ld
  Multiplexer #(.select(1), .width(32), .disabled("Z"), .enable("false")) multiplexer_15 (
    .in0(ram_1_data), .in1(bit_extender_3_out), .out(multiplexer_15_out), .sel(\流水线寄存器_3_out_lb ));
  \流水线寄存器  \u_流水线寄存器_4  (
    .IN_MemToReg(\流水线寄存器_3_out_memtoreg ), .IN_RegWrite(\流水线寄存器_3_out_regwrite ),
    .IN_equal(\流水线寄存器_3_out_equal ), .IN_ALU(\流水线寄存器_3_out_alu ), .IN_MD(multiplexer_15_out), .IN_PC(M_PC),
    .IN_IR(MEM_IR), .OUT_MemToReg(\流水线寄存器_4_out_memtoreg ), .OUT_RegWrite(RegWrite),
    .OUT_Syscall(\流水线寄存器_4_out_syscall ), .OUT_equal(\流水线寄存器_4_out_equal ), .OUT_ALU(\流水线寄存器_4_out_alu ),
    .OUT_MD(\流水线寄存器_4_out_md ), .OUT_PC(WB_PC), .OUT_IR(WB_IR), .EN(EN), .CLK(CLK), .RST(RST),
    .In_RegDst(\流水线寄存器_3_out_regdst ), .OUT_RegDst(\流水线寄存器_4_out_regdst ), .IN_JAL(\流水线寄存器_3_out_jal ),
    .OUT_JAL(\流水线寄存器_4_out_jal ), .CLR(1'b0), .IN_WriteReg_num(\流水线寄存器_3_out_writereg_num ),
    .OUT_WriteReg_num(\流水线寄存器_4_out_writereg_num ), .In_Syscall(\流水线寄存器_3_out_syscall ));  // open: IN_MemWrite, IN_AluOP, IN_AluSrcB, IN_R1, IN_R2, IN_Imm, OUT_MemWrite, OUT_AluOP, OUT_AluSrcB, OUT_R1, OUT_R2, OUT_Imm, IN_Bne, OUT_Bne, IN_Beq, OUT_Beq, IN_shamt, OUT_shamt, IN_offset, OUT_offset, IN_JMP, OUT_JMP, IN_JR, OUT_JR, IN_BGEZ, OUT_BGEZ, IN_SV, OUT_SV, IN_LB, OUT_LB, IN_Rs_num, IN_Rt_num, OUT_Rs_num, OUT_Rt_num
  Multiplexer #(.select(1), .width(32), .disabled("Z"), .enable("false")) multiplexer_16 (
    .in0(\流水线寄存器_4_out_alu ), .in1(\流水线寄存器_4_out_md ), .out(multiplexer_16_out), .sel(\流水线寄存器_4_out_memtoreg ));
  Multiplexer #(.select(1), .width(5), .disabled("Z"), .enable("false")) multiplexer_17 (
    .in0(WB_IR[20:16]), .in1(WB_IR[15:11]), .out(multiplexer_17_out), .sel(\流水线寄存器_4_out_regdst ));
  Multiplexer #(.select(1), .width(32), .disabled("Z"), .enable("false")) multiplexer_18 (
    .in0(multiplexer_16_out), .in1(adder_4_out), .out(RDin), .sel(\流水线寄存器_4_out_jal ));
  Multiplexer #(.select(1), .width(5), .disabled("Z"), .enable("false")) multiplexer_19 (
    .in0(multiplexer_17_out), .in1({5{1'b1}}), .out(multiplexer_19_out), .sel(\流水线寄存器_4_out_jal ));
  Adder #(.width(32)) adder_4 (.a(32'h4), .b(WB_PC), .out(adder_4_out));  // open: cin, cout

  // Other names for the same wires on the sheet: ID_IR[5:0] = Func; OP[5:0] = ID_IR[31:26];
  //   J_ADDR[31:28] = EX_PC[31:28]; MEM_PC[31:0] = M_PC; MEM_R2[31:0] = MDin

  // Notes on the sheet:
  //   中断源
  //   时空图监测，可删除
  //   中断等待指示
  //   数码管输出
  //   指令存储器
  //   contents of rom_1 (hex, n*v repeats v):
  //   20110001 8000c05 20110001 20120002 20130003 8000c09 20110001 20120002 20130003 8000c0d 20110001
  //   20120002 20130003 8000c11 20110001 20120002 20130003 c000cf3 20100001 20110001 118fc0 112020
  //   20020022 c 118882 12200001 8000c15 112020 20020022 c 20110001 118880 112020 20020022 c 12200001
  //   8000c1f 20110001 118fc0 112020 20020022 c 1188c3 112020 20020022 c 118903 112020 20020022 c 118903
  //   112020 20020022 c 118903 112020 20020022 c 118903 112020 20020022 c 118903 112020 20020022 c 118903
  //   112020 20020022 c 118903 112020 20020022 c 20100001 109fc0 139fc3 8021 2012000c 24160003 26100001
  //   3210000f 20080008 20090001 139900 2709825 132020 20020022 c 1094022 1500fff9 22100001 2018000f
  //   2188024 108700 20080008 20090001 139902 2709825 132021 20020022 c 1094022 1500fff9 108702 2c9b022
  //   12c00001 8000c50 4020 1084027 84400 3508ffff 82021 20020022 c 2010ffff 20110000 ae300000 22100001
  //   22310004 ae300000 22100001 22310004 ae300000 22100001 22310004 ae300000 22100001 22310004 ae300000
  //   22100001 22310004 ae300000 22100001 22310004 ae300000 22100001 22310004 ae300000 22100001 22310004
  //   ae300000 22100001 22310004 ae300000 22100001 22310004 ae300000 22100001 22310004 ae300000 22100001
  //   22310004 ae300000 22100001 22310004 ae300000 22100001 22310004 ae300000 22100001 22310004 ae300000
  //   22100001 22310004 22100001 8020 2011003c 8e130000 8e340000 274402a 11000002 ae330000 ae140000
  //   2231fffc 1611fff8 102020 20020022 c 22100004 2011003c 1611fff2 20020032 c 20080001 20090003 20110876
  //   112020 20020022 c 200b0008 1118804 1318804 112020 20020022 c 216bffff 1560fff9 2002000a c 2008ffff
  //   20090000 20111997 112020 20020022 c 2288820 2e291949 1120fffa 2002000a c 20090000 200b0010 34118483
  //   20120404 118c00 129400 36318281 22520404 ad310000 2328820 21290004 216bffff 1560fffb 200b0020
  //   20090000 91310000 112020 20020022 c 21290001 216bffff 1560fff9 2002000a c 2011fff1 112020 20020022 c
  //   22310001 620fffb 2002000a c 20100000 22100001 102020 20020022 c 22100002 102020 20020022 c 22100003
  //   102020 20020022 c 22100004 102020 20020022 c 22100005 102020 20020022 c 22100006 102020 20020022 c
  //   22100007 102020 20020022 c 22100008 102020 20020022 20020022 c 3e00008
  //   控制位
  //   指令字
  //   流水调试日志用
  //   暂停节拍，不能为0
  //   JMP
  //   JR
  //   SignedExt
  //   OP
  //   Func
  //   Syscall
  //   rs
  //   rt
  //   rd
  //   戳工具置1进入计数暂停模式，ctrl+k时钟自动运行到对应节拍暂停
  //   ctrl+k关闭时钟连续运行，将控制位置零，进入单步调试模式调试
  //   BGEZ
  //   Beq
  //   Bne
  //   MemToReg
  //   MemWrite
  //   AluOP
  //   AluSrcB
  //   RegWrite
  //   JAL
  //   RegDst
  //   可计数暂停的时钟源
  //   为方便自动评测，需要输出流水线各段保存的PC值，注意是PC不是PC+4，另外ID段寄存器写入信息，Mem段内存写入信息也要输出
  //   rt
  //   rd
  //   rd
endmodule

module \中断按键参考电路  (
  input  CLK,
  input  Eret,
  input  RST,
  input  IntR,
  input  Int1,
  input  Int2,
  input  Int3,
  output [1:0] IntNo,
  output PriorInt
);

  wire and_1_out, and_2_out, and_3_out, and_4_out, and_5_out, buffer_1_out, CLR1, CLR2, CLR3, d_ff_1_q,
       d_ff_2_q, d_ff_3_q, IR1_q, IR2_q, IR3_q, nand_1_out, not_1_out, or_1_out, or_2_out, or_3_out,
       or_4_out, or_5_out, or_6_out, or_7_out, priority_encoder_1_gs;
  wire [1:0] IntNo_t, xor_1_out;

  LED #(.active("true")) \_1号中断等待指示灯  (.in(or_1_out));
  or or_1 (or_1_out, IR1_q, d_ff_1_q);
  LED #(.active("true")) \_2号中断等待指示灯  (.in(or_2_out));
  or or_2 (or_2_out, IR2_q, d_ff_2_q);
  or or_3 (or_3_out, IR3_q, d_ff_3_q);
  LED #(.active("true")) \_3号中断等待指示灯  (.in(or_3_out));
  D_Flip_Flop #(.trigger("rising"), .Pre_Clr_Positions("LEGACY"), .NegatePresetClear("false"), .enable("true"), .NewFFLayout("false")) d_ff_1 (
    .clk(Int1), .D(1'b1), .Q(d_ff_1_q), .reset(IR1_q));  // open: Qn, preset, en
  D_Flip_Flop #(.trigger("rising"), .Pre_Clr_Positions("LEGACY"), .NegatePresetClear("false"), .enable("true"), .NewFFLayout("false")) d_ff_2 (
    .clk(Int2), .D(1'b1), .Q(d_ff_2_q), .reset(IR2_q));  // open: Qn, preset, en
  D_Flip_Flop #(.trigger("rising"), .Pre_Clr_Positions("LEGACY"), .NegatePresetClear("false"), .enable("true"), .NewFFLayout("false")) d_ff_3 (
    .clk(Int3), .D(1'b1), .Q(d_ff_3_q), .reset(IR3_q));  // open: Qn, preset, en
  or or_4 (or_4_out, d_ff_1_q, IR1_q);
  or or_5 (or_5_out, d_ff_2_q, IR2_q);
  or or_6 (or_6_out, d_ff_3_q, IR3_q);
  and and_1 (and_1_out, or_4_out, ~CLR1);  // AND_Gate
  and and_2 (and_2_out, or_5_out, ~CLR2);  // AND_Gate
  and and_3 (and_3_out, or_6_out, ~CLR3);  // AND_Gate
  D_Flip_Flop #(.trigger("rising"), .Pre_Clr_Positions("LEGACY"), .NegatePresetClear("false"), .enable("true"), .NewFFLayout("false")) IR1 (
    .clk(CLK), .D(and_1_out), .Q(IR1_q), .reset(RST));  // open: Qn, preset, en
  D_Flip_Flop #(.trigger("rising"), .Pre_Clr_Positions("LEGACY"), .NegatePresetClear("false"), .enable("true"), .NewFFLayout("false")) IR2 (
    .clk(CLK), .D(and_2_out), .Q(IR2_q), .reset(RST));  // open: Qn, preset, en
  D_Flip_Flop #(.trigger("rising"), .Pre_Clr_Positions("LEGACY"), .NegatePresetClear("false"), .enable("true"), .NewFFLayout("false")) IR3 (
    .clk(CLK), .D(and_3_out), .Q(IR3_q), .reset(RST));  // open: Qn, preset, en
  not not_1 (not_1_out, IntNo_t[1]);
  nand nand_1 (nand_1_out, IntNo_t[1], IntNo_t[0]);
  and and_4 (and_4_out, IR1_q, not_1_out);
  and and_5 (and_5_out, IR2_q, nand_1_out);
  buf buffer_1 (buffer_1_out, IR3_q);
  Pull_Resistor #(.pull(0)) pull_resistor_1 (.node(IntNo));
  Priority_Encoder #(.select(2), .disabled("Z")) priority_encoder_1 (
    .in0(1'b0), .in1(and_4_out), .in2(and_5_out), .in3(buffer_1_out), .out(IntNo), .gs(priority_encoder_1_gs));  // open: en_out, en_in
  Demultiplexer #(.select(2), .width(1), .tristate("false"), .disabled("Z"), .enable("false")) demultiplexer_1 (
    .out1(CLR1), .out2(CLR2), .out3(CLR3), .in(Eret), .sel(IntNo_t));  // open: out0
  \嵌套中断堆栈  \u_嵌套中断堆栈_1  (.PUSH(IntR), .Din(IntNo), .POP(Eret), .RST(RST), .CLK(CLK), .Dout(IntNo_t));
  or or_7 (or_7_out, xor_1_out[0], xor_1_out[1]);
  assign xor_1_out = IntNo ^ IntNo_t;  // XOR_Gate xor_1, 2 bits wide
  and and_6 (PriorInt, or_7_out, priority_encoder_1_gs);

  // Notes on the sheet:
  //   1号中断信号采样电路
  //   2号中断信号采样电路
  //   3号中断信号采样电路
  //   Reset 
  //   Reset 
  //   Reset 
endmodule

module \单周期MIPS_单级中断  (
  input  IR1,
  input  IR2,
  input  IR3,
  output RegWrite,
  output MemWrite,
  output [31:0] PC,
  output [31:0] IR,
  output [31:0] RDin,
  output [31:0] MDin,
  output [31:0] LedData
);

  wire and_1_out, CLK, clock_2_out, comparator_1_eq, comparator_1_lt, comparator_2_eq, comparator_3_eq,
       comparator_4_eq, comparator_5_eq, d_ff_1_q, d_ff_3_qn, d_ff_4_q, d_ff_5_q, EN, equal, Eret, Go, IntR,
       IntR_Eret, IR1_t, IR2_t, IR3_t, IRA, IRB, IRC, multiplexer_12_out, nand_1_out, not_1_out, or_3_out,
       or_5_out, or_6_out, or_8_out, RST, SignedExt, Syscall, W1, W2, W3, \中断按键参考电路_1_priorint ,
       \单周期硬布线控制器_1_alu_src , \单周期硬布线控制器_1_beq , \单周期硬布线控制器_1_bne , \单周期硬布线控制器_1_jal , \单周期硬布线控制器_1_jmp ,
       \单周期硬布线控制器_1_jr , \单周期硬布线控制器_1_memtoreg , \单周期硬布线控制器_1_regdst ;
  wire [1:0] IntNo;
  wire [3:0] \单周期硬布线控制器_1_alu_op ;
  wire [4:0] multiplexer_5_out, multiplexer_6_out, multiplexer_7_out, multiplexer_8_out;
  wire [12:0] CNT_num;
  wire [15:0] \总周期数 ;
  wire [31:0] bit_extender_1_out, BR_ADDR, EPCR_q, Int_EretAddr, IntAddr, JR_ADDR, mips_alu_1_result,
       multiplexer_1_out, multiplexer_2_out, multiplexer_4_out, multiplexer_9_out, multiplexer_10_out,
       multiplexer_11_out, NextPC, PC_4, ram_1_data, shifter_1_out;

  Button button_1 (.out(RST));
  Clock #(.highDuration(1), .lowDuration(1)) clock_1 ();  // open: out
  Button _1 ();  // open: out
  Button _2 ();  // open: out
  Button _3 ();  // open: out
  Button \u_继续运行  (.out(Go));
  LED #(.active("true")) led_1 (.in(W1));
  LED #(.active("true")) led_2 (.in(W2));
  LED #(.active("true")) led_3 (.in(W3));
  Multiplexer #(.select(1), .width(32), .disabled("Z"), .enable("false")) multiplexer_1 (
    .in0({PC[31:28], IR[25:0], 2'b00}), .in1(JR_ADDR), .out(multiplexer_1_out), .sel(\单周期硬布线控制器_1_jr ));
  D_Flip_Flop #(.trigger("high"), .Pre_Clr_Positions("LEGACY"), .NegatePresetClear("false"), .enable("true"), .NewFFLayout("false")) d_ff_1 (.Q(d_ff_1_q));  // open: clk, D, Qn, preset, en, reset
  // Probe on 13'hc
  Hex_Digit_Display hex_digit_display_1 (.value(LedData[31:28]));  // open: dp
  Multiplexer #(.select(1), .width(32), .disabled("Z"), .enable("false")) multiplexer_2 (
    .in0(PC_4), .in1(multiplexer_1_out), .out(multiplexer_2_out), .sel(\单周期硬布线控制器_1_jmp ));
  Adder #(.width(32)) adder_1 (.a(PC), .b(32'h4), .out(PC_4));  // open: cin, cout
  Clock #(.highDuration(1), .lowDuration(1)) clock_2 (.out(clock_2_out));
  Hex_Digit_Display hex_digit_display_2 (.value(LedData[23:20]));  // open: dp
  Hex_Digit_Display hex_digit_display_3 (.value(LedData[27:24]));  // open: dp
  Multiplexer #(.select(1), .width(32), .disabled("Z"), .enable("false")) multiplexer_3 (
    .in0(multiplexer_2_out), .in1(BR_ADDR), .out(NextPC), .sel(multiplexer_12_out));
  Comparator #(.width(13), .mode("twosComplement")) comparator_1 (
    .a(CNT_num), .b(13'hc), .eq(comparator_1_eq), .lt(comparator_1_lt));  // open: gt
  Hex_Digit_Display hex_digit_display_4 (.value(LedData[19:16]));  // open: dp
  Hex_Digit_Display hex_digit_display_5 (.value(LedData[15:12]));  // open: dp
  Multiplexer #(.select(1), .width(32), .disabled("Z"), .enable("false")) multiplexer_4 (
    .in0(NextPC), .in1(Int_EretAddr), .out(multiplexer_4_out), .sel(IntR_Eret));
  nand nand_1 (nand_1_out, d_ff_1_q, comparator_1_eq);
  Counter #(.width(13), .max('h1fff), .ongoal("stay"), .trigger("rising"), .behavior("old")) counter_1 (
    .count(comparator_1_lt), .Q(CNT_num), .clk(clock_2_out));  // open: load, D, carry, clr, preset
  Hex_Digit_Display hex_digit_display_6 (.value(LedData[11:8]));  // open: dp
  Hex_Digit_Display hex_digit_display_7 (.value(LedData[7:4]));  // open: dp
  // Probe on \总周期数 
  Register #(.width(32), .trigger("rising"), .Select("low")) u_PC (
    .D(multiplexer_4_out), .en(EN), .Q(PC), .clk(CLK), .clr(RST));
  Hex_Digit_Display hex_digit_display_8 (.value(LedData[3:0]));  // open: dp
  assign CLK = nand_1_out ? clock_2_out : 1'bz;  // Controlled_Buffer controlled_buffer_1
  Pull_Resistor #(.pull(1)) pull_resistor_1 (.node(CLK));
  ROM #(.addrWidth(10), .dataWidth(32), .Select("high")) rom_1 (.addr(PC[11:2]), .data(IR));
  or or_1 (IR1_t, IR1, IRA);
  // Mips_Probe mips_probe_1: pin names not known; wires that end beside it: IR
  or or_2 (IR2_t, IR2, IRB);
  \单周期硬布线控制器  \u_单周期硬布线控制器_1  (
    .Func(IR[5:0]), .OP(IR[31:26]), .ALU_OP(\单周期硬布线控制器_1_alu_op ), .MemToReg(\单周期硬布线控制器_1_memtoreg ),
    .MemWrite(MemWrite), .ALU_SRC(\单周期硬布线控制器_1_alu_src ), .RegWrite(RegWrite), .SysCALL(Syscall),
    .SignedExt(SignedExt), .RegDst(\单周期硬布线控制器_1_regdst ), .JR(\单周期硬布线控制器_1_jr ), .JMP(\单周期硬布线控制器_1_jmp ),
    .Beq(\单周期硬布线控制器_1_beq ), .JAL(\单周期硬布线控制器_1_jal ), .Bne(\单周期硬布线控制器_1_bne ), .ERET(Eret));  // open: BGEZ, MFC0, MTC0, MF, SV, LB
  Multiplexer #(.select(1), .width(5), .disabled("Z"), .enable("false")) multiplexer_5 (
    .in0(IR[25:21]), .in1(5'b00010), .out(multiplexer_5_out), .sel(Syscall));
  not not_1 (not_1_out, Syscall);
  Multiplexer #(.select(1), .width(5), .disabled("Z"), .enable("false")) multiplexer_6 (
    .in0(IR[20:16]), .in1(5'b00100), .out(multiplexer_6_out), .sel(Syscall));
  Multiplexer #(.select(1), .width(5), .disabled("Z"), .enable("false")) multiplexer_7 (
    .in0(IR[20:16]), .in1(IR[15:11]), .out(multiplexer_7_out), .sel(\单周期硬布线控制器_1_regdst ));
  Multiplexer #(.select(1), .width(5), .disabled("Z"), .enable("false")) multiplexer_8 (
    .in0(multiplexer_7_out), .in1({5{1'b1}}), .out(multiplexer_8_out), .sel(\单周期硬布线控制器_1_jal ));
  or or_3 (or_3_out, equal, not_1_out);
  or or_4 (IR3_t, IR3, IRC);
  MIPS_Regifile mips_regifile_1 (
    .Din(RDin), .Clk(CLK), .R1(JR_ADDR), .R2(MDin), .WE(RegWrite), .W_num(multiplexer_8_out),
    .R1_num(multiplexer_5_out), .R2_num(multiplexer_6_out));
  assign bit_extender_1_out = {{16{IR[15]}}, IR[15:0]};  // Bit_Extender bit_extender_1
  or or_5 (or_5_out, not_1_out, Go);
  D_Flip_Flop #(.trigger("falling"), .Pre_Clr_Positions("ABOVE_BELOW"), .NegatePresetClear("false"), .enable("false"), .NewFFLayout("true")) d_ff_2 (
    .clk(CLK), .D(or_3_out), .Q(EN), .preset(or_5_out));  // open: Qn, reset
  Multiplexer #(.select(1), .width(32), .disabled("Z"), .enable("false")) multiplexer_9 (
    .in0(MDin), .in1(bit_extender_1_out), .out(multiplexer_9_out), .sel(\单周期硬布线控制器_1_alu_src ));
  Multiplexer #(.select(1), .width(32), .disabled("Z"), .enable("false")) multiplexer_10 (
    .in0(multiplexer_9_out), .in1(32'h22), .out(multiplexer_10_out), .sel(Syscall));
  Shifter #(.width(32), .shift("ll")) shifter_1 (.in(bit_extender_1_out), .\dist (5'b00010), .out(shifter_1_out));
  MIPS_ALU mips_alu_1 (
    .X(JR_ADDR), .Y(multiplexer_10_out), .AluOP(\单周期硬布线控制器_1_alu_op ), .Equal(equal),
    .Result(mips_alu_1_result), .shamt(IR[10:6]));  // open: Result_2
  Adder #(.width(32)) adder_2 (.a(shifter_1_out), .b(PC_4), .out(BR_ADDR));  // open: cin, cout
  Counter #(.width(16), .max('hffff), .ongoal("wrap"), .trigger("rising"), .behavior("new")) counter_2 (
    .count(EN), .Q(\总周期数 ), .clk(CLK), .clr(RST));  // open: load, D, carry, preset, down
  Multiplexer #(.select(1), .width(32), .disabled("Z"), .enable("false")) multiplexer_11 (
    .in0(mips_alu_1_result), .in1(ram_1_data), .out(multiplexer_11_out), .sel(\单周期硬布线控制器_1_memtoreg ));
  RAM #(.addrWidth(10), .dataWidth(32), .bus("separate"), .Select("high")) ram_1 (
    .addr(mips_alu_1_result[11:2]), .din(MDin), .data(ram_1_data), .str(MemWrite), .clk(CLK), .clr(RST));  // open: sel, ld
  and and_1 (and_1_out, Syscall, equal);
  Register #(.width(32), .trigger("rising"), .Select("low")) register_1 (
    .D(MDin), .en(and_1_out), .Q(LedData), .clk(CLK), .clr(RST));
  Multiplexer #(.select(1), .width(1), .disabled("Z"), .enable("false")) multiplexer_12 (
    .in0(\单周期硬布线控制器_1_bne ), .in1(\单周期硬布线控制器_1_beq ), .out(multiplexer_12_out), .sel(equal));
  Multiplexer #(.select(1), .width(32), .disabled("Z"), .enable("false")) multiplexer_13 (
    .in0(multiplexer_11_out), .in1(PC_4), .out(RDin), .sel(\单周期硬布线控制器_1_jal ));
  \中断按键参考电路  \u_中断按键参考电路_1  (
    .CLK(CLK), .RST(RST), .Eret(Eret), .Int1(IR1_t), .Int2(IR2_t), .Int3(IR3_t),
    .PriorInt(\中断按键参考电路_1_priorint ), .IntNo(IntNo), .IntR(IntR));
  D_Flip_Flop #(.trigger("rising"), .Pre_Clr_Positions("LEGACY"), .NegatePresetClear("false"), .enable("true"), .NewFFLayout("false")) d_ff_3 (
    .Qn(d_ff_3_qn), .preset(d_ff_4_q), .reset(or_6_out));  // open: clk, D, Q, en
  D_Flip_Flop #(.trigger("rising"), .Pre_Clr_Positions("LEGACY"), .NegatePresetClear("false"), .enable("true"), .NewFFLayout("false")) d_ff_4 (
    .clk(CLK), .D(IntR), .Q(d_ff_4_q), .reset(RST));  // open: Qn, preset, en
  or or_6 (or_6_out, d_ff_5_q, RST);
  D_Flip_Flop #(.trigger("rising"), .Pre_Clr_Positions("LEGACY"), .NegatePresetClear("false"), .enable("true"), .NewFFLayout("false")) d_ff_5 (
    .clk(CLK), .D(Eret), .Q(d_ff_5_q), .reset(RST));  // open: Qn, preset, en
  and and_2 (IntR, \中断按键参考电路_1_priorint , d_ff_3_qn);
  or or_7 (IntR_Eret, IntR, Eret);
  Multiplexer #(.select(2), .width(32), .disabled("Z"), .enable("false")) multiplexer_14 (
    .in1(32'h30ac), .in2(32'h3150), .in3(32'h31f4), .out(IntAddr), .sel(IntNo));  // open: in0
  Register #(.width(32), .trigger("rising"), .Select("low")) EPCR (
    .D(NextPC), .en(IntR), .Q(EPCR_q), .clk(CLK), .clr(RST));
  Comparator #(.width(16), .mode("twosComplement")) comparator_2 (
    .a(16'h23b), .b(\总周期数 ), .eq(comparator_2_eq));  // open: gt, lt
  Comparator #(.width(16), .mode("twosComplement")) comparator_3 (
    .a(\总周期数 ), .b(16'h1), .eq(comparator_3_eq));  // open: gt, lt
  Comparator #(.width(16), .mode("twosComplement")) comparator_4 (
    .a(\总周期数 ), .b(16'h4), .eq(comparator_4_eq));  // open: gt, lt
  Comparator #(.width(16), .mode("twosComplement")) comparator_5 (
    .a(\总周期数 ), .b(16'h7), .eq(comparator_5_eq));  // open: gt, lt
  Multiplexer #(.select(1), .width(32), .disabled("Z"), .enable("false")) multiplexer_15 (
    .in0(IntAddr), .in1(EPCR_q), .out(Int_EretAddr), .sel(Eret));
  Pull_Resistor #(.pull(0)) pull_resistor_2 (.node(IRA));
  or or_8 (or_8_out, comparator_2_eq, comparator_3_eq);
  assign IRA = or_8_out ? ~CLK : 1'bz;  // Controlled_Inverter controlled_inverter_1
  Pull_Resistor #(.pull(0)) pull_resistor_3 (.node(IRB));
  assign IRB = comparator_4_eq ? ~CLK : 1'bz;  // Controlled_Inverter controlled_inverter_2
  Pull_Resistor #(.pull(0)) pull_resistor_4 (.node(IRC));
  assign IRC = comparator_5_eq ? ~CLK : 1'bz;  // Controlled_Inverter controlled_inverter_3

  // Other names for the same wires on the sheet: Func[5:0] = IR[5:0]; imm[25:0] = IR[25:0];
  //   J_ADDR[31:2] = {PC[31:28], IR[25:0]}; OP[5:0] = IR[31:26]

  // Notes on the sheet:
  //   中断源
  //   控制位
  //   中断等待指示
  //   总复位信号应将除ROM以外所有存储组件全部清零
  //   暂停节拍，不能为0
  //   戳工具置1进入计数暂停模式，ctrl+k时钟自动运行到对应节拍暂停
  //   ctrl+k关闭时钟连续运行，将控制位置零，进入单步调试模式调试
  //   用这个时钟源需要去掉电路中的其他时钟源
  //   数码管输出
  //   数码管输出应该用寄存器锁存，否则显示数据只能一闪而过
  //   指令存储器
  //   指令字
  //   contents of rom_1 (hex, n*v repeats v):
  //   201d07d0 20100001 109fc0 139fc3 8021 2012000c 24160008 26100001 3210000f 20080008 20090001 139900
  //   2709825 132020 20020022 c 1094022 1500fff9 22100001 2018000f 2188024 108700 20080008 20090001 139902
  //   2709825 132021 20020022 c 1094022 1500fff9 108702 2c9b022 12c00001 8000c07 4020 1084027 84400
  //   3508ffff 82021 20020022 c 8000c01 afa20000 23bd0004 afa40000 23bd0004 afb00000 23bd0004 afb30000
  //   23bd0004 afb40000 23bd0004 afb50000 23bd0004 afb60000 23bd0004 20160001 20140003 20150001 168020
  //   108100 2149825 132020 20020022 c 1600fffa 295a022 1680fff7 23bdfffc 8fb60000 23bdfffc 8fb50000
  //   23bdfffc 8fb40000 23bdfffc 8fb30000 23bdfffc 8fb00000 23bdfffc 8fa40000 23bdfffc 8fa20000 42000018
  //   afa20000 23bd0004 afa40000 23bd0004 afb00000 23bd0004 afb30000 23bd0004 afb40000 23bd0004 afb50000
  //   23bd0004 afb60000 23bd0004 20160002 20140003 20150001 168020 108100 2149825 132020 20020022 c
  //   1600fffa 295a022 1680fff7 23bdfffc 8fb60000 23bdfffc 8fb50000 23bdfffc 8fb40000 23bdfffc 8fb30000
  //   23bdfffc 8fb00000 23bdfffc 8fa40000 23bdfffc 8fa20000 42000018 afa20000 23bd0004 afa40000 23bd0004
  //   afb00000 23bd0004 afb30000 23bd0004 afb40000 23bd0004 afb50000 23bd0004 afb60000 23bd0004 20160003
  //   20140003 20150001 168020 108100 2149825 132020 20020022 c 1600fffa 295a022 1680fff7 23bdfffc
  //   8fb60000 23bdfffc 8fb50000 23bdfffc 8fb40000 23bdfffc 8fb30000 23bdfffc 8fb00000 23bdfffc 8fa40000
  //   23bdfffc 8fa20000 42000018
  //   可计数暂停的时钟源
  //   JMP
  //   JR
  //   OP
  //   Func
  //   rs
  //   rt
  //   rd
  //   Beq
  //   Bne
  //   AluOP
  //   AluSrcB
  //   RegWrite
  //   JAL
  //   RegDst
  //   Syscall
  //   MemToReg
  //   MemWrite
  //   为方便自动评测，需要输出PC，IR，寄存器堆写如数据RDin
  //   RAM写使能MemWrite、RAM写入数据MDin等信号
  //   控制与调试模块
  //   中断响应/返回控制模块
  //   单级中断支持模块
  //   EPC寄存器保存中断返回地址
  //   单级中断测试信号模拟器
endmodule

module \单周期MIPS_多级中断  (
  input  IR1,
  input  IR2,
  input  IR3,
  output RegWrite,
  output MemWrite,
  output [31:0] PC,
  output [31:0] IR,
  output [31:0] RDin,
  output [31:0] MDin,
  output [31:0] LedData
);

  wire and_1_out, CLK, clock_2_out, comparator_1_eq, comparator_1_lt, comparator_2_eq, comparator_3_eq,
       comparator_4_eq, comparator_5_eq, comparator_6_eq, d_ff_1_q, d_ff_3_q, d_ff_4_q, d_ff_5_qn, EN, equal,
       Eret, Go, IntR, IntR_Eret, IR1_t, IR2_t, IR3_t, IRA, IRB, IRC, mfc0, mtc0, multiplexer_13_out,
       nand_1_out, not_1_out, or_3_out, or_5_out, or_6_out, or_7_out, or_8_out, or_10_out, or_11_out, RST,
       SignedExt, Syscall, W1, W2, W3, \中断按键参考电路_1_priorint , \单周期硬布线控制器_1_alu_src , \单周期硬布线控制器_1_beq ,
       \单周期硬布线控制器_1_bne , \单周期硬布线控制器_1_jal , \单周期硬布线控制器_1_jmp , \单周期硬布线控制器_1_jr , \单周期硬布线控制器_1_memtoreg ,
       \单周期硬布线控制器_1_regdst ;
  wire [1:0] IntNo;
  wire [3:0] \单周期硬布线控制器_1_alu_op ;
  wire [4:0] multiplexer_5_out, multiplexer_6_out, multiplexer_7_out, multiplexer_8_out;
  wire [12:0] CNT_num;
  wire [15:0] \总周期数 ;
  wire [31:0] bit_extender_1_out, BR_ADDR, Int_EretAddr, IntAddr, JR_ADDR, mips_alu_1_result,
       multiplexer_1_out, multiplexer_2_out, multiplexer_4_out, multiplexer_9_out, multiplexer_10_out,
       multiplexer_11_out, NextPC, PC_4, ram_1_data, shifter_1_out, \硬件堆栈_1_dout ;

  Button button_1 (.out(RST));
  Clock #(.highDuration(1), .lowDuration(1)) clock_1 ();  // open: out
  Button _1 ();  // open: out
  Button _2 ();  // open: out
  Button _3 ();  // open: out
  Button \u_继续运行  (.out(Go));
  LED #(.active("true")) led_1 (.in(W1));
  LED #(.active("true")) led_2 (.in(W2));
  LED #(.active("true")) led_3 (.in(W3));
  Multiplexer #(.select(1), .width(32), .disabled("Z"), .enable("false")) multiplexer_1 (
    .in0({PC[31:28], IR[25:0], 2'b00}), .in1(JR_ADDR), .out(multiplexer_1_out), .sel(\单周期硬布线控制器_1_jr ));
  D_Flip_Flop #(.trigger("high"), .Pre_Clr_Positions("LEGACY"), .NegatePresetClear("false"), .enable("true"), .NewFFLayout("false")) d_ff_1 (.Q(d_ff_1_q));  // open: clk, D, Qn, preset, en, reset
  // Probe on 13'hc
  Hex_Digit_Display hex_digit_display_1 (.value(LedData[31:28]));  // open: dp
  Multiplexer #(.select(1), .width(32), .disabled("Z"), .enable("false")) multiplexer_2 (
    .in0(PC_4), .in1(multiplexer_1_out), .out(multiplexer_2_out), .sel(\单周期硬布线控制器_1_jmp ));
  Adder #(.width(32)) adder_1 (.a(PC), .b(32'h4), .out(PC_4));  // open: cin, cout
  Clock #(.highDuration(1), .lowDuration(1)) clock_2 (.out(clock_2_out));
  Hex_Digit_Display hex_digit_display_2 (.value(LedData[23:20]));  // open: dp
  Hex_Digit_Display hex_digit_display_3 (.value(LedData[27:24]));  // open: dp
  Multiplexer #(.select(1), .width(32), .disabled("Z"), .enable("false")) multiplexer_3 (
    .in0(multiplexer_2_out), .in1(BR_ADDR), .out(NextPC), .sel(multiplexer_13_out));
  Comparator #(.width(13), .mode("twosComplement")) comparator_1 (
    .a(CNT_num), .b(13'hc), .eq(comparator_1_eq), .lt(comparator_1_lt));  // open: gt
  Hex_Digit_Display hex_digit_display_4 (.value(LedData[15:12]));  // open: dp
  Hex_Digit_Display hex_digit_display_5 (.value(LedData[19:16]));  // open: dp
  Multiplexer #(.select(1), .width(32), .disabled("Z"), .enable("false")) multiplexer_4 (
    .in0(NextPC), .in1(Int_EretAddr), .out(multiplexer_4_out), .sel(IntR_Eret));
  nand nand_1 (nand_1_out, d_ff_1_q, comparator_1_eq);
  Counter #(.width(13), .max('h1fff), .ongoal("stay"), .trigger("rising"), .behavior("old")) counter_1 (
    .count(comparator_1_lt), .Q(CNT_num), .clk(clock_2_out));  // open: load, D, carry, clr, preset
  Hex_Digit_Display hex_digit_display_6 (.value(LedData[11:8]));  // open: dp
  Hex_Digit_Display hex_digit_display_7 (.value(LedData[7:4]));  // open: dp
  // Probe on \总周期数 
  Register #(.width(32), .trigger("rising"), .Select("low")) u_PC (
    .D(multiplexer_4_out), .en(EN), .Q(PC), .clk(CLK), .clr(RST));
  Hex_Digit_Display hex_digit_display_8 (.value(LedData[3:0]));  // open: dp
  assign CLK = nand_1_out ? clock_2_out : 1'bz;  // Controlled_Buffer controlled_buffer_1
  Pull_Resistor #(.pull(1)) pull_resistor_1 (.node(CLK));
  // Mips_Probe mips_probe_1: pin names not known; wires that end beside it: IR
  ROM #(.addrWidth(10), .dataWidth(32), .Select("high")) rom_1 (.addr(PC[11:2]), .data(IR));
  or or_1 (IR1_t, IR1, IRA);
  or or_2 (IR2_t, IR2, IRB);
  \单周期硬布线控制器  \u_单周期硬布线控制器_1  (
    .Func(IR[5:0]), .OP(IR[31:26]), .ALU_OP(\单周期硬布线控制器_1_alu_op ), .MemToReg(\单周期硬布线控制器_1_memtoreg ),
    .MemWrite(MemWrite), .ALU_SRC(\单周期硬布线控制器_1_alu_src ), .RegWrite(RegWrite), .SysCALL(Syscall),
    .SignedExt(SignedExt), .RegDst(\单周期硬布线控制器_1_regdst ), .JR(\单周期硬布线控制器_1_jr ), .JMP(\单周期硬布线控制器_1_jmp ),
    .Beq(\单周期硬布线控制器_1_beq ), .JAL(\单周期硬布线控制器_1_jal ), .Bne(\单周期硬布线控制器_1_bne ), .ERET(Eret), .MFC0(mfc0),
    .MTC0(mtc0), .MF(IR[25:21]));  // open: BGEZ, SV, LB
  Multiplexer #(.select(1), .width(5), .disabled("Z"), .enable("false")) multiplexer_5 (
    .in0(IR[25:21]), .in1(5'b00010), .out(multiplexer_5_out), .sel(Syscall));
  Multiplexer #(.select(1), .width(5), .disabled("Z"), .enable("false")) multiplexer_6 (
    .in0(IR[20:16]), .in1(IR[15:11]), .out(multiplexer_6_out), .sel(\单周期硬布线控制器_1_regdst ));
  not not_1 (not_1_out, Syscall);
  Multiplexer #(.select(1), .width(5), .disabled("Z"), .enable("false")) multiplexer_7 (
    .in0(IR[20:16]), .in1(5'b00100), .out(multiplexer_7_out), .sel(Syscall));
  Multiplexer #(.select(1), .width(5), .disabled("Z"), .enable("false")) multiplexer_8 (
    .in0(multiplexer_6_out), .in1({5{1'b1}}), .out(multiplexer_8_out), .sel(\单周期硬布线控制器_1_jal ));
  assign bit_extender_1_out = {{16{IR[15]}}, IR[15:0]};  // Bit_Extender bit_extender_1
  or or_3 (or_3_out, equal, not_1_out);
  or or_4 (IR3_t, IR3, IRC);
  MIPS_Regifile mips_regifile_1 (
    .Din(RDin), .Clk(CLK), .R1(JR_ADDR), .R2(MDin), .WE(RegWrite), .W_num(multiplexer_8_out),
    .R1_num(multiplexer_5_out), .R2_num(multiplexer_7_out));
  or or_5 (or_5_out, not_1_out, Go);
  D_Flip_Flop #(.trigger("falling"), .Pre_Clr_Positions("ABOVE_BELOW"), .NegatePresetClear("false"), .enable("false"), .NewFFLayout("true")) d_ff_2 (
    .clk(CLK), .D(or_3_out), .Q(EN), .preset(or_5_out));  // open: Qn, reset
  Multiplexer #(.select(1), .width(32), .disabled("Z"), .enable("false")) multiplexer_9 (
    .in0(MDin), .in1(bit_extender_1_out), .out(multiplexer_9_out), .sel(\单周期硬布线控制器_1_alu_src ));
  Shifter #(.width(32), .shift("ll")) shifter_1 (.in(bit_extender_1_out), .\dist (5'b00010), .out(shifter_1_out));
  Multiplexer #(.select(1), .width(32), .disabled("Z"), .enable("false")) multiplexer_10 (
    .in0(multiplexer_9_out), .in1(32'h22), .out(multiplexer_10_out), .sel(Syscall));
  MIPS_ALU mips_alu_1 (
    .X(JR_ADDR), .Y(multiplexer_10_out), .AluOP(\单周期硬布线控制器_1_alu_op ), .Equal(equal),
    .Result(mips_alu_1_result), .shamt(IR[10:6]));  // open: Result_2
  Adder #(.width(32)) adder_2 (.a(shifter_1_out), .b(PC_4), .out(BR_ADDR));  // open: cin, cout
  Counter #(.width(16), .max('hffff), .ongoal("wrap"), .trigger("rising"), .behavior("new")) counter_2 (
    .count(EN), .Q(\总周期数 ), .clk(CLK), .clr(RST));  // open: load, D, carry, preset, down
  Multiplexer #(.select(1), .width(32), .disabled("Z"), .enable("false")) multiplexer_11 (
    .in0(mips_alu_1_result), .in1(ram_1_data), .out(multiplexer_11_out), .sel(\单周期硬布线控制器_1_memtoreg ));
  RAM #(.addrWidth(10), .dataWidth(32), .bus("separate"), .Select("high")) ram_1 (
    .addr(mips_alu_1_result[11:2]), .din(MDin), .data(ram_1_data), .str(MemWrite), .clk(CLK), .clr(RST));  // open: sel, ld
  and and_1 (and_1_out, Syscall, equal);
  Multiplexer #(.select(1), .width(32), .disabled("Z"), .enable("false")) multiplexer_12 (
    .in0(multiplexer_11_out), .in1(PC_4), .out(RDin), .sel(\单周期硬布线控制器_1_jal ));
  Register #(.width(32), .trigger("rising"), .Select("low")) register_1 (
    .D(MDin), .en(and_1_out), .Q(LedData), .clk(CLK), .clr(RST));
  Multiplexer #(.select(1), .width(1), .disabled("Z"), .enable("false")) multiplexer_13 (
    .in0(\单周期硬布线控制器_1_bne ), .in1(\单周期硬布线控制器_1_beq ), .out(multiplexer_13_out), .sel(equal));
  or or_6 (or_6_out, mtc0, IntR);
  or or_7 (or_7_out, mfc0, Eret);
  \中断按键参考电路  \u_中断按键参考电路_1  (
    .CLK(CLK), .RST(RST), .Eret(Eret), .Int1(IR1_t), .Int2(IR2_t), .Int3(IR3_t),
    .PriorInt(\中断按键参考电路_1_priorint ), .IntNo(IntNo), .IntR(IntR));
  D_Flip_Flop #(.trigger("rising"), .Pre_Clr_Positions("LEGACY"), .NegatePresetClear("false"), .enable("true"), .NewFFLayout("false")) d_ff_3 (
    .clk(CLK), .D(or_6_out), .Q(d_ff_3_q), .reset(RST));  // open: Qn, preset, en
  D_Flip_Flop #(.trigger("rising"), .Pre_Clr_Positions("LEGACY"), .NegatePresetClear("false"), .enable("true"), .NewFFLayout("false")) d_ff_4 (
    .clk(CLK), .D(or_7_out), .Q(d_ff_4_q), .reset(RST));  // open: Qn, preset, en
  D_Flip_Flop #(.trigger("rising"), .Pre_Clr_Positions("LEGACY"), .NegatePresetClear("false"), .enable("true"), .NewFFLayout("false")) d_ff_5 (
    .Qn(d_ff_5_qn), .preset(d_ff_3_q), .reset(or_8_out));  // open: clk, D, Q, en
  or or_8 (or_8_out, d_ff_4_q, RST);
  and and_2 (IntR, \中断按键参考电路_1_priorint , d_ff_5_qn);
  or or_9 (IntR_Eret, IntR, Eret);
  Multiplexer #(.select(2), .width(32), .disabled("Z"), .enable("false")) multiplexer_14 (
    .in1(32'h30ac), .in2(32'h3158), .in3(32'h3204), .out(IntAddr), .sel(IntNo));  // open: in0
  Comparator #(.width(16), .mode("twosComplement")) comparator_2 (
    .a(16'h258), .b(\总周期数 ), .eq(comparator_2_eq));  // open: gt, lt
  or or_10 (or_10_out, comparator_2_eq, comparator_3_eq);
  Comparator #(.width(16), .mode("twosComplement")) comparator_3 (
    .a(\总周期数 ), .b(16'h1), .eq(comparator_3_eq));  // open: gt, lt
  Comparator #(.width(16), .mode("twosComplement")) comparator_4 (
    .a(\总周期数 ), .b(16'h4), .eq(comparator_4_eq));  // open: gt, lt
  Comparator #(.width(16), .mode("twosComplement")) comparator_5 (
    .a(\总周期数 ), .b(16'h7), .eq(comparator_5_eq));  // open: gt, lt
  or or_11 (or_11_out, comparator_5_eq, comparator_6_eq);
  Comparator #(.width(16), .mode("twosComplement")) comparator_6 (
    .a(\总周期数 ), .b(16'h241), .eq(comparator_6_eq));  // open: gt, lt
  \硬件堆栈  \u_硬件堆栈_1  (.PUSH(IntR), .POP(Eret), .CLK(CLK), .RST(RST), .Din(NextPC), .Dout(\硬件堆栈_1_dout ));
  Pull_Resistor #(.pull(0)) pull_resistor_2 (.node(IRA));
  assign IRA = or_10_out ? ~CLK : 1'bz;  // Controlled_Inverter controlled_inverter_1
  Pull_Resistor #(.pull(0)) pull_resistor_3 (.node(IRB));
  assign IRB = comparator_4_eq ? ~CLK : 1'bz;  // Controlled_Inverter controlled_inverter_2
  Pull_Resistor #(.pull(0)) pull_resistor_4 (.node(IRC));
  assign IRC = or_11_out ? ~CLK : 1'bz;  // Controlled_Inverter controlled_inverter_3
  Multiplexer #(.select(1), .width(32), .disabled("Z"), .enable("false")) multiplexer_15 (
    .in0(IntAddr), .in1(\硬件堆栈_1_dout ), .out(Int_EretAddr), .sel(Eret));

  // Other names for the same wires on the sheet: Func[5:0] = IR[5:0]; imm[25:0] = IR[25:0];
  //   J_ADDR[31:2] = {PC[31:28], IR[25:0]}; OP[5:0] = IR[31:26]

  // Notes on the sheet:
  //   中断源
  //   控制位
  //   中断等待指示
  //   总复位信号应将除ROM以外所有存储组件全部清零
  //   暂停节拍，不能为0
  //   戳工具置1进入计数暂停模式，ctrl+k时钟自动运行到对应节拍暂停
  //   ctrl+k关闭时钟连续运行，将控制位置零，进入单步调试模式调试
  //   用这个时钟源需要去掉电路中的其他时钟源
  //   数码管输出
  //   数码管输出应该用寄存器锁存，否则显示数据只能一闪而过
  //   指令存储器
  //   指令字
  //   contents of rom_1 (hex, n*v repeats v):
  //   201d07d0 20100001 109fc0 139fc3 8021 2012000c 24160008 26100001 3210000f 20080008 20090001 139900
  //   2709825 132020 20020022 c 1094022 1500fff9 22100001 2018000f 2188024 108700 20080008 20090001 139902
  //   2709825 132021 20020022 c 1094022 1500fff9 108702 2c9b022 12c00001 8000c07 4020 1084027 84400
  //   3508ffff 82021 20020022 c 8000c01 afa20000 23bd0004 afa40000 23bd0004 afb00000 23bd0004 afb30000
  //   23bd0004 afb40000 23bd0004 afb50000 23bd0004 afb60000 23bd0004 40000000 20160001 20140003 20150001
  //   168020 108100 2149825 132020 20020022 c 1600fffa 295a022 1680fff7 40800000 23bdfffc 8fb60000
  //   23bdfffc 8fb50000 23bdfffc 8fb40000 23bdfffc 8fb30000 23bdfffc 8fb00000 23bdfffc 8fa40000 23bdfffc
  //   8fa20000 42000018 afa20000 23bd0004 afa40000 23bd0004 afb00000 23bd0004 afb30000 23bd0004 afb40000
  //   23bd0004 afb50000 23bd0004 afb60000 23bd0004 40000000 20160002 20140003 20150001 168020 108100
  //   2149825 132020 20020022 c 1600fffa 295a022 1680fff7 40800000 23bdfffc 8fb60000 23bdfffc 8fb50000
  //   23bdfffc 8fb40000 23bdfffc 8fb30000 23bdfffc 8fb00000 23bdfffc 8fa40000 23bdfffc 8fa20000 42000018
  //   afa20000 23bd0004 afa40000 23bd0004 afb00000 23bd0004 afb30000 23bd0004 afb40000 23bd0004 afb50000
  //   23bd0004 afb60000 23bd0004 40000000 20160003 20140003 20150001 168020 108100 2149825 132020 20020022
  //   c 1600fffa 295a022 1680fff7 40800000 23bdfffc 8fb60000 23bdfffc 8fb50000 23bdfffc 8fb40000 23bdfffc
  //   8fb30000 23bdfffc 8fb00000 23bdfffc 8fa40000 23bdfffc 8fa20000 42000018
  //   可计数暂停的时钟源
  //   JMP
  //   JR
  //   OP
  //   Func
  //   MF
  //   Syscall
  //   rs
  //   rt
  //   rd
  //   Bne
  //   MemToReg
  //   MemWrite
  //   AluOP
  //   AluSrcB
  //   RegWrite
  //   JAL
  //   RegDst
  //   为方便自动评测，需要输出PC，IR，寄存器堆写如数据RDin
  //   RAM写使能MemWrite、RAM写入数据MDin等信号
  //   单周期MIPS
  //   控制与调试模块
  //   多级中断响应/返回控制模块
  //   多级中断测试信号模拟器
  //   硬件堆栈保存多级中断返回地址
endmodule

module \封装正确性测试  (
);

  wire IR1, IR2, IR3, MemW, RegW;
  wire [31:0] EX_PC, ID_PC, IF_PC, IR, LED, MDin, MDinr, MEM_PC, PC, RDin, RDinr, WB_PC;

  \单周期MIPS  \u_单周期mips_1  (
    .RegWrite(RegW), .MemWrite(MemW), .PC(PC), .IR(IR), .RDin(RDin), .MDin(MDin), .LedData(LED));  // open: IR1, IR2, IR3
  \气泡流水线  \u_气泡流水线_1  (
    .RegWrite(RegW), .MemWrite(MemW), .IF_PC(IF_PC), .ID_PC(ID_PC), .EX_PC(EX_PC), .M_PC(MEM_PC),
    .WB_PC(WB_PC), .RDin(RDinr), .MDin(MDinr), .LedData(LED));
  \单周期MIPS_单级中断  \u_单周期mips_单级中断_1  (
    .IR1(IR1), .IR2(IR2), .IR3(IR3), .RegWrite(RegW), .MemWrite(MemW), .PC(PC), .IR(IR), .RDin(RDin),
    .MDin(MDin), .LedData(LED));
  \理想流水线  \u_理想流水线_1  (
    .RegWrite(RegW), .MemWrite(MemW), .IF_PC(IF_PC), .ID_PC(ID_PC), .EX_PC(EX_PC), .M_PC(MEM_PC),
    .WB_PC(WB_PC), .RDin(RDinr), .MDin(MDinr), .LedData(LED));
  \重定向流水线  \u_重定向流水线_1  (
    .RegWrite(RegW), .MemWrite(MemW), .IF_PC(IF_PC), .ID_PC(ID_PC), .EX_PC(EX_PC), .M_PC(MEM_PC),
    .WB_PC(WB_PC), .RDin(RDinr), .MDin(MDinr), .LedData(LED));
  \单周期MIPS_多级中断  \u_单周期mips_多级中断_1  (
    .IR1(IR1), .IR2(IR2), .IR3(IR3), .RegWrite(RegW), .MemWrite(MemW), .PC(PC), .IR(IR), .RDin(RDin),
    .MDin(MDin), .LedData(LED));

  // Notes on the sheet:
  //   单周期封装测试
  //   气泡流水封装测试
  //   单周期+单级中断封装测试
  //   请检查上面封装有无位宽不匹配，引脚标签是否和连接的标签相对应，否则无法在educoder平台上正确测试
  //   理想流水封装测试
  //   重定向流水封装测试
  //   单周期+多级中断封装测试
endmodule

module \硬件堆栈  (
  input  PUSH,
  input  [31:0] Din,
  input  POP,
  input  RST,
  input  CLK,
  output [31:0] Dout
);

  wire [31:0] controlled_buffer_1_out, controlled_buffer_2_out, controlled_buffer_4_out,
       controlled_buffer_6_out, controlled_buffer_8_out, controlled_buffer_11_out, controlled_buffer_13_out,
       controlled_buffer_14_out, register_2_q, register_3_q, register_4_q, register_5_q, register_6_q,
       register_7_q, register_8_q;

  assign controlled_buffer_1_out = PUSH ? Din : 32'bz;  // Controlled_Buffer controlled_buffer_1
  Register #(.width(32), .trigger("rising"), .Select("low")) register_1 (
    .D(controlled_buffer_1_out), .Q(Dout), .clk(CLK), .clr(RST));  // open: en
  assign controlled_buffer_2_out = PUSH ? Dout : 32'bz;  // Controlled_Buffer controlled_buffer_2
  assign controlled_buffer_1_out = POP ? register_2_q : 32'bz;  // Controlled_Buffer controlled_buffer_3
  assign controlled_buffer_4_out = PUSH ? register_2_q : 32'bz;  // Controlled_Buffer controlled_buffer_4
  Register #(.width(32), .trigger("rising"), .Select("low")) register_2 (
    .D(controlled_buffer_2_out), .Q(register_2_q), .clk(CLK), .clr(RST));  // open: en
  assign controlled_buffer_2_out = POP ? register_3_q : 32'bz;  // Controlled_Buffer controlled_buffer_5
  Register #(.width(32), .trigger("rising"), .Select("low")) register_3 (
    .D(controlled_buffer_4_out), .Q(register_3_q), .clk(CLK), .clr(RST));  // open: en
  assign controlled_buffer_6_out = PUSH ? register_3_q : 32'bz;  // Controlled_Buffer controlled_buffer_6
  assign controlled_buffer_4_out = POP ? register_4_q : 32'bz;  // Controlled_Buffer controlled_buffer_7
  Register #(.width(32), .trigger("rising"), .Select("low")) register_4 (
    .D(controlled_buffer_6_out), .Q(register_4_q), .clk(CLK), .clr(RST));  // open: en
  assign controlled_buffer_8_out = PUSH ? register_4_q : 32'bz;  // Controlled_Buffer controlled_buffer_8
  assign controlled_buffer_6_out = POP ? register_5_q : 32'bz;  // Controlled_Buffer controlled_buffer_9
  Register #(.width(32), .trigger("rising"), .Select("low")) register_5 (
    .D(controlled_buffer_8_out), .Q(register_5_q), .clk(CLK), .clr(RST));  // open: en
  assign controlled_buffer_8_out = POP ? register_6_q : 32'bz;  // Controlled_Buffer controlled_buffer_10
  Register #(.width(32), .trigger("rising"), .Select("low")) register_6 (
    .D(controlled_buffer_11_out), .Q(register_6_q), .clk(CLK), .clr(RST));  // open: en
  assign controlled_buffer_11_out = PUSH ? register_5_q : 32'bz;  // Controlled_Buffer controlled_buffer_11
  assign controlled_buffer_11_out = POP ? register_7_q : 32'bz;  // Controlled_Buffer controlled_buffer_12
  assign controlled_buffer_13_out = PUSH ? register_6_q : 32'bz;  // Controlled_Buffer controlled_buffer_13
  Register #(.width(32), .trigger("rising"), .Select("low")) register_7 (
    .D(controlled_buffer_13_out), .Q(register_7_q), .clk(CLK), .clr(RST));  // open: en
  Register #(.width(32), .trigger("rising"), .Select("low")) register_8 (
    .D(controlled_buffer_14_out), .Q(register_8_q), .clk(CLK), .clr(RST));  // open: en
  assign controlled_buffer_14_out = PUSH ? register_7_q : 32'bz;  // Controlled_Buffer controlled_buffer_14
  assign controlled_buffer_13_out = POP ? register_8_q : 32'bz;  // Controlled_Buffer controlled_buffer_15
endmodule

module \嵌套中断堆栈  (
  input  PUSH,
  input  [1:0] Din,
  input  POP,
  input  RST,
  input  CLK,
  output [1:0] Dout
);

  wire [1:0] controlled_buffer_1_out, controlled_buffer_2_out, controlled_buffer_4_out,
       controlled_buffer_6_out, controlled_buffer_9_out, controlled_buffer_11_out, controlled_buffer_12_out,
       controlled_buffer_14_out, register_2_q, register_3_q, register_4_q, register_5_q, register_6_q,
       register_7_q, register_8_q;

  assign controlled_buffer_1_out = PUSH ? Din : 2'bz;  // Controlled_Buffer controlled_buffer_1
  Register #(.width(2), .trigger("rising"), .Select("low")) register_1 (
    .D(controlled_buffer_1_out), .Q(Dout), .clk(CLK), .clr(RST));  // open: en
  assign controlled_buffer_2_out = PUSH ? Dout : 2'bz;  // Controlled_Buffer controlled_buffer_2
  assign controlled_buffer_1_out = POP ? register_2_q : 2'bz;  // Controlled_Buffer controlled_buffer_3
  Register #(.width(2), .trigger("rising"), .Select("low")) register_2 (
    .D(controlled_buffer_2_out), .Q(register_2_q), .clk(CLK), .clr(RST));  // open: en
  assign controlled_buffer_4_out = PUSH ? register_2_q : 2'bz;  // Controlled_Buffer controlled_buffer_4
  assign controlled_buffer_2_out = POP ? register_3_q : 2'bz;  // Controlled_Buffer controlled_buffer_5
  Register #(.width(2), .trigger("rising"), .Select("low")) register_3 (
    .D(controlled_buffer_4_out), .Q(register_3_q), .clk(CLK), .clr(RST));  // open: en
  assign controlled_buffer_6_out = PUSH ? register_3_q : 2'bz;  // Controlled_Buffer controlled_buffer_6
  assign controlled_buffer_4_out = POP ? register_4_q : 2'bz;  // Controlled_Buffer controlled_buffer_7
  Register #(.width(2), .trigger("rising"), .Select("low")) register_4 (
    .D(controlled_buffer_6_out), .Q(register_4_q), .clk(CLK), .clr(RST));  // open: en
  assign controlled_buffer_6_out = POP ? register_5_q : 2'bz;  // Controlled_Buffer controlled_buffer_8
  assign controlled_buffer_9_out = PUSH ? register_4_q : 2'bz;  // Controlled_Buffer controlled_buffer_9
  Register #(.width(2), .trigger("rising"), .Select("low")) register_5 (
    .D(controlled_buffer_9_out), .Q(register_5_q), .clk(CLK), .clr(RST));  // open: en
  assign controlled_buffer_9_out = POP ? register_6_q : 2'bz;  // Controlled_Buffer controlled_buffer_10
  Register #(.width(2), .trigger("rising"), .Select("low")) register_6 (
    .D(controlled_buffer_11_out), .Q(register_6_q), .clk(CLK), .clr(RST));  // open: en
  assign controlled_buffer_11_out = PUSH ? register_5_q : 2'bz;  // Controlled_Buffer controlled_buffer_11
  Register #(.width(2), .trigger("rising"), .Select("low")) register_7 (
    .D(controlled_buffer_12_out), .Q(register_7_q), .clk(CLK), .clr(RST));  // open: en
  assign controlled_buffer_12_out = PUSH ? register_6_q : 2'bz;  // Controlled_Buffer controlled_buffer_12
  assign controlled_buffer_11_out = POP ? register_7_q : 2'bz;  // Controlled_Buffer controlled_buffer_13
  assign controlled_buffer_14_out = PUSH ? register_7_q : 2'bz;  // Controlled_Buffer controlled_buffer_14
  Register #(.width(2), .trigger("rising"), .Select("low")) register_8 (
    .D(controlled_buffer_14_out), .Q(register_8_q), .clk(CLK), .clr(RST));  // open: en
  assign controlled_buffer_12_out = POP ? register_8_q : 2'bz;  // Controlled_Buffer controlled_buffer_15
endmodule

module \流水线寄存器  (
  input  IN_JMP,
  input  IN_JR,
  input  IN_Beq,
  input  IN_Bne,
  input  IN_MemToReg,
  input  IN_MemWrite,
  input  [3:0] IN_AluOP,
  input  IN_AluSrcB,
  input  IN_RegWrite,
  input  In_RegDst,
  input  In_Syscall,
  input  IN_equal,
  input  [31:0] IN_R1,
  input  [31:0] IN_ALU,
  input  [31:0] IN_R2,
  input  [31:0] IN_MD,
  input  [31:0] IN_PC,
  input  [31:0] IN_IR,
  input  [31:0] IN_Imm,
  input  [4:0] IN_shamt,
  input  [25:0] IN_offset,
  input  IN_JAL,
  input  [4:0] IN_WriteReg_num,
  input  IN_BGEZ,
  input  IN_SV,
  input  IN_LB,
  input  [4:0] IN_Rs_num,
  input  [4:0] IN_Rt_num,
  input  CLR,
  input  EN,
  input  CLK,
  input  RST,
  output OUT_JMP,
  output OUT_JR,
  output OUT_Beq,
  output OUT_Bne,
  output OUT_MemToReg,
  output OUT_MemWrite,
  output [3:0] OUT_AluOP,
  output OUT_AluSrcB,
  output OUT_RegWrite,
  output OUT_RegDst,
  output OUT_Syscall,
  output OUT_equal,
  output [31:0] OUT_R1,
  output [31:0] OUT_ALU,
  output [31:0] OUT_R2,
  output [31:0] OUT_MD,
  output [31:0] OUT_PC,
  output [31:0] OUT_IR,
  output [31:0] OUT_Imm,
  output [4:0] OUT_shamt,
  output [25:0] OUT_offset,
  output OUT_JAL,
  output [4:0] OUT_WriteReg_num,
  output OUT_BGEZ,
  output OUT_SV,
  output OUT_LB,
  output [4:0] OUT_Rs_num,
  output [4:0] OUT_Rt_num
);

  wire multiplexer_1_out, multiplexer_2_out, multiplexer_3_out, multiplexer_4_out, multiplexer_5_out,
       multiplexer_6_out, multiplexer_8_out, multiplexer_9_out, multiplexer_10_out, multiplexer_11_out,
       multiplexer_12_out, multiplexer_22_out, multiplexer_24_out, multiplexer_25_out, multiplexer_26_out;
  wire [3:0] multiplexer_7_out;
  wire [4:0] multiplexer_20_out, multiplexer_23_out, multiplexer_27_out, multiplexer_28_out;
  wire [25:0] multiplexer_21_out;
  wire [31:0] multiplexer_13_out, multiplexer_14_out, multiplexer_15_out, multiplexer_16_out,
       multiplexer_17_out, multiplexer_18_out, multiplexer_19_out;

  Multiplexer #(.select(1), .width(1), .disabled("Z"), .enable("false")) multiplexer_1 (
    .in0(IN_JMP), .in1(1'b0), .out(multiplexer_1_out), .sel(CLR));
  Multiplexer #(.select(1), .width(1), .disabled("Z"), .enable("false")) multiplexer_2 (
    .in0(IN_JR), .in1(1'b0), .out(multiplexer_2_out), .sel(CLR));
  Multiplexer #(.select(1), .width(1), .disabled("Z"), .enable("false")) multiplexer_3 (
    .in0(IN_Beq), .in1(1'b0), .out(multiplexer_3_out), .sel(CLR));
  Multiplexer #(.select(1), .width(1), .disabled("Z"), .enable("false")) multiplexer_4 (
    .in0(IN_Bne), .in1(1'b0), .out(multiplexer_4_out), .sel(CLR));
  Multiplexer #(.select(1), .width(1), .disabled("Z"), .enable("false")) multiplexer_5 (
    .in0(IN_MemToReg), .in1(1'b0), .out(multiplexer_5_out), .sel(CLR));
  Multiplexer #(.select(1), .width(1), .disabled("Z"), .enable("false")) multiplexer_6 (
    .in0(IN_MemWrite), .in1(1'b0), .out(multiplexer_6_out), .sel(CLR));
  Multiplexer #(.select(1), .width(4), .disabled("Z"), .enable("false")) multiplexer_7 (
    .in0(IN_AluOP), .in1(4'b0000), .out(multiplexer_7_out), .sel(CLR));
  Multiplexer #(.select(1), .width(1), .disabled("Z"), .enable("false")) multiplexer_8 (
    .in0(IN_AluSrcB), .in1(1'b0), .out(multiplexer_8_out), .sel(CLR));
  Multiplexer #(.select(1), .width(1), .disabled("Z"), .enable("false")) multiplexer_9 (
    .in0(IN_RegWrite), .in1(1'b0), .out(multiplexer_9_out), .sel(CLR));
  Multiplexer #(.select(1), .width(1), .disabled("Z"), .enable("false")) multiplexer_10 (
    .in0(In_RegDst), .in1(1'b0), .out(multiplexer_10_out), .sel(CLR));
  Multiplexer #(.select(1), .width(1), .disabled("Z"), .enable("false")) multiplexer_11 (
    .in0(In_Syscall), .in1(1'b0), .out(multiplexer_11_out), .sel(CLR));
  Multiplexer #(.select(1), .width(1), .disabled("Z"), .enable("false")) multiplexer_12 (
    .in0(IN_equal), .in1(1'b0), .out(multiplexer_12_out), .sel(CLR));
  Multiplexer #(.select(1), .width(32), .disabled("Z"), .enable("false")) multiplexer_13 (
    .in0(IN_R1), .in1({32{1'b0}}), .out(multiplexer_13_out), .sel(CLR));
  Multiplexer #(.select(1), .width(32), .disabled("Z"), .enable("false")) multiplexer_14 (
    .in0(IN_ALU), .in1({32{1'b0}}), .out(multiplexer_14_out), .sel(CLR));
  Multiplexer #(.select(1), .width(32), .disabled("Z"), .enable("false")) multiplexer_15 (
    .in0(IN_R2), .in1({32{1'b0}}), .out(multiplexer_15_out), .sel(CLR));
  Multiplexer #(.select(1), .width(32), .disabled("Z"), .enable("false")) multiplexer_16 (
    .in0(IN_MD), .in1({32{1'b0}}), .out(multiplexer_16_out), .sel(CLR));
  Multiplexer #(.select(1), .width(32), .disabled("Z"), .enable("false")) multiplexer_17 (
    .in0(IN_PC), .in1({32{1'b0}}), .out(multiplexer_17_out), .sel(CLR));
  Multiplexer #(.select(1), .width(32), .disabled("Z"), .enable("false")) multiplexer_18 (
    .in0(IN_IR), .in1({32{1'b0}}), .out(multiplexer_18_out), .sel(CLR));
  Multiplexer #(.select(1), .width(32), .disabled("Z"), .enable("false")) multiplexer_19 (
    .in0(IN_Imm), .in1({32{1'b0}}), .out(multiplexer_19_out), .sel(CLR));
  Multiplexer #(.select(1), .width(5), .disabled("Z"), .enable("false")) multiplexer_20 (
    .in0(IN_shamt), .in1({5{1'b0}}), .out(multiplexer_20_out), .sel(CLR));
  Multiplexer #(.select(1), .width(26), .disabled("Z"), .enable("false")) multiplexer_21 (
    .in0(IN_offset), .in1({26{1'b0}}), .out(multiplexer_21_out), .sel(CLR));
  Multiplexer #(.select(1), .width(1), .disabled("Z"), .enable("false")) multiplexer_22 (
    .in0(IN_JAL), .in1(1'b0), .out(multiplexer_22_out), .sel(CLR));
  Multiplexer #(.select(1), .width(5), .disabled("Z"), .enable("false")) multiplexer_23 (
    .in0(IN_WriteReg_num), .in1({5{1'b0}}), .out(multiplexer_23_out), .sel(CLR));
  Multiplexer #(.select(1), .width(1), .disabled("Z"), .enable("false")) multiplexer_24 (
    .in0(IN_BGEZ), .in1(1'b0), .out(multiplexer_24_out), .sel(CLR));
  Multiplexer #(.select(1), .width(1), .disabled("Z"), .enable("false")) multiplexer_25 (
    .in0(IN_SV), .in1(1'b0), .out(multiplexer_25_out), .sel(CLR));
  Multiplexer #(.select(1), .width(1), .disabled("Z"), .enable("false")) multiplexer_26 (
    .in0(IN_LB), .in1(1'b0), .out(multiplexer_26_out), .sel(CLR));
  Multiplexer #(.select(1), .width(5), .disabled("Z"), .enable("false")) multiplexer_27 (
    .in0(IN_Rs_num), .in1({5{1'b0}}), .out(multiplexer_27_out), .sel(CLR));
  Multiplexer #(.select(1), .width(5), .disabled("Z"), .enable("false")) multiplexer_28 (
    .in0(IN_Rt_num), .in1({5{1'b0}}), .out(multiplexer_28_out), .sel(CLR));
  Register #(.width(1), .trigger("rising"), .Select("low")) MemToReg (
    .D(multiplexer_1_out), .en(EN), .Q(OUT_JMP), .clk(CLK), .clr(RST));
  Register #(.width(1), .trigger("rising"), .Select("low")) MemToReg_2 (
    .D(multiplexer_2_out), .en(EN), .Q(OUT_JR), .clk(CLK), .clr(RST));
  Register #(.width(1), .trigger("rising"), .Select("low")) MemToReg_3 (
    .D(multiplexer_3_out), .en(EN), .Q(OUT_Beq), .clk(CLK), .clr(RST));
  Register #(.width(1), .trigger("rising"), .Select("low")) MemToReg_4 (
    .D(multiplexer_4_out), .en(EN), .Q(OUT_Bne), .clk(CLK), .clr(RST));
  Register #(.width(1), .trigger("rising"), .Select("low")) MemToReg_5 (
    .D(multiplexer_5_out), .en(EN), .Q(OUT_MemToReg), .clk(CLK), .clr(RST));
  Register #(.width(1), .trigger("rising"), .Select("low")) MemWrite (
    .D(multiplexer_6_out), .en(EN), .Q(OUT_MemWrite), .clk(CLK), .clr(RST));
  Register #(.width(4), .trigger("rising"), .Select("low")) AluOP (
    .D(multiplexer_7_out), .en(EN), .Q(OUT_AluOP), .clk(CLK), .clr(RST));
  Register #(.width(1), .trigger("rising"), .Select("low")) ALuSrcB (
    .D(multiplexer_8_out), .en(EN), .Q(OUT_AluSrcB), .clk(CLK), .clr(RST));
  Register #(.width(1), .trigger("rising"), .Select("low")) RegWrite (
    .D(multiplexer_9_out), .en(EN), .Q(OUT_RegWrite), .clk(CLK), .clr(RST));
  Register #(.width(1), .trigger("rising"), .Select("low")) RegDst (
    .D(multiplexer_10_out), .en(EN), .Q(OUT_RegDst), .clk(CLK), .clr(RST));
  Register #(.width(1), .trigger("rising"), .Select("low")) Syscall (
    .D(multiplexer_11_out), .en(EN), .Q(OUT_Syscall), .clk(CLK), .clr(RST));
  Register #(.width(1), .trigger("rising"), .Select("low")) equal (
    .D(multiplexer_12_out), .en(EN), .Q(OUT_equal), .clk(CLK), .clr(RST));
  Register #(.width(32), .trigger("rising"), .Select("low")) R1 (
    .D(multiplexer_13_out), .en(EN), .Q(OUT_R1), .clk(CLK), .clr(RST));
  Register #(.width(32), .trigger("rising"), .Select("low")) ALU (
    .D(multiplexer_14_out), .en(EN), .Q(OUT_ALU), .clk(CLK), .clr(RST));
  Register #(.width(32), .trigger("rising"), .Select("low")) R2 (
    .D(multiplexer_15_out), .en(EN), .Q(OUT_R2), .clk(CLK), .clr(RST));
  Register #(.width(32), .trigger("rising"), .Select("low")) MD (
    .D(multiplexer_16_out), .en(EN), .Q(OUT_MD), .clk(CLK), .clr(RST));
  Register #(.width(32), .trigger("rising"), .Select("low")) PC (
    .D(multiplexer_17_out), .en(EN), .Q(OUT_PC), .clk(CLK), .clr(RST));
  Register #(.width(32), .trigger("rising"), .Select("low")) IR (
    .D(multiplexer_18_out), .en(EN), .Q(OUT_IR), .clk(CLK), .clr(RST));
  Register #(.width(32), .trigger("rising"), .Select("low")) Imm (
    .D(multiplexer_19_out), .en(EN), .Q(OUT_Imm), .clk(CLK), .clr(RST));
  Register #(.width(5), .trigger("rising"), .Select("low")) shamt (
    .D(multiplexer_20_out), .en(EN), .Q(OUT_shamt), .clk(CLK), .clr(RST));
  Register #(.width(26), .trigger("rising"), .Select("low")) offset (
    .D(multiplexer_21_out), .en(EN), .Q(OUT_offset), .clk(CLK), .clr(RST));
  Register #(.width(1), .trigger("rising"), .Select("low")) JAL (
    .D(multiplexer_22_out), .en(EN), .Q(OUT_JAL), .clk(CLK), .clr(RST));
  Register #(.width(5), .trigger("rising"), .Select("low")) MemToReg_6 (
    .D(multiplexer_23_out), .en(EN), .Q(OUT_WriteReg_num), .clk(CLK), .clr(RST));
  Register #(.width(1), .trigger("rising"), .Select("low")) BGEZ (
    .D(multiplexer_24_out), .en(EN), .Q(OUT_BGEZ), .clk(CLK), .clr(RST));
  Register #(.width(1), .trigger("rising"), .Select("low")) SV (
    .D(multiplexer_25_out), .en(EN), .Q(OUT_SV), .clk(CLK), .clr(RST));
  Register #(.width(1), .trigger("rising"), .Select("low")) LB (
    .D(multiplexer_26_out), .en(EN), .Q(OUT_LB), .clk(CLK), .clr(RST));
  Register #(.width(5), .trigger("rising"), .Select("low")) Rs_num (
    .D(multiplexer_27_out), .en(EN), .Q(OUT_Rs_num), .clk(CLK), .clr(RST));
  Register #(.width(5), .trigger("rising"), .Select("low")) Rt_num (
    .D(multiplexer_28_out), .en(EN), .Q(OUT_Rt_num), .clk(CLK), .clr(RST));
endmodule

module \寄存器相关  (
  input  OP0,
  input  OP1,
  input  OP2,
  input  OP3,
  input  OP4,
  input  OP5,
  input  F0,
  input  F1,
  input  F2,
  input  F3,
  input  F4,
  input  F5,
  output RsUsed,
  output RtUsed
);

  wire and_1_out, and_2_out, and_3_out, and_4_out, and_5_out, and_6_out, and_7_out, and_8_out, and_9_out,
       and_10_out, and_11_out, and_12_out, and_13_out, and_14_out, and_15_out, and_16_out, and_17_out,
       and_18_out, and_19_out, and_20_out, and_21_out, and_22_out, and_23_out, and_24_out, and_25_out,
       and_26_out, and_27_out, and_28_out, and_29_out, and_30_out, and_31_out, and_32_out, and_33_out,
       and_34_out, and_35_out, and_36_out, and_37_out, and_38_out, and_39_out, not_1_out, not_2_out,
       not_3_out, not_4_out, not_5_out, not_6_out, not_7_out, not_8_out, not_9_out, not_10_out, not_11_out,
       not_12_out, not_13_out, not_14_out, not_15_out, not_16_out, not_17_out, not_18_out, not_19_out,
       not_20_out, not_21_out, not_22_out, not_23_out, not_24_out, not_25_out, not_26_out, not_27_out,
       not_28_out, not_29_out, not_30_out, not_31_out, not_32_out, not_33_out, not_34_out, not_35_out,
       not_36_out, not_37_out, not_38_out, not_39_out, not_40_out, not_41_out, not_42_out, not_43_out,
       not_44_out, not_45_out, not_46_out, not_47_out, not_48_out, not_49_out, not_50_out, not_51_out,
       not_52_out, not_53_out, not_54_out, not_55_out, not_56_out, not_57_out, not_58_out, not_59_out,
       not_60_out, not_61_out, not_62_out, not_63_out, not_64_out, not_65_out, not_66_out, not_67_out,
       not_68_out, not_69_out, not_70_out, not_71_out, not_72_out, not_73_out, not_74_out, not_75_out,
       not_76_out, not_77_out, not_78_out, not_79_out, not_80_out, not_81_out, not_82_out, not_83_out,
       not_84_out, not_85_out, not_86_out, not_87_out, not_88_out, not_89_out, not_90_out, not_91_out,
       not_92_out, not_93_out, not_94_out, not_95_out, not_96_out, not_97_out, not_98_out, not_99_out,
       not_100_out, not_101_out, not_102_out, not_103_out, not_104_out, not_105_out, not_106_out,
       not_107_out, not_108_out, not_109_out, not_110_out, not_111_out, not_112_out, not_113_out,
       not_114_out, not_115_out, not_116_out, not_117_out, not_118_out, not_119_out, not_120_out,
       not_121_out, not_122_out, not_123_out, not_124_out, not_125_out, not_126_out, not_127_out,
       not_128_out, not_129_out, not_130_out, not_131_out, not_132_out, not_133_out, not_134_out,
       not_135_out, not_136_out, not_137_out, not_138_out, not_139_out, not_140_out, not_141_out,
       not_142_out, not_143_out, not_144_out, not_145_out, not_146_out, not_147_out, not_148_out,
       not_149_out, not_150_out, not_151_out, not_152_out, not_153_out, not_154_out, not_155_out,
       not_156_out, not_157_out, not_158_out, not_159_out, not_160_out, not_161_out, not_162_out,
       not_163_out, not_164_out, not_165_out, not_166_out, not_167_out, not_168_out, not_169_out,
       not_170_out, not_171_out, not_172_out, not_173_out, not_174_out, not_175_out, not_176_out,
       not_177_out, not_178_out, not_179_out, not_180_out, not_181_out, not_182_out, not_183_out,
       not_184_out, not_185_out, not_186_out, not_187_out, not_188_out, not_189_out, not_190_out,
       not_191_out, not_192_out, not_193_out, not_194_out, not_195_out, not_196_out, not_197_out,
       not_198_out, not_199_out, not_200_out, not_201_out, not_202_out, not_203_out, not_204_out,
       not_205_out, not_206_out, not_207_out, not_208_out, not_209_out, not_210_out, not_211_out,
       not_212_out, not_213_out, not_214_out, not_215_out, not_216_out, not_217_out, not_218_out,
       not_219_out, not_220_out, not_221_out, not_222_out, not_223_out, not_224_out, not_225_out,
       not_226_out, not_227_out, not_228_out, not_229_out, not_230_out, not_231_out, not_232_out,
       not_233_out, not_234_out, not_235_out, not_236_out, not_237_out, not_238_out, not_239_out,
       not_240_out, not_241_out, not_242_out, not_243_out, not_244_out, not_245_out, not_246_out,
       not_247_out, not_248_out, not_249_out, not_250_out, not_251_out, not_252_out, not_253_out,
       not_254_out, not_255_out, not_256_out, not_257_out, not_258_out, not_259_out, not_260_out,
       not_261_out, not_262_out, not_263_out, not_264_out, not_265_out, not_266_out, not_267_out,
       not_268_out, not_269_out, not_270_out, not_271_out, not_272_out, not_273_out, not_274_out,
       not_275_out, not_276_out, not_277_out, not_278_out, not_279_out, not_280_out, not_281_out,
       not_282_out, not_283_out, not_284_out, not_285_out, not_286_out, not_287_out, not_288_out,
       not_289_out, not_290_out, not_291_out, not_292_out;

  not not_1 (not_1_out, OP5);
  not not_2 (not_2_out, OP4);
  not not_3 (not_3_out, OP3);
  not not_4 (not_4_out, OP2);
  not not_5 (not_5_out, OP1);
  not not_6 (not_6_out, OP0);
  not not_7 (not_7_out, F4);
  not not_8 (not_8_out, F3);
  not not_9 (not_9_out, F2);
  not not_10 (not_10_out, F1);
  not not_11 (not_11_out, F0);
  not not_12 (not_12_out, OP5);
  not not_13 (not_13_out, OP4);
  not not_14 (not_14_out, OP3);
  not not_15 (not_15_out, OP2);
  not not_16 (not_16_out, OP1);
  not not_17 (not_17_out, OP0);
  not not_18 (not_18_out, F4);
  not not_19 (not_19_out, F3);
  not not_20 (not_20_out, F2);
  not not_21 (not_21_out, F1);
  not not_22 (not_22_out, OP5);
  not not_23 (not_23_out, OP4);
  not not_24 (not_24_out, OP3);
  not not_25 (not_25_out, OP2);
  not not_26 (not_26_out, OP1);
  not not_27 (not_27_out, OP0);
  not not_28 (not_28_out, F4);
  not not_29 (not_29_out, F3);
  not not_30 (not_30_out, F2);
  not not_31 (not_31_out, F0);
  not not_32 (not_32_out, OP5);
  not not_33 (not_33_out, OP4);
  not not_34 (not_34_out, OP3);
  not not_35 (not_35_out, OP2);
  not not_36 (not_36_out, OP1);
  not not_37 (not_37_out, OP0);
  not not_38 (not_38_out, F4);
  not not_39 (not_39_out, F3);
  not not_40 (not_40_out, F1);
  not not_41 (not_41_out, F0);
  not not_42 (not_42_out, OP5);
  not not_43 (not_43_out, OP4);
  not not_44 (not_44_out, OP3);
  not not_45 (not_45_out, OP2);
  not not_46 (not_46_out, OP1);
  not not_47 (not_47_out, OP0);
  not not_48 (not_48_out, F4);
  not not_49 (not_49_out, F3);
  not not_50 (not_50_out, F1);
  not not_51 (not_51_out, OP5);
  not not_52 (not_52_out, OP4);
  not not_53 (not_53_out, OP3);
  not not_54 (not_54_out, OP2);
  not not_55 (not_55_out, OP1);
  not not_56 (not_56_out, OP0);
  not not_57 (not_57_out, F4);
  not not_58 (not_58_out, F3);
  not not_59 (not_59_out, OP5);
  not not_60 (not_60_out, OP4);
  not not_61 (not_61_out, OP3);
  not not_62 (not_62_out, OP2);
  not not_63 (not_63_out, OP1);
  not not_64 (not_64_out, OP0);
  not not_65 (not_65_out, F4);
  not not_66 (not_66_out, F2);
  not not_67 (not_67_out, F0);
  not not_68 (not_68_out, OP5);
  not not_69 (not_69_out, OP4);
  not not_70 (not_70_out, OP3);
  not not_71 (not_71_out, OP2);
  not not_72 (not_72_out, OP1);
  not not_73 (not_73_out, OP0);
  not not_74 (not_74_out, F4);
  not not_75 (not_75_out, F2);
  not not_76 (not_76_out, OP5);
  not not_77 (not_77_out, OP4);
  not not_78 (not_78_out, OP3);
  not not_79 (not_79_out, OP2);
  not not_80 (not_80_out, OP1);
  not not_81 (not_81_out, OP0);
  not not_82 (not_82_out, F5);
  not not_83 (not_83_out, F4);
  not not_84 (not_84_out, F2);
  not not_85 (not_85_out, F1);
  not not_86 (not_86_out, F0);
  not not_87 (not_87_out, OP5);
  not not_88 (not_88_out, OP4);
  not not_89 (not_89_out, OP3);
  not not_90 (not_90_out, OP2);
  not not_91 (not_91_out, OP1);
  not not_92 (not_92_out, OP0);
  not not_93 (not_93_out, F5);
  not not_94 (not_94_out, F4);
  not not_95 (not_95_out, F1);
  not not_96 (not_96_out, F0);
  not not_97 (not_97_out, OP5);
  not not_98 (not_98_out, OP4);
  not not_99 (not_99_out, OP3);
  not not_100 (not_100_out, OP1);
  not not_101 (not_101_out, OP0);
  not not_102 (not_102_out, OP5);
  not not_103 (not_103_out, OP4);
  not not_104 (not_104_out, OP3);
  not not_105 (not_105_out, OP1);
  not not_106 (not_106_out, OP5);
  not not_107 (not_107_out, OP4);
  not not_108 (not_108_out, OP2);
  not not_109 (not_109_out, OP1);
  not not_110 (not_110_out, OP0);
  not not_111 (not_111_out, OP5);
  not not_112 (not_112_out, OP4);
  not not_113 (not_113_out, OP1);
  not not_114 (not_114_out, OP0);
  not not_115 (not_115_out, OP5);
  not not_116 (not_116_out, OP4);
  not not_117 (not_117_out, OP2);
  not not_118 (not_118_out, OP1);
  not not_119 (not_119_out, OP5);
  not not_120 (not_120_out, OP4);
  not not_121 (not_121_out, OP2);
  not not_122 (not_122_out, OP0);
  not not_123 (not_123_out, OP5);
  not not_124 (not_124_out, OP4);
  not not_125 (not_125_out, OP1);
  not not_126 (not_126_out, OP4);
  not not_127 (not_127_out, OP3);
  not not_128 (not_128_out, OP2);
  not not_129 (not_129_out, OP4);
  not not_130 (not_130_out, OP2);
  not not_131 (not_131_out, OP5);
  not not_132 (not_132_out, OP4);
  not not_133 (not_133_out, OP3);
  not not_134 (not_134_out, OP2);
  not not_135 (not_135_out, OP1);
  not not_136 (not_136_out, OP0);
  not not_137 (not_137_out, F5);
  not not_138 (not_138_out, F4);
  not not_139 (not_139_out, F3);
  not not_140 (not_140_out, F0);
  not not_141 (not_141_out, OP5);
  not not_142 (not_142_out, OP4);
  not not_143 (not_143_out, OP0);
  not not_144 (not_144_out, OP4);
  not not_145 (not_145_out, OP3);
  not not_146 (not_146_out, OP2);
  not not_147 (not_147_out, OP1);
  not not_148 (not_148_out, OP0);
  not not_149 (not_149_out, OP5);
  not not_150 (not_150_out, OP4);
  not not_151 (not_151_out, OP3);
  not not_152 (not_152_out, OP2);
  not not_153 (not_153_out, OP1);
  not not_154 (not_154_out, OP5);
  not not_155 (not_155_out, OP4);
  not not_156 (not_156_out, OP3);
  not not_157 (not_157_out, OP2);
  not not_158 (not_158_out, OP1);
  not not_159 (not_159_out, OP0);
  not not_160 (not_160_out, F5);
  not not_161 (not_161_out, F4);
  not not_162 (not_162_out, F3);
  not not_163 (not_163_out, F2);
  not not_164 (not_164_out, F1);
  not not_165 (not_165_out, F0);
  not not_166 (not_166_out, OP5);
  not not_167 (not_167_out, OP4);
  not not_168 (not_168_out, OP3);
  not not_169 (not_169_out, OP2);
  not not_170 (not_170_out, OP1);
  not not_171 (not_171_out, OP0);
  not not_172 (not_172_out, F5);
  not not_173 (not_173_out, F4);
  not not_174 (not_174_out, F3);
  not not_175 (not_175_out, F2);
  not not_176 (not_176_out, OP5);
  not not_177 (not_177_out, OP4);
  not not_178 (not_178_out, OP3);
  not not_179 (not_179_out, OP2);
  not not_180 (not_180_out, OP1);
  not not_181 (not_181_out, OP0);
  not not_182 (not_182_out, F5);
  not not_183 (not_183_out, F4);
  not not_184 (not_184_out, F3);
  not not_185 (not_185_out, F2);
  not not_186 (not_186_out, F0);
  not not_187 (not_187_out, OP5);
  not not_188 (not_188_out, OP4);
  not not_189 (not_189_out, OP3);
  not not_190 (not_190_out, OP2);
  not not_191 (not_191_out, OP1);
  not not_192 (not_192_out, OP0);
  not not_193 (not_193_out, F4);
  not not_194 (not_194_out, F3);
  not not_195 (not_195_out, F2);
  not not_196 (not_196_out, F1);
  not not_197 (not_197_out, F0);
  not not_198 (not_198_out, OP5);
  not not_199 (not_199_out, OP4);
  not not_200 (not_200_out, OP3);
  not not_201 (not_201_out, OP2);
  not not_202 (not_202_out, OP1);
  not not_203 (not_203_out, OP0);
  not not_204 (not_204_out, F4);
  not not_205 (not_205_out, F3);
  not not_206 (not_206_out, F2);
  not not_207 (not_207_out, F1);
  not not_208 (not_208_out, OP5);
  not not_209 (not_209_out, OP4);
  not not_210 (not_210_out, OP3);
  not not_211 (not_211_out, OP2);
  not not_212 (not_212_out, OP1);
  not not_213 (not_213_out, OP0);
  not not_214 (not_214_out, F4);
  not not_215 (not_215_out, F3);
  not not_216 (not_216_out, F2);
  not not_217 (not_217_out, F0);
  not not_218 (not_218_out, OP5);
  not not_219 (not_219_out, OP4);
  not not_220 (not_220_out, OP3);
  not not_221 (not_221_out, OP2);
  not not_222 (not_222_out, OP1);
  not not_223 (not_223_out, OP0);
  not not_224 (not_224_out, F4);
  not not_225 (not_225_out, F3);
  not not_226 (not_226_out, F1);
  not not_227 (not_227_out, F0);
  not not_228 (not_228_out, OP5);
  not not_229 (not_229_out, OP4);
  not not_230 (not_230_out, OP3);
  not not_231 (not_231_out, OP2);
  not not_232 (not_232_out, OP1);
  not not_233 (not_233_out, OP0);
  not not_234 (not_234_out, F4);
  not not_235 (not_235_out, F3);
  not not_236 (not_236_out, F1);
  not not_237 (not_237_out, OP5);
  not not_238 (not_238_out, OP4);
  not not_239 (not_239_out, OP3);
  not not_240 (not_240_out, OP2);
  not not_241 (not_241_out, OP1);
  not not_242 (not_242_out, OP0);
  not not_243 (not_243_out, F4);
  not not_244 (not_244_out, F3);
  not not_245 (not_245_out, OP5);
  not not_246 (not_246_out, OP4);
  not not_247 (not_247_out, OP3);
  not not_248 (not_248_out, OP2);
  not not_249 (not_249_out, OP1);
  not not_250 (not_250_out, OP0);
  not not_251 (not_251_out, F4);
  not not_252 (not_252_out, F2);
  not not_253 (not_253_out, F0);
  not not_254 (not_254_out, OP5);
  not not_255 (not_255_out, OP4);
  not not_256 (not_256_out, OP3);
  not not_257 (not_257_out, OP2);
  not not_258 (not_258_out, OP1);
  not not_259 (not_259_out, OP0);
  not not_260 (not_260_out, F4);
  not not_261 (not_261_out, F2);
  not not_262 (not_262_out, OP5);
  not not_263 (not_263_out, OP4);
  not not_264 (not_264_out, OP3);
  not not_265 (not_265_out, OP2);
  not not_266 (not_266_out, OP1);
  not not_267 (not_267_out, OP0);
  not not_268 (not_268_out, F5);
  not not_269 (not_269_out, F4);
  not not_270 (not_270_out, F1);
  not not_271 (not_271_out, F0);
  not not_272 (not_272_out, OP5);
  not not_273 (not_273_out, OP4);
  not not_274 (not_274_out, OP3);
  not not_275 (not_275_out, OP1);
  not not_276 (not_276_out, OP0);
  not not_277 (not_277_out, OP5);
  not not_278 (not_278_out, OP4);
  not not_279 (not_279_out, OP3);
  not not_280 (not_280_out, OP1);
  not not_281 (not_281_out, OP4);
  not not_282 (not_282_out, OP2);
  not not_283 (not_283_out, OP5);
  not not_284 (not_284_out, OP4);
  not not_285 (not_285_out, OP3);
  not not_286 (not_286_out, OP2);
  not not_287 (not_287_out, OP1);
  not not_288 (not_288_out, OP0);
  not not_289 (not_289_out, F5);
  not not_290 (not_290_out, F4);
  not not_291 (not_291_out, F3);
  not not_292 (not_292_out, F0);
  and and_1 (and_1_out, not_1_out, not_2_out, not_3_out, not_4_out, not_5_out, not_6_out, F5, not_7_out, not_8_out, not_9_out, not_10_out, not_11_out);
  and and_2 (and_2_out, not_12_out, not_13_out, not_14_out, not_15_out, not_16_out, not_17_out, F5, not_18_out, not_19_out, not_20_out, not_21_out, F0);
  and and_3 (and_3_out, not_22_out, not_23_out, not_24_out, not_25_out, not_26_out, not_27_out, F5, not_28_out, not_29_out, not_30_out, F1, not_31_out);
  and and_4 (and_4_out, not_32_out, not_33_out, not_34_out, not_35_out, not_36_out, not_37_out, F5, not_38_out, not_39_out, F2, not_40_out, not_41_out);
  and and_5 (and_5_out, not_42_out, not_43_out, not_44_out, not_45_out, not_46_out, not_47_out, F5, not_48_out, not_49_out, F2, not_50_out, F0);
  and and_6 (and_6_out, not_51_out, not_52_out, not_53_out, not_54_out, not_55_out, not_56_out, F5, not_57_out, not_58_out, F2, F1, F0);
  and and_7 (and_7_out, not_59_out, not_60_out, not_61_out, not_62_out, not_63_out, not_64_out, F5, not_65_out, F3, not_66_out, F1, not_67_out);
  and and_8 (and_8_out, not_68_out, not_69_out, not_70_out, not_71_out, not_72_out, not_73_out, F5, not_74_out, F3, not_75_out, F1, F0);
  and and_9 (and_9_out, not_76_out, not_77_out, not_78_out, not_79_out, not_80_out, not_81_out, not_82_out, not_83_out, F3, not_84_out, not_85_out, not_86_out);
  and and_10 (and_10_out, not_87_out, not_88_out, not_89_out, not_90_out, not_91_out, not_92_out, not_93_out, not_94_out, F3, F2, not_95_out, not_96_out);
  and and_11 (and_11_out, not_97_out, not_98_out, not_99_out, OP2, not_100_out, not_101_out);
  and and_12 (and_12_out, not_102_out, not_103_out, not_104_out, OP2, not_105_out, OP0);
  and and_13 (and_13_out, not_106_out, not_107_out, OP3, not_108_out, not_109_out, not_110_out);
  and and_14 (and_14_out, not_111_out, not_112_out, OP3, OP2, not_113_out, not_114_out);
  and and_15 (and_15_out, not_115_out, not_116_out, OP3, not_117_out, not_118_out, OP0);
  and and_16 (and_16_out, not_119_out, not_120_out, OP3, not_121_out, OP1, not_122_out);
  and and_17 (and_17_out, not_123_out, not_124_out, OP3, OP2, not_125_out, OP0);
  and and_18 (and_18_out, OP5, not_126_out, not_127_out, not_128_out, OP1, OP0);
  and and_19 (and_19_out, OP5, not_129_out, OP3, not_130_out, OP1, OP0);
  and and_20 (and_20_out, not_131_out, not_132_out, not_133_out, not_134_out, not_135_out, not_136_out, not_137_out, not_138_out, not_139_out, F2, F1, not_140_out);
  and and_21 (and_21_out, not_141_out, not_142_out, OP3, OP2, OP1, not_143_out);
  and and_22 (and_22_out, OP5, not_144_out, not_145_out, not_146_out, not_147_out, not_148_out);
  and and_23 (and_23_out, not_149_out, not_150_out, not_151_out, not_152_out, not_153_out, OP0);
  and and_24 (and_24_out, not_154_out, not_155_out, not_156_out, not_157_out, not_158_out, not_159_out, not_160_out, not_161_out, not_162_out, not_163_out, not_164_out, not_165_out);
  and and_25 (and_25_out, not_166_out, not_167_out, not_168_out, not_169_out, not_170_out, not_171_out, not_172_out, not_173_out, not_174_out, not_175_out, F1, F0);
  and and_26 (and_26_out, not_176_out, not_177_out, not_178_out, not_179_out, not_180_out, not_181_out, not_182_out, not_183_out, not_184_out, not_185_out, F1, not_186_out);
  and and_27 (and_27_out, not_187_out, not_188_out, not_189_out, not_190_out, not_191_out, not_192_out, F5, not_193_out, not_194_out, not_195_out, not_196_out, not_197_out);
  and and_28 (and_28_out, not_198_out, not_199_out, not_200_out, not_201_out, not_202_out, not_203_out, F5, not_204_out, not_205_out, not_206_out, not_207_out, F0);
  and and_29 (and_29_out, not_208_out, not_209_out, not_210_out, not_211_out, not_212_out, not_213_out, F5, not_214_out, not_215_out, not_216_out, F1, not_217_out);
  and and_30 (and_30_out, not_218_out, not_219_out, not_220_out, not_221_out, not_222_out, not_223_out, F5, not_224_out, not_225_out, F2, not_226_out, not_227_out);
  and and_31 (and_31_out, not_228_out, not_229_out, not_230_out, not_231_out, not_232_out, not_233_out, F5, not_234_out, not_235_out, F2, not_236_out, F0);
  and and_32 (and_32_out, not_237_out, not_238_out, not_239_out, not_240_out, not_241_out, not_242_out, F5, not_243_out, not_244_out, F2, F1, F0);
  and and_33 (and_33_out, not_245_out, not_246_out, not_247_out, not_248_out, not_249_out, not_250_out, F5, not_251_out, F3, not_252_out, F1, not_253_out);
  and and_34 (and_34_out, not_254_out, not_255_out, not_256_out, not_257_out, not_258_out, not_259_out, F5, not_260_out, F3, not_261_out, F1, F0);
  and and_35 (and_35_out, not_262_out, not_263_out, not_264_out, not_265_out, not_266_out, not_267_out, not_268_out, not_269_out, F3, F2, not_270_out, not_271_out);
  and and_36 (and_36_out, not_272_out, not_273_out, not_274_out, OP2, not_275_out, not_276_out);
  and and_37 (and_37_out, not_277_out, not_278_out, not_279_out, OP2, not_280_out, OP0);
  and and_38 (and_38_out, OP5, not_281_out, OP3, not_282_out, OP1, OP0);
  and and_39 (and_39_out, not_283_out, not_284_out, not_285_out, not_286_out, not_287_out, not_288_out, not_289_out, not_290_out, not_291_out, F2, F1, not_292_out);
  or or_1 (RsUsed, and_1_out, and_2_out, and_3_out, and_4_out, and_5_out, and_6_out, and_7_out, and_8_out, and_9_out, and_10_out, and_11_out, and_12_out, and_13_out, and_14_out, and_15_out, and_16_out, and_17_out, and_18_out, and_19_out, and_20_out, and_21_out, and_22_out, and_23_out);
  or or_2 (RtUsed, and_24_out, and_25_out, and_26_out, and_27_out, and_28_out, and_29_out, and_30_out, and_31_out, and_32_out, and_33_out, and_34_out, and_35_out, and_36_out, and_37_out, and_38_out, and_39_out);
endmodule

module \数据相关处理  (
  input  [31:0] Instruction,
  input  EX_RegWrite,
  input  [4:0] R1_num,
  input  [4:0] EX_WriteReg_num,
  input  MEM_RegWrite,
  input  [4:0] MEM_WriteReg_num,
  input  [4:0] R2_num,
  output DataHazard
);

  wire and_1_out, and_2_out, and_3_out, and_4_out, comparator_1_eq, comparator_2_eq, comparator_3_eq,
       comparator_4_eq, comparator_5_eq, comparator_6_eq, \寄存器相关_1_rsused , \寄存器相关_1_rtused ;

  \寄存器相关  \u_寄存器相关_1  (
    .OP0(Instruction[26]), .OP1(Instruction[27]), .OP2(Instruction[28]), .OP3(Instruction[29]),
    .OP4(Instruction[30]), .OP5(Instruction[31]), .F0(Instruction[0]), .F1(Instruction[1]),
    .F2(Instruction[2]), .F3(Instruction[3]), .F4(Instruction[4]), .F5(Instruction[5]),
    .RsUsed(\寄存器相关_1_rsused ), .RtUsed(\寄存器相关_1_rtused ));
  Comparator #(.width(5), .mode("unsigned")) comparator_1 (
    .a(R1_num), .b({5{1'b0}}), .eq(comparator_1_eq));  // open: gt, lt
  Comparator #(.width(5), .mode("unsigned")) comparator_2 (
    .a({5{1'b0}}), .b(R2_num), .eq(comparator_2_eq));  // open: gt, lt
  Comparator #(.width(5), .mode("unsigned")) comparator_3 (
    .a(R1_num), .b(EX_WriteReg_num), .eq(comparator_3_eq));  // open: gt, lt
  Comparator #(.width(5), .mode("unsigned")) comparator_4 (
    .a(EX_WriteReg_num), .b(R2_num), .eq(comparator_4_eq));  // open: gt, lt
  Comparator #(.width(5), .mode("unsigned")) comparator_5 (
    .a(R1_num), .b(MEM_WriteReg_num), .eq(comparator_5_eq));  // open: gt, lt
  Comparator #(.width(5), .mode("unsigned")) comparator_6 (
    .a(MEM_WriteReg_num), .b(R2_num), .eq(comparator_6_eq));  // open: gt, lt
  and and_1 (and_1_out, ~comparator_1_eq, EX_RegWrite, comparator_3_eq, \寄存器相关_1_rsused );  // AND_Gate
  and and_2 (and_2_out, ~comparator_2_eq, EX_RegWrite, comparator_4_eq, \寄存器相关_1_rtused );  // AND_Gate
  and and_3 (and_3_out, ~comparator_1_eq, MEM_RegWrite, comparator_5_eq, \寄存器相关_1_rsused );  // AND_Gate
  and and_4 (and_4_out, ~comparator_2_eq, MEM_RegWrite, comparator_6_eq, \寄存器相关_1_rtused );  // AND_Gate
  or or_1 (DataHazard, and_1_out, and_2_out, and_3_out, and_4_out);

  // Notes on the sheet:
  //   rt
endmodule

module \重定向逻辑  (
  input  [31:0] ID_IR,
  input  [31:0] EX_IR,
  input  WB_RegWrite,
  input  [4:0] Rs_num,
  input  [4:0] WB_WriteReg_num,
  input  MEM_RegWrite,
  input  [4:0] MEM_WriteReg_num,
  input  [4:0] Rt_num,
  input  [31:0] Rs,
  input  [31:0] WB_RDin,
  input  [31:0] MEM_ALU,
  input  [31:0] Rt,
  output Load_Use,
  output [31:0] Rs_F,
  output [31:0] Rt_F
);

  wire and_1_out, and_2_out, and_3_out, and_4_out, and_5_out, and_6_out, and_7_out, comparator_1_eq,
       comparator_2_eq, comparator_3_eq, comparator_4_eq, comparator_5_eq, comparator_6_eq, comparator_7_eq,
       comparator_8_eq, comparator_9_eq, \寄存器相关_1_rsused , \寄存器相关_1_rtused , \寄存器相关_2_rsused ,
       \寄存器相关_2_rtused ;
  wire [31:0] multiplexer_1_out, multiplexer_2_out;

  \寄存器相关  \u_寄存器相关_1  (
    .OP0(ID_IR[26]), .OP1(ID_IR[27]), .OP2(ID_IR[28]), .OP3(ID_IR[29]), .OP4(ID_IR[30]), .OP5(ID_IR[31]),
    .F0(ID_IR[0]), .F1(ID_IR[1]), .F2(ID_IR[2]), .F3(ID_IR[3]), .F4(ID_IR[4]), .F5(ID_IR[5]),
    .RsUsed(\寄存器相关_1_rsused ), .RtUsed(\寄存器相关_1_rtused ));
  and and_1 (and_1_out, EX_IR[26], EX_IR[27], ~EX_IR[28], ~EX_IR[29], ~EX_IR[30], EX_IR[31]);  // AND_Gate
  \寄存器相关  \u_寄存器相关_2  (
    .OP0(EX_IR[26]), .OP1(EX_IR[27]), .OP2(EX_IR[28]), .OP3(EX_IR[29]), .OP4(EX_IR[30]), .OP5(EX_IR[31]),
    .F0(EX_IR[0]), .F1(EX_IR[1]), .F2(EX_IR[2]), .F3(EX_IR[3]), .F4(EX_IR[4]), .F5(EX_IR[5]),
    .RsUsed(\寄存器相关_2_rsused ), .RtUsed(\寄存器相关_2_rtused ));
  Comparator #(.width(5), .mode("unsigned")) comparator_1 (
    .a(Rs_num), .b({5{1'b0}}), .eq(comparator_1_eq));  // open: gt, lt
  Comparator #(.width(5), .mode("unsigned")) comparator_2 (
    .a({5{1'b0}}), .b(Rt_num), .eq(comparator_2_eq));  // open: gt, lt
  Comparator #(.width(5), .mode("unsigned")) comparator_3 (
    .a(Rs_num), .b(WB_WriteReg_num), .eq(comparator_3_eq));  // open: gt, lt
  Comparator #(.width(5), .mode("unsigned")) comparator_4 (
    .a(WB_WriteReg_num), .b(Rt_num), .eq(comparator_4_eq));  // open: gt, lt
  Comparator #(.width(5), .mode("unsigned")) comparator_5 (
    .a(Rs_num), .b(MEM_WriteReg_num), .eq(comparator_5_eq));  // open: gt, lt
  Comparator #(.width(5), .mode("unsigned")) comparator_6 (
    .a(MEM_WriteReg_num), .b(Rt_num), .eq(comparator_6_eq));  // open: gt, lt
  Comparator #(.width(5), .mode("unsigned")) comparator_7 (
    .a(ID_IR[25:21]), .b(EX_IR[20:16]), .eq(comparator_7_eq));  // open: gt, lt
  Comparator #(.width(5), .mode("unsigned")) comparator_8 (
    .a(ID_IR[20:16]), .b(EX_IR[20:16]), .eq(comparator_8_eq));  // open: gt, lt
  Comparator #(.width(5), .mode("unsigned")) comparator_9 (
    .a(EX_IR[20:16]), .b({5{1'b0}}), .eq(comparator_9_eq));  // open: gt, lt
  and and_2 (and_2_out, \寄存器相关_1_rsused , comparator_7_eq, ~comparator_9_eq, and_1_out);  // AND_Gate
  and and_3 (and_3_out, \寄存器相关_1_rtused , comparator_8_eq, and_1_out, ~comparator_9_eq);  // AND_Gate
  and and_4 (and_4_out, ~comparator_1_eq, WB_RegWrite, comparator_3_eq, \寄存器相关_2_rsused );  // AND_Gate
  and and_5 (and_5_out, ~comparator_2_eq, WB_RegWrite, comparator_4_eq, \寄存器相关_2_rtused );  // AND_Gate
  and and_6 (and_6_out, ~comparator_1_eq, MEM_RegWrite, comparator_5_eq, \寄存器相关_2_rsused );  // AND_Gate
  and and_7 (and_7_out, ~comparator_2_eq, MEM_RegWrite, comparator_6_eq, \寄存器相关_2_rtused );  // AND_Gate
  Multiplexer #(.select(1), .width(32), .disabled("Z"), .enable("false")) multiplexer_1 (
    .in0(Rs), .in1(WB_RDin), .out(multiplexer_1_out), .sel(and_4_out));
  Multiplexer #(.select(1), .width(32), .disabled("Z"), .enable("false")) multiplexer_2 (
    .in0(Rt), .in1(WB_RDin), .out(multiplexer_2_out), .sel(and_5_out));
  or or_1 (Load_Use, and_2_out, and_3_out);
  Multiplexer #(.select(1), .width(32), .disabled("Z"), .enable("false")) multiplexer_3 (
    .in0(multiplexer_2_out), .in1(MEM_ALU), .out(Rt_F), .sel(and_7_out));
  Multiplexer #(.select(1), .width(32), .disabled("Z"), .enable("false")) multiplexer_4 (
    .in0(multiplexer_1_out), .in1(MEM_ALU), .out(Rs_F), .sel(and_6_out));

  // Notes on the sheet:
  //   rs
  //   rt
  //   Load
endmodule
module BTB (
  input  CLK,
  input  EX_Branch,
  input  EX_BranchTaken,
  input  [31:0] PC,
  input  [31:0] EX_BranchAddr,
  input  [31:0] EX_PC,
  output [31:0] JumpAddr,
  output PredictJump
);

  wire Add, and_17_out, B0, B1, B2, B3, B4, B5, B6, B7, comparator_1_eq, comparator_2_eq, comparator_3_eq,
       comparator_4_eq, comparator_5_eq, comparator_6_eq, comparator_7_eq, comparator_8_eq, comparator_9_eq,
       comparator_10_eq, comparator_11_eq, comparator_12_eq, comparator_13_eq, comparator_14_eq,
       comparator_15_eq, comparator_16_eq, eli0, eli1, eli2, eli3, eli4, eli5, eli6, eli7, Feedback, full,
       Hit, L0, L1, L2, L3, L4, L5, L6, L7, Miss, not_1_out, not_2_out, not_3_out, not_4_out, not_5_out,
       not_6_out, not_7_out, not_8_out, not_10_out, or_1_out, or_2_out, or_3_out, or_4_out, or_5_out,
       or_6_out, or_7_out, or_8_out, or_9_out, or_10_out, or_11_out, or_12_out, or_13_out, or_14_out,
       or_15_out, or_16_out, Pr0, Pr1, Pr2, Pr3, Pr4, Pr5, Pr6, Pr7, valid0, valid1, valid2, valid3, valid4,
       valid5, valid6, valid7;
  wire [0:0] register_25_q, register_26_q, register_27_q, register_28_q, register_29_q, register_30_q,
       register_31_q, register_32_q;
  wire [1:0] fsm_1_b, fsm_2_b, fsm_3_b, fsm_4_b, fsm_5_b, fsm_6_b, fsm_7_b, fsm_8_b, multiplexer_1_out,
       multiplexer_2_out, multiplexer_3_out, multiplexer_4_out, multiplexer_5_out, multiplexer_6_out,
       multiplexer_7_out, multiplexer_8_out, offset;
  wire [2:0] max, max_1_max_num, max_2_max_num, max_3_max_num, max_4_max_num, max_5_max_num, max_6_max_num,
       multiplexer_9_out, priority_encoder_1_out, vacancy;
  wire [7:0] DataOut;
  wire [31:0] LRU0, LRU1, LRU2, LRU3, LRU4, LRU5, LRU6, LRU7, max_1_max, max_2_max, max_3_max, max_4_max,
       max_5_max, max_6_max, register_17_q, register_18_q, register_19_q, register_20_q, register_21_q,
       register_22_q, register_23_q, register_24_q, tag0, tag1, tag2, tag3, tag4, tag5, tag6, tag7;

  Register #(.width(1), .trigger("rising"), .Select("low")) register_1 (
    .D(1'b1), .en(eli0), .Q(valid0), .clk(CLK));  // open: clr
  Register #(.width(1), .trigger("rising"), .Select("low")) register_2 (
    .D(1'b1), .en(eli1), .Q(valid1), .clk(CLK));  // open: clr
  Register #(.width(1), .trigger("rising"), .Select("low")) register_3 (
    .D(1'b1), .en(eli2), .Q(valid2), .clk(CLK));  // open: clr
  Register #(.width(1), .trigger("rising"), .Select("low")) register_4 (
    .D(1'b1), .en(eli3), .Q(valid3), .clk(CLK));  // open: clr
  Register #(.width(1), .trigger("rising"), .Select("low")) register_5 (
    .D(1'b1), .en(eli4), .Q(valid4), .clk(CLK));  // open: clr
  Register #(.width(1), .trigger("rising"), .Select("low")) register_6 (
    .D(1'b1), .en(eli5), .Q(valid5), .clk(CLK));  // open: clr
  Register #(.width(1), .trigger("rising"), .Select("low")) register_7 (
    .D(1'b1), .en(eli6), .Q(valid6), .clk(CLK));  // open: clr
  Register #(.width(1), .trigger("rising"), .Select("low")) register_8 (
    .D(1'b1), .en(eli7), .Q(valid7), .clk(CLK));  // open: clr
  Register #(.width(32), .trigger("rising"), .Select("low")) register_9 (
    .D(EX_PC), .en(eli0), .Q(tag0), .clk(CLK));  // open: clr
  Register #(.width(32), .trigger("rising"), .Select("low")) register_10 (
    .D(EX_PC), .en(eli1), .Q(tag1), .clk(CLK));  // open: clr
  Register #(.width(32), .trigger("rising"), .Select("low")) register_11 (
    .D(EX_PC), .en(eli2), .Q(tag2), .clk(CLK));  // open: clr
  Register #(.width(32), .trigger("rising"), .Select("low")) register_12 (
    .D(EX_PC), .en(eli3), .Q(tag3), .clk(CLK));  // open: clr
  Register #(.width(32), .trigger("rising"), .Select("low")) register_13 (
    .D(EX_PC), .en(eli4), .Q(tag4), .clk(CLK));  // open: clr
  Register #(.width(32), .trigger("rising"), .Select("low")) register_14 (
    .D(EX_PC), .en(eli5), .Q(tag5), .clk(CLK));  // open: clr
  Register #(.width(32), .trigger("rising"), .Select("low")) register_15 (
    .D(EX_PC), .en(eli6), .Q(tag6), .clk(CLK));  // open: clr
  Register #(.width(32), .trigger("rising"), .Select("low")) register_16 (
    .D(EX_PC), .en(eli7), .Q(tag7), .clk(CLK));  // open: clr
  or or_1 (or_1_out, L0, eli0);
  or or_2 (or_2_out, L1, eli1);
  or or_3 (or_3_out, L2, eli2);
  or or_4 (or_4_out, L3, eli3);
  or or_5 (or_5_out, L4, eli4);
  or or_6 (or_6_out, L5, eli5);
  or or_7 (or_7_out, L6, eli6);
  or or_8 (or_8_out, L7, eli7);
  Counter #(.width(32), .max('hffffffff), .ongoal("wrap"), .trigger("rising"), .behavior("new")) counter_1 (
    .load(or_1_out), .D({32{1'b0}}), .Q(LRU0), .clk(CLK));  // open: count, carry, clr, preset, down
  Counter #(.width(32), .max('hffffffff), .ongoal("wrap"), .trigger("rising"), .behavior("new")) counter_2 (
    .load(or_2_out), .D({32{1'b0}}), .Q(LRU1), .clk(CLK));  // open: count, carry, clr, preset, down
  Counter #(.width(32), .max('hffffffff), .ongoal("wrap"), .trigger("rising"), .behavior("new")) counter_3 (
    .load(or_3_out), .D({32{1'b0}}), .Q(LRU2), .clk(CLK));  // open: count, carry, clr, preset, down
  Counter #(.width(32), .max('hffffffff), .ongoal("wrap"), .trigger("rising"), .behavior("new")) counter_4 (
    .load(or_4_out), .D({32{1'b0}}), .Q(LRU3), .clk(CLK));  // open: count, carry, clr, preset, down
  Counter #(.width(32), .max('hffffffff), .ongoal("wrap"), .trigger("rising"), .behavior("new")) counter_5 (
    .load(or_5_out), .D({32{1'b0}}), .Q(LRU4), .clk(CLK));  // open: count, carry, clr, preset, down
  Counter #(.width(32), .max('hffffffff), .ongoal("wrap"), .trigger("rising"), .behavior("new")) counter_6 (
    .load(or_6_out), .D({32{1'b0}}), .Q(LRU5), .clk(CLK));  // open: count, carry, clr, preset, down
  Counter #(.width(32), .max('hffffffff), .ongoal("wrap"), .trigger("rising"), .behavior("new")) counter_7 (
    .load(or_7_out), .D({32{1'b0}}), .Q(LRU6), .clk(CLK));  // open: count, carry, clr, preset, down
  Counter #(.width(32), .max('hffffffff), .ongoal("wrap"), .trigger("rising"), .behavior("new")) counter_8 (
    .load(or_8_out), .D({32{1'b0}}), .Q(LRU7), .clk(CLK));  // open: count, carry, clr, preset, down
  or or_9 (or_9_out, eli0, B0);
  or or_10 (or_10_out, eli1, B1);
  or or_11 (or_11_out, eli2, B2);
  or or_12 (or_12_out, eli3, B3);
  or or_13 (or_13_out, eli4, B4);
  or or_14 (or_14_out, eli5, B5);
  or or_15 (or_15_out, eli6, B6);
  or or_16 (or_16_out, eli7, B7);
  Register #(.width(32), .trigger("rising"), .Select("low")) register_17 (
    .D(EX_BranchAddr), .en(or_9_out), .Q(register_17_q), .clk(CLK));  // open: clr
  assign JumpAddr = L0 ? register_17_q : 32'bz;  // Controlled_Buffer controlled_buffer_1
  assign JumpAddr = L1 ? register_18_q : 32'bz;  // Controlled_Buffer controlled_buffer_2
  Register #(.width(32), .trigger("rising"), .Select("low")) register_18 (
    .D(EX_BranchAddr), .en(or_10_out), .Q(register_18_q), .clk(CLK));  // open: clr
  assign JumpAddr = L2 ? register_19_q : 32'bz;  // Controlled_Buffer controlled_buffer_3
  Register #(.width(32), .trigger("rising"), .Select("low")) register_19 (
    .D(EX_BranchAddr), .en(or_11_out), .Q(register_19_q), .clk(CLK));  // open: clr
  assign JumpAddr = L3 ? register_20_q : 32'bz;  // Controlled_Buffer controlled_buffer_4
  Register #(.width(32), .trigger("rising"), .Select("low")) register_20 (
    .D(EX_BranchAddr), .en(or_12_out), .Q(register_20_q), .clk(CLK));  // open: clr
  assign JumpAddr = L4 ? register_21_q : 32'bz;  // Controlled_Buffer controlled_buffer_5
  Register #(.width(32), .trigger("rising"), .Select("low")) register_21 (
    .D(EX_BranchAddr), .en(or_13_out), .Q(register_21_q), .clk(CLK));  // open: clr
  Register #(.width(32), .trigger("rising"), .Select("low")) register_22 (
    .D(EX_BranchAddr), .en(or_14_out), .Q(register_22_q), .clk(CLK));  // open: clr
  assign JumpAddr = L5 ? register_22_q : 32'bz;  // Controlled_Buffer controlled_buffer_6
  assign JumpAddr = L6 ? register_23_q : 32'bz;  // Controlled_Buffer controlled_buffer_7
  Register #(.width(32), .trigger("rising"), .Select("low")) register_23 (
    .D(EX_BranchAddr), .en(or_15_out), .Q(register_23_q), .clk(CLK));  // open: clr
  Register #(.width(32), .trigger("rising"), .Select("low")) register_24 (
    .D(EX_BranchAddr), .en(or_16_out), .Q(register_24_q), .clk(CLK));  // open: clr
  assign JumpAddr = L7 ? register_24_q : 32'bz;  // Controlled_Buffer controlled_buffer_8
  Multiplexer #(.select(1), .width(2), .disabled("Z"), .enable("false")) multiplexer_1 (
    .in0(fsm_1_b), .in1({EX_BranchTaken, 1'b1}), .out(multiplexer_1_out), .sel(eli0));
  Multiplexer #(.select(1), .width(2), .disabled("Z"), .enable("false")) multiplexer_2 (
    .in0(fsm_2_b), .in1({EX_BranchTaken, 1'b1}), .out(multiplexer_2_out), .sel(eli1));
  Multiplexer #(.select(1), .width(2), .disabled("Z"), .enable("false")) multiplexer_3 (
    .in0(fsm_3_b), .in1({EX_BranchTaken, 1'b1}), .out(multiplexer_3_out), .sel(eli2));
  Multiplexer #(.select(1), .width(2), .disabled("Z"), .enable("false")) multiplexer_4 (
    .in0(fsm_4_b), .in1({EX_BranchTaken, 1'b1}), .out(multiplexer_4_out), .sel(eli3));
  Multiplexer #(.select(1), .width(2), .disabled("Z"), .enable("false")) multiplexer_5 (
    .in0(fsm_5_b), .in1({EX_BranchTaken, 1'b1}), .out(multiplexer_5_out), .sel(eli4));
  Multiplexer #(.select(1), .width(2), .disabled("Z"), .enable("false")) multiplexer_6 (
    .in0(fsm_6_b), .in1({EX_BranchTaken, 1'b1}), .out(multiplexer_6_out), .sel(eli5));
  Multiplexer #(.select(1), .width(2), .disabled("Z"), .enable("false")) multiplexer_7 (
    .in0(fsm_7_b), .in1({EX_BranchTaken, 1'b1}), .out(multiplexer_7_out), .sel(eli6));
  Multiplexer #(.select(1), .width(2), .disabled("Z"), .enable("false")) multiplexer_8 (
    .in0(fsm_8_b), .in1({EX_BranchTaken, 1'b1}), .out(multiplexer_8_out), .sel(eli7));
  Register #(.width(2), .trigger("rising"), .Select("low")) register_25 (
    .D(multiplexer_1_out), .en(or_9_out), .Q({Pr0, register_25_q[0]}), .clk(CLK));  // open: clr
  Register #(.width(2), .trigger("rising"), .Select("low")) register_26 (
    .D(multiplexer_2_out), .en(or_10_out), .Q({Pr1, register_26_q[0]}), .clk(CLK));  // open: clr
  Register #(.width(2), .trigger("rising"), .Select("low")) register_27 (
    .D(multiplexer_3_out), .en(or_11_out), .Q({Pr2, register_27_q[0]}), .clk(CLK));  // open: clr
  Register #(.width(2), .trigger("rising"), .Select("low")) register_28 (
    .D(multiplexer_4_out), .en(or_12_out), .Q({Pr3, register_28_q[0]}), .clk(CLK));  // open: clr
  Register #(.width(2), .trigger("rising"), .Select("low")) register_29 (
    .D(multiplexer_5_out), .en(or_13_out), .Q({Pr4, register_29_q[0]}), .clk(CLK));  // open: clr
  Register #(.width(2), .trigger("rising"), .Select("low")) register_30 (
    .D(multiplexer_6_out), .en(or_14_out), .Q({Pr5, register_30_q[0]}), .clk(CLK));  // open: clr
  Register #(.width(2), .trigger("rising"), .Select("low")) register_31 (
    .D(multiplexer_7_out), .en(or_15_out), .Q({Pr6, register_31_q[0]}), .clk(CLK));  // open: clr
  Register #(.width(2), .trigger("rising"), .Select("low")) register_32 (
    .D(multiplexer_8_out), .en(or_16_out), .Q({Pr7, register_32_q[0]}), .clk(CLK));  // open: clr
  FSM fsm_1 (.EX_BranchTaken(EX_BranchTaken), .A({Pr0, register_25_q[0]}), .B(fsm_1_b));
  FSM fsm_2 (.EX_BranchTaken(EX_BranchTaken), .A({Pr1, register_26_q[0]}), .B(fsm_2_b));
  FSM fsm_3 (.EX_BranchTaken(EX_BranchTaken), .A({Pr2, register_27_q[0]}), .B(fsm_3_b));
  FSM fsm_4 (.EX_BranchTaken(EX_BranchTaken), .A({Pr3, register_28_q[0]}), .B(fsm_4_b));
  FSM fsm_5 (.EX_BranchTaken(EX_BranchTaken), .A({Pr4, register_29_q[0]}), .B(fsm_5_b));
  FSM fsm_6 (.EX_BranchTaken(EX_BranchTaken), .A({Pr5, register_30_q[0]}), .B(fsm_6_b));
  FSM fsm_7 (.EX_BranchTaken(EX_BranchTaken), .A({Pr6, register_31_q[0]}), .B(fsm_7_b));
  FSM fsm_8 (.EX_BranchTaken(EX_BranchTaken), .A({Pr7, register_32_q[0]}), .B(fsm_8_b));
  Comparator #(.width(32), .mode("unsigned")) comparator_1 (.a(tag0), .b(PC), .eq(comparator_1_eq));  // open: gt, lt
  Comparator #(.width(32), .mode("unsigned")) comparator_2 (.a(tag1), .b(PC), .eq(comparator_2_eq));  // open: gt, lt
  Comparator #(.width(32), .mode("unsigned")) comparator_3 (.a(tag2), .b(PC), .eq(comparator_3_eq));  // open: gt, lt
  Comparator #(.width(32), .mode("unsigned")) comparator_4 (.a(tag3), .b(PC), .eq(comparator_4_eq));  // open: gt, lt
  Comparator #(.width(32), .mode("unsigned")) comparator_5 (.a(tag4), .b(PC), .eq(comparator_5_eq));  // open: gt, lt
  Comparator #(.width(32), .mode("unsigned")) comparator_6 (.a(tag5), .b(PC), .eq(comparator_6_eq));  // open: gt, lt
  Comparator #(.width(32), .mode("unsigned")) comparator_7 (.a(tag6), .b(PC), .eq(comparator_7_eq));  // open: gt, lt
  Comparator #(.width(32), .mode("unsigned")) comparator_8 (.a(tag7), .b(PC), .eq(comparator_8_eq));  // open: gt, lt
  and and_1 (L0, comparator_1_eq, valid0);
  and and_2 (L1, comparator_2_eq, valid0);
  and and_3 (L2, comparator_3_eq, valid0);
  and and_4 (L3, comparator_4_eq, valid0);
  and and_5 (L4, comparator_5_eq, valid0);
  and and_6 (L5, comparator_6_eq, valid0);
  and and_7 (L6, comparator_7_eq, valid0);
  and and_8 (L7, comparator_8_eq, valid0);
  Comparator #(.width(32), .mode("unsigned")) comparator_9 (.a(tag0), .b(EX_PC), .eq(comparator_9_eq));  // open: gt, lt
  Comparator #(.width(32), .mode("unsigned")) comparator_10 (
    .a(tag1), .b(EX_PC), .eq(comparator_10_eq));  // open: gt, lt
  Comparator #(.width(32), .mode("unsigned")) comparator_11 (
    .a(tag2), .b(EX_PC), .eq(comparator_11_eq));  // open: gt, lt
  Comparator #(.width(32), .mode("unsigned")) comparator_12 (
    .a(tag3), .b(EX_PC), .eq(comparator_12_eq));  // open: gt, lt
  Comparator #(.width(32), .mode("unsigned")) comparator_13 (
    .a(tag4), .b(EX_PC), .eq(comparator_13_eq));  // open: gt, lt
  Comparator #(.width(32), .mode("unsigned")) comparator_14 (
    .a(tag5), .b(EX_PC), .eq(comparator_14_eq));  // open: gt, lt
  Comparator #(.width(32), .mode("unsigned")) comparator_15 (
    .a(tag6), .b(EX_PC), .eq(comparator_15_eq));  // open: gt, lt
  Comparator #(.width(32), .mode("unsigned")) comparator_16 (
    .a(tag7), .b(EX_PC), .eq(comparator_16_eq));  // open: gt, lt
  and and_9 (B0, comparator_9_eq, valid0, EX_Branch);
  and and_10 (B1, comparator_10_eq, valid0, EX_Branch);
  and and_11 (B2, comparator_11_eq, valid0, EX_Branch);
  and and_12 (B3, comparator_12_eq, valid0, EX_Branch);
  and and_13 (B4, comparator_13_eq, valid0, EX_Branch);
  and and_14 (B5, comparator_14_eq, valid0, EX_Branch);
  and and_15 (B6, comparator_15_eq, valid0, EX_Branch);
  and and_16 (B7, comparator_16_eq, valid0, EX_Branch);
  MAX max_1 (.Y(LRU1), .X(LRU0), .Y_num(3'b001), .X_num(3'b000), .MAX(max_1_max), .Max_num(max_1_max_num));
  MAX max_2 (.Y(LRU3), .X(LRU2), .Y_num(3'b011), .X_num(3'b010), .MAX(max_2_max), .Max_num(max_2_max_num));
  MAX max_3 (.Y(LRU5), .X(LRU4), .Y_num(3'b101), .X_num(3'b100), .MAX(max_3_max), .Max_num(max_3_max_num));
  MAX max_4 (.Y(LRU7), .X(LRU6), .Y_num(3'b111), .X_num(3'b110), .MAX(max_4_max), .Max_num(max_4_max_num));
  not not_1 (not_1_out, valid7);
  not not_2 (not_2_out, valid6);
  not not_3 (not_3_out, valid5);
  not not_4 (not_4_out, valid4);
  not not_5 (not_5_out, valid3);
  not not_6 (not_6_out, valid2);
  not not_7 (not_7_out, valid1);
  not not_8 (not_8_out, valid0);
  Demultiplexer #(.select(3), .width(1), .tristate("false"), .disabled("Z"), .enable("false")) demultiplexer_1 (
    .out0(eli0), .out1(eli1), .out2(eli2), .out3(eli3), .out4(eli4), .out5(eli5), .out6(eli6), .out7(eli7),
    .in(and_17_out), .sel(multiplexer_9_out));
  and and_17 (and_17_out, 1'b1, Add);
  Multiplexer #(.select(1), .width(3), .disabled("Z"), .enable("false")) multiplexer_9 (
    .in0(vacancy), .in1(max), .out(multiplexer_9_out), .sel(full));
  BitSelector #(.width(32), .group(8)) bitselector_1 (.in(JumpAddr), .out(DataOut), .sel(offset));
  or or_17 (Hit, L0, L1, L2, L3, L4, L5, L6, L7);
  not not_9 (Miss, Hit);
  or or_18 (Feedback, B0, B1, B2, B3, B4, B5, B6, B7);
  not not_10 (not_10_out, Feedback);
  MAX max_5 (
    .Y(max_2_max), .X(max_1_max), .Y_num(max_2_max_num), .X_num(max_1_max_num), .MAX(max_5_max),
    .Max_num(max_5_max_num));
  MAX max_6 (
    .Y(max_4_max), .X(max_3_max), .Y_num(max_4_max_num), .X_num(max_3_max_num), .MAX(max_6_max),
    .Max_num(max_6_max_num));
  and and_18 (full, valid0, valid1, valid2, valid3, valid4, valid5, valid6, valid7);
  assign vacancy = ~priority_encoder_1_out;  // NOT_Gate not_11, 3 bits wide
  Priority_Encoder #(.select(3), .disabled("Z")) priority_encoder_1 (
    .in0(not_1_out), .in1(not_2_out), .in2(not_3_out), .in3(not_4_out), .in4(not_5_out), .in5(not_6_out),
    .in6(not_7_out), .in7(not_8_out), .out(priority_encoder_1_out));  // open: gs, en_out, en_in
  and and_19 (Add, not_10_out, EX_Branch);
  MAX max_7 (.Y(max_6_max), .X(max_5_max), .Y_num(max_6_max_num), .X_num(max_5_max_num), .Max_num(max));  // open: MAX
  assign PredictJump = L0 ? Pr0 : 1'bz;  // Controlled_Buffer controlled_buffer_9
  assign PredictJump = L1 ? Pr1 : 1'bz;  // Controlled_Buffer controlled_buffer_10
  assign PredictJump = L2 ? Pr2 : 1'bz;  // Controlled_Buffer controlled_buffer_11
  assign PredictJump = L3 ? Pr3 : 1'bz;  // Controlled_Buffer controlled_buffer_12
  assign PredictJump = L4 ? Pr4 : 1'bz;  // Controlled_Buffer controlled_buffer_13
  assign PredictJump = L5 ? Pr5 : 1'bz;  // Controlled_Buffer controlled_buffer_14
  assign PredictJump = L6 ? Pr6 : 1'bz;  // Controlled_Buffer controlled_buffer_15
  assign PredictJump = L7 ? Pr7 : 1'bz;  // Controlled_Buffer controlled_buffer_16
  Pull_Resistor #(.pull(0)) pull_resistor_1 (.node(PredictJump));

  // Other names for the same wires on the sheet: Initial[1] = EX_BranchTaken; SlotData[31:0] = JumpAddr
endmodule

module MAX (
  input  [31:0] Y,
  input  [31:0] X,
  input  [2:0] Y_num,
  input  [2:0] X_num,
  output [31:0] MAX,
  output [2:0] Max_num
);

  wire comparator_1_eq, comparator_1_gt, or_1_out;

  Multiplexer #(.select(1), .width(32), .disabled("Z"), .enable("false")) multiplexer_1 (
    .in0(Y), .in1(X), .out(MAX), .sel(or_1_out));
  Comparator #(.width(32), .mode("unsigned")) comparator_1 (
    .a(X), .b(Y), .gt(comparator_1_gt), .eq(comparator_1_eq));  // open: lt
  or or_1 (or_1_out, comparator_1_gt, comparator_1_eq);
  Multiplexer #(.select(1), .width(3), .disabled("Z"), .enable("false")) multiplexer_2 (
    .in0(Y_num), .in1(X_num), .out(Max_num), .sel(or_1_out));

  // Notes on the sheet:
  //   输出两个输入中的较大值，并输出较大值的3位编号
endmodule

module FSM (
  input  [1:0] A,
  input  EX_BranchTaken,
  output [1:0] B
);

  wire and_1_out, and_2_out, and_3_out, and_4_out, not_1_out, not_2_out, not_3_out, not_4_out, not_5_out;

  not not_1 (not_1_out, A[0]);
  not not_2 (not_2_out, A[1]);
  not not_3 (not_3_out, A[0]);
  not not_4 (not_4_out, A[0]);
  not not_5 (not_5_out, EX_BranchTaken);
  and and_1 (and_1_out, A[0], EX_BranchTaken);
  and and_2 (and_2_out, A[1], not_1_out);
  and and_3 (and_3_out, not_2_out, not_3_out, EX_BranchTaken);
  and and_4 (and_4_out, A[1], not_4_out, not_5_out);
  or or_1 (B[1], and_1_out, and_2_out);
  or or_2 (B[0], and_3_out, and_4_out);
endmodule
